// Digital circuit BTB.dig as structural Verilog
module BTB (
  input  [3:0] id,
  input  [11:0] tag,
  input  E,
  input  C,
  input  [1:0] pred,
  input  [31:0] tar,
  input  [3:0] R_id,
  input  [11:0] R_tag,
  input  V_in,
  output [31:0] tar_O,
  output J,
  output [1:0] pred_O,
  output V
);

  wire comparator_1_eq, F_V;
  wire [11:0] tag_O;

  Comparator #(.Bits(12)) comparator_1 (.a(tag_O), .b(R_tag), .eq(comparator_1_eq));  // open: gt, lt
  and and_1 (V, F_V, comparator_1_eq);
  and and_2 (J, comparator_1_eq, pred_O[1], F_V);
  RegisterFile #(.AddrBits(4), .Bits(47)) registerfile_1 (
    .Din({V_in, pred, tag, tar}), .we(E), .Rw(id), .C(C), .Ra(R_id), .Rb(4'b0000),
    .Da({F_V, pred_O, tag_O, tar_O}));  // open: Db

  // Other names for the same wires on the sheet: target_O[31:0] = tar_O; predict_O[1:0] = pred_O; index[3:0] = id;
  //   predict[1:0] = pred; target[31:0] = tar
endmodule
