// Digital circuit ROB-gen.dig as structural Verilog
module ROB_gen (
  input  [3:0] inst1,
  input  [3:0] com1_id,
  input  E1,
  input  C,
  input  [3:0] com2_id,
  input  [31:0] D2,
  input  [3:0] inst2,
  input  [31:0] D1,
  input  E2,
  input  [7:0] R1,
  input  [7:0] R2,
  input  com1,
  input  com2,
  input  [3:0] ret_id,
  input  [15:0] clr_16,
  input  EX1,
  input  EX2,
  output [31:0] D1_O,
  output [7:0] R1_O,
  output [31:0] D2_O,
  output [7:0] R2_O,
  output W1_O,
  output W2_O,
  output [31:0] DR_O,
  output EX2_O,
  output EX1_O
);

  wire R1_e, R2_e, R3_e, R4_e, R5_e, R6_e, R7_e, R8_e, R9_e, R10_e, R11_e, R12_e, R13_e, R14_e, R15_e, R16_e;
  wire [1:0] R1_M, R2_M, R3_M, R4_M, R5_M, R6_M, R7_M, R8_M, R9_M, R10_M, R11_M, R12_M, R13_M, R14_M, R15_M,
       R16_M;
  wire [15:0] demultiplexer_1_out_0, demultiplexer_2_out_0, demultiplexer_3_out_0;
  wire [41:0] multiplexer_1_out, multiplexer_2_out, multiplexer_3_out, multiplexer_4_out, multiplexer_5_out,
       multiplexer_6_out, multiplexer_7_out, multiplexer_8_out, multiplexer_9_out, multiplexer_10_out,
       multiplexer_11_out, multiplexer_12_out, multiplexer_13_out, multiplexer_14_out, multiplexer_15_out,
       multiplexer_16_out, multiplexer_19_out, R1_t, R2_t, R3, R4, R5, R6, R7, R8, R9, R10, R11, R12, R13,
       R14, R15, R16;

  Multiplexer #(.Selector_Bits(2), .Bits(42)) multiplexer_1 (
    .sel(R1_M), .in_0({EX1, R1, D1, 1'b1}), .in_1({EX2, R2, D2, 1'b1}), .in_2({42{1'b0}}), .in_3({42{1'b0}}),
    .out(multiplexer_1_out));
  Multiplexer #(.Selector_Bits(2), .Bits(42)) multiplexer_2 (
    .sel(R5_M), .in_0({EX1, R1, D1, 1'b1}), .in_1({EX2, R2, D2, 1'b1}), .in_2({42{1'b0}}), .in_3({42{1'b0}}),
    .out(multiplexer_2_out));
  Multiplexer #(.Selector_Bits(2), .Bits(42)) multiplexer_3 (
    .sel(R9_M), .in_0({EX1, R1, D1, 1'b1}), .in_1({EX2, R2, D2, 1'b1}), .in_2({42{1'b0}}), .in_3({42{1'b0}}),
    .out(multiplexer_3_out));
  Multiplexer #(.Selector_Bits(2), .Bits(42)) multiplexer_4 (
    .sel(R13_M), .in_0({EX1, R1, D1, 1'b1}), .in_1({EX2, R2, D2, 1'b1}), .in_2({42{1'b0}}),
    .in_3({42{1'b0}}), .out(multiplexer_4_out));
  Demultiplexer #(.Selector_Bits(4)) demultiplexer_1 (
    .sel(com1_id), .in(com1), .out_0(demultiplexer_1_out_0[15]), .out_1(demultiplexer_1_out_0[14]),
    .out_2(demultiplexer_1_out_0[13]), .out_3(demultiplexer_1_out_0[12]), .out_4(demultiplexer_1_out_0[11]),
    .out_5(demultiplexer_1_out_0[10]), .out_6(demultiplexer_1_out_0[9]), .out_7(demultiplexer_1_out_0[8]),
    .out_8(demultiplexer_1_out_0[7]), .out_9(demultiplexer_1_out_0[6]), .out_10(demultiplexer_1_out_0[5]),
    .out_11(demultiplexer_1_out_0[4]), .out_12(demultiplexer_1_out_0[3]), .out_13(demultiplexer_1_out_0[2]),
    .out_14(demultiplexer_1_out_0[1]), .out_15(demultiplexer_1_out_0[0]));
  Demultiplexer #(.Selector_Bits(4)) demultiplexer_2 (
    .sel(inst1), .in(E1), .out_0(demultiplexer_2_out_0[15]), .out_1(demultiplexer_2_out_0[14]),
    .out_2(demultiplexer_2_out_0[13]), .out_3(demultiplexer_2_out_0[12]), .out_4(demultiplexer_2_out_0[11]),
    .out_5(demultiplexer_2_out_0[10]), .out_6(demultiplexer_2_out_0[9]), .out_7(demultiplexer_2_out_0[8]),
    .out_8(demultiplexer_2_out_0[7]), .out_9(demultiplexer_2_out_0[6]), .out_10(demultiplexer_2_out_0[5]),
    .out_11(demultiplexer_2_out_0[4]), .out_12(demultiplexer_2_out_0[3]), .out_13(demultiplexer_2_out_0[2]),
    .out_14(demultiplexer_2_out_0[1]), .out_15(demultiplexer_2_out_0[0]));
  Register #(.Bits(42)) register_1 (.D(multiplexer_1_out), .C(C), .en(R1_e), .Q(R1_t));
  Register #(.Bits(42)) register_2 (.D(multiplexer_2_out), .C(C), .en(R5_e), .Q(R5));
  Register #(.Bits(42)) register_3 (.D(multiplexer_3_out), .C(C), .en(R9_e), .Q(R9));
  Register #(.Bits(42)) register_4 (.D(multiplexer_4_out), .C(C), .en(R13_e), .Q(R13));
  Demultiplexer #(.Selector_Bits(4)) demultiplexer_3 (
    .sel(com2_id), .in(com2), .out_0(demultiplexer_3_out_0[15]), .out_1(demultiplexer_3_out_0[14]),
    .out_2(demultiplexer_3_out_0[13]), .out_3(demultiplexer_3_out_0[12]), .out_4(demultiplexer_3_out_0[11]),
    .out_5(demultiplexer_3_out_0[10]), .out_6(demultiplexer_3_out_0[9]), .out_7(demultiplexer_3_out_0[8]),
    .out_8(demultiplexer_3_out_0[7]), .out_9(demultiplexer_3_out_0[6]), .out_10(demultiplexer_3_out_0[5]),
    .out_11(demultiplexer_3_out_0[4]), .out_12(demultiplexer_3_out_0[3]), .out_13(demultiplexer_3_out_0[2]),
    .out_14(demultiplexer_3_out_0[1]), .out_15(demultiplexer_3_out_0[0]));
  Demultiplexer #(.Selector_Bits(4)) demultiplexer_4 (
    .sel(inst2), .in(E2), .out_0(R1_M[0]), .out_1(R2_M[0]), .out_2(R3_M[0]), .out_3(R4_M[0]),
    .out_4(R5_M[0]), .out_5(R6_M[0]), .out_6(R7_M[0]), .out_7(R8_M[0]), .out_8(R9_M[0]), .out_9(R10_M[0]),
    .out_10(R11_M[0]), .out_11(R12_M[0]), .out_12(R13_M[0]), .out_13(R14_M[0]), .out_14(R15_M[0]),
    .out_15(R16_M[0]));
  Multiplexer #(.Selector_Bits(2), .Bits(42)) multiplexer_5 (
    .sel(R2_M), .in_0({EX1, R1, D1, 1'b1}), .in_1({EX2, R2, D2, 1'b1}), .in_2({42{1'b0}}), .in_3({42{1'b0}}),
    .out(multiplexer_5_out));
  Register #(.Bits(42)) register_5 (.D(multiplexer_5_out), .C(C), .en(R2_e), .Q(R2_t));
  Multiplexer #(.Selector_Bits(2), .Bits(42)) multiplexer_6 (
    .sel(R6_M), .in_0({EX1, R1, D1, 1'b1}), .in_1({EX2, R2, D2, 1'b1}), .in_2({42{1'b0}}), .in_3({42{1'b0}}),
    .out(multiplexer_6_out));
  Register #(.Bits(42)) register_6 (.D(multiplexer_6_out), .C(C), .en(R6_e), .Q(R6));
  Multiplexer #(.Selector_Bits(2), .Bits(42)) multiplexer_7 (
    .sel(R10_M), .in_0({EX1, R1, D1, 1'b1}), .in_1({EX2, R2, D2, 1'b1}), .in_2({42{1'b0}}),
    .in_3({42{1'b0}}), .out(multiplexer_7_out));
  Register #(.Bits(42)) register_7 (.D(multiplexer_7_out), .C(C), .en(R10_e), .Q(R10));
  Multiplexer #(.Selector_Bits(2), .Bits(42)) multiplexer_8 (
    .sel(R14_M), .in_0({EX1, R1, D1, 1'b1}), .in_1({EX2, R2, D2, 1'b1}), .in_2({42{1'b0}}),
    .in_3({42{1'b0}}), .out(multiplexer_8_out));
  Register #(.Bits(42)) register_8 (.D(multiplexer_8_out), .C(C), .en(R14_e), .Q(R14));
  assign {R1_M[1], R2_M[1], R3_M[1], R4_M[1], R5_M[1], R6_M[1], R7_M[1], R8_M[1], R9_M[1], R10_M[1], R11_M[1], R12_M[1], R13_M[1], R14_M[1], R15_M[1], R16_M[1]} = demultiplexer_3_out_0 | {clr_16[0], clr_16[1], clr_16[2], clr_16[3], clr_16[4], clr_16[5], clr_16[6], clr_16[7], clr_16[8], clr_16[9], clr_16[10], clr_16[11], clr_16[12], clr_16[13], clr_16[14], clr_16[15]} | demultiplexer_1_out_0;  // Or or_1, 16 bits wide
  assign {R1_e, R2_e, R3_e, R4_e, R5_e, R6_e, R7_e, R8_e, R9_e, R10_e, R11_e, R12_e, R13_e, R14_e, R15_e, R16_e} = demultiplexer_3_out_0 | demultiplexer_1_out_0 | {clr_16[0], clr_16[1], clr_16[2], clr_16[3], clr_16[4], clr_16[5], clr_16[6], clr_16[7], clr_16[8], clr_16[9], clr_16[10], clr_16[11], clr_16[12], clr_16[13], clr_16[14], clr_16[15]} | {R1_M[0], R2_M[0], R3_M[0], R4_M[0], R5_M[0], R6_M[0], R7_M[0], R8_M[0], R9_M[0], R10_M[0], R11_M[0], R12_M[0], R13_M[0], R14_M[0], R15_M[0], R16_M[0]} | demultiplexer_2_out_0;  // Or or_2, 16 bits wide
  Multiplexer #(.Selector_Bits(2), .Bits(42)) multiplexer_9 (
    .sel(R3_M), .in_0({EX1, R1, D1, 1'b1}), .in_1({EX2, R2, D2, 1'b1}), .in_2({42{1'b0}}), .in_3({42{1'b0}}),
    .out(multiplexer_9_out));
  Multiplexer #(.Selector_Bits(2), .Bits(42)) multiplexer_10 (
    .sel(R7_M), .in_0({EX1, R1, D1, 1'b1}), .in_1({EX2, R2, D2, 1'b1}), .in_2({42{1'b0}}), .in_3({42{1'b0}}),
    .out(multiplexer_10_out));
  Multiplexer #(.Selector_Bits(2), .Bits(42)) multiplexer_11 (
    .sel(R11_M), .in_0({EX1, R1, D1, 1'b1}), .in_1({EX2, R2, D2, 1'b1}), .in_2({42{1'b0}}),
    .in_3({42{1'b0}}), .out(multiplexer_11_out));
  Multiplexer #(.Selector_Bits(2), .Bits(42)) multiplexer_12 (
    .sel(R15_M), .in_0({EX1, R1, D1, 1'b1}), .in_1({EX2, R2, D2, 1'b1}), .in_2({42{1'b0}}),
    .in_3({42{1'b0}}), .out(multiplexer_12_out));
  Register #(.Bits(42)) register_9 (.D(multiplexer_9_out), .C(C), .en(R3_e), .Q(R3));
  Register #(.Bits(42)) register_10 (.D(multiplexer_10_out), .C(C), .en(R7_e), .Q(R7));
  Register #(.Bits(42)) register_11 (.D(multiplexer_11_out), .C(C), .en(R11_e), .Q(R11));
  Register #(.Bits(42)) register_12 (.D(multiplexer_12_out), .C(C), .en(R15_e), .Q(R15));
  Multiplexer #(.Selector_Bits(2), .Bits(42)) multiplexer_13 (
    .sel(R4_M), .in_0({EX1, R1, D1, 1'b1}), .in_1({EX2, R2, D2, 1'b1}), .in_2({42{1'b0}}), .in_3({42{1'b0}}),
    .out(multiplexer_13_out));
  Register #(.Bits(42)) register_13 (.D(multiplexer_13_out), .C(C), .en(R4_e), .Q(R4));
  Multiplexer #(.Selector_Bits(2), .Bits(42)) multiplexer_14 (
    .sel(R8_M), .in_0({EX1, R1, D1, 1'b1}), .in_1({EX2, R2, D2, 1'b1}), .in_2({42{1'b0}}), .in_3({42{1'b0}}),
    .out(multiplexer_14_out));
  Register #(.Bits(42)) register_14 (.D(multiplexer_14_out), .C(C), .en(R8_e), .Q(R8));
  Multiplexer #(.Selector_Bits(2), .Bits(42)) multiplexer_15 (
    .sel(R12_M), .in_0({EX1, R1, D1, 1'b1}), .in_1({EX2, R2, D2, 1'b1}), .in_2({42{1'b0}}),
    .in_3({42{1'b0}}), .out(multiplexer_15_out));
  Register #(.Bits(42)) register_15 (.D(multiplexer_15_out), .C(C), .en(R12_e), .Q(R12));
  Multiplexer #(.Selector_Bits(2), .Bits(42)) multiplexer_16 (
    .sel(R16_M), .in_0({EX1, R1, D1, 1'b1}), .in_1({EX2, R2, D2, 1'b1}), .in_2({42{1'b0}}),
    .in_3({42{1'b0}}), .out(multiplexer_16_out));
  Register #(.Bits(42)) register_16 (.D(multiplexer_16_out), .C(C), .en(R16_e), .Q(R16));
  Multiplexer #(.Selector_Bits(4), .Bits(42)) multiplexer_17 (
    .sel(com1_id), .in_0(R1_t), .in_1(R2_t), .in_2(R3), .in_3(R4), .in_4(R5), .in_5(R6), .in_6(R7),
    .in_7(R8), .in_8(R9), .in_9(R10), .in_10(R11), .in_11(R12), .in_12(R13), .in_13(R14), .in_14(R15),
    .in_15(R16), .out({EX1_O, R1_O, D1_O, W1_O}));
  Multiplexer #(.Selector_Bits(4), .Bits(42)) multiplexer_18 (
    .sel(com2_id), .in_0(R1_t), .in_1(R2_t), .in_2(R3), .in_3(R4), .in_4(R5), .in_5(R6), .in_6(R7),
    .in_7(R8), .in_8(R9), .in_9(R10), .in_10(R11), .in_11(R12), .in_12(R13), .in_13(R14), .in_14(R15),
    .in_15(R16), .out({EX2_O, R2_O, D2_O, W2_O}));
  Multiplexer #(.Selector_Bits(4), .Bits(42)) multiplexer_19 (
    .sel(ret_id), .in_0(R1_t), .in_1(R2_t), .in_2(R3), .in_3(R4), .in_4(R5), .in_5(R6), .in_6(R7), .in_7(R8),
    .in_8(R9), .in_9(R10), .in_10(R11), .in_11(R12), .in_12(R13), .in_13(R14), .in_14(R15), .in_15(R16),
    .out({multiplexer_19_out[41:33], DR_O, multiplexer_19_out[0]}));

  // Other names for the same wires on the sheet: D3_O[31:0] = DR_O;
  //   clr_16_t[15:0] = {clr_16[0], clr_16[1], clr_16[2], clr_16[3], clr_16[4], clr_16[5], clr_16[6], clr_16[7], clr_16[8], clr_16[9], clr_16[10], clr_16[11], clr_16[12], clr_16[13], clr_16[14], clr_16[15]};
  //   clri[15:0] = clr_16; L1[41:1] = {EX1, R1, D1}; L2[41:1] = {EX2, R2, D2}; EX1_I = EX1; EX2_I = EX2;
  //   R1_I[7:0] = R1; R2_I[7:0] = R2
endmodule
