// Digital circuit cpu-32.dig as structural Verilog
module cpu_32 (
  input  bus_e,
  input  E,
  input  [31:0] I_D__bus,
  input  [31:0] D_D__bus,
  input  [31:0] I_A__bus,
  input  [31:0] D_A__bus,
  input  INT_nor,
  input  INT_nmk,
  input  run,
  input  I_valid,
  input  D_valid,
  input  C,
  output I_LD,
  output D_LD,
  output D_ST,
  output [1:0] MMU_sel,
  output MMU_str,
  output [2:0] DMA_sel,
  output DMA_str,
  output INT_str,
  output CLK_str,
  output [1:0] CSH_mode,
  output CSH_run,
  output INT_out,
  output [1:0] D_MD
);

  wire alu_32_1_p6, alu_32_1_p9, ALU_A_CLR, ALU_A_CMP, ALU_A_DRD, ALU_A_DRE, ALU_A_FRD, ALU_A_FRE, ALU_A_LD,
       ALU_A_LRD, ALU_A_STD, ALU_A_STF, ALU_A_UUD, ALU_A_UUF, ALU_A_V, ALU_A_VD, ALU_A_VF, ALU_B_CLR,
       ALU_B_CMP, ALU_B_DRD, ALU_B_DRE, ALU_B_FRD, ALU_B_FRE, ALU_B_LD, ALU_B_LRD, ALU_B_STD, ALU_B_STF,
       ALU_B_UUD, ALU_B_UUF, ALU_B_V, ALU_B_VD, ALU_B_VF, ALU_busy, ALU_free, and_1_out, and_2_out,
       and_3_out, and_4_out, and_6_out, and_7_out, and_8_out, and_12_out, and_14_out, and_15_out, and_16_out,
       and_17_out, and_18_out, and_20_out, and_21_out, and_22_out, and_23_out, and_24_out, and_25_out,
       and_26_out, and_27_out, and_28_out, and_29_out, and_30_out, and_31_out, and_32_out, and_33_out,
       and_38_out, and_39_out, and_40_out, and_41_out, and_42_out, and_43_out, and_44_out, and_45_out,
       and_46_out, and_47_out, and_48_out, and_49_out, and_50_out, and_51_out, and_52_out, and_53_out,
       and_56_out, and_57_out, and_59_out, and_62_out, and_63_out, and_64_out, and_65_out, and_66_out,
       and_67_out, and_69_out, and_70_out, and_71_out, and_72_out, and_73_out, and_74_out, and_75_out,
       and_77_out, and_78_out, and_79_out, and_82_out, and_83_out, and_89_out, and_90_out, and_91_out,
       and_92_out, and_93_out, and_94_out, and_95_out, and_96_out, and_97_out, and_98_out, and_99_out,
       and_102_out, and_105_out, and_106_out, and_114_out, and_115_out, and_116_out, and_117_out,
       and_118_out, and_119_out, and_120_out, and_123_out, and_124_out, and_125_out, and_126_out,
       and_128_out, and_129_out, and_130_out, and_132_out, and_133_out, and_134_out, and_135_out,
       and_136_out, and_137_out, and_142_out, and_143_out, and_144_out, and_148_out, and_149_out,
       and_150_out, and_151_out, and_152_out, and_157_out, and_162_out, and_164_out, and_165_out,
       and_166_out, and_167_out, and_168_out, and_169_out, and_170_out, and_171_out, and_172_out,
       and_174_out, and_175_out, and_176_out, and_177_out, and_180_out, bitselector_1_out, BTB_JP,
       BTB_override, C_ct, clr, clr_ep, com1, com1_ep, com1_M, com2, comparator_1_gt, comparator_2_gt,
       comparator_2_lt, comparator_3_eq, comparator_4_eq, CT_ALU__LD, CT_ALU__M, CT_ALU__M2, CT_ALU__WD,
       CT_ALU__WF, CT_BUS__DAG, CT_BUS__DAM, CT_BUS__DAR, CT_BUS__DDG, CT_BUS__DDM, CT_BUS__DDR, CT_BUS__IAG,
       CT_BUS__IAR, CT_BUS__IDM, CT_BUS__IDR, CT_CALL__LD, CT_CALLM, CT_DIR__LD, CT_DIR__M, CT_DIR__MS,
       CT_DISP, CT_FL__W1, CT_FL__W2, CT_FU__EPOCH, CT_FU__MF, CT_ISS__OFL, CT_ISS__OLDB, CT_ISS__ORC,
       CT_ISS__OSC, CT_ISS__OSTB, CT_ISS__UFL, CT_ISS__URA, CT_ISS__URB, CT_ISS__USC, CT_JPU__JP, CT_JPU__LD,
       CT_LDB__LD, CT_MB__LD, CT_MB__OFFM, CT_MB__ST, CT_MVR, CT_OBLOCK, CT_RET__LD, CT_RF__DM, CT_RF__E,
       CT_RF__FLS, CT_RF__PCAE, CT_RF__PCH, CT_RF__PCJ, CT_RF__PCR, CT_RF__PCSE, CT_RF__SCAE, CT_RF__SCD,
       CT_RF__SCSE, CT_RF__SCSRE, CT_RF__SCSS, CT_RF__W1, CT_RF__W2, CT_ROB__EX__E, CT_ROB__FL__STA,
       CT_ROB__FL__STB, CT_ROB__GEN__STA, CT_ROB__GEN__STB, CT_ROB__ST__E, CT_rollback, CT_SC__W1, CT_SC__W2,
       CT_STB__LD, CT_UBTB, CT_USCB, d_ff_16_q, d_ff_17_nq, d_ff_24_q, DC_B_q, dc_e, DC_q, dipswitch_1_out,
       dipswitch_2_out, dipswitch_3_out, dipswitch_6_out, DIR_busy, DIR_CLR, DIR_free, DIR_LD, DIR_RD,
       DIR_ST, DIR_V, dp_e, epoch_DP, epoch_IS, ex_nop, ext_en, Fl_JPU, Fl_JPU__EP, Fl_MEM, FL_MEM__EP, ft_e,
       FT_q, halt_FT_DC_ISS, hlt, id_full, id_manager_1_v, inst_comp_1_a_old, inst_comp_2_a_old,
       inst_comp_3_a_old, inst_comp_4_a_old, inst_comp_5_a_old, inst_comp_6_a_old, inst_comp_7_a_old,
       inst_comp_8_a_old, inst_comp_10_a_old, inst_comp_11_a_old, inst_comp_13_a_old, inst_comp_14_a_old,
       int_run, ISS_B_q, issue, issue_e, issue_e__bf, JPU_A__ST, JPU_BTB__J, JPU_BTB__ST, JPU_BTB__V,
       JPU_CALL, JPU_free, JPU_JP, JPU_LD, JPU_MF, JPU_MFE, JPU_MISS, JPU_RET, kernel_inst, LDB_B__D,
       LDB_B__MF, LDB_B__RD, LDB_B__ST, LDB_busy, LDB_forward, LDB_ldV, LDB_M__EP, LDB_M__V,
       load_buffer_1_p28, load_buffer_1_p29, load_buffer_1_p33, load_buffer_1_p39, load_buffer_1_p40,
       MB_busy, MB_ep, MB_free, MB_LD, MB_ld__e, MB_LDB__LD, MB_MF, MB_MFE, MB_st__e, MB_STB__LD,
       MB_type__st, MEM_AC, MEM_BF__free, MEM_CLR, MEM_EP, MEM_LD, MEM_LD__CLR, MEM_LD__EP, MEM_LD__RD,
       MEM_LD__REC, MEM_RD, MEM_TYPE__ST, mode, multiplexer_2_out, multiplexer_4_out, multiplexer_8_out,
       multiplexer_10_out, multiplexer_12_out, multiplexer_13_out, multiplexer_15_out, multiplexer_16_out,
       multiplexer_17_out, multiplexer_23_out, multiplexer_25_out, multiplexer_29_out, multiplexer_30_out,
       multiplexer_31_out, multiplexer_39_out, multiplexer_44_out, multiplexer_45_out, multiplexer_51_out,
       multiplexer_54_out, multiplexer_55_out, multiplexer_56_out, multiplexer_57_out, multiplexer_58_out,
       multiplexer_59_out, multiplexer_61_out, multiplexer_65_out, multiplexer_66_out, multiplexer_72_out,
       multiplexer_73_out, multiplexer_74_out, multiplexer_75_out, multiplexer_76_out, multiplexer_84_out,
       nand_16_out, nand_17_out, nor_1_out, nor_2_out, nor_5_out, nor_6_out, not_1_out, not_6_out, not_8_out,
       not_9_out, not_10_out, not_11_out, not_12_out, not_13_out, not_14_out, not_15_out, not_17_out,
       not_18_out, not_19_out, not_21_out, not_23_out, not_24_out, not_25_out, not_26_out, not_27_out,
       not_29_out, not_32_out, not_34_out, not_36_out, not_37_out, not_38_out, not_39_out, not_40_out,
       not_43_out, not_44_out, or_3_out, or_4_out, or_5_out, or_6_out, or_15_out, or_17_out, or_18_out,
       or_22_out, or_23_out, or_25_out, or_26_out, or_27_out, or_30_out, or_31_out, or_32_out, or_33_out,
       or_34_out, or_36_out, or_40_out, or_41_out, or_42_out, or_43_out, or_44_out, or_45_out, or_47_out,
       or_49_out, or_50_out, or_51_out, or_52_out, or_53_out, or_54_out, or_55_out, or_56_out, or_57_out,
       or_59_out, or_60_out, or_61_out, or_65_out, or_66_out, or_69_out, priorityencoder_1_any,
       register_15_q, register_16_q, register_17_q, register_24_q, register_25_q, register_26_q,
       register_33_q, register_37_q, register_38_q, register_44_q, register_49_q, register_56_q,
       register_60_q, register_61_q, register_67_q, register_71_q, register_84_q, register_90_q, RET_EPOCH,
       rs_ff_1_nq, rs_ff_1_q, rs_ff_2_nq, rs_ff_2_q, rs_ff_3_nq, rs_ff_4_nq, rs_ff_5_nq, rs_ff_6_nq,
       rs_ff_7_nq, rs_ff_12_q, rs_ff_13_q, rs_ff_14_q, rs_ff_15_q, rs_ff_18_nq, RS_full, STB_busy, STB_M__EP,
       STB_M__V, store_buffer_1_full, V_q, xor_1_out;
  wire [0:0] and_68_out, JPU_BTBPK;
  wire [1:0] and_84_out, and_86_out, and_100_out, and_101_out, bitextender_5_out, bitextender_6_out,
       d_ff_1_q, d_ff_4_q, d_ff_5_q, d_ff_6_q, d_ff_7_q, JPU_BTB__pred, JPU_pred, LDB_M__MD, MB_MD,
       multiplexer_6_out, multiplexer_49_out, multiplexer_70_out, or_19_out, register_8_q, register_42_q,
       register_65_q, STB_M__MD;
  wire [1:1] or_16_out, register_45_q, register_68_q, register_69_q;
  wire [2:0] ALU_A_RM, ALU_B_RM, and_76_out, and_80_out, and_81_out, CT_ISS__UFU, CT_RF__MA, CT_RF__MB,
       CT_RF__SCN, CT_RF__WM, CT_SP__MOF, multiplexer_11_out, multiplexer_37_out, multiplexer_42_out,
       nand_1_out, nand_2_out, nand_4_out, nand_5_out, nand_10_out, nand_11_out, not_16_out, not_20_out,
       not_22_out, register_13_q, register_46_q, register_47_q, store_controller_1_d1_sel,
       store_controller_1_d2_sel, store_controller_2_d1_sel, store_controller_2_d2_sel;
  wire [2:1] nor_3_out;
  wire [3:0] ALU_A_INST, ALU_B_INST, clr_id, com1_inst, com2_inst, CT_FU__INST, DIR_INST, Fl_JPU__INST,
       FL_MEM__ID, inst_DP, inst_IS, LD_id, LDB_B__INST, LDB_M__ID, load_buffer_1_p31, MB_INST, MEM_INST,
       MEM_LD__INST, multiplexer_1_out, multiplexer_14_out, multiplexer_28_out, multiplexer_38_out,
       multiplexer_43_out, multiplexer_60_out, multiplexer_64_out, multiplexer_78_out, multiplexer_83_out,
       priorityencoder_1_num, register_14_q, register_23_q, register_32_q, register_36_q, register_55_q,
       register_59_q, RET_INST, ROB_FL_INSTA, ROB_FL_INSTB, ROB_GEN_INSTA, ROB_GEN_INSTB, STB_M__ID, undriven;
  wire [4:0] CT_ISS__RA, CT_ISS__RB, CT_ISS__RC, CT_RF__RA, CT_RF__RB, CT_RF__WS, d_ff_18_q;
  wire [6:6] and_173_out;
  wire [7:0] ALU_A_F, ALU_A_FI, ALU_A_T__F, ALU_B_F, ALU_B_FI, ALU_B_T__F, bitextender_2_out, byte_D0,
       byte_D0_iv, byte_D1, byte_D2, byte_D3, byte_I0, byte_I0_iv, byte_I1, byte_I2, byte_I3, CT_FL__D1,
       CT_FL__D2, CT_FU__WR, CT_RF__R1, CT_RF__R2, DIR_WR, fl_i, FU_free, LDB_B__WR, load_buffer_1_p32,
       MB_WR, multiplexer_3_out, multiplexer_20_out, multiplexer_22_out, multiplexer_34_out,
       multiplexer_36_out, multiplexer_41_out, multiplexer_50_out, multiplexer_63_out, multiplexer_71_out,
       RCLR, register_20_q, register_22_q, register_29_q, register_31_q, register_35_q, register_43_q,
       register_58_q, register_66_q, ROB_FL_A, ROB_FL_B, ROB_GEN_WA, ROB_GEN_WB, xor_2_out;
  wire [7:2] FU_F__V;
  wire [7:3] ALU_A_WR, ALU_B_WR, FU_D__V;
  wire [8:0] ALU_A_CT, ALU_B_CT, CT_ALU__CT, multiplexer_21_out, multiplexer_35_out, register_21_q,
       register_30_q;
  wire [9:0] and_19_out;
  wire [15:0] and_154_out, and_156_out, and_158_out, and_159_out, and_161_out, bitextender_3_out,
       bitextender_4_out, bitextender_8_out, bitextender_10_out, bitextender_11_out, clr_16, d_ff_21_q,
       demultiplexer_1_out_0, demultiplexer_2_out_0, icmk_16, id_manager_1_c16, id_manager_1_cm1,
       id_manager_1_cm2, id_manager_1_us, id_manager_1_vv1, id_manager_1_vv2, multiplexer_27_out,
       multiplexer_48_out, multiplexer_69_out, multiplexer_86_out, not_41_out, not_42_out, or_62_out,
       or_63_out, or_64_out, register_41_q, register_64_q, register_79_q, register_99_q, register_103_q,
       register_104_q, V1_inst, V2_inst;
  wire [31:0] add_1_s, add_4c32_1_s, add_4c32_2_s, addsub_4c32_1_s, alu_32_1_p8, alu_32_1_p11, alu_32_1_p12,
       alu_32_1_p14, ALU_A_A, ALU_A_B, ALU_A_R, ALU_A_T__R, ALU_B_A, ALU_B_B, ALU_B_R, ALU_B_T__R,
       and_153_out, bitextender_1_out, bitextender_7_out, CT_RF__D1, CT_RF__D2, CT_RF__DR, CT_SC__D1,
       CT_SC__D2, CT_SC__FD, d_ff_20_q, DIR, FL, I_A__R_q, I_D__R_q, JPU_ADDR, JPU_BTB__tar, JPU_PC, LD_addr,
       LDB_ldD, LDB_M__A, MB_addr, MB_data, MEM_LD__D, multiplexer_5_out, multiplexer_9_out,
       multiplexer_18_out, multiplexer_19_out, multiplexer_24_out, multiplexer_26_out, multiplexer_32_out,
       multiplexer_33_out, multiplexer_40_out, multiplexer_46_out, multiplexer_47_out, multiplexer_62_out,
       multiplexer_67_out, multiplexer_68_out, multiplexer_77_out, multiplexer_80_out, multiplexer_82_out,
       multiplexer_85_out, mVec, pc_read, pc_ret, PCA, pca_i, PCS, PCS_DC, PCS_FT, pcs_i, PCS_IS, R_A, R_B,
       register_7_q, register_9_q, register_18_q, register_19_q, register_27_q, register_28_q, register_34_q,
       register_39_q, register_40_q, register_57_q, register_62_q, register_63_q, register_78_q,
       register_98_q, ROB_GEN_DA, ROB_GEN_DB, SCA, sca_i, SCS, scs_i, STB_M__A, STB_M__D;
  wire [31:24] res_station_1_disp_32;
  wire [36:0] and_155_out, bitextender_9_out, BTB_D_q, BTB_DP, BTB_fetch, BTB_pack__iss, BTB_packet;

  not not_1 (not_1_out, I_valid);
  not not_2 (C_ct, C);
  assign CT_BUS__IDM = not_1_out ? 1'b1 : 1'bz;  // Driver driver_1
  assign CT_RF__PCSE = ft_e ? 1'b1 : 1'bz;  // Driver driver_2
  assign CT_BUS__IAR = ft_e ? 1'b1 : 1'bz;  // Driver driver_3
  assign CT_BUS__IAG = ft_e ? 1'b1 : 1'bz;  // Driver driver_4
  assign I_LD = ft_e ? 1'b1 : 1'bz;  // Driver driver_5
  id_manager id_manager_1 (
    .C(C_ct), .\use (issue), .S1_inst(V1_inst), .S2_inst(V2_inst), .clr(clr), .clr_ep(clr_ep),
    .clr_id(clr_id), .epoch(epoch_IS), .id(inst_IS), .V(id_manager_1_v), .com1(com1), .com1_id(com1_inst),
    .com1_ep(com1_ep), .com2(com2), .com2_id(com2_inst), .ext_en(ext_en), .cmk_16(icmk_16), .clr_16(clr_16),
    .VV1(id_manager_1_vv1), .VV2(id_manager_1_vv2), .US(id_manager_1_us), .CM1(id_manager_1_cm1),
    .CM2(id_manager_1_cm2), .C16(id_manager_1_c16));
  inst_min inst_min_1 (
    .A_v(Fl_MEM), .A_id(FL_MEM__ID), .A_ep(FL_MEM__EP), .B_v(Fl_JPU), .B_id(Fl_JPU__INST), .B_ep(Fl_JPU__EP),
    .m_v(clr), .m_id(clr_id), .m_ep(clr_ep));
  Comparator #(.Bits(32)) comparator_1 (.a(PCS), .b(mVec), .gt(comparator_1_gt));  // open: eq, lt
  BitExtender #(.inputBits(16), .outputBits(32)) bitextender_1 (.in({byte_D2, byte_D3}), .out(bitextender_1_out));
  // Probe V1_inst on V1_inst
  // Probe VG1_inst on id_manager_1_vv1
  // Probe V2_inst on V2_inst
  // Probe VG2_inst on id_manager_1_vv2
  // Probe U_inst on id_manager_1_us
  // Probe CLR_inst on id_manager_1_c16
  // Probe CM2_inst on id_manager_1_cm2
  // Probe CM1_inst on id_manager_1_cm1
  and and_1 (and_1_out, 1'b0, ~comparator_1_gt);  // And
  Add #(.Bits(32)) add_1 (.a(R_A), .b(bitextender_1_out), .c_i(1'b0), .s(add_1_s));  // open: c_o
  and and_2 (and_2_out, FL[14], INT_nor);
  nor nor_1 (nor_1_out, clr, hlt);
  not not_3 (id_full, id_manager_1_v);
  or or_1 (int_run, and_2_out, INT_nmk);
  assign byte_I0_iv = ~byte_I0;  // Not not_4, 8 bits wide
  assign byte_D0_iv = ~byte_D0;  // Not not_5, 8 bits wide
  RS_FF FT (.S(run), .C(C_ct), .R(hlt), .Q(FT_q));  // open: nQ
  not not_6 (not_6_out, halt_FT_DC_ISS);
  RS_FF u_mode (.S(and_1_out), .C(C), .R(comparator_1_gt), .Q(mode));  // open: nQ
  Register #(.Bits(32)) MVR (.D(add_1_s), .C(C), .en(CT_MVR), .Q(mVec));
  and and_3 (and_3_out, nor_1_out, FT_q);
  and and_4 (and_4_out, nor_1_out, FT_q);
  Register DC (.D(and_4_out), .C(C_ct), .en(1'b1), .Q(DC_q));
  and and_5 (ft_e, FT_q, not_6_out);
  Register DC_B (.D(and_3_out), .C(C), .en(1'b1), .Q(DC_B_q));
  Register #(.Bits(32)) register_1 (.D(PCS), .C(C), .en(CT_RF__PCSE), .Q(PCS_FT));
  DipSwitch dipswitch_1 (.out(dipswitch_1_out));
  DipSwitch dipswitch_2 (.out(dipswitch_2_out));
  PullDown pulldown_1 (.out(CT_DISP));
  PullDown pulldown_2 (.out(CT_rollback));
  PullDown pulldown_3 (.out(com2));
  PullDown #(.Bits(4)) pulldown_4 (.out(com2_inst));
  PullDown pulldown_5 (.out(com1_M));
  PullDown pulldown_6 (.out(com1));
  PullDown #(.Bits(4)) pulldown_7 (.out(com1_inst));
  and and_6 (and_6_out, nor_1_out, DC_B_q);
  and and_7 (and_7_out, DC_B_q, not_6_out);
  DipSwitch dipswitch_3 (.out(dipswitch_3_out));
  and and_8 (and_8_out, nor_1_out, DC_q);
  Register ISS (.D(and_8_out), .C(C_ct), .en(1'b1), .Q(dp_e));
  and and_9 (dc_e, DC_q, not_6_out);
  Register ISS_B (.D(and_6_out), .C(C), .en(1'b1), .Q(ISS_B_q));
  Register #(.Bits(32)) register_2 (.D(PCS_FT), .C(C), .en(CT_RF__PCSE), .Q(PCS_DC));
  or or_2 (halt_FT_DC_ISS, id_full, RS_full, dipswitch_1_out, dipswitch_3_out, dipswitch_2_out, LDB_busy, STB_busy);
  and and_10 (issue_e__bf, ISS_B_q, not_6_out);
  and and_11 (issue_e, dp_e, not_6_out);
  Register #(.Bits(32)) register_3 (.D(PCS_DC), .C(C), .en(CT_RF__PCSE), .Q(PCS_IS));
  Multiplexer #(.Bits(4)) multiplexer_1 (.sel(com2), .in_0(com1_inst), .in_1(com2_inst), .out(multiplexer_1_out));
  or or_3 (or_3_out, MEM_AC, MEM_CLR);
  not not_7 (MEM_LD__REC, LDB_forward);
  inst_comp inst_comp_1 (.A_id(MEM_INST), .A_ep(MEM_EP), .B_id(clr_id), .B_ep(clr_ep), .A_old(inst_comp_1_a_old));
  inst_comp inst_comp_2 (
    .A_id(MEM_LD__INST), .A_ep(MEM_LD__EP), .B_id(clr_id), .B_ep(clr_ep), .A_old(inst_comp_2_a_old));
  PullDown pulldown_8 (.out(CT_RF__SCSRE));
  D_FF #(.Bits(2)) d_ff_1 (.D({LDB_M__V, STB_M__V}), .C(C_ct), .Q(d_ff_1_q));  // open: nQ
  and and_12 (and_12_out, ~MEM_LD, or_3_out);  // And
  ROB_gen rob_gen_1 (
    .D1_O(CT_RF__D1), .R1_O(CT_RF__R1), .W1_O(CT_RF__W1), .D2_O(CT_RF__D2), .R2_O(CT_RF__R2),
    .W2_O(CT_RF__W2), .DR_O(CT_RF__DR), .C(C), .E1(CT_ROB__GEN__STA), .E2(CT_ROB__GEN__STB), .D1(ROB_GEN_DA),
    .D2(ROB_GEN_DB), .R1(ROB_GEN_WA), .R2(ROB_GEN_WB), .inst1(ROB_GEN_INSTA), .inst2(ROB_GEN_INSTB),
    .com1(com1), .com2(com2), .com1_id(com1_inst), .com2_id(com2_inst), .clr_16(clr_16), .ret_id(RET_INST));
  ROB_PC rob_pc_1 (
    .C(C), .E(issue), .D(PCS_DC), .inst(inst_IS), .com_id(multiplexer_1_out), .read_id(inst_DP),
    .ret_id(RET_INST), .D1(pca_i), .D2(pc_read), .D3(pc_ret));
  ROB_SC rob_sc_1 (
    .C(C), .E(CT_RF__SCSRE), .D(scs_i), .inst(inst_DP), .com1(com1), .com2(com2), .com1_id(com1_inst),
    .com2_id(com2_inst), .clr_16(clr_16), .roll(clr_id), .SCA(SCA), .W1(CT_SC__W1), .D1(CT_SC__D1),
    .W2(CT_SC__W2), .D2(CT_SC__D2), .D3(CT_SC__FD));
  DipSwitch dipswitch_4 (.out(BTB_packet[0]));
  or or_4 (or_4_out, multiplexer_4_out, MEM_BF__free);
  or or_5 (or_5_out, d_ff_1_q[0], d_ff_1_q[1], MEM_CLR);
  RS_FF rs_ff_1 (.S(MEM_LD), .C(C_ct), .R(and_12_out), .Q(rs_ff_1_q), .nQ(rs_ff_1_nq));
  and and_13 (MEM_LD__CLR, inst_comp_2_a_old, clr);
  and and_14 (and_14_out, byte_D0[3], byte_D0[0]);
  and and_15 (and_15_out, byte_D0[2], byte_D0[0]);
  and and_16 (and_16_out, byte_D0_iv[3], byte_D0_iv[2], byte_D0[1], byte_D0_iv[0]);
  and and_17 (and_17_out, byte_D0_iv[4], byte_D0[3], byte_D0[2], byte_D0[1]);
  and and_18 (and_18_out, byte_D0[4], byte_D0_iv[3], byte_D0_iv[2], byte_D0[1], byte_D0[0]);
  and and_19 (and_19_out[7], byte_D0_iv[4], byte_D0[3], byte_D0[2]);
  and and_20 (and_20_out, byte_D0[4], byte_D0[2], byte_D0_iv[1]);
  and and_21 (and_21_out, byte_D0[4], byte_D0_iv[3], byte_D0_iv[2]);
  and and_22 (and_22_out, byte_D0_iv[4], byte_D0_iv[3], byte_D0_iv[2]);
  and and_23 (and_23_out, byte_D0_iv[4], byte_D0_iv[3]);
  and and_24 (and_24_out, byte_D0_iv[4], byte_D0[3], byte_D0_iv[2], byte_D0_iv[1]);
  and and_25 (and_25_out, byte_D0_iv[4], byte_D0[3], byte_D0_iv[2]);
  and and_26 (and_26_out, byte_D0[4], byte_D0[3]);
  and and_27 (and_27_out, byte_D0_iv[4], byte_D0_iv[3], byte_D0[2], byte_D0_iv[1]);
  and and_28 (and_28_out, byte_D0[4], byte_D0[2], byte_D0[1]);
  and and_29 (and_29_out, byte_D0_iv[4], byte_D0_iv[3], byte_D0_iv[2], byte_D0[1], byte_D0[0]);
  and and_30 (and_30_out, byte_D0_iv[2], byte_D0_iv[0]);
  and and_31 (and_31_out, byte_D0[2], byte_D0[0]);
  and and_32 (and_32_out, byte_D0[1], byte_D0[2], byte_D0[4]);
  and and_33 (and_33_out, byte_D0[3], byte_D0[4]);
  not not_8 (not_8_out, MEM_CLR);
  not not_9 (not_9_out, MEM_CLR);
  and and_34 (MEM_CLR, inst_comp_1_a_old, ~MEM_TYPE__ST, clr);  // And
  BTB btb_1 (
    .C(C), .E(JPU_BTB__ST), .V_in(1'b1), .id(JPU_PC[5:2]), .tag(JPU_PC[17:6]), .pred(JPU_pred),
    .tar(JPU_ADDR), .R_id(PCS[5:2]), .R_tag(PCS[17:6]), .V(BTB_packet[1]), .J(BTB_JP),
    .pred_O(BTB_packet[4:3]), .tar_O(BTB_packet[36:5]));
  // And and_35 has open pins: In_1=or_4_out, In_2=D_valid, In_3=not_8_out, out=open
  and and_36 (MEM_RD, not_9_out, rs_ff_1_q);
  or or_6 (or_6_out, rs_ff_1_nq, MEM_AC, MEM_CLR);
  or or_7 (and_19_out[9], and_14_out, and_15_out, and_16_out);
  or or_8 (and_19_out[6], and_20_out, and_17_out, and_18_out);
  or or_9 (and_19_out[5], and_19_out[7], and_20_out, and_21_out);
  or or_10 (and_19_out[4], and_27_out, and_28_out, and_22_out);
  or or_11 (and_19_out[3], and_23_out, and_28_out, and_24_out);
  or or_12 (and_19_out[2], and_25_out, and_26_out);
  or or_13 (and_19_out[1], and_27_out, and_28_out, and_29_out);
  or or_14 (and_19_out[0], byte_D0[3], byte_D0[1], and_30_out, and_31_out);
  nor nor_2 (nor_2_out, and_32_out, and_33_out);
  xor xor_1 (xor_1_out, STB_M__EP, LDB_M__EP);
  Comparator #(.Bits(4)) comparator_2 (
    .a(LDB_M__ID), .b(STB_M__ID), .gt(comparator_2_gt), .lt(comparator_2_lt));  // open: eq
  DipSwitch #(.dipDefault("true")) dipswitch_5 (.out(MEM_AC));
  and and_37 (MEM_LD, or_5_out, or_6_out);
  nor nor_3 (nor_3_out[1], byte_D1[1], nor_3_out[2]);
  nor nor_4 (nor_3_out[2], byte_D1[0], byte_D1[1], byte_D1[2]);
  and and_38 (and_38_out, byte_D0_iv[7], byte_D0_iv[6], byte_D0[5]);
  and and_39 (and_39_out, byte_D0_iv[7], byte_D0[6], byte_D0_iv[5]);
  and and_40 (and_40_out, STB_M__V, LDB_M__V);
  Multiplexer multiplexer_2 (.sel(xor_1_out), .in_0(comparator_2_gt), .in_1(comparator_2_lt), .out(multiplexer_2_out));
  and and_41 (and_41_out, MEM_AC, MEM_RD, not_10_out, not_11_out);
  not not_10 (not_10_out, MEM_TYPE__ST);
  not not_11 (not_11_out, MEM_LD__CLR);
  or or_15 (or_15_out, MEM_LD__REC, MEM_LD__CLR);
  and and_42 (and_42_out, byte_D0_iv[0], byte_D0_iv[1], byte_D0[2], byte_D0[3], byte_D0[4], byte_D0_iv[5], byte_D0_iv[6], byte_D0_iv[7]);
  and and_43 (and_43_out, byte_D0[1], byte_D0_iv[2], byte_D0[3], byte_D0[4], byte_D0_iv[5], byte_D0_iv[6], byte_D0_iv[7]);
  not not_12 (not_12_out, byte_D0[0]);
  and and_44 (and_44_out, byte_D0[1], byte_D0[2], byte_D0[3], byte_D0[4], byte_D0_iv[5], byte_D0_iv[6], byte_D0_iv[7]);
  or or_16 (or_16_out[1], byte_D1[1], byte_D1[2], byte_D1[0]);
  or or_17 (or_17_out, and_39_out, and_38_out);
  and and_45 (and_45_out, com1, CT_RF__W1);
  and and_46 (and_46_out, com2, CT_RF__W2);
  ROB_FL rob_fl_1 (
    .C(C), .E1(CT_ROB__FL__STA), .E2(CT_ROB__FL__STB), .D1(ROB_FL_A), .D2(ROB_FL_B), .inst1(ROB_FL_INSTA),
    .inst2(ROB_FL_INSTB), .com1(com1), .com2(com2), .com1_id(com1_inst), .com2_id(com2_inst),
    .clr_16(clr_16), .W1_O(CT_FL__W1), .D1_O(CT_FL__D1), .W2_O(CT_FL__W2), .D2_O(CT_FL__D2));
  and and_47 (and_47_out, ft_e, CT_BUS__IAR);
  and and_48 (and_48_out, ft_e, CT_BUS__IAR);
  Multiplexer #(.Bits(8)) multiplexer_3 (
    .sel(CT_BUS__IDM), .in_0(I_D__bus[31:24]), .in_1(8'h72), .out(multiplexer_3_out));
  Multiplexer multiplexer_4 (.sel(and_40_out), .in_0(STB_M__V), .in_1(multiplexer_2_out), .out(multiplexer_4_out));
  and and_49 (and_49_out, byte_D0[4], byte_D0[3], byte_D0_iv[1], byte_D0_iv[2], byte_D0_iv[5], byte_D0_iv[6], byte_D0_iv[7]);
  or or_18 (or_18_out, and_42_out, and_43_out);
  and and_50 (and_50_out, BTB_JP, ~CT_RF__PCJ);  // And
  not not_13 (not_13_out, multiplexer_4_out);
  Multiplexer #(.Bits(32)) multiplexer_5 (
    .sel(multiplexer_4_out), .in_0(LDB_M__A), .in_1(STB_M__A), .out(multiplexer_5_out));
  Multiplexer #(.Bits(2)) multiplexer_6 (
    .sel(multiplexer_4_out), .in_0(LDB_M__MD), .in_1(STB_M__MD), .out(multiplexer_6_out));
  and and_51 (and_51_out, or_15_out, ~and_41_out);  // And
  and and_52 (and_52_out, and_44_out, byte_D0[0]);
  and and_53 (and_53_out, not_12_out, and_44_out);
  regFile4 regfile4_1 (
    .C(C), .E1(and_45_out), .E2(and_46_out), .D1(CT_RF__D1), .D2(CT_RF__D2), .RW1(CT_RF__R1[7:3]),
    .MW1(CT_RF__R1[2:0]), .RW2(CT_RF__R2[7:3]), .MW2(CT_RF__R2[2:0]), .RA(CT_RF__RA), .MA(CT_RF__MA),
    .RB(CT_RF__RB), .MB(CT_RF__MB), .PCS_i(pcs_i), .PCS_e(CT_RF__PCSE), .PCA_i(pca_i), .PCA_e(CT_RF__PCAE),
    .SCS_i(scs_i), .SC_sel(CT_RF__SCSS), .SCS_e(CT_RF__SCSE), .SCA_i(sca_i), .SCA_sel(CT_RF__SCAE),
    .SCA_e(CT_RF__SCAE), .FL_i({{24{1'b0}}, fl_i}), .FL_sel(CT_RF__FLS), .FL_e(4'b0001), .PC_read(pc_read),
    .R_A(R_A), .R_B(R_B), .PCS_O(PCS), .PCA_O(PCA), .SCS_O(SCS), .SCA_O(SCA), .FL_O(FL));
  or or_19 (or_19_out[0], CT_RF__PCH, CT_RF__PCJ);
  or or_20 (or_19_out[1], CT_RF__PCH, and_50_out);
  add_4c32 add_4c32_1 (.a(PCS), .b(4'b0100), .s(add_4c32_1_s));  // open: c
  Register #(.Bits(37)) BTB_F (.D({BTB_packet[36:3], BTB_JP, BTB_packet[1:0]}), .C(C), .en(and_47_out), .Q(BTB_fetch));
  Register #(.Bits(32)) I_A__R (.D(PCS), .C(C), .en(and_48_out), .Q(I_A__R_q));
  Register #(.Bits(32)) I_D__R (.D({multiplexer_3_out, I_D__bus[23:0]}), .C(C), .en(dc_e), .Q(I_D__R_q));
  Register #(.Bits(37)) BTB_D (.D(BTB_fetch), .C(C), .en(dc_e), .Q(BTB_D_q));
  and and_54 (MB_LDB__LD, LDB_M__V, MEM_LD, not_13_out);
  and and_55 (MB_STB__LD, multiplexer_4_out, MEM_LD);
  Register register_4 (.D(multiplexer_4_out), .C(C), .en(MEM_LD), .Q(MEM_TYPE__ST));
  Register register_5 (.D(LDB_M__EP), .C(C), .en(MEM_LD), .Q(MEM_EP));
  Register #(.Bits(4)) register_6 (.D(LDB_M__ID), .C(C), .en(MEM_LD), .Q(MEM_INST));
  Register #(.Bits(32)) register_7 (.D(multiplexer_5_out), .C(C), .en(MEM_LD), .Q(register_7_q));
  Register #(.Bits(2)) register_8 (.D(multiplexer_6_out), .C(C), .en(MEM_LD), .Q(register_8_q));
  Register #(.Bits(32)) register_9 (.D(STB_M__D), .C(C), .en(MEM_LD), .Q(register_9_q));
  not not_14 (not_14_out, MEM_LD__CLR);
  RS_FF rs_ff_2 (.S(and_41_out), .C(C), .R(and_51_out), .Q(rs_ff_2_q), .nQ(rs_ff_2_nq));
  Register #(.Bits(32)) register_10 (.D(D_D__bus), .C(C), .en(MEM_AC), .Q(MEM_LD__D));
  Register #(.Bits(4)) register_11 (.D(MEM_INST), .C(C), .en(MEM_AC), .Q(MEM_LD__INST));
  Register register_12 (.D(MEM_EP), .C(C), .en(MEM_AC), .Q(MEM_LD__EP));
  and and_56 (and_56_out, byte_D0_iv[7], byte_D0_iv[6], byte_D0_iv[5], byte_D0_iv[4]);
  and and_57 (and_57_out, byte_D0_iv[7], byte_D0_iv[6], byte_D0_iv[5], byte_D0[4], byte_D0_iv[3]);
  assign {CT_RF__RA, CT_RF__MA} = or_22_out ? byte_D1 : 8'bz;  // Driver driver_6
  assign {CT_RF__RB, CT_RF__MB} = or_22_out ? byte_D2 : 8'bz;  // Driver driver_7
  assign CT_ALU__LD = or_22_out ? CT_DISP : 1'bz;  // Driver driver_8
  assign CT_ALU__CT = or_22_out ? {1'b0, and_19_out[7:0]} : 9'bz;  // Driver driver_9
  assign CT_ALU__M = or_22_out ? and_19_out[9] : 1'bz;  // Driver driver_10
  assign CT_FU__INST = or_22_out ? inst_DP : 4'bz;  // Driver driver_11
  assign CT_FU__EPOCH = or_22_out ? epoch_DP : 1'bz;  // Driver driver_12
  assign CT_FU__WR = or_22_out ? byte_D1 : 8'bz;  // Driver driver_13
  assign CT_ALU__WD = or_22_out ? nor_2_out : 1'bz;  // Driver driver_14
  assign CT_ALU__WF = or_22_out ? 1'b1 : 1'bz;  // Driver driver_15
  assign {CT_RF__RA, CT_RF__MA} = or_18_out ? byte_D2 : 8'bz;  // Driver driver_16
  assign CT_DIR__LD = or_18_out ? CT_DISP : 1'bz;  // Driver driver_17
  assign CT_DIR__M = or_18_out ? and_43_out : 1'bz;  // Driver driver_18
  assign CT_DIR__MS = or_18_out ? byte_D0[0] : 1'bz;  // Driver driver_19
  assign CT_FU__INST = or_18_out ? inst_DP : 4'bz;  // Driver driver_20
  assign CT_FU__EPOCH = or_18_out ? epoch_DP : 1'bz;  // Driver driver_21
  assign CT_FU__WR = or_18_out ? byte_D1 : 8'bz;  // Driver driver_22
  assign CT_RF__SCSS = and_44_out ? 1'b1 : 1'bz;  // Driver driver_23
  assign {CT_RF__RB, CT_RF__MB} = and_44_out ? 8'hf0 : 8'bz;  // Driver driver_24
  assign {CT_RF__RA, CT_RF__MA} = and_52_out ? byte_D1 : 8'bz;  // Driver driver_25
  assign CT_FU__WR = and_53_out ? byte_D1 : 8'bz;  // Driver driver_26
  assign CT_MB__LD = and_44_out ? CT_DISP : 1'bz;  // Driver driver_27
  assign CT_MB__ST = and_52_out ? 1'b1 : 1'bz;  // Driver driver_28
  assign CT_SP__MOF = and_52_out ? {1'b1, or_16_out[1], byte_D1[1]} : 3'bz;  // Driver driver_29
  assign CT_MB__OFFM = and_44_out ? 1'b1 : 1'bz;  // Driver driver_30
  assign CT_RF__SCSE = and_44_out ? 1'b1 : 1'bz;  // Driver driver_31
  assign CT_RF__SCN = and_44_out ? {nor_3_out, byte_D1[1]} : 3'bz;  // Driver driver_32
  assign CT_RF__SCD = and_52_out ? 1'b1 : 1'bz;  // Driver driver_33
  assign CT_FU__INST = and_44_out ? inst_DP : 4'bz;  // Driver driver_34
  assign CT_FU__EPOCH = and_44_out ? epoch_DP : 1'bz;  // Driver driver_35
  assign CT_RF__SCSRE = and_44_out ? 1'b1 : 1'bz;  // Driver driver_36
  assign CT_FU__EPOCH = or_17_out ? epoch_DP : 1'bz;  // Driver driver_37
  assign CT_FU__INST = or_17_out ? inst_DP : 4'bz;  // Driver driver_38
  assign {CT_RF__RB, CT_RF__MB} = or_17_out ? {byte_D0[4:0], 3'b000} : 8'bz;  // Driver driver_39
  assign {CT_RF__RA, CT_RF__MA} = and_39_out ? byte_D1 : 8'bz;  // Driver driver_40
  assign CT_FU__WR = and_38_out ? byte_D1 : 8'bz;  // Driver driver_41
  assign CT_MB__LD = or_17_out ? CT_DISP : 1'bz;  // Driver driver_42
  assign CT_MB__ST = and_39_out ? 1'b1 : 1'bz;  // Driver driver_43
  Multiplexer #(.Selector_Bits(2), .Bits(32)) multiplexer_7 (
    .sel(or_19_out), .in_0(add_4c32_1_s), .in_1(JPU_ADDR), .in_2(BTB_packet[36:5]), .in_3(BTB_packet[36:5]),
    .out(pcs_i));
  assign I_A__bus = and_59_out ? I_A__R_q : 32'bz;  // Driver driver_44
  D_FF #(.Bits(32)) d_ff_2 (.D(I_D__R_q), .C(C_ct), .Q({byte_I0, byte_I1, byte_I2, byte_I3}));  // open: nQ
  D_FF #(.Bits(37)) d_ff_3 (.D(BTB_D_q), .C(C_ct), .Q(BTB_pack__iss));  // open: nQ
  assign D_A__bus = MEM_RD ? register_7_q : 32'bz;  // Driver driver_45
  assign D_MD = MEM_RD ? register_8_q : 2'bz;  // Driver driver_46
  assign D_D__bus = D_ST ? register_9_q : 32'bz;  // Driver driver_47
  and and_58 (MEM_LD__RD, not_14_out, rs_ff_2_q);
  or or_21 (MEM_BF__free, rs_ff_2_nq, MEM_LD__RD, MEM_LD__CLR);
  and and_59 (and_59_out, CT_BUS__IAG, bus_e);
  and and_60 (D_LD, ~MEM_TYPE__ST, MEM_RD);  // And
  and and_61 (D_ST, MEM_RD, MEM_TYPE__ST);
  or or_22 (or_22_out, and_56_out, and_49_out, and_57_out);
  PullDown pulldown_9 (.out(CT_RF__PCAE));
  PullDown pulldown_10 (.out(CT_RF__SCAE));
  PullDown #(.Bits(16)) pulldown_11 (.out(V1_inst));
  PullDown #(.Bits(16)) pulldown_12 (.out(V2_inst));
  BitExtender #(.inputBits(1), .outputBits(8)) bitextender_2 (.in(byte_D0[3]), .out(bitextender_2_out));
  DipSwitch dipswitch_6 (.out(dipswitch_6_out));
  assign xor_2_out = FL[7:0] ^ bitextender_2_out;  // XOr xor_2, 8 bits wide
  and and_62 (and_62_out, and_71_out, dipswitch_6_out);
  and and_63 (and_63_out, com1, CT_SC__W1);
  and and_64 (and_64_out, com2, CT_SC__W2);
  not not_15 (not_15_out, clr);
  and and_65 (and_65_out, byte_D2[7], CT_DIR__MS);
  assign CT_RF__SCSE = clr ? 1'b1 : 1'bz;  // Driver driver_48
  assign CT_RF__SCSS = clr ? 1'b1 : 1'bz;  // Driver driver_49
  Multiplexer multiplexer_8 (.sel(and_76_out[2]), .in_0(nand_1_out[2]), .in_1(not_15_out), .out(multiplexer_8_out));
  not not_16 (not_16_out[0], register_13_q[0]);
  xor xor_3 (not_16_out[1], register_13_q[0], register_13_q[1]);
  xor xor_4 (not_16_out[2], register_13_q[1], register_13_q[2]);
  Multiplexer #(.Bits(32)) multiplexer_9 (
    .sel(CT_ALU__M), .in_0(R_B), .in_1({{16{1'b0}}, byte_D2, byte_D3}), .out(multiplexer_9_out));
  BitExtender #(.inputBits(1)) bitextender_3 (.in(and_65_out), .out(bitextender_3_out));
  or or_23 (or_23_out, CT_FU__WR[0], CT_FU__WR[2]);
  not not_17 (not_17_out, CT_FU__WR[1]);
  and and_66 (and_66_out, byte_D0_iv[4], byte_D0[5], byte_D0[6], byte_D0_iv[7]);
  Multiplexer #(.Selector_Bits(3)) multiplexer_10 (
    .sel(byte_D0[2:0]), .in_0(xor_2_out[0]), .in_1(xor_2_out[1]), .in_2(xor_2_out[2]), .in_3(xor_2_out[3]),
    .in_4(xor_2_out[4]), .in_5(xor_2_out[5]), .in_6(xor_2_out[6]), .in_7(xor_2_out[7]),
    .out(multiplexer_10_out));
  bus16_demux bus16_demux_1 (.bus(V1_inst), .E(and_62_out), .id(inst_DP));
  or or_24 (CT_RF__SCAE, and_63_out, and_64_out);
  and and_67 (and_67_out, multiplexer_8_out, CT_ALU__LD);
  Register register_13 (.D(and_67_out), .C(C_ct), .en(or_25_out), .Q(register_13_q[2]));
  not not_18 (not_18_out, multiplexer_8_out);
  or or_25 (or_25_out, not_18_out, multiplexer_11_out[2]);
  Multiplexer #(.Bits(3)) multiplexer_11 (
    .sel(or_26_out), .in_0(not_16_out), .in_1(and_76_out), .out(multiplexer_11_out));
  or or_26 (or_26_out, and_76_out[0], and_76_out[1], and_76_out[2]);
  Register #(.Bits(4)) register_14 (.D(CT_FU__INST), .C(C_ct), .en(multiplexer_11_out[2]), .Q(register_14_q));
  Register register_15 (.D(CT_FU__EPOCH), .C(C_ct), .en(multiplexer_11_out[2]), .Q(register_15_q));
  Register register_16 (.D(CT_ALU__WD), .C(C_ct), .en(multiplexer_11_out[2]), .Q(register_16_q));
  Register register_17 (.D(CT_ALU__WF), .C(C_ct), .en(multiplexer_11_out[2]), .Q(register_17_q));
  Register #(.Bits(32)) register_18 (.D(R_A), .C(C), .en(multiplexer_11_out[2]), .Q(register_18_q));
  Register #(.Bits(32)) register_19 (.D(multiplexer_9_out), .C(C), .en(multiplexer_11_out[2]), .Q(register_19_q));
  Register #(.Bits(8)) register_20 (.D(FL[7:0]), .C(C), .en(multiplexer_11_out[2]), .Q(register_20_q));
  Register #(.Bits(9)) register_21 (.D(CT_ALU__CT), .C(C_ct), .en(multiplexer_11_out[2]), .Q(register_21_q));
  Register #(.Bits(8)) register_22 (.D(CT_FU__WR), .C(C_ct), .en(multiplexer_11_out[2]), .Q(register_22_q));
  add_4c32 add_4c32_2 (.a(pc_read), .b(4'b0100), .s(add_4c32_2_s));  // open: c
  BitExtender #(.inputBits(3)) bitextender_4 (.in(CT_SP__MOF), .out(bitextender_4_out));
  and and_68 (and_68_out[0], or_23_out, not_17_out);
  and and_69 (and_69_out, byte_D0_iv[0], byte_D0_iv[1], byte_D0_iv[2], byte_D0_iv[3], byte_D0[4], byte_D0[5], byte_D0[6], byte_D0_iv[7]);
  and and_70 (and_70_out, byte_D0[0], byte_D0_iv[1], byte_D0_iv[2], byte_D0_iv[3], byte_D0[4], byte_D0[5], byte_D0[6], byte_D0_iv[7]);
  and and_71 (and_71_out, byte_D0[0], byte_D0[1], byte_D0_iv[2], byte_D0_iv[3], byte_D0[4], byte_D0[5], byte_D0[6], byte_D0_iv[7]);
  and and_72 (and_72_out, byte_D0[0], byte_D0_iv[1], byte_D0[2], byte_D0[3], byte_D0[4], byte_D0_iv[5], byte_D0_iv[6], byte_D0_iv[7]);
  Multiplexer multiplexer_12 (
    .sel(and_76_out[1]), .in_0(nand_1_out[1]), .in_1(nand_1_out[2]), .out(multiplexer_12_out));
  Multiplexer multiplexer_13 (
    .sel(register_13_q[2]), .in_0(CT_ALU__LD), .in_1(register_13_q[2]), .out(multiplexer_13_out));
  Multiplexer #(.Bits(4)) multiplexer_14 (
    .sel(register_13_q[2]), .in_0(CT_FU__INST), .in_1(register_14_q), .out(multiplexer_14_out));
  inst_comp inst_comp_3 (
    .A_id(register_14_q), .A_ep(register_15_q), .B_id(clr_id), .B_ep(clr_ep), .A_old(inst_comp_3_a_old));
  Multiplexer multiplexer_15 (
    .sel(register_13_q[2]), .in_0(CT_FU__EPOCH), .in_1(register_15_q), .out(multiplexer_15_out));
  Multiplexer multiplexer_16 (
    .sel(register_13_q[2]), .in_0(CT_ALU__WD), .in_1(register_16_q), .out(multiplexer_16_out));
  Multiplexer multiplexer_17 (
    .sel(register_13_q[2]), .in_0(CT_ALU__WF), .in_1(register_17_q), .out(multiplexer_17_out));
  Multiplexer #(.Bits(32)) multiplexer_18 (
    .sel(register_13_q[2]), .in_0(R_A), .in_1(register_18_q), .out(multiplexer_18_out));
  Multiplexer #(.Bits(32)) multiplexer_19 (
    .sel(register_13_q[2]), .in_0(multiplexer_9_out), .in_1(register_19_q), .out(multiplexer_19_out));
  Multiplexer #(.Bits(8)) multiplexer_20 (
    .sel(register_13_q[2]), .in_0(FL[7:0]), .in_1(register_20_q), .out(multiplexer_20_out));
  Multiplexer #(.Bits(9)) multiplexer_21 (
    .sel(register_13_q[2]), .in_0(CT_ALU__CT), .in_1(register_21_q), .out(multiplexer_21_out));
  Multiplexer #(.Bits(8)) multiplexer_22 (
    .sel(register_13_q[2]), .in_0(CT_FU__WR), .in_1(register_22_q), .out(multiplexer_22_out));
  Multiplexer multiplexer_23 (.sel(and_80_out[2]), .in_0(nand_4_out[2]), .in_1(not_19_out), .out(multiplexer_23_out));
  not not_19 (not_19_out, clr);
  not not_20 (not_20_out[0], register_46_q[0]);
  xor xor_5 (not_20_out[1], register_46_q[0], register_46_q[1]);
  xor xor_6 (not_20_out[2], register_46_q[1], register_46_q[2]);
  Multiplexer #(.Bits(32)) multiplexer_24 (
    .sel(CT_DIR__M), .in_0(R_A), .in_1({bitextender_3_out, byte_D2, byte_D3}), .out(multiplexer_24_out));
  Multiplexer multiplexer_25 (.sel(and_81_out[2]), .in_0(nand_5_out[2]), .in_1(not_21_out), .out(multiplexer_25_out));
  not not_21 (not_21_out, clr);
  not not_22 (not_22_out[0], register_47_q[0]);
  xor xor_7 (not_22_out[1], register_47_q[0], register_47_q[1]);
  xor xor_8 (not_22_out[2], register_47_q[1], register_47_q[2]);
  Multiplexer #(.Bits(32)) multiplexer_26 (.sel(CT_CALLM), .in_0(R_A), .in_1(add_4c32_2_s), .out(multiplexer_26_out));
  Multiplexer #(.Bits(16)) multiplexer_27 (
    .sel(CT_MB__OFFM), .in_0({byte_D2, byte_D3}), .in_1(bitextender_4_out), .out(multiplexer_27_out));
  and and_73 (and_73_out, multiplexer_12_out, multiplexer_13_out);
  not not_23 (not_23_out, multiplexer_12_out);
  or or_27 (or_27_out, not_23_out, multiplexer_11_out[1]);
  or or_28 (register_13_q[1], register_45_q[1], register_13_q[2]);
  nand nand_1 (nand_1_out[2], inst_comp_3_a_old, clr);
  Register #(.Bits(4)) register_23 (.D(multiplexer_14_out), .C(C_ct), .en(multiplexer_11_out[1]), .Q(register_23_q));
  Register register_24 (.D(multiplexer_15_out), .C(C_ct), .en(multiplexer_11_out[1]), .Q(register_24_q));
  Register register_25 (.D(multiplexer_16_out), .C(C_ct), .en(multiplexer_11_out[1]), .Q(register_25_q));
  Register register_26 (.D(multiplexer_17_out), .C(C_ct), .en(multiplexer_11_out[1]), .Q(register_26_q));
  Register #(.Bits(32)) register_27 (.D(multiplexer_18_out), .C(C), .en(multiplexer_11_out[1]), .Q(register_27_q));
  Register #(.Bits(32)) register_28 (.D(multiplexer_19_out), .C(C), .en(multiplexer_11_out[1]), .Q(register_28_q));
  Register #(.Bits(8)) register_29 (.D(multiplexer_20_out), .C(C), .en(multiplexer_11_out[1]), .Q(register_29_q));
  Register #(.Bits(9)) register_30 (.D(multiplexer_21_out), .C(C_ct), .en(multiplexer_11_out[1]), .Q(register_30_q));
  Register #(.Bits(8)) register_31 (.D(multiplexer_22_out), .C(C_ct), .en(multiplexer_11_out[1]), .Q(register_31_q));
  and and_74 (and_74_out, multiplexer_23_out, CT_DIR__LD);
  not not_24 (not_24_out, multiplexer_23_out);
  Register #(.Bits(4)) register_32 (.D(CT_FU__INST), .C(C_ct), .en(multiplexer_37_out[2]), .Q(register_32_q));
  Register register_33 (.D(CT_FU__EPOCH), .C(C_ct), .en(multiplexer_37_out[2]), .Q(register_33_q));
  Register #(.Bits(32)) register_34 (.D(multiplexer_24_out), .C(C), .en(multiplexer_37_out[2]), .Q(register_34_q));
  Register #(.Bits(8)) register_35 (.D(CT_FU__WR), .C(C_ct), .en(multiplexer_37_out[2]), .Q(register_35_q));
  and and_75 (and_75_out, multiplexer_25_out, CT_MB__LD);
  not not_25 (not_25_out, multiplexer_25_out);
  Register #(.Bits(4)) register_36 (.D(CT_FU__INST), .C(C_ct), .en(multiplexer_42_out[2]), .Q(register_36_q));
  Register register_37 (.D(CT_FU__EPOCH), .C(C_ct), .en(multiplexer_42_out[2]), .Q(register_37_q));
  Register register_38 (.D(CT_MB__ST), .C(C_ct), .en(multiplexer_42_out[2]), .Q(register_38_q));
  Register #(.Bits(32)) register_39 (.D(multiplexer_26_out), .C(C), .en(multiplexer_42_out[2]), .Q(register_39_q));
  Register #(.Bits(32)) register_40 (.D(R_B), .C(C), .en(multiplexer_42_out[2]), .Q(register_40_q));
  Register #(.Bits(16)) register_41 (.D(multiplexer_27_out), .C(C), .en(multiplexer_42_out[2]), .Q(register_41_q));
  Register #(.Bits(2)) register_42 (
    .D({CT_FU__WR[1], and_68_out[0]}), .C(C_ct), .en(multiplexer_42_out[2]), .Q(register_42_q));
  Register #(.Bits(8)) register_43 (.D(CT_FU__WR), .C(C_ct), .en(multiplexer_42_out[2]), .Q(register_43_q));
  Register register_44 (.D(CT_FU__MF), .C(C_ct), .en(multiplexer_42_out[2]), .Q(register_44_q));
  assign CT_FU__EPOCH = and_66_out ? epoch_DP : 1'bz;  // Driver driver_50
  assign CT_FU__INST = and_66_out ? inst_DP : 4'bz;  // Driver driver_51
  assign {CT_RF__RA, CT_RF__MA} = and_66_out ? byte_D1 : 8'bz;  // Driver driver_52
  assign CT_JPU__LD = and_66_out ? CT_DISP : 1'bz;  // Driver driver_53
  assign CT_JPU__JP = and_66_out ? multiplexer_10_out : 1'bz;  // Driver driver_54
  assign JPU_A__ST = and_66_out ? 1'b1 : 1'bz;  // Driver driver_55
  assign CT_FU__EPOCH = and_69_out ? epoch_DP : 1'bz;  // Driver driver_56
  assign CT_FU__INST = and_69_out ? inst_DP : 4'bz;  // Driver driver_57
  assign {CT_RF__RA, CT_RF__MA} = and_69_out ? 8'he8 : 8'bz;  // Driver driver_58
  assign {CT_RF__RB, CT_RF__MB} = and_69_out ? 8'hf0 : 8'bz;  // Driver driver_59
  assign CT_JPU__LD = and_69_out ? 1'b1 : 1'bz;  // Driver driver_60
  assign CT_JPU__JP = and_69_out ? CT_DISP : 1'bz;  // Driver driver_61
  assign JPU_A__ST = and_69_out ? 1'b1 : 1'bz;  // Driver driver_62
  assign CT_MB__LD = and_69_out ? 1'b1 : 1'bz;  // Driver driver_63
  assign CT_MB__ST = and_69_out ? 1'b1 : 1'bz;  // Driver driver_64
  assign CT_CALLM = and_69_out ? 1'b1 : 1'bz;  // Driver driver_65
  assign CT_SP__MOF = and_69_out ? 3'b100 : 3'bz;  // Driver driver_66
  assign CT_MB__OFFM = and_69_out ? 1'b1 : 1'bz;  // Driver driver_67
  assign CT_RF__SCSE = and_69_out ? 1'b1 : 1'bz;  // Driver driver_68
  assign CT_RF__SCSS = and_69_out ? 1'b1 : 1'bz;  // Driver driver_69
  assign CT_RF__SCD = and_69_out ? 1'b1 : 1'bz;  // Driver driver_70
  assign CT_RF__SCN = and_69_out ? 3'b100 : 3'bz;  // Driver driver_71
  assign CT_FU__MF = and_69_out ? 1'b1 : 1'bz;  // Driver driver_72
  assign JPU_CALL = and_69_out ? 1'b1 : 1'bz;  // Driver driver_73
  assign CT_RF__SCSRE = and_69_out ? 1'b1 : 1'bz;  // Driver driver_74
  assign CT_FU__EPOCH = and_70_out ? epoch_DP : 1'bz;  // Driver driver_75
  assign CT_FU__INST = and_70_out ? inst_DP : 4'bz;  // Driver driver_76
  assign {CT_RF__RB, CT_RF__MB} = and_70_out ? 8'hf0 : 8'bz;  // Driver driver_77
  assign CT_FU__WR = and_70_out ? 8'he8 : 8'bz;  // Driver driver_78
  assign CT_MB__LD = and_70_out ? 1'b1 : 1'bz;  // Driver driver_79
  assign CT_MB__OFFM = and_70_out ? 1'b1 : 1'bz;  // Driver driver_80
  assign CT_RF__SCSE = and_70_out ? 1'b1 : 1'bz;  // Driver driver_81
  assign CT_RF__SCSS = and_70_out ? 1'b1 : 1'bz;  // Driver driver_82
  assign CT_RF__SCN = and_70_out ? 3'b100 : 3'bz;  // Driver driver_83
  assign CT_FU__MF = and_70_out ? 1'b1 : 1'bz;  // Driver driver_84
  assign CT_RET__LD = and_70_out ? 1'b1 : 1'bz;  // Driver driver_85
  assign CT_RF__SCSRE = and_70_out ? 1'b1 : 1'bz;  // Driver driver_86
  assign CT_FU__EPOCH = 1'b0 ? epoch_DP : 1'bz;  // Driver driver_87
  assign CT_FU__INST = 1'b0 ? inst_DP : 4'bz;  // Driver driver_88
  assign ex_nop = 1'b0 ? 1'b1 : 1'bz;  // Driver driver_89
  assign hlt = 1'b0 ? 1'b1 : 1'bz;  // Driver driver_90
  assign CT_BUS__IDM = 1'b0 ? 1'b1 : 1'bz;  // Driver driver_91
  assign CT_BUS__IDM = 1'b0 ? 1'b1 : 1'bz;  // Driver driver_92
  assign CT_RF__PCH = 1'b0 ? 1'b1 : 1'bz;  // Driver driver_93
  assign CT_RF__PCSE = 1'b0 ? 1'b1 : 1'bz;  // Driver driver_94
  assign CT_BUS__IDM = 1'b0 ? 1'b1 : 1'bz;  // Driver driver_95
  bus16x2_demux bus16x2_demux_1 (.bus_1(V1_inst), .bus_2(V2_inst), .E(and_72_out), .id(inst_DP));
  addsub_4c32 addsub_4c32_1 (.a(SCS), .b({1'b0, CT_RF__SCN}), .sub(CT_RF__SCD), .s(addsub_4c32_1_s));  // open: c
  Register register_45 (.D(and_73_out), .C(C_ct), .en(or_27_out), .Q(register_45_q[1]));
  or or_29 (register_13_q[0], ALU_busy, register_45_q[1], register_13_q[2]);
  assign and_76_out = nand_2_out & register_13_q;  // And and_76, 3 bits wide
  Multiplexer #(.Bits(4)) multiplexer_28 (
    .sel(register_13_q[1]), .in_0(CT_FU__INST), .in_1(register_23_q), .out(multiplexer_28_out));
  inst_comp inst_comp_4 (
    .A_id(register_23_q), .A_ep(register_24_q), .B_id(clr_id), .B_ep(clr_ep), .A_old(inst_comp_4_a_old));
  Multiplexer multiplexer_29 (
    .sel(register_13_q[1]), .in_0(CT_FU__EPOCH), .in_1(register_24_q), .out(multiplexer_29_out));
  Multiplexer multiplexer_30 (
    .sel(register_13_q[1]), .in_0(CT_ALU__WD), .in_1(register_25_q), .out(multiplexer_30_out));
  Multiplexer multiplexer_31 (
    .sel(register_13_q[1]), .in_0(CT_ALU__WF), .in_1(register_26_q), .out(multiplexer_31_out));
  Multiplexer #(.Bits(32)) multiplexer_32 (
    .sel(register_13_q[1]), .in_0(R_A), .in_1(register_27_q), .out(multiplexer_32_out));
  Multiplexer #(.Bits(32)) multiplexer_33 (
    .sel(register_13_q[1]), .in_0(multiplexer_9_out), .in_1(register_28_q), .out(multiplexer_33_out));
  Multiplexer #(.Bits(8)) multiplexer_34 (
    .sel(register_13_q[1]), .in_0(FL[7:0]), .in_1(register_29_q), .out(multiplexer_34_out));
  Multiplexer #(.Bits(9)) multiplexer_35 (
    .sel(register_13_q[1]), .in_0(CT_ALU__CT), .in_1(register_30_q), .out(multiplexer_35_out));
  Multiplexer #(.Bits(8)) multiplexer_36 (
    .sel(register_13_q[1]), .in_0(CT_FU__WR), .in_1(register_31_q), .out(multiplexer_36_out));
  Register register_46 (.D(and_74_out), .C(C_ct), .en(or_30_out), .Q(register_46_q[2]));
  or or_30 (or_30_out, not_24_out, multiplexer_37_out[2]);
  Multiplexer #(.Bits(3)) multiplexer_37 (
    .sel(or_31_out), .in_0(not_20_out), .in_1(and_80_out), .out(multiplexer_37_out));
  or or_31 (or_31_out, and_80_out[0], and_80_out[1], and_80_out[2]);
  Multiplexer #(.Bits(4)) multiplexer_38 (
    .sel(register_46_q[2]), .in_0(CT_FU__INST), .in_1(register_32_q), .out(multiplexer_38_out));
  inst_comp inst_comp_5 (
    .A_id(register_32_q), .A_ep(register_33_q), .B_id(clr_id), .B_ep(clr_ep), .A_old(inst_comp_5_a_old));
  Multiplexer multiplexer_39 (
    .sel(register_46_q[2]), .in_0(CT_FU__EPOCH), .in_1(register_33_q), .out(multiplexer_39_out));
  Multiplexer #(.Bits(32)) multiplexer_40 (
    .sel(register_46_q[2]), .in_0(multiplexer_24_out), .in_1(register_34_q), .out(multiplexer_40_out));
  Multiplexer #(.Bits(8)) multiplexer_41 (
    .sel(register_46_q[2]), .in_0(CT_FU__WR), .in_1(register_35_q), .out(multiplexer_41_out));
  Register register_47 (.D(and_75_out), .C(C_ct), .en(or_32_out), .Q(register_47_q[2]));
  or or_32 (or_32_out, not_25_out, multiplexer_42_out[2]);
  Multiplexer #(.Bits(3)) multiplexer_42 (
    .sel(or_33_out), .in_0(not_22_out), .in_1(and_81_out), .out(multiplexer_42_out));
  or or_33 (or_33_out, and_81_out[0], and_81_out[1], and_81_out[2]);
  Multiplexer #(.Bits(4)) multiplexer_43 (
    .sel(register_47_q[2]), .in_0(CT_FU__INST), .in_1(register_36_q), .out(multiplexer_43_out));
  inst_comp inst_comp_6 (
    .A_id(register_36_q), .A_ep(register_37_q), .B_id(clr_id), .B_ep(clr_ep), .A_old(inst_comp_6_a_old));
  Multiplexer multiplexer_44 (
    .sel(register_47_q[2]), .in_0(CT_FU__EPOCH), .in_1(register_37_q), .out(multiplexer_44_out));
  Multiplexer multiplexer_45 (.sel(register_47_q[2]), .in_0(CT_MB__ST), .in_1(register_38_q), .out(multiplexer_45_out));
  Multiplexer #(.Bits(32)) multiplexer_46 (
    .sel(register_47_q[2]), .in_0(multiplexer_26_out), .in_1(register_39_q), .out(multiplexer_46_out));
  Multiplexer #(.Bits(32)) multiplexer_47 (
    .sel(register_47_q[2]), .in_0(R_B), .in_1(register_40_q), .out(multiplexer_47_out));
  Multiplexer #(.Bits(16)) multiplexer_48 (
    .sel(register_47_q[2]), .in_0(multiplexer_27_out), .in_1(register_41_q), .out(multiplexer_48_out));
  Multiplexer #(.Bits(2)) multiplexer_49 (
    .sel(register_47_q[2]), .in_0({CT_FU__WR[1], and_68_out[0]}), .in_1(register_42_q),
    .out(multiplexer_49_out));
  Multiplexer #(.Bits(8)) multiplexer_50 (
    .sel(register_47_q[2]), .in_0(CT_FU__WR), .in_1(register_43_q), .out(multiplexer_50_out));
  Multiplexer multiplexer_51 (.sel(register_47_q[2]), .in_0(CT_FU__MF), .in_1(register_44_q), .out(multiplexer_51_out));
  Multiplexer #(.Bits(32)) multiplexer_52 (.sel(clr), .in_0(addsub_4c32_1_s), .in_1(CT_SC__FD), .out(scs_i));
  Multiplexer #(.Bits(32)) multiplexer_53 (.sel(and_64_out), .in_0(CT_SC__D1), .in_1(CT_SC__D2), .out(sca_i));
  Multiplexer multiplexer_54 (
    .sel(and_76_out[0]), .in_0(nand_1_out[0]), .in_1(nand_1_out[1]), .out(multiplexer_54_out));
  Multiplexer multiplexer_55 (
    .sel(register_13_q[1]), .in_0(CT_ALU__LD), .in_1(register_45_q[1]), .out(multiplexer_55_out));
  and and_77 (and_77_out, multiplexer_54_out, multiplexer_55_out);
  nand nand_2 (nand_2_out[2], ALU_busy, register_45_q[1], register_13_q[2]);
  nand nand_3 (nand_1_out[1], inst_comp_4_a_old, clr);
  Register #(.Bits(4)) register_48 (.D(multiplexer_28_out), .C(C_ct), .en(ALU_A_LD), .Q(ALU_A_INST));
  Register register_49 (.D(multiplexer_29_out), .C(C_ct), .en(ALU_A_LD), .Q(register_49_q));
  Register #(.Bits(32)) register_50 (.D(multiplexer_32_out), .C(C), .en(ALU_A_LD), .Q(ALU_A_A));
  Register #(.Bits(32)) register_51 (.D(multiplexer_33_out), .C(C), .en(ALU_A_LD), .Q(ALU_A_B));
  Register #(.Bits(8)) register_52 (.D(multiplexer_34_out), .C(C), .en(ALU_A_LD), .Q(ALU_A_FI));
  Register #(.Bits(9)) register_53 (.D(multiplexer_35_out), .C(C_ct), .en(ALU_A_LD), .Q(ALU_A_CT));
  Register #(.Bits(8)) register_54 (.D(multiplexer_36_out), .C(C_ct), .en(ALU_A_LD), .Q({ALU_A_WR, ALU_A_RM}));
  Multiplexer multiplexer_56 (
    .sel(and_80_out[1]), .in_0(nand_4_out[1]), .in_1(nand_4_out[2]), .out(multiplexer_56_out));
  Multiplexer multiplexer_57 (
    .sel(register_46_q[2]), .in_0(CT_DIR__LD), .in_1(register_46_q[2]), .out(multiplexer_57_out));
  and and_78 (and_78_out, multiplexer_56_out, multiplexer_57_out);
  not not_26 (not_26_out, multiplexer_56_out);
  nand nand_4 (nand_4_out[2], inst_comp_5_a_old, clr);
  Register #(.Bits(4)) register_55 (.D(multiplexer_38_out), .C(C_ct), .en(multiplexer_37_out[1]), .Q(register_55_q));
  Register register_56 (.D(multiplexer_39_out), .C(C_ct), .en(multiplexer_37_out[1]), .Q(register_56_q));
  Register #(.Bits(32)) register_57 (.D(multiplexer_40_out), .C(C), .en(multiplexer_37_out[1]), .Q(register_57_q));
  Register #(.Bits(8)) register_58 (.D(multiplexer_41_out), .C(C_ct), .en(multiplexer_37_out[1]), .Q(register_58_q));
  Multiplexer multiplexer_58 (
    .sel(and_81_out[1]), .in_0(nand_5_out[1]), .in_1(nand_5_out[2]), .out(multiplexer_58_out));
  Multiplexer multiplexer_59 (
    .sel(register_47_q[2]), .in_0(CT_MB__LD), .in_1(register_47_q[2]), .out(multiplexer_59_out));
  and and_79 (and_79_out, multiplexer_58_out, multiplexer_59_out);
  not not_27 (not_27_out, multiplexer_58_out);
  nand nand_5 (nand_5_out[2], inst_comp_6_a_old, clr);
  Register #(.Bits(4)) register_59 (.D(multiplexer_43_out), .C(C_ct), .en(multiplexer_42_out[1]), .Q(register_59_q));
  Register register_60 (.D(multiplexer_44_out), .C(C_ct), .en(multiplexer_42_out[1]), .Q(register_60_q));
  Register register_61 (.D(multiplexer_45_out), .C(C_ct), .en(multiplexer_42_out[1]), .Q(register_61_q));
  Register #(.Bits(32)) register_62 (.D(multiplexer_46_out), .C(C), .en(multiplexer_42_out[1]), .Q(register_62_q));
  Register #(.Bits(32)) register_63 (.D(multiplexer_47_out), .C(C), .en(multiplexer_42_out[1]), .Q(register_63_q));
  Register #(.Bits(16)) register_64 (.D(multiplexer_48_out), .C(C), .en(multiplexer_42_out[1]), .Q(register_64_q));
  Register #(.Bits(2)) register_65 (.D(multiplexer_49_out), .C(C_ct), .en(multiplexer_42_out[1]), .Q(register_65_q));
  Register #(.Bits(8)) register_66 (.D(multiplexer_50_out), .C(C_ct), .en(multiplexer_42_out[1]), .Q(register_66_q));
  Register register_67 (.D(multiplexer_51_out), .C(C_ct), .en(multiplexer_42_out[1]), .Q(register_67_q));
  nand nand_6 (nand_2_out[1], ALU_busy, register_45_q[1]);
  Register register_68 (.D(and_78_out), .C(C_ct), .en(or_34_out), .Q(register_68_q[1]));
  or or_34 (or_34_out, not_26_out, multiplexer_37_out[1]);
  or or_35 (register_46_q[1], register_68_q[1], register_46_q[2]);
  assign and_80_out = nand_10_out & register_46_q;  // And and_80, 3 bits wide
  Multiplexer #(.Bits(4)) multiplexer_60 (
    .sel(register_46_q[1]), .in_0(CT_FU__INST), .in_1(register_55_q), .out(multiplexer_60_out));
  inst_comp inst_comp_7 (
    .A_id(register_55_q), .A_ep(register_56_q), .B_id(clr_id), .B_ep(clr_ep), .A_old(inst_comp_7_a_old));
  Multiplexer multiplexer_61 (
    .sel(register_46_q[1]), .in_0(CT_FU__EPOCH), .in_1(register_56_q), .out(multiplexer_61_out));
  Multiplexer #(.Bits(32)) multiplexer_62 (
    .sel(register_46_q[1]), .in_0(multiplexer_24_out), .in_1(register_57_q), .out(multiplexer_62_out));
  Multiplexer #(.Bits(8)) multiplexer_63 (
    .sel(register_46_q[1]), .in_0(CT_FU__WR), .in_1(register_58_q), .out(multiplexer_63_out));
  Register register_69 (.D(and_79_out), .C(C_ct), .en(or_36_out), .Q(register_69_q[1]));
  or or_36 (or_36_out, not_27_out, multiplexer_42_out[1]);
  or or_37 (register_47_q[1], register_69_q[1], register_47_q[2]);
  assign and_81_out = nand_11_out & register_47_q;  // And and_81, 3 bits wide
  Multiplexer #(.Bits(4)) multiplexer_64 (
    .sel(register_47_q[1]), .in_0(CT_FU__INST), .in_1(register_59_q), .out(multiplexer_64_out));
  inst_comp inst_comp_8 (
    .A_id(register_59_q), .A_ep(register_60_q), .B_id(clr_id), .B_ep(clr_ep), .A_old(inst_comp_8_a_old));
  Multiplexer multiplexer_65 (
    .sel(register_47_q[1]), .in_0(CT_FU__EPOCH), .in_1(register_60_q), .out(multiplexer_65_out));
  Multiplexer multiplexer_66 (.sel(register_47_q[1]), .in_0(CT_MB__ST), .in_1(register_61_q), .out(multiplexer_66_out));
  Multiplexer #(.Bits(32)) multiplexer_67 (
    .sel(register_47_q[1]), .in_0(multiplexer_26_out), .in_1(register_62_q), .out(multiplexer_67_out));
  Multiplexer #(.Bits(32)) multiplexer_68 (
    .sel(register_47_q[1]), .in_0(R_B), .in_1(register_63_q), .out(multiplexer_68_out));
  Multiplexer #(.Bits(16)) multiplexer_69 (
    .sel(register_47_q[1]), .in_0(multiplexer_27_out), .in_1(register_64_q), .out(multiplexer_69_out));
  Multiplexer #(.Bits(2)) multiplexer_70 (
    .sel(register_47_q[1]), .in_0({CT_FU__WR[1], and_68_out[0]}), .in_1(register_65_q),
    .out(multiplexer_70_out));
  Multiplexer #(.Bits(8)) multiplexer_71 (
    .sel(register_47_q[1]), .in_0(CT_FU__WR), .in_1(register_66_q), .out(multiplexer_71_out));
  Multiplexer multiplexer_72 (.sel(register_47_q[1]), .in_0(CT_FU__MF), .in_1(register_67_q), .out(multiplexer_72_out));
  not not_28 (nand_2_out[0], ALU_busy);
  nand nand_7 (nand_1_out[0], or_41_out, clr);
  inst_comp inst_comp_9 (.A_id(ALU_A_INST), .A_ep(register_49_q), .B_id(clr_id), .B_ep(clr_ep), .A_old(ALU_A_CMP));
  Multiplexer multiplexer_73 (
    .sel(and_80_out[0]), .in_0(nand_4_out[0]), .in_1(nand_4_out[1]), .out(multiplexer_73_out));
  Multiplexer multiplexer_74 (
    .sel(register_46_q[1]), .in_0(CT_DIR__LD), .in_1(register_68_q[1]), .out(multiplexer_74_out));
  and and_82 (and_82_out, multiplexer_73_out, multiplexer_74_out);
  or or_38 (register_46_q[0], DIR_busy, register_68_q[1], register_46_q[2]);
  nand nand_8 (nand_4_out[1], inst_comp_7_a_old, clr);
  Register #(.Bits(4)) register_70 (.D(multiplexer_60_out), .C(C_ct), .en(DIR_LD), .Q(DIR_INST));
  Register register_71 (.D(multiplexer_61_out), .C(C_ct), .en(DIR_LD), .Q(register_71_q));
  Register #(.Bits(32)) register_72 (.D(multiplexer_62_out), .C(C), .en(DIR_LD), .Q(DIR));
  Register #(.Bits(8)) register_73 (.D(multiplexer_63_out), .C(C_ct), .en(DIR_LD), .Q(DIR_WR));
  Multiplexer multiplexer_75 (
    .sel(and_81_out[0]), .in_0(nand_5_out[0]), .in_1(nand_5_out[1]), .out(multiplexer_75_out));
  Multiplexer multiplexer_76 (
    .sel(register_47_q[1]), .in_0(CT_MB__LD), .in_1(register_69_q[1]), .out(multiplexer_76_out));
  and and_83 (and_83_out, multiplexer_75_out, multiplexer_76_out);
  or or_39 (register_47_q[0], MB_busy, register_69_q[1], register_47_q[2]);
  nand nand_9 (nand_5_out[1], inst_comp_8_a_old, clr);
  Register #(.Bits(4)) register_74 (.D(multiplexer_64_out), .C(C_ct), .en(MB_LD), .Q(MB_INST));
  Register register_75 (.D(multiplexer_65_out), .C(C_ct), .en(MB_LD), .Q(MB_ep));
  Register register_76 (.D(multiplexer_66_out), .C(C_ct), .en(MB_LD), .Q(MB_type__st));
  Register #(.Bits(32)) register_77 (.D(multiplexer_67_out), .C(C), .en(MB_LD), .Q(MB_data));
  Register #(.Bits(32)) register_78 (.D(multiplexer_68_out), .C(C), .en(MB_LD), .Q(register_78_q));
  Register #(.Bits(16)) register_79 (.D(multiplexer_69_out), .C(C), .en(MB_LD), .Q(register_79_q));
  Register #(.Bits(2)) register_80 (.D(multiplexer_70_out), .C(C_ct), .en(MB_LD), .Q(MB_MD));
  Register #(.Bits(8)) register_81 (.D(multiplexer_71_out), .C(C_ct), .en(MB_LD), .Q(MB_WR));
  Register register_82 (.D(multiplexer_72_out), .C(C_ct), .en(MB_LD), .Q(MB_MF));
  Register #(.Bits(4)) register_83 (.D(multiplexer_28_out), .C(C_ct), .en(ALU_B_LD), .Q(ALU_B_INST));
  Register register_84 (.D(multiplexer_29_out), .C(C_ct), .en(ALU_B_LD), .Q(register_84_q));
  Register #(.Bits(32)) register_85 (.D(multiplexer_32_out), .C(C), .en(ALU_B_LD), .Q(ALU_B_A));
  Register #(.Bits(32)) register_86 (.D(multiplexer_33_out), .C(C), .en(ALU_B_LD), .Q(ALU_B_B));
  Register #(.Bits(8)) register_87 (.D(multiplexer_34_out), .C(C), .en(ALU_B_LD), .Q(ALU_B_FI));
  Register #(.Bits(9)) register_88 (.D(multiplexer_35_out), .C(C_ct), .en(ALU_B_LD), .Q(ALU_B_CT));
  Register #(.Bits(8)) register_89 (.D(multiplexer_36_out), .C(C_ct), .en(ALU_B_LD), .Q({ALU_B_WR, ALU_B_RM}));
  nand nand_10 (nand_10_out[2], DIR_busy, register_68_q[1], register_46_q[2]);
  Register register_90 (.D(and_83_out), .C(C_ct), .en(or_40_out), .Q(register_90_q));
  not not_29 (not_29_out, multiplexer_75_out);
  or or_40 (or_40_out, not_29_out, multiplexer_42_out[0]);
  nand nand_11 (nand_11_out[2], MB_busy, register_69_q[1], register_47_q[2]);
  and and_84 (and_84_out[0], ALU_A_LD, multiplexer_30_out);
  BitExtender #(.inputBits(1), .outputBits(2)) bitextender_5 (.in(ALU_A_CLR), .out(bitextender_5_out));
  and and_85 (and_84_out[1], ALU_A_LD, multiplexer_31_out);
  and and_86 (and_86_out[0], ALU_B_LD, multiplexer_30_out);
  BitExtender #(.inputBits(1), .outputBits(2)) bitextender_6 (.in(ALU_B_CLR), .out(bitextender_6_out));
  and and_87 (and_86_out[1], ALU_B_LD, multiplexer_31_out);
  or or_41 (or_41_out, ALU_A_CMP, ALU_B_CMP);
  nand nand_12 (nand_10_out[1], DIR_busy, register_68_q[1]);
  not not_30 (nand_10_out[0], DIR_busy);
  inst_comp inst_comp_10 (
    .A_id(DIR_INST), .A_ep(register_71_q), .B_id(clr_id), .B_ep(clr_ep), .A_old(inst_comp_10_a_old));
  and and_88 (MB_LD, MB_free, and_83_out);
  nand nand_13 (nand_11_out[1], MB_busy, register_69_q[1]);
  not not_31 (nand_11_out[0], MB_busy);
  inst_comp inst_comp_11 (.A_id(MB_INST), .A_ep(MB_ep), .B_id(clr_id), .B_ep(clr_ep), .A_old(inst_comp_11_a_old));
  add_s16c32 add_s16c32_1 (.a(register_78_q), .b(register_79_q), .s(MB_addr));  // open: c
  and and_89 (and_89_out, ~and_84_out[0], ALU_A_STD);  // And
  and and_90 (and_90_out, ~and_84_out[1], ALU_A_STF);  // And
  and and_91 (and_91_out, ~and_86_out[0], ALU_B_STD);  // And
  and and_92 (and_92_out, ~and_86_out[1], ALU_B_STF);  // And
  inst_comp inst_comp_12 (.A_id(ALU_B_INST), .A_ep(register_84_q), .B_id(clr_id), .B_ep(clr_ep), .A_old(ALU_B_CMP));
  nand nand_14 (nand_4_out[0], inst_comp_10_a_old, clr);
  nand nand_15 (nand_5_out[0], inst_comp_11_a_old, clr);
  and and_93 (and_93_out, byte_I0[3], byte_I0[0]);
  and and_94 (and_94_out, byte_I0[2], byte_I0[0]);
  and and_95 (and_95_out, byte_I0_iv[3], byte_I0_iv[2], byte_I0[1], byte_I0_iv[0]);
  and and_96 (and_96_out, byte_I0_iv[2], byte_I0_iv[0]);
  and and_97 (and_97_out, byte_I0[2], byte_I0[0]);
  and and_98 (and_98_out, byte_I0[1], byte_I0[2], byte_I0[4]);
  and and_99 (and_99_out, byte_I0[3], byte_I0[4]);
  D_FF #(.Bits(2)) d_ff_4 (.D(and_84_out), .C(C_ct), .Q(d_ff_4_q));  // open: nQ
  assign and_100_out = d_ff_4_q & ~bitextender_5_out;  // And and_100, 2 bits wide
  RS_FF rs_ff_3 (.S(and_84_out[0]), .C(C_ct), .R(and_89_out), .nQ(rs_ff_3_nq));  // open: Q
  RS_FF rs_ff_4 (.S(and_84_out[1]), .C(C_ct), .R(and_90_out), .nQ(rs_ff_4_nq));  // open: Q
  D_FF #(.Bits(2)) d_ff_5 (.D(and_86_out), .C(C_ct), .Q(d_ff_5_q));  // open: nQ
  assign and_101_out = d_ff_5_q & ~bitextender_6_out;  // And and_101, 2 bits wide
  RS_FF rs_ff_5 (.S(and_86_out[0]), .C(C_ct), .R(and_91_out), .nQ(rs_ff_5_nq));  // open: Q
  RS_FF rs_ff_6 (.S(and_86_out[1]), .C(C_ct), .R(and_92_out), .nQ(rs_ff_6_nq));  // open: Q
  and and_102 (and_102_out, ~and_82_out, DIR_ST);  // And
  and and_103 (DIR_CLR, clr, inst_comp_10_a_old);
  and and_104 (LDB_forward, MB_ld__e, LDB_ldV);
  or or_42 (or_42_out, MEM_LD__RD, LDB_forward);
  and and_105 (and_105_out, byte_I0_iv[7], byte_I0_iv[6], byte_I0[5]);
  and and_106 (and_106_out, byte_I0_iv[7], byte_I0[6], byte_I0_iv[5]);
  D_FF #(.Bits(2)) d_ff_6 (.D(and_100_out), .C(C_ct), .Q(d_ff_6_q));  // open: nQ
  and and_107 (ALU_A_UUD, rs_ff_3_nq, ALU_A_V);
  and and_108 (ALU_A_UUF, rs_ff_4_nq, ALU_A_V);
  D_FF #(.Bits(2)) d_ff_7 (.D(and_101_out), .C(C_ct), .Q(d_ff_7_q));  // open: nQ
  and and_109 (ALU_B_UUD, rs_ff_5_nq, ALU_B_V);
  and and_110 (ALU_B_UUF, rs_ff_6_nq, ALU_B_V);
  or or_43 (or_43_out, ALU_A_CLR, and_134_out);
  or or_44 (or_44_out, ALU_B_CLR, and_135_out);
  // alu_32 alu_32_1: pin names not known; wires that end beside it: ALU_A_A, ALU_A_B, ALU_A_FI, ALU_A_CT, ALU_A_RM, alu_32_1_p6, alu_32_1_p6, alu_32_1_p8, alu_32_1_p9, alu_32_1_p9, alu_32_1_p11, alu_32_1_p12, alu_32_1_p12, alu_32_1_p14, ALU_A_R, ALU_A_F
  alu_32 alu_32_2 (
    .A(ALU_B_A), .B(ALU_B_B), .F_I(ALU_B_FI), .CT(ALU_B_CT), .RM(ALU_B_RM), .E_A(alu_32_1_p8),
    .E_B(alu_32_1_p11), .E(alu_32_1_p14), .R_O(ALU_B_R), .F_O(ALU_B_F));
  RS_FF rs_ff_7 (.S(and_82_out), .C(C_ct), .R(and_102_out), .nQ(rs_ff_7_nq));  // open: Q
  D_FF V (.D(DIR_LD), .C(C_ct), .Q(V_q));  // open: nQ
  bus16x2_demux bus16x2_demux_2 (.bus_1(V1_inst), .bus_2(V2_inst), .E(DIR_V), .id(DIR_INST));
  and and_111 (MB_MFE, MB_MF, register_90_q);
  and and_112 (MB_st__e, register_90_q, nand_5_out[0], MB_type__st);
  and and_113 (MB_ld__e, register_90_q, nand_5_out[0], ~MB_type__st);  // And
  and and_114 (and_114_out, CT_ISS__OSTB, ~clr);  // And
  Multiplexer #(.Bits(32)) multiplexer_77 (
    .sel(LDB_forward), .in_0(MEM_LD__D), .in_1(LDB_ldD), .out(multiplexer_77_out));
  Multiplexer #(.Bits(4)) multiplexer_78 (
    .sel(LDB_forward), .in_0(MEM_LD__INST), .in_1(MB_INST), .out(multiplexer_78_out));
  and and_115 (and_115_out, CT_ISS__OLDB, ~clr);  // And
  and and_116 (and_116_out, byte_I0[4], byte_I0[3], byte_I0_iv[1], byte_I0_iv[2], byte_I0_iv[5], byte_I0_iv[6], byte_I0_iv[7]);
  or or_45 (or_45_out, and_93_out, and_94_out, and_95_out);
  nor nor_5 (nor_5_out, byte_I0[3], byte_I0[1], and_96_out, and_97_out);
  nor nor_6 (nor_6_out, and_98_out, and_99_out);
  and and_117 (and_117_out, byte_I0_iv[0], byte_I0_iv[1], byte_I0[2], byte_I0[3], byte_I0[4], byte_I0_iv[5], byte_I0_iv[6], byte_I0_iv[7]);
  and and_118 (and_118_out, byte_I0[1], byte_I0_iv[2], byte_I0[3], byte_I0[4], byte_I0_iv[5], byte_I0_iv[6], byte_I0_iv[7]);
  and and_119 (and_119_out, com1, CT_FL__W1);
  and and_120 (and_120_out, com2, CT_FL__W2);
  assign {ALU_A_FRE, ALU_A_DRE} = d_ff_6_q & ~bitextender_5_out;  // And and_121, 2 bits wide
  assign {ALU_B_FRE, ALU_B_DRE} = d_ff_7_q & ~bitextender_6_out;  // And and_122, 2 bits wide
  and and_123 (and_123_out, ALU_A_VD, ~or_43_out);  // And
  and and_124 (and_124_out, ALU_A_VF, ~or_43_out);  // And
  and and_125 (and_125_out, ALU_B_VD, ~or_44_out);  // And
  and and_126 (and_126_out, ALU_B_VF, ~or_44_out);  // And
  PullDown #(.Bits(32)) pulldown_13 (.out(alu_32_1_p12));
  PullDown #(.Bits(32)) pulldown_14 (.out(alu_32_1_p14));
  or or_46 (DIR_free, DIR_ST, rs_ff_7_nq);
  and and_127 (DIR_RD, V_q, ~DIR_CLR);  // And
  not not_32 (not_32_out, byte_I0[0]);
  and and_128 (and_128_out, byte_I0[1], byte_I0[2], byte_I0[3], byte_I0[4], byte_I0_iv[5], byte_I0_iv[6], byte_I0_iv[7]);
  or or_47 (or_47_out, and_105_out, and_106_out);
  or or_48 (CT_RF__FLS, and_119_out, and_120_out);
  RS_FF rs_ff_8 (.S(ALU_A_DRE), .C(C_ct), .R(ALU_A_DRD), .Q(ALU_A_DRD));  // open: nQ
  RS_FF rs_ff_9 (.S(ALU_A_FRE), .C(C_ct), .R(ALU_A_FRD), .Q(ALU_A_FRD));  // open: nQ
  RS_FF rs_ff_10 (.S(ALU_B_DRE), .C(C_ct), .R(ALU_B_DRD), .Q(ALU_B_DRD));  // open: nQ
  RS_FF rs_ff_11 (.S(ALU_B_FRE), .C(C_ct), .R(ALU_B_FRD), .Q(ALU_B_FRD));  // open: nQ
  RS_FF rs_ff_12 (.S(and_123_out), .C(C_ct), .R(or_43_out), .Q(rs_ff_12_q));  // open: nQ
  RS_FF rs_ff_13 (.S(and_124_out), .C(C_ct), .R(or_43_out), .Q(rs_ff_13_q));  // open: nQ
  RS_FF rs_ff_14 (.S(and_125_out), .C(C_ct), .R(or_44_out), .Q(rs_ff_14_q));  // open: nQ
  RS_FF rs_ff_15 (.S(and_126_out), .C(C_ct), .R(or_44_out), .Q(rs_ff_15_q));  // open: nQ
  store_buffer store_buffer_1 (
    .C(C), .LD(MB_STB__LD), .W_d(MB_st__e), .inst_W(MB_INST), .D(MB_data), .A(MB_addr), .MD(MB_MD),
    .W_id(and_114_out), .epoch(epoch_IS), .inst(inst_IS), .com1(com1), .com2(com2), .com1_id(com1_inst),
    .com2_id(com2_inst), .ld_ep(MB_ep), .ld_id(MB_INST), .ld_addr(MB_addr), .clr(clr), .clr_ep(clr_ep),
    .clr_id(clr_id), .full(store_buffer_1_full), .V(STB_M__V), .D_O(STB_M__D), .A_O(STB_M__A),
    .MD_O(STB_M__MD), .id_O(STB_M__ID), .ep_O(STB_M__EP), .ld_V(LDB_ldV), .ld_D(LDB_ldD));
  // load_buffer load_buffer_1: pin names not known; wires that end beside it: C, MB_LDB__LD, FU_D__V[3], or_42_out, multiplexer_78_out, multiplexer_77_out, MB_ld__e, MB_INST, MB_addr, MB_MD, MB_MF, MB_WR, and_115_out, epoch_IS, inst_IS, com1, com2, com1_inst, com2_inst, MB_st__e, MB_ep, MB_INST, MB_addr, MB_data, clr, clr_ep, clr_id, load_buffer_1_p28, load_buffer_1_p29, LDB_B__D, load_buffer_1_p31, load_buffer_1_p32, load_buffer_1_p33, LDB_M__V, LDB_M__A, LDB_M__MD, LDB_M__ID, LDB_M__EP, load_buffer_1_p39, load_buffer_1_p40
  and and_129 (and_129_out, byte_I0_iv[7], byte_I0_iv[6], byte_I0_iv[5], byte_I0_iv[4]);
  and and_130 (and_130_out, byte_I0_iv[7], byte_I0_iv[6], byte_I0_iv[5], byte_I0[4], byte_I0_iv[3]);
  or or_49 (or_49_out, and_117_out, and_118_out);
  or or_50 (or_50_out, ALU_A_VD, ALU_A_UUD, rs_ff_12_q);
  or or_51 (or_51_out, ALU_A_VF, ALU_A_UUF, rs_ff_13_q);
  or or_52 (or_52_out, ALU_B_VD, ALU_B_UUD, rs_ff_14_q);
  or or_53 (or_53_out, ALU_B_VF, ALU_B_UUF, rs_ff_15_q);
  and and_131 (DIR_LD, and_82_out, DIR_free);
  not not_33 (DIR_busy, DIR_free);
  not not_34 (not_34_out, or_45_out);
  and and_132 (and_132_out, and_128_out, byte_I0[0]);
  and and_133 (and_133_out, not_32_out, and_128_out);
  or or_54 (or_54_out, ALU_A_STD, rs_ff_3_nq);
  or or_55 (or_55_out, ALU_A_STF, rs_ff_4_nq);
  or or_56 (or_56_out, ALU_B_STD, rs_ff_5_nq);
  or or_57 (or_57_out, ALU_B_STF, rs_ff_6_nq);
  and and_134 (and_134_out, or_50_out, ~ALU_A_CLR, or_51_out);  // And
  bus16x2_demux bus16x2_demux_3 (.bus_1(V1_inst), .bus_2(V2_inst), .E(and_134_out), .id(ALU_A_INST));
  and and_135 (and_135_out, or_52_out, ~ALU_B_CLR, or_53_out);  // And
  bus16x2_demux bus16x2_demux_4 (.bus_1(V1_inst), .bus_2(V2_inst), .E(and_135_out), .id(ALU_B_INST));
  nor nor_7 (ALU_busy, ALU_A_LRD, ALU_B_LRD);
  or or_58 (ALU_free, ALU_A_LRD, ALU_B_LRD);
  Register #(.Bits(32)) register_91 (.D(ALU_A_R), .C(C), .en(ALU_A_DRE), .Q(ALU_A_T__R));
  Register #(.Bits(8)) register_92 (.D(ALU_A_F), .C(C), .en(ALU_A_FRE), .Q(ALU_A_T__F));
  Register #(.Bits(32)) register_93 (.D(ALU_B_R), .C(C), .en(ALU_B_DRE), .Q(ALU_B_T__R));
  Register #(.Bits(8)) register_94 (.D(ALU_B_F), .C(C), .en(ALU_B_FRE), .Q(ALU_B_T__F));
  and and_136 (and_136_out, ~MB_MF, MB_st__e);  // And
  and and_137 (and_137_out, ~LDB_B__MF, FU_D__V[3]);  // And
  D_FF d_ff_8 (.D(store_buffer_1_full), .C(C_ct), .Q(STB_busy));  // open: nQ
  D_FF d_ff_9 (.D(load_buffer_1_p28), .C(C_ct), .Q(LDB_busy));  // open: nQ
  D_FF #(.Bits(4)) d_ff_10 (.D(load_buffer_1_p31), .C(C_ct), .Q(LDB_B__INST));  // open: nQ
  D_FF d_ff_11 (.D(load_buffer_1_p33), .C(C_ct), .Q(LDB_B__MF));  // open: nQ
  D_FF d_ff_12 (.D(load_buffer_1_p39), .C(C_ct), .Q(Fl_MEM));  // open: nQ
  D_FF #(.Bits(4)) d_ff_13 (.D(undriven), .C(C_ct), .Q(FL_MEM__ID));  // open: nQ
  or or_59 (or_59_out, and_129_out, and_116_out, and_130_out);
  assign issue = or_59_out ? issue_e : 1'bz;  // Driver driver_96
  assign CT_ISS__URA = or_59_out ? 1'b1 : 1'bz;  // Driver driver_97
  assign CT_ISS__URB = or_59_out ? not_34_out : 1'bz;  // Driver driver_98
  assign CT_ISS__RA = or_59_out ? byte_I1[7:3] : 5'bz;  // Driver driver_99
  assign CT_ISS__RB = or_59_out ? byte_I2[7:3] : 5'bz;  // Driver driver_100
  assign CT_ISS__UFL = or_59_out ? nor_5_out : 1'bz;  // Driver driver_101
  assign CT_ISS__ORC = or_59_out ? nor_6_out : 1'bz;  // Driver driver_102
  assign CT_ISS__RC = or_59_out ? byte_I1[7:3] : 5'bz;  // Driver driver_103
  assign CT_ISS__OFL = or_59_out ? 1'b1 : 1'bz;  // Driver driver_104
  assign CT_ISS__UFU = or_59_out ? 3'b001 : 3'bz;  // Driver driver_105
  assign CT_ISS__URA = and_117_out ? 1'b1 : 1'bz;  // Driver driver_106
  assign CT_ISS__RA = and_117_out ? byte_I2[7:3] : 5'bz;  // Driver driver_107
  assign issue = or_49_out ? issue_e : 1'bz;  // Driver driver_108
  assign CT_ISS__ORC = or_49_out ? 1'b1 : 1'bz;  // Driver driver_109
  assign CT_ISS__RC = or_49_out ? byte_I1[7:3] : 5'bz;  // Driver driver_110
  assign CT_ISS__UFU = or_49_out ? 3'b010 : 3'bz;  // Driver driver_111
  assign issue = and_128_out ? issue_e : 1'bz;  // Driver driver_112
  assign CT_ISS__USC = and_128_out ? 1'b1 : 1'bz;  // Driver driver_113
  assign CT_ISS__OSC = and_128_out ? 1'b1 : 1'bz;  // Driver driver_114
  assign CT_ISS__UFU = and_128_out ? 3'b011 : 3'bz;  // Driver driver_115
  assign CT_ISS__URA = and_132_out ? 1'b1 : 1'bz;  // Driver driver_116
  assign CT_ISS__RA = and_132_out ? byte_I1[7:3] : 5'bz;  // Driver driver_117
  assign CT_ISS__OSTB = and_132_out ? issue_e : 1'bz;  // Driver driver_118
  assign CT_ISS__ORC = and_133_out ? 1'b1 : 1'bz;  // Driver driver_119
  assign CT_ISS__RC = and_133_out ? byte_I1[7:3] : 5'bz;  // Driver driver_120
  assign CT_ISS__OLDB = and_133_out ? issue_e : 1'bz;  // Driver driver_121
  assign issue = or_47_out ? issue_e : 1'bz;  // Driver driver_122
  assign CT_ISS__URA = or_47_out ? 1'b1 : 1'bz;  // Driver driver_123
  assign CT_ISS__RA = or_47_out ? byte_I0[4:0] : 5'bz;  // Driver driver_124
  assign CT_ISS__UFU = or_47_out ? 3'b011 : 3'bz;  // Driver driver_125
  assign CT_ISS__URB = and_106_out ? 1'b1 : 1'bz;  // Driver driver_126
  assign CT_ISS__RB = and_106_out ? byte_I1[7:3] : 5'bz;  // Driver driver_127
  assign CT_ISS__ORC = and_105_out ? 1'b1 : 1'bz;  // Driver driver_128
  assign CT_ISS__RC = and_105_out ? byte_I1[7:3] : 5'bz;  // Driver driver_129
  assign CT_ISS__OLDB = and_105_out ? issue_e : 1'bz;  // Driver driver_130
  assign CT_ISS__OSTB = and_106_out ? issue_e : 1'bz;  // Driver driver_131
  bus16_demux bus16_demux_2 (.bus(V1_inst), .E(MB_st__e), .id(MB_INST));
  bus16_demux bus16_demux_3 (.bus(V2_inst), .E(and_136_out), .id(MB_INST));
  bus16_demux bus16_demux_4 (.bus(V1_inst), .E(FU_D__V[3]), .id(LDB_B__INST));
  bus16_demux bus16_demux_5 (.bus(V2_inst), .E(and_137_out), .id(LDB_B__INST));
  DipSwitch dipswitch_7 (.out(MB_busy));
  not not_35 (MB_free, MB_busy);
  D_FF #(.Bits(8)) d_ff_14 (.D(load_buffer_1_p32), .C(C_ct), .Q(LDB_B__WR));  // open: nQ
  D_FF d_ff_15 (.D(load_buffer_1_p40), .C(C_ct), .Q(FL_MEM__EP));  // open: nQ
  Multiplexer #(.Bits(8)) multiplexer_79 (.sel(and_120_out), .in_0(CT_FL__D1), .in_1(CT_FL__D2), .out(fl_i));
  and and_138 (ALU_A_LD, and_77_out, or_55_out, or_54_out);
  and and_139 (ALU_A_LRD, or_54_out, or_55_out);
  nand nand_16 (nand_16_out, or_54_out, or_55_out);
  and and_140 (ALU_B_LD, nand_16_out, and_77_out, or_57_out, or_56_out);
  and and_141 (ALU_B_LRD, or_56_out, or_57_out);
  and and_142 (and_142_out, ~ALU_A_LD, or_43_out);  // And
  and and_143 (and_143_out, ~ALU_B_LD, or_44_out);  // And
  and and_144 (and_144_out, d_ff_16_q, ~FU_D__V[3]);  // And
  and and_145 (ALU_A_CLR, clr, ALU_A_CMP);
  and and_146 (ALU_B_CLR, clr, ALU_B_CMP);
  D_FF d_ff_16 (.D(load_buffer_1_p29), .C(C_ct), .Q(d_ff_16_q));  // open: nQ
  D_FF d_ff_17 (.D(and_144_out), .C(C_ct), .nQ(d_ff_17_nq));  // open: Q
  and and_147 (LDB_B__RD, d_ff_16_q, d_ff_17_nq);
  RS_FF rs_ff_16 (.S(ALU_A_LD), .C(C_ct), .R(and_142_out), .Q(ALU_A_V));  // open: nQ
  RS_FF rs_ff_17 (.S(ALU_B_LD), .C(C_ct), .R(and_143_out), .Q(ALU_B_V));  // open: nQ
  and and_148 (and_148_out, byte_I0_iv[4], byte_I0[5], byte_I0[6], byte_I0_iv[7]);
  Comparator #(.Bits(3)) comparator_3 (.a(byte_I0[2:0]), .b(3'b110), .eq(comparator_3_eq));  // open: gt, lt
  not not_36 (not_36_out, E);
  D_FF #(.Bits(5)) d_ff_18 (.D(CT_RF__R1[7:3]), .C(C), .Q(d_ff_18_q));  // open: nQ
  D_FF #(.Bits(5)) d_ff_19 (.D(CT_RF__R2[7:3]), .C(C));  // open: Q, nQ
  and and_149 (and_149_out, byte_I0[0], byte_I0_iv[1], byte_I0[2], byte_I0[3], byte_I0[4], byte_I0_iv[5], byte_I0_iv[6], byte_I0_iv[7]);
  not not_37 (not_37_out, comparator_3_eq);
  and and_150 (and_150_out, byte_I0_iv[0], byte_I0_iv[1], byte_I0_iv[2], byte_I0_iv[3], byte_I0[4], byte_I0[5], byte_I0[6], byte_I0_iv[7]);
  and and_151 (and_151_out, byte_I0[0], byte_I0_iv[1], byte_I0_iv[2], byte_I0_iv[3], byte_I0[4], byte_I0[5], byte_I0[6], byte_I0_iv[7]);
  and and_152 (and_152_out, byte_I0[0], byte_I0[1], byte_I0_iv[2], byte_I0_iv[3], byte_I0[4], byte_I0[5], byte_I0[6], byte_I0_iv[7]);
  res_station res_station_1 (
    .C(C_ct), .res(not_36_out), .E(issue), .D({byte_I0, byte_I1, byte_I2, byte_I3}), .BTB_PK(BTB_pack__iss),
    .ep_I(epoch_IS), .inst(inst_IS), .URA(CT_ISS__URA), .URB(CT_ISS__URB), .RA(CT_ISS__RA), .RB(CT_ISS__RB),
    .USC(CT_ISS__USC), .UFL(CT_ISS__UFL), .UFU(CT_ISS__UFU), .ORC(CT_ISS__ORC), .RC(CT_ISS__RC),
    .OSC(CT_ISS__OSC), .OFL(CT_ISS__OFL), .com1(com1), .com2(com2), .com1_inst(com1_inst),
    .com2_inst(com2_inst), .com1_ep(com1_ep), .clr(clr), .clr_ep(clr_ep), .clr_id(clr_id), .FU_free(FU_free),
    .V(CT_DISP), .disp_32({res_station_1_disp_32, byte_D1, byte_D2, byte_D3}), .BTB_DP(BTB_DP),
    .ep_O(epoch_DP), .disp(inst_DP), .full(RS_full), .RCLR(RCLR));
  store_controller store_controller_1 (
    .C(C_ct), .in1(ALU_A_DRD), .in2(ALU_B_DRD), .in3(DIR_RD), .in4(LDB_B__RD), .in5(1'b0), .in6(1'b0),
    .in7(1'b0), .in8(1'b0), .clr({{5{1'b0}}, DIR_CLR, ALU_B_CLR, ALU_A_CLR}),
    .D1_sel(store_controller_1_d1_sel), .D2_sel(store_controller_1_d2_sel), .ST1(CT_ROB__GEN__STA),
    .ST2(CT_ROB__GEN__STB), .out1(ALU_A_STD), .out2(ALU_B_STD), .out3(DIR_ST), .out4(LDB_B__ST),
    .V({FU_D__V, DIR_V, ALU_B_VD, ALU_A_VD}));  // open: out5, out6, out7, out8
  store_controller store_controller_2 (
    .C(C_ct), .in1(ALU_A_FRD), .in2(ALU_B_FRD), .in3(1'b0), .in4(1'b0), .in5(1'b0), .in6(1'b0), .in7(1'b0),
    .in8(1'b0), .clr({{5{1'b0}}, DIR_CLR, ALU_B_CLR, ALU_A_CLR}), .D1_sel(store_controller_2_d1_sel),
    .D2_sel(store_controller_2_d2_sel), .ST1(CT_ROB__FL__STA), .ST2(CT_ROB__FL__STB), .out1(ALU_A_STF),
    .out2(ALU_B_STF), .V({FU_F__V, ALU_B_VF, ALU_A_VF}));  // open: out3, out4, out5, out6, out7, out8
  Demultiplexer #(.Selector_Bits(4)) demultiplexer_1 (
    .sel(priorityencoder_1_num), .in(and_164_out), .out_0(demultiplexer_1_out_0[0]),
    .out_1(demultiplexer_1_out_0[1]), .out_2(demultiplexer_1_out_0[2]), .out_3(demultiplexer_1_out_0[3]),
    .out_4(demultiplexer_1_out_0[4]), .out_5(demultiplexer_1_out_0[5]), .out_6(demultiplexer_1_out_0[6]),
    .out_7(demultiplexer_1_out_0[7]), .out_8(demultiplexer_1_out_0[8]), .out_9(demultiplexer_1_out_0[9]),
    .out_10(demultiplexer_1_out_0[10]), .out_11(demultiplexer_1_out_0[11]),
    .out_12(demultiplexer_1_out_0[12]), .out_13(demultiplexer_1_out_0[13]),
    .out_14(demultiplexer_1_out_0[14]), .out_15(demultiplexer_1_out_0[15]));
  Demultiplexer #(.Selector_Bits(4)) demultiplexer_2 (
    .sel(CT_FU__INST), .in(CT_RET__LD), .out_0(demultiplexer_2_out_0[0]), .out_1(demultiplexer_2_out_0[1]),
    .out_2(demultiplexer_2_out_0[2]), .out_3(demultiplexer_2_out_0[3]), .out_4(demultiplexer_2_out_0[4]),
    .out_5(demultiplexer_2_out_0[5]), .out_6(demultiplexer_2_out_0[6]), .out_7(demultiplexer_2_out_0[7]),
    .out_8(demultiplexer_2_out_0[8]), .out_9(demultiplexer_2_out_0[9]), .out_10(demultiplexer_2_out_0[10]),
    .out_11(demultiplexer_2_out_0[11]), .out_12(demultiplexer_2_out_0[12]),
    .out_13(demultiplexer_2_out_0[13]), .out_14(demultiplexer_2_out_0[14]), .out_15(demultiplexer_2_out_0[15]));
  Multiplexer #(.Bits(32)) multiplexer_80 (.sel(JPU_RET), .in_0(R_A), .in_1(CT_RF__DR), .out(multiplexer_80_out));
  not not_38 (not_38_out, JPU_CALL);
  not not_39 (not_39_out, JPU_RET);
  not not_40 (not_40_out, JPU_RET);
  assign issue = and_149_out ? issue_e : 1'bz;  // Driver driver_132
  assign CT_UBTB = and_148_out ? issue_e : 1'bz;  // Driver driver_133
  assign issue = and_148_out ? issue_e : 1'bz;  // Driver driver_134
  assign CT_ISS__URA = and_148_out ? 1'b1 : 1'bz;  // Driver driver_135
  assign CT_ISS__RA = and_148_out ? byte_I1[7:3] : 5'bz;  // Driver driver_136
  assign CT_ISS__UFL = and_148_out ? not_37_out : 1'bz;  // Driver driver_137
  assign CT_ISS__UFU = and_148_out ? 3'b111 : 3'bz;  // Driver driver_138
  assign issue = and_152_out ? issue_e : 1'bz;  // Driver driver_139
  PullDown #(.Bits(3)) pulldown_15 (.out(CT_ISS__UFU));
  PullDown pulldown_16 (.out(CT_ISS__OSTB));
  PullDown pulldown_17 (.out(clr));
  PullDown pulldown_18 (.out(clr_ep));
  PullDown #(.Bits(4)) pulldown_19 (.out(clr_id));
  BitExtender #(.inputBits(1), .outputBits(32)) bitextender_7 (.in(not_38_out), .out(bitextender_7_out));
  BitExtender #(.inputBits(1)) bitextender_8 (.in(not_39_out), .out(bitextender_8_out));
  BitExtender #(.inputBits(1), .outputBits(37)) bitextender_9 (.in(not_40_out), .out(bitextender_9_out));
  BitExtender #(.inputBits(1)) bitextender_10 (.in(CT_FU__EPOCH), .out(bitextender_10_out));
  assign not_41_out = ~demultiplexer_2_out_0;  // Not not_41, 16 bits wide
  BitExtender #(.inputBits(1)) bitextender_11 (.in(CT_FU__EPOCH), .out(bitextender_11_out));
  assign issue = and_150_out ? issue_e : 1'bz;  // Driver driver_140
  assign CT_ISS__URA = and_150_out ? 1'b1 : 1'bz;  // Driver driver_141
  assign CT_ISS__RA = and_150_out ? byte_I1[7:3] : 5'bz;  // Driver driver_142
  assign CT_ISS__USC = and_150_out ? 1'b1 : 1'bz;  // Driver driver_143
  assign CT_ISS__OSC = and_150_out ? 1'b1 : 1'bz;  // Driver driver_144
  assign CT_ISS__UFU = and_150_out ? 3'b110 : 3'bz;  // Driver driver_145
  assign CT_ISS__OSTB = and_150_out ? issue_e : 1'bz;  // Driver driver_146
  assign CT_UBTB = and_150_out ? issue_e : 1'bz;  // Driver driver_147
  assign issue = and_151_out ? issue_e : 1'bz;  // Driver driver_148
  assign CT_ISS__USC = and_151_out ? 1'b1 : 1'bz;  // Driver driver_149
  assign CT_ISS__OSC = and_151_out ? 1'b1 : 1'bz;  // Driver driver_150
  assign CT_ISS__UFU = and_151_out ? 3'b110 : 3'bz;  // Driver driver_151
  assign CT_ISS__OLDB = and_151_out ? issue_e : 1'bz;  // Driver driver_152
  assign CT_UBTB = and_151_out ? issue_e : 1'bz;  // Driver driver_153
  Multiplexer #(.Bits(8)) multiplexer_81 (.sel(CT_DISP), .in_0(8'h72), .in_1(res_station_1_disp_32), .out(byte_D0));
  Multiplexer #(.Bits(32)) multiplexer_82 (.sel(JPU_RET), .in_0(pc_read), .in_1(pc_ret), .out(multiplexer_82_out));
  Multiplexer #(.Bits(4)) multiplexer_83 (.sel(JPU_RET), .in_0(CT_FU__INST), .in_1(RET_INST), .out(multiplexer_83_out));
  Multiplexer multiplexer_84 (.sel(JPU_RET), .in_0(CT_FU__EPOCH), .in_1(RET_EPOCH), .out(multiplexer_84_out));
  assign and_153_out = multiplexer_80_out & bitextender_7_out;  // And and_153, 32 bits wide
  assign and_154_out = {byte_D2, byte_D3} & bitextender_8_out;  // And and_154, 16 bits wide
  assign and_155_out = BTB_DP & bitextender_9_out;  // And and_155, 37 bits wide
  or or_60 (or_60_out, CT_JPU__JP, JPU_RET);
  or or_61 (or_61_out, CT_FU__MF, JPU_RET);
  assign not_42_out = ~demultiplexer_1_out_0;  // Not not_42, 16 bits wide
  assign or_62_out = bitextender_10_out | not_41_out;  // Or or_62, 16 bits wide
  assign and_156_out = bitextender_11_out & demultiplexer_2_out_0;  // And and_156, 16 bits wide
  and and_157 (and_157_out, ~CT_JPU__LD, JPU_BTB__ST);  // And
  assign or_63_out = register_103_q | demultiplexer_2_out_0;  // Or or_63, 16 bits wide
  assign or_64_out = register_104_q | and_156_out;  // Or or_64, 16 bits wide
  // data_select_32 data_select_32_1: pin names not known; wires that end beside it: store_controller_1_d1_sel, store_controller_1_d2_sel, ALU_A_T__R, ALU_B_T__R, DIR, LDB_B__D, {32{1'b0}}, {32{1'b0}}, {32{1'b0}}, {32{1'b0}}, ROB_GEN_DA, ROB_GEN_DB
  data_select_8 data_select_8_1 (
    .D1_sel(store_controller_2_d1_sel), .D2_sel(store_controller_2_d2_sel), .in1(ALU_A_T__F),
    .in2(ALU_B_T__F), .in3({8{1'b0}}), .in4({8{1'b0}}), .in5({8{1'b0}}), .in6({8{1'b0}}), .in7({8{1'b0}}),
    .in8({8{1'b0}}), .out1(ROB_FL_A), .out2(ROB_FL_B));
  RS_FF rs_ff_18 (.S(CT_JPU__LD), .C(C_ct), .R(and_157_out), .Q(JPU_BTB__ST), .nQ(rs_ff_18_nq));
  Register #(.Bits(32)) register_95 (.D(multiplexer_82_out), .C(C), .en(JPU_LD), .Q(JPU_PC));
  Register #(.Bits(4)) register_96 (.D(multiplexer_83_out), .C(C_ct), .en(JPU_LD), .Q(Fl_JPU__INST));
  Register register_97 (.D(multiplexer_84_out), .C(C_ct), .en(JPU_LD), .Q(Fl_JPU__EP));
  Register #(.Bits(32)) register_98 (.D(and_153_out), .C(C), .en(JPU_LD), .Q(register_98_q));
  Register #(.Bits(16)) register_99 (.D(and_154_out), .C(C), .en(JPU_LD), .Q(register_99_q));
  Register #(.Bits(37)) register_100 (
    .D(and_155_out), .C(C_ct), .en(JPU_LD),
    .Q({JPU_BTB__tar, JPU_BTB__pred, JPU_BTB__J, JPU_BTB__V, JPU_BTBPK[0]}));
  Register register_101 (.D(or_60_out), .C(C_ct), .en(JPU_LD), .Q(JPU_JP));
  Register register_102 (.D(or_61_out), .C(C_ct), .en(JPU_LD), .Q(JPU_MF));
  assign and_158_out = icmk_16 & not_42_out & or_63_out;  // And and_158, 16 bits wide
  or or_65 (or_65_out, CT_RET__LD, and_164_out, ext_en);
  assign and_159_out = or_62_out & or_64_out;  // And and_159, 16 bits wide
  or or_66 (or_66_out, rs_ff_18_nq, JPU_BTB__ST);
  D_FF #(.Bits(32)) d_ff_20 (.D(register_98_q), .C(C_ct), .Q(d_ff_20_q));  // open: nQ
  D_FF #(.Bits(16)) d_ff_21 (.D(register_99_q), .C(C_ct), .Q(d_ff_21_q));  // open: nQ
  and and_160 (JPU_LD, CT_JPU__LD, or_66_out);
  Register #(.Bits(16)) register_103 (.D(and_158_out), .C(C_ct), .en(or_65_out), .Q(register_103_q));
  Register #(.Bits(16)) register_104 (.D(and_159_out), .C(C_ct), .en(or_65_out), .Q(register_104_q));
  add_s16c32 add_s16c32_2 (.a(multiplexer_85_out), .b(multiplexer_86_out), .s(JPU_ADDR));  // open: c
  Multiplexer #(.Bits(32)) multiplexer_85 (.sel(JPU_JP), .in_0(JPU_PC), .in_1(d_ff_20_q), .out(multiplexer_85_out));
  Multiplexer #(.Bits(16)) multiplexer_86 (.sel(JPU_JP), .in_0(16'h4), .in_1(d_ff_21_q), .out(multiplexer_86_out));
  assign and_161_out = V1_inst & register_103_q;  // And and_161, 16 bits wide
  BitSelector #(.Selector_Bits(4)) bitselector_1 (
    .in(register_104_q), .sel(priorityencoder_1_num), .out(bitselector_1_out));
  and and_162 (and_162_out, ~JPU_MF, JPU_BTB__ST);  // And
  PullDown pulldown_20 (.out(CT_ALU__M));
  PullDown pulldown_21 (.out(CT_ALU__LD));
  PullDown pulldown_22 (.out(CT_ALU__WD));
  PullDown pulldown_23 (.out(CT_ALU__WF));
  PullDown pulldown_24 (.out(CT_FU__EPOCH));
  PullDown #(.Bits(4)) pulldown_25 (.out(CT_FU__INST));
  PullDown #(.Bits(8)) pulldown_26 (.out(CT_FU__WR));
  PullDown pulldown_27 (.out(CT_DIR__LD));
  PullDown pulldown_28 (.out(CT_DIR__M));
  PullDown pulldown_29 (.out(CT_DIR__MS));
  PullDown pulldown_30 (.out(MB_ep));
  PullDown #(.Bits(4)) pulldown_31 (.out(LD_id));
  PullDown #(.Bits(32)) pulldown_32 (.out(LD_addr));
  PullDown pulldown_33 (.out(CT_STB__LD));
  PullDown pulldown_34 (.out(CT_LDB__LD));
  PullDown pulldown_35 (.out(CT_MB__LD));
  PullDown pulldown_36 (.out(CT_MB__ST));
  PullDown pulldown_37 (.out(CT_ISS__OLDB));
  PullDown pulldown_38 (.out(CT_UBTB));
  PullDown pulldown_39 (.out(CT_USCB));
  data_select_8 data_select_8_2 (
    .D1_sel(store_controller_1_d1_sel), .D2_sel(store_controller_1_d2_sel), .in1({ALU_A_WR, ALU_A_RM}),
    .in2({ALU_B_WR, ALU_B_RM}), .in3(DIR_WR), .in4(LDB_B__WR), .in5({8{1'b0}}), .in6({8{1'b0}}),
    .in7({8{1'b0}}), .in8({8{1'b0}}), .out1(ROB_GEN_WA), .out2(ROB_GEN_WB));
  data_select_4 data_select_4_1 (
    .D1_sel(store_controller_2_d1_sel), .D2_sel(store_controller_2_d2_sel), .in1(ALU_A_INST),
    .in2(ALU_B_INST), .in3(4'b0000), .in4(4'b0000), .in5(4'b0000), .in6(4'b0000), .in7(4'b0000),
    .in8(4'b0000), .out1(ROB_FL_INSTA), .out2(ROB_FL_INSTB));
  PriorityEncoder #(.Selector_Bits(4)) priorityencoder_1 (
    .in0(and_161_out[0]), .in1(and_161_out[1]), .in2(and_161_out[2]), .in3(and_161_out[3]),
    .in4(and_161_out[4]), .in5(and_161_out[5]), .in6(and_161_out[6]), .in7(and_161_out[7]),
    .in8(and_161_out[8]), .in9(and_161_out[9]), .in10(and_161_out[10]), .in11(and_161_out[11]),
    .in12(and_161_out[12]), .in13(and_161_out[13]), .in14(and_161_out[14]), .in15(and_161_out[15]),
    .num(priorityencoder_1_num), .any(priorityencoder_1_any));
  and and_163 (JPU_MFE, JPU_MF, JPU_BTB__ST);
  bus16_demux bus16_demux_6 (.bus(V1_inst), .E(and_162_out), .id(Fl_JPU__INST));
  bus16_demux bus16_demux_7 (.bus(V2_inst), .E(JPU_BTB__ST), .id(Fl_JPU__INST));
  not not_43 (not_43_out, BTB_override);
  and and_164 (and_164_out, FU_D__V[3], priorityencoder_1_any);
  PullDown pulldown_40 (.out(CT_RF__SCSS));
  xor xor_9 (JPU_MISS, JPU_BTB__J, JPU_JP);
  not not_44 (not_44_out, JPU_BTB__pred[0]);
  PullDown pulldown_41 (.out(CT_OBLOCK));
  and and_165 (and_165_out, JPU_BTB__pred[0], JPU_BTB__pred[1]);
  and and_166 (and_166_out, JPU_BTB__pred[0], JPU_JP);
  and and_167 (and_167_out, JPU_BTB__pred[1], JPU_JP);
  and and_168 (and_168_out, not_44_out, not_43_out, JPU_BTB__pred[1]);
  and and_169 (and_169_out, not_44_out, not_43_out, JPU_JP);
  and and_170 (and_170_out, JPU_BTB__pred[1], not_43_out, JPU_JP);
  D_FF #(.Bits(4)) d_ff_22 (.D(priorityencoder_1_num), .C(C_ct), .Q(RET_INST));  // open: nQ
  D_FF d_ff_23 (.D(bitselector_1_out), .C(C_ct), .Q(RET_EPOCH));  // open: nQ
  and and_171 (and_171_out, ~and_175_out, and_164_out);  // And
  inst_comp inst_comp_13 (.A_id(RET_INST), .A_ep(RET_EPOCH), .B_id(clr_id), .B_ep(clr_ep), .A_old(inst_comp_13_a_old));
  and and_172 (and_172_out, ~and_175_out, and_164_out);  // And
  inst_comp inst_comp_14 (
    .A_id(priorityencoder_1_num), .A_ep(bitselector_1_out), .B_id(clr_id), .B_ep(clr_ep),
    .A_old(inst_comp_14_a_old));
  data_select_4 data_select_4_2 (
    .D1_sel(store_controller_1_d1_sel), .D2_sel(store_controller_1_d2_sel), .in1(ALU_A_INST),
    .in2(ALU_B_INST), .in3(DIR_INST), .in4(LDB_B__INST), .in5(4'b0000), .in6(4'b0000), .in7(4'b0000),
    .in8(4'b0000), .out1(ROB_GEN_INSTA), .out2(ROB_GEN_INSTB));
  and and_173 (and_173_out[6], MB_free, JPU_free);
  or or_67 (JPU_pred[1], and_165_out, and_166_out, and_167_out, BTB_override);
  or or_68 (JPU_pred[0], and_168_out, and_169_out, and_170_out);
  PullDown pulldown_42 (.out(kernel_inst));
  PullDown pulldown_43 (.out(CT_RF__E));
  PullDown pulldown_44 (.out(CT_RF__DM));
  PullDown #(.Bits(5)) pulldown_45 (.out(CT_RF__WS));
  PullDown #(.Bits(3)) pulldown_46 (.out(CT_RF__WM));
  PullDown #(.Bits(5)) pulldown_47 (.out(CT_RF__RA));
  PullDown #(.Bits(3)) pulldown_48 (.out(CT_RF__MA));
  PullDown #(.Bits(5)) pulldown_49 (.out(CT_RF__RB));
  PullDown #(.Bits(3)) pulldown_50 (.out(CT_RF__MB));
  PullDown pulldown_51 (.out(CT_RF__PCSE));
  PullDown pulldown_52 (.out(CT_RF__PCJ));
  PullDown pulldown_53 (.out(CT_RF__PCR));
  PullDown #(.Bits(3)) pulldown_54 (.out(CT_RF__SCN));
  PullDown pulldown_55 (.out(CT_RF__SCD));
  PullDown pulldown_56 (.out(CT_RF__SCSRE));
  PullDown pulldown_57 (.out(CT_RF__FLS));
  PullDown #(.Bits(4)) pulldown_58 (.out(4'b0001));
  PullDown #(.Bits(9)) pulldown_59 (.out(CT_ALU__CT));
  PullDown pulldown_60 (.out(CT_ALU__M));
  PullDown pulldown_61 (.out(CT_ALU__M2));
  PullDown pulldown_62 (.out(CT_BUS__IAR));
  PullDown pulldown_63 (.out(CT_BUS__IAG));
  PullDown pulldown_64 (.out(CT_BUS__IDR));
  PullDown pulldown_65 (.out(CT_BUS__IDM));
  PullDown pulldown_66 (.out(CT_BUS__DAR));
  PullDown pulldown_67 (.out(CT_BUS__DAM));
  PullDown pulldown_68 (.out(CT_BUS__DAG));
  PullDown pulldown_69 (.out(CT_BUS__DDR));
  PullDown pulldown_70 (.out(CT_BUS__DDG));
  PullDown pulldown_71 (.out(I_LD));
  PullDown pulldown_72 (.out(D_LD));
  PullDown pulldown_73 (.out(D_ST));
  PullDown #(.Bits(2)) pulldown_74 (.out(D_MD));
  PullDown pulldown_75 (.out(CT_MVR));
  not not_45 (JPU_free, and_171_out);
  and and_174 (and_174_out, inst_comp_13_a_old, clr);
  D_FF d_ff_24 (.D(and_172_out), .C(C_ct), .Q(d_ff_24_q));  // open: nQ
  and and_175 (and_175_out, inst_comp_14_a_old, clr);
  Comparator #(.Bits(32)) comparator_4 (.a(JPU_ADDR), .b(JPU_BTB__tar), .eq(comparator_4_eq));  // open: gt, lt
  and and_176 (and_176_out, ~and_174_out, d_ff_24_q);  // And
  PullDown pulldown_76 (.out(issue));
  PullDown pulldown_77 (.out(CT_ISS__URA));
  PullDown pulldown_78 (.out(CT_ISS__URB));
  PullDown #(.Bits(5)) pulldown_79 (.out(CT_ISS__RA));
  PullDown #(.Bits(5)) pulldown_80 (.out(CT_ISS__RB));
  PullDown pulldown_81 (.out(CT_ISS__USC));
  PullDown pulldown_82 (.out(CT_ISS__UFL));
  PullDown pulldown_83 (.out(CT_ISS__ORC));
  PullDown #(.Bits(5)) pulldown_84 (.out(CT_ISS__RC));
  PullDown pulldown_85 (.out(CT_ISS__OSC));
  PullDown pulldown_86 (.out(CT_ISS__OFL));
  PullDown pulldown_87 (.out(CT_ROB__EX__E));
  PullDown pulldown_88 (.out(CT_ROB__ST__E));
  PullDown #(.Bits(3)) pulldown_89 (.out(CT_SP__MOF));
  PullDown pulldown_90 (.out(CT_BUS__DDM));
  PullDown pulldown_91 (.out(CT_RF__PCH));
  PullDown pulldown_92 (.out(hlt));
  D_FF #(.Bits(8)) d_ff_25 (
    .D({JPU_free, and_173_out[6], 2'b00, MB_free, DIR_free, ALU_free, 1'b1}), .C(C_ct), .Q(FU_free));  // open: nQ
  nand nand_17 (nand_17_out, JPU_BTB__V, comparator_4_eq);
  and and_177 (and_177_out, JPU_MISS, JPU_BTB__V, comparator_4_eq);
  and and_178 (Fl_JPU, or_69_out, JPU_BTB__ST);
  PullDown pulldown_93 (.out(ex_nop));
  assign CT_JPU__LD = and_176_out ? 1'b1 : 1'bz;  // Driver driver_154
  assign JPU_RET = and_176_out ? 1'b1 : 1'bz;  // Driver driver_155
  and and_179 (BTB_override, JPU_JP, nand_17_out);
  and and_180 (and_180_out, nand_17_out, JPU_BTB__J);
  or or_69 (or_69_out, and_177_out, and_180_out, BTB_override);
  assign CT_RF__PCSE = Fl_JPU ? 1'b1 : 1'bz;  // Driver driver_156
  assign CT_RF__PCJ = Fl_JPU ? 1'b1 : 1'bz;  // Driver driver_157
  PullDown pulldown_94 (.out(CT_JPU__JP));
  PullDown pulldown_95 (.out(JPU_A__ST));
  PullDown pulldown_96 (.out(CT_MB__OFFM));
  PullDown pulldown_97 (.out(JPU_BTB__ST));
  PullDown pulldown_98 (.out(CT_JPU__LD));
  PullDown pulldown_99 (.out(CT_FU__MF));
  PullDown pulldown_100 (.out(CT_CALL__LD));
  PullDown pulldown_101 (.out(CT_RET__LD));
  PullDown pulldown_102 (.out(JPU_RET));
  PullDown pulldown_103 (.out(JPU_free));
  PullDown pulldown_104 (.out(JPU_CALL));
  PullDown pulldown_105 (.out(CT_CALLM));

  assign CLK_str = 1'b0;
  assign CSH_mode = 2'b00;
  assign CSH_run = 1'b0;
  assign DMA_sel = 3'b000;
  assign DMA_str = 1'b0;
  assign INT_out = 1'b0;
  assign INT_str = 1'b0;
  assign MMU_sel = 2'b00;
  assign MMU_str = 1'b0;

  // Other names for the same wires on the sheet: disp_32[31:0] = {byte_D0, byte_D1, byte_D2, byte_D3};
  //   imm16_2[15:0] = {byte_D2, byte_D3}; FU_CLR[2:0] = {DIR_CLR, ALU_B_CLR, ALU_A_CLR}; ALU_A_WR[2:0] = ALU_A_RM;
  //   ALU_B_WR[2:0] = ALU_B_RM; BTB_packet[2] = BTB_JP; BTB_pred[1:0] = BTB_packet[4:3];
  //   BTB_tar[31:0] = BTB_packet[36:5]; BTB_V = BTB_packet[1]; C_dt = C; C_i = C; CT_RF__SCAS = CT_RF__SCAE;
  //   D_recieved = D_valid; int_proc = FL[14]; trap = FL[15]; FU_D__V[2:0] = {DIR_V, ALU_B_VD, ALU_A_VD};
  //   LDB_B__V = FU_D__V[3]; FU_F__V[1:0] = {ALU_B_VF, ALU_A_VF};
  //   issue_32[31:0] = {byte_I0, byte_I1, byte_I2, byte_I3};
  //   JPU_BTBPK[36:1] = {JPU_BTB__tar, JPU_BTB__pred, JPU_BTB__J, JPU_BTB__V}; JPU_EN = JPU_BTB__ST;
  //   JPU_ST = JPU_BTB__ST

  // Notes on the sheet:
  //   bus_e: default 1
  //   D_MD: 0:32
  //   1:16
  //   2:8
  //   3:u.u
  //   I_valid: default 1
  //   D_valid: default 1
  //   C: Hz: 64
  //   IO pins
  //   primeary signals
  //   pipeline controller
  //   inst id manager
  //   kernal mode system
  //   interrupt system
  //   decode circuit
  //   ALU
  //   register
  //   stack
  //   RAM
  //   register system
  //   ROB
  //   program counter controller
  //   bus system
  //   data bus ctrl
  //   jump
  //   call
  //   return
  //   halt
  //   block
  //   stack circuit
  //   ALU system
  //   dir circuit
  //   load/store circuit
  //   issue circuit
  //   flag circuit
  //   FU aribiter
  //   jmp circuit
  //   return unit
  //   control bus
endmodule
