// Digital circuit cpu-test.dig as structural Verilog
module cpu_test (
  input  E,
  input  run,
  input  C,
  input  boot,
  input  [31:0] reset_vec,
  input  [31:0] I_D__bus,
  input  [31:0] D_D__bus,
  input  [31:0] I_A__bus,
  input  [31:0] D_A__bus,
  input  I_responce,
  input  D_recieved,
  input  INT_in,
  input  [3:0] INT_lev,
  input  [31:0] INT_vec,
  input  INT_rqac,
  input  [31:0] MMU_abs,
  input  [5:0] INT_id__bus,
  input  [31:0] INT_d__bus,
  input  INT_ker,
  input  [31:0] MMU_phys,
  input  MMU_acp,
  input  [5:0] MMU_amid,
  input  [5:0] D_AMID,
  input  D_responce,
  input  B_used,
  output MMU_dis,
  output MMU_en,
  output [31:0] MMU_base,
  output [31:0] MMU_limit,
  output MMU_req,
  output I_LD,
  output D_LD,
  output D_ST,
  output [1:0] D_MD,
  output INT_acp,
  output INT_req,
  output INT_pstr,
  output INT_vstr,
  output INT_ret,
  output [31:0] MMU_src,
  output [31:0] MMU_virt,
  output [1:0] MMU_md,
  output [5:0] MMU_mid,
  output [1:0] CSH_mode,
  output CSH_run,
  output [5:0] D_MID,
  output D_MMU,
  output D_listen
);

  wire alu_32_1_p6, alu_32_1_p9, ALU_A_CLR, ALU_A_CMP, ALU_A_DRD, ALU_A_DRE, ALU_A_FRD, ALU_A_FRE, ALU_A_LD,
       ALU_A_LRD, ALU_A_STD, ALU_A_STF, ALU_A_UUD, ALU_A_UUF, ALU_A_V, ALU_A_VD, ALU_A_VF, ALU_B_CLR,
       ALU_B_CMP, ALU_B_DRD, ALU_B_DRE, ALU_B_FRD, ALU_B_FRE, ALU_B_LD, ALU_B_LRD, ALU_B_STD, ALU_B_STF,
       ALU_B_UUD, ALU_B_UUF, ALU_B_V, ALU_B_VD, ALU_B_VF, ALU_busy, ALU_free, and_1_out, and_2_out,
       and_3_out, and_4_out, and_5_out, and_6_out, and_7_out, and_8_out, and_9_out, and_10_out, and_11_out,
       and_12_out, and_13_out, and_14_out, and_15_out, and_17_out, and_18_out, and_19_out, and_21_out,
       and_23_out, and_24_out, and_25_out, and_27_out, and_29_out, and_33_out, and_34_out, and_35_out,
       and_37_out, and_39_out, and_40_out, and_41_out, and_42_out, and_43_out, and_45_out, and_46_out,
       and_47_out, and_48_out, and_49_out, and_50_out, and_51_out, and_52_out, and_53_out, and_54_out,
       and_55_out, and_56_out, and_57_out, and_58_out, and_59_out, and_61_out, and_62_out, and_64_out,
       and_65_out, and_66_out, and_67_out, and_68_out, and_69_out, and_70_out, and_71_out, and_72_out,
       and_73_out, and_75_out, and_76_out, and_77_out, and_81_out, and_82_out, and_85_out, and_86_out,
       and_87_out, and_88_out, and_89_out, and_90_out, and_91_out, and_92_out, and_93_out, and_94_out,
       and_95_out, and_96_out, and_98_out, and_99_out, and_101_out, and_102_out, and_106_out, and_112_out,
       and_113_out, and_114_out, and_115_out, and_116_out, and_117_out, and_118_out, and_119_out,
       and_120_out, and_121_out, and_122_out, and_123_out, and_124_out, and_125_out, and_128_out,
       and_130_out, and_131_out, and_136_out, and_137_out, and_138_out, and_139_out, and_142_out,
       and_143_out, and_144_out, and_145_out, and_147_out, and_148_out, and_149_out, and_150_out,
       and_152_out, and_153_out, and_154_out, and_155_out, and_156_out, and_157_out, and_158_out,
       and_159_out, and_160_out, and_166_out, and_167_out, and_170_out, and_171_out, and_172_out,
       and_173_out, and_174_out, and_175_out, and_176_out, and_177_out, and_178_out, and_179_out,
       and_183_out, and_186_out, and_189_out, and_191_out, and_192_out, and_194_out, and_195_out,
       and_196_out, and_197_out, and_198_out, and_199_out, and_200_out, and_201_out, and_204_out,
       and_209_out, B, bitselector_1_out, boot_t, BTB_JP, BTB_override, BUS_INSTV, C_t, clr, clr_ep,
       clr_self, com1, com1_ep, com2, com2_ep, comparator_1_eq, comparator_2_eq, comparator_3_eq,
       comparator_4_eq, comparator_5_eq, comparator_6_eq, comparator_7_eq, comparator_8_eq, comparator_9_eq,
       comparator_10_eq, comparator_11_eq, comparator_12_eq, comparator_13_eq, comparator_14_gt,
       comparator_15_gt, comparator_16_eq, comparator_17_eq, comparator_18_eq, comparator_19_gt,
       comparator_19_lt, comparator_20_eq, comparator_21_eq, comparator_22_eq, comparator_23_eq, CT_ALU__LD,
       CT_ALU__M, CT_ALU__M2, CT_ALU__WD, CT_ALU__WF, CT_BLOCK, CT_BUS__DAG, CT_BUS__DAM, CT_BUS__DAR,
       CT_BUS__DDG, CT_BUS__DDM, CT_BUS__DDR, CT_BUS__IAG, CT_BUS__IAR, CT_BUS__IDM, CT_BUS__IDR,
       CT_CALL__LD, CT_CALLM, CT_DIR__EXM, CT_DIR__LD, CT_DIR__M, CT_DIR__MS, CT_DISP, CT_FL__W1, CT_FL__W2,
       CT_FU__EPOCH, CT_FU__EX, CT_FU__MF, CT_ILVE, CT_ILVSM, CT_INT, CT_INT__W, CT_INTM, CT_ISCE, CT_ISCM,
       CT_ISCS, CT_ISS__HALT, CT_ISS__OFL, CT_ISS__OLDB, CT_ISS__ORC, CT_ISS__OSC, CT_ISS__OSTB, CT_ISS__UFL,
       CT_ISS__UMM, CT_ISS__URA, CT_ISS__URB, CT_JMP, CT_JPU__JP, CT_JPU__LD, CT_KILL, CT_LDB__LD, CT_MB__LD,
       CT_MB__OFFM, CT_MB__ST, CT_MVR, CT_PVECE, CT_RET__LD, CT_RF__DM, CT_RF__E, CT_RF__EX1, CT_RF__EX2,
       CT_RF__FLS, CT_RF__PCAE, CT_RF__PCH, CT_RF__PCJ, CT_RF__PCR, CT_RF__PCSE, CT_RF__SCAE, CT_RF__SCD,
       CT_RF__SCSE, CT_RF__SCSRE, CT_RF__SCSS, CT_RF__W1, CT_RF__W2, CT_ROB__EX__E, CT_ROB__FL__STA,
       CT_ROB__FL__STB, CT_ROB__GEN__STA, CT_ROB__GEN__STB, CT_ROB__INT__STA, CT_ROB__INT__STB,
       CT_ROB__ST__E, CT_SC__W1, CT_SC__W2, CT_STB__LD, CT_TRAP__LD, CT_UBTB, CT_USCB, d_ff_1_q, d_ff_5_q,
       d_ff_6_q, d_ff_7_nq, d_ff_9_q, d_ff_10_q, d_ff_15_nq, d_ff_18_q, D_recieved_t, dc_e, DC_q,
       dipswitch_1_out, dipswitch_2_out, dipswitch_3_out, dipswitch_4_out, dipswitch_5_out, dipswitch_6_out,
       dipswitch_7_out, dipswitch_8_out, dipswitch_9_out, DIR_busy, DIR_CLR, DIR_EX, DIR_free, DIR_LD,
       DIR_RD, DIR_ST, DIR_V, E_t, epoch_DP, epoch_IS, ex_nop, ext_en, Fl_ECLR, Fl_INT, Fl_JPU, Fl_JPU__EP,
       Fl_MEM, FL_MEM__EP, Fl_MFM__SF, flush_mux_1_e_acp, ft_e, FT_q, halt_frontend, halted, hlt,
       I_responce_t, id_full, id_manager_debug_1_eclr_ep, id_manager_debug_1_v, inst_sfcomp_1_a_new,
       inst_sfcomp_2_a_new, inst_sfcomp_3_a_new, inst_sfcomp_4_a_new, inst_sfcomp_5_a_new,
       inst_sfcomp_7_a_new, inst_sfcomp_9_a_new, inst_sfcomp_10_a_new, inst_sfcomp_11_a_new,
       inst_sfcomp_12_a_new, int_accept, int_epoch, INT_HALT, ISS_kernel, ISS_q, issue, issue_e, JPU_A__ST,
       JPU_BTB__J, JPU_BTB__ST, JPU_BTB__V, JPU_CALL, JPU_free, JPU_INT, JPU_JP, JPU_LD, JPU_MF, JPU_MISS,
       JPU_RET, kernel_inst, keyboard_1_av, LDB_B__MF, LDB_B__RD, LDB_B__ST, LDB_busy, LDB_D__MMU,
       LDB_forward, LDB_ldV, LDB_M__EP, LDB_M__V, load_buffer_debug_1_v, MB_any__e, MB_busy, MB_ep, MB_free,
       MB_ld__e, MB_LDB__LD, MB_MF, MB_st__e, MB_STB__LD, MB_type__st, MEM_EP, MEM_LD, MEM_LD__EP,
       MEM_LD__RD, MEM_LD__REC, MEM_RD, MEM_TYPE__ST, MMU_acp_t, MMU_CLR, MMU_LD, MMU_MB__MF, MMU_store,
       mode, multiplexer_8_out, multiplexer_10_out, multiplexer_17_out, multiplexer_19_out,
       multiplexer_23_out, multiplexer_24_out, multiplexer_26_out, multiplexer_27_out, multiplexer_28_out,
       multiplexer_34_out, multiplexer_40_out, multiplexer_41_out, multiplexer_42_out, multiplexer_50_out,
       multiplexer_53_out, multiplexer_55_out, multiplexer_56_out, multiplexer_57_out, multiplexer_58_out,
       multiplexer_61_out, multiplexer_64_out, multiplexer_65_out, multiplexer_66_out, multiplexer_70_out,
       multiplexer_73_out, multiplexer_79_out, multiplexer_80_out, multiplexer_81_out, multiplexer_82_out,
       multiplexer_84_out, multiplexer_85_out, multiplexer_86_out, multiplexer_88_out, multiplexer_92_out,
       multiplexer_93_out, nand_11_out, nand_18_out, nand_19_out, nor_1_out, nor_2_out, nor_3_out, nor_4_out,
       nor_7_out, nor_8_out, nor_10_out, nor_11_out, not_1_out, not_5_out, not_6_out, not_7_out, not_10_out,
       not_13_out, not_14_out, not_16_out, not_17_out, not_18_out, not_21_out, not_23_out, not_27_out,
       not_28_out, not_30_out, not_31_out, not_33_out, or_2_out, or_3_out, or_4_out, or_6_out, or_7_out,
       or_8_out, or_9_out, or_11_out, or_12_out, or_13_out, or_14_out, or_23_out, or_24_out, or_26_out,
       or_27_out, or_28_out, or_30_out, or_32_out, or_33_out, or_34_out, or_35_out, or_36_out, or_39_out,
       or_40_out, or_41_out, or_44_out, or_45_out, or_46_out, or_47_out, or_48_out, or_50_out, or_51_out,
       or_52_out, or_53_out, or_54_out, or_55_out, or_56_out, or_57_out, or_58_out, or_59_out, or_61_out,
       or_63_out, or_64_out, or_65_out, or_67_out, or_68_out, or_71_out, or_72_out, or_74_out, or_76_out,
       or_80_out, priorityencoder_3_any, register_17_q, register_24_q, register_28_q, register_29_q,
       register_30_q, register_37_q, register_38_q, register_39_q, register_46_q, register_49_q,
       register_64_q, register_71_q, register_74_q, register_77_q, register_82_q, register_93_q,
       register_97_q, register_98_q, register_110_q, register_114_q, register_115_q, register_119_q,
       RET_EPOCH, ROB_GEN_DA, ROB_GEN_DB, ROB_GEN_EX1, ROB_GEN_EX2, rs_ff_1_nq, rs_ff_2_nq, rs_ff_4_q,
       rs_ff_6_nq, rs_ff_6_q, rs_ff_8_q, rs_ff_9_nq, rs_ff_10_nq, rs_ff_11_nq, rs_ff_12_nq, rs_ff_13_nq,
       rs_ff_18_q, rs_ff_19_q, rs_ff_20_q, rs_ff_21_q, rs_ff_24_nq, rs_ff_25_nq, rs_ff_as_1_q, RS_full,
       run_t, RX_ILVE, RX_ILVM, RX_ISCE, RX_ISCM, RX_PGBSE, RX_PGLME, RX_PGLMM, RX_PVECE, RX_PVECM, STB_busy,
       STB_M__EP, STB_M__V, TRAP_busy, TRAP_EP, TRAP_free, TRAP_IRD, TRAP_RD, TRAP_ST, V_q, \wait , waiting,
       xor_1_out;
  wire [0:0] and_97_out, JPU_BTBPK, rs_ff_1_q;
  wire [1:0] and_108_out, and_110_out, and_126_out, and_127_out, bitextender_6_out, bitextender_7_out,
       d_ff_11_q, d_ff_12_q, d_ff_13_q, d_ff_14_q, JPU_BTB__pred, JPU_pred, LDB_M__MD, MB_MD,
       multiplexer_12_out, multiplexer_77_out, multiplexer_90_out, or_73_out, priorityencoder_1_num,
       priorityencoder_2_num, register_22_q, register_95_q, register_112_q, STB_M__MD,
       store_controller_half_1_d1_sel, store_controller_half_1_d2_sel, store_controller_half_2_d1_sel,
       store_controller_half_2_d2_sel;
  wire [1:1] or_25_out, register_50_q, register_75_q;
  wire [2:0] ALU_A_RM, ALU_B_RM, and_100_out, and_103_out, and_187_out, CT_ISS__UFU, CT_RF__MA, CT_RF__MB,
       CT_RF__SCN, CT_RF__WM, CT_SP__MOF, multiplexer_16_out, multiplexer_20_out, multiplexer_48_out,
       multiplexer_75_out, nand_1_out, nand_2_out, nand_4_out, nand_8_out, nand_12_out, nand_13_out,
       not_12_out, not_15_out, not_24_out, register_26_q, register_51_q, store_controller_1_d1_sel,
       store_controller_1_d2_sel;
  wire [2:1] nor_5_out, register_99_q;
  wire [3:0] ALU_A_INST, ALU_B_INST, clr_id, clr_sel, com1_inst, com2_inst, CT_FU__INST, d_ff_2_q, DIR_INST,
       Fl_JPU__INST, FL_MEM__ID, FU_I__V, id_manager_debug_1_eclr_id, inst_DP, inst_IS, int_inst_t, LD_id,
       LDB_B__INST, LDB_M__ID, MB_INST, MMU_INST, multiplexer_25_out, multiplexer_39_out, multiplexer_49_out,
       multiplexer_60_out, multiplexer_72_out, multiplexer_83_out, multiplexer_87_out, priorityencoder_3_num,
       register_27_q, register_36_q, register_45_q, register_70_q, register_92_q, register_109_q, RET_INST,
       ROB_FL_INSTA, ROB_FL_INSTB, ROB_GEN_INSTA, ROB_GEN_INSTB, ROB_INT_INSTA, ROB_INT_INSTB, STB_M__ID,
       TRAP_INST;
  wire [3:2] FU_F__V;
  wire [4:0] CT_ISS__RA, CT_ISS__RB, CT_ISS__RC, CT_RF__RA, CT_RF__RB, CT_RF__WS, ILV, ILV_i,
       multiplexer_3_out;
  wire [4:4] FU_CLR;
  wire [5:0] CT_INT__D, INT_rid__bus, LDB_MID, MB_mid, MEM_LD__AMID, MMU_amid_t, multiplexer_78_out,
       multiplexer_91_out, register_20_q, register_96_q, register_113_q, ROB_INT_A, ROB_INT_B, TRAP_INT;
  wire [6:6] and_202_out;
  wire [7:0] ALU_A_F, ALU_A_FI, ALU_A_T__F, ALU_B_F, ALU_B_FI, ALU_B_T__F, bitextender_3_out, byte_D0,
       byte_D0_iv, byte_D1, byte_D2, byte_D3, byte_I0, byte_I0_iv, byte_I1, byte_I2, byte_I3, CT_DIR__EXID,
       CT_FL__D1, CT_FL__D2, CT_FU__WR, CT_INTID, CT_RF__R1, CT_RF__R2, demultiplexer_1_out_0,
       demultiplexer_2_out_0, DIR_WR, fl_i, FU_free, LDB_B__WR, MB_WR, multiplexer_31_out,
       multiplexer_33_out, multiplexer_45_out, multiplexer_47_out, multiplexer_52_out, multiplexer_63_out,
       or_5_out, register_33_q, register_35_q, register_42_q, register_44_q, register_48_q, register_73_q,
       ROB_FL_A, ROB_FL_B, ROB_GEN_WA, ROB_GEN_WB, xor_2_out;
  wire [7:3] ALU_A_WR, ALU_B_WR, FU_D__V;
  wire [7:6] register_10_q;
  wire [8:0] ALU_A_CT, ALU_B_CT, CT_ALU__CT, multiplexer_32_out, multiplexer_46_out, register_34_q,
       register_43_q;
  wire [9:0] and_44_out;
  wire [15:0] and_180_out, and_182_out, and_184_out, and_185_out, and_190_out, bitextender_4_out,
       bitextender_5_out, bitextender_8_out, bitextender_10_out, bitextender_11_out, clrs_16,
       demultiplexer_3_out_0, demultiplexer_4_out_0, icmks_16, id_manager_debug_1_c16, id_manager_debug_1_us,
       id_manager_debug_1_vv1, id_manager_debug_1_vv2, INT_inst, keyboard_1_d, multiplexer_38_out,
       multiplexer_95_out, not_25_out, not_26_out, or_66_out, or_69_out, or_70_out, register_2_q,
       register_58_q, register_104_q, register_116_q, register_117_q, V1_inst, V2_inst;
  wire [31:0] add_1_s, add_4c32_1_s, add_4c32_2_s, alu_32_1_p8, alu_32_1_p11, alu_32_1_p12, alu_32_1_p14,
       ALU_A_A, ALU_A_B, ALU_A_R, ALU_A_T__R, ALU_B_A, ALU_B_B, ALU_B_R, ALU_B_T__R, bitextender_1_out,
       bitextender_2_out, counter_1_out, counter_2_out, CT_RF__D1, CT_RF__D2, CT_RF__DR, CT_SC__D1,
       CT_SC__D2, CT_SC__FD, DIR, FL, HALT_PC, I_A__R_q, int_pc, int_vec_t, ISC, ISC_i, ISC_sc, JPU_ADDR,
       JPU_BTB__tar, JPU_PC, LD_addr, LDB_B__D, LDB_ldD, LDB_M__A, MB_addr, MB_data, MB_PC, MD_A__bus,
       MEM_FPC, MEM_LD__D, MMU_phys_t, multiplexer_2_out, multiplexer_4_out, multiplexer_9_out,
       multiplexer_11_out, multiplexer_13_out, multiplexer_18_out, multiplexer_21_out, multiplexer_22_out,
       multiplexer_29_out, multiplexer_30_out, multiplexer_35_out, multiplexer_36_out, multiplexer_37_out,
       multiplexer_43_out, multiplexer_44_out, multiplexer_51_out, multiplexer_54_out, multiplexer_59_out,
       multiplexer_62_out, multiplexer_67_out, multiplexer_69_out, multiplexer_71_out, multiplexer_74_out,
       multiplexer_76_out, multiplexer_89_out, multiplexer_94_out, mVec, pc_read, pc_ret, PCA, pca_i, PCS,
       PCS_DC, PCS_FT, pcs_i, PVEC, PVEC_i, R_A, R_B, register_1_q, register_21_q, register_23_q,
       register_31_q, register_32_q, register_40_q, register_41_q, register_47_q, register_57_q,
       register_72_q, register_94_q, register_103_q, register_111_q, RX_SEL, SCA, sca_i, SCS, STB_M__A,
       STB_M__D;
  wire [36:0] and_181_out, bitextender_9_out, BTB_DP, BTB_fetch, BTB_pack__iss, BTB_packet;

  PullDown #(.Bits(32)) pulldown_1 (.out(I_A__bus));
  PullUp pullup_1 (.out(I_responce_t));
  // Probe on CT_RF__WS
  // Probe on CT_RF__WM
  // Probe on CT_RF__RA
  // Probe on CT_RF__MA
  // Probe on CT_RF__RB
  // Probe on CT_RF__MB
  PullDown #(.Bits(32)) pulldown_2 (.out(D_A__bus));
  MMU_D mmu_d_1 (
    .addr_b(D_A__bus), .md_b(D_MD), .ld(D_LD), .st(D_ST), .base({32{1'b0}}), .limit({32{1'b0}}),
    .req_c(MMU_req), .mid_c(MMU_mid), .virt_c(MMU_virt), .md_c(MMU_md), .addr_o(MD_A__bus),
    .phys_c(MMU_phys_t), .acp(MMU_acp_t), .mid_o(MMU_amid_t));  // open: err_o, err_c
  or or_1 (D_recieved_t, D_LD, D_ST);
  PullDown #(.Bits(32)) pulldown_3 (.out(MD_A__bus));
  // Probe inst on {byte_I0, byte_I1, byte_I2, byte_I3}
  // Probe R_A on R_A
  // Probe R_B on R_B
  // Probe PC on PCS
  // Probe SCS on SCS
  // Probe SCA on SCA
  // Probe FL on FL
  // Probe CT_BUS-_IDM on CT_BUS__IDM
  // Probe C_i on C_t
  Comparator #(.Bits(22)) comparator_1 (.a(I_A__bus[31:10]), .b({22{1'b1}}), .eq(comparator_1_eq));  // open: gt, lt
  Comparator #(.Bits(10)) comparator_2 (.a(MD_A__bus[31:22]), .b(10'h3f0), .eq(comparator_2_eq));  // open: gt, lt
  Comparator #(.Bits(10)) comparator_3 (.a(I_A__bus[31:22]), .b(10'h3f0), .eq(comparator_3_eq));  // open: gt, lt
  Comparator #(.Bits(6)) comparator_4 (.a(MD_A__bus[31:26]), .b({6{1'b0}}), .eq(comparator_4_eq));  // open: gt, lt
  Comparator #(.Bits(6)) comparator_5 (.a(I_A__bus[31:26]), .b({6{1'b0}}), .eq(comparator_5_eq));  // open: gt, lt
  Comparator #(.Bits(6)) comparator_6 (.a(MD_A__bus[31:26]), .b(6'b000010), .eq(comparator_6_eq));  // open: gt, lt
  and and_1 (and_1_out, comparator_1_eq, I_LD);
  and and_2 (and_2_out, D_LD, comparator_2_eq);
  and and_3 (and_3_out, I_LD, comparator_3_eq);
  and and_4 (and_4_out, D_ST, comparator_4_eq);
  and and_5 (and_5_out, comparator_4_eq, D_LD);
  and and_6 (and_6_out, I_LD, comparator_5_eq);
  and and_7 (and_7_out, comparator_6_eq, D_LD);
  and and_8 (and_8_out, D_ST, comparator_6_eq);
  Comparator #(.Bits(30)) comparator_7 (.a(MD_A__bus[31:2]), .b(30'h1000000), .eq(comparator_7_eq));  // open: gt, lt
  Comparator #(.Bits(30)) comparator_8 (.a(MD_A__bus[31:2]), .b(30'h1000001), .eq(comparator_8_eq));  // open: gt, lt
  Comparator #(.Bits(30)) comparator_9 (.a(MD_A__bus[31:2]), .b(30'h1000002), .eq(comparator_9_eq));  // open: gt, lt
  Comparator #(.Bits(30)) comparator_10 (.a(MD_A__bus[31:2]), .b(30'h1000003), .eq(comparator_10_eq));  // open: gt, lt
  ROM #(.AddrBits(6), .Bits(32)) rom_1 (.A(I_A__bus[7:2]), .sel(and_1_out), .D(I_D__bus));
  and and_9 (and_9_out, D_LD, comparator_7_eq);
  and and_10 (and_10_out, D_LD, comparator_8_eq);
  and and_11 (and_11_out, D_ST, comparator_9_eq);
  and and_12 (and_12_out, D_ST, comparator_10_eq);
  // Probe com1 on com1
  // Probe com2 on com2
  // Probe com1_inst on com1_inst
  // Probe com2_inst on com2_inst
  // Probe PC_inst on inst_IS
  rom_test rom_test_1 (
    .D1(D_D__bus), .D2(I_D__bus), .C(C_t), .mode(D_MD), .ld1(and_2_out), .ld2(and_3_out), ._1A(MD_A__bus),
    ._2A(I_A__bus));
  ram_test ram_test_1 (
    .D1(D_D__bus), .D2(I_D__bus), .D2_V(I_responce_t), .str(and_4_out), .C(C_t), .mode(D_MD),
    .ld1(and_5_out), .ld2(and_6_out), .D_in(D_D__bus), ._1A(MD_A__bus), ._2A(I_A__bus));
  GraphicCard #(.graphicHeight(90), .Bits(32)) graphiccard_1 (
    .A(MD_A__bus[16:2]), .str(and_8_out), .C(C_t), .ld(and_7_out), .B(dipswitch_1_out), .D(D_D__bus));
  DipSwitch dipswitch_1 (.out(dipswitch_1_out));
  Register #(.Bits(32)) register_1 (.D(D_D__bus), .C(C_t), .en(and_8_out), .Q(register_1_q));
  or or_2 (or_2_out, and_11_out, and_13_out);
  and and_13 (and_13_out, rs_ff_1_nq, keyboard_1_av);
  Terminal #(.termWidth(100), .termHeight(50)) terminal_1 (.D(D_D__bus), .C(C_t), .en(and_12_out));
  // Probe on register_1_q
  Keyboard keyboard_1 (.C(C_t), .en(or_2_out), .D(keyboard_1_d), .av(keyboard_1_av));
  and and_14 (and_14_out, and_11_out, ~keyboard_1_av);  // And
  Register #(.Bits(16)) register_2 (.D(keyboard_1_d), .C(C_t), .en(or_2_out), .Q(register_2_q));
  RS_FF rs_ff_1 (.S(keyboard_1_av), .C(C_t), .R(and_14_out), .Q(rs_ff_1_q[0]), .nQ(rs_ff_1_nq));
  RS_FF_AS rs_ff_as_1 (.S(run_t), .R(dipswitch_2_out), .Q(rs_ff_as_1_q));  // open: nQ
  DipSwitch dipswitch_2 (.out(dipswitch_2_out));
  assign D_D__bus = and_9_out ? {{16{1'b0}}, register_2_q} : 32'bz;  // Driver driver_1
  assign D_D__bus = and_10_out ? {{31{1'b0}}, rs_ff_1_q[0]} : 32'bz;  // Driver driver_2
  DipSwitch #(.dipDefault("true")) dipswitch_3 (.out(dipswitch_3_out));
  DipSwitch dipswitch_4 (.out(dipswitch_4_out));
  // Probe E on E_t
  // Probe R on run_t
  // Probe issue_e on issue_e
  // Probe CT_ISS-_OLDB on CT_ISS__OLDB
  // Probe clr on clr
  // Probe halt-FT-DC-ISS on halt_frontend
  // Probe issue_32 on {byte_I0, byte_I1, byte_I2, byte_I3}
  // Probe disp_32 on {byte_D0, byte_D1, byte_D2, byte_D3}
  // Probe FL_MEM on Fl_MEM
  // Probe FL_JPU on Fl_JPU
  // Probe FL_ECLR on Fl_ECLR
  // Probe FL_INT on Fl_INT
  // Probe on com1
  // Probe on com2
  // Probe on com1_inst
  // Probe on com2_inst
  // Probe on epoch_IS
  // Probe on inst_IS
  Comparator #(.Bits(32)) comparator_11 (.a(counter_1_out), .b(32'h4), .eq(comparator_11_eq));  // open: gt, lt
  Comparator #(.Bits(32)) comparator_12 (.a(counter_1_out), .b(32'h8), .eq(comparator_12_eq));  // open: gt, lt
  Comparator #(.Bits(32)) comparator_13 (.a(counter_1_out), .b(32'ha), .eq(comparator_13_eq));  // open: gt, lt
  Counter #(.Bits(32)) counter_1 (
    .en(dipswitch_3_out), .C(C_t), .clr(dipswitch_4_out), .out(counter_1_out));  // open: ovf
  Counter #(.Bits(32)) counter_2 (.en(rs_ff_as_1_q), .C(C_t), .clr(dipswitch_2_out), .out(counter_2_out));  // open: ovf
  // Probe cycle on counter_1_out
  // Probe hc on C_t
  // Probe Ecycle on counter_2_out
  RS_FF_AS rs_ff_as_2 (.S(comparator_11_eq), .R(dipswitch_5_out), .Q(E_t), .nQ(B));
  DipSwitch dipswitch_5 (.out(dipswitch_5_out));
  RS_FF_AS rs_ff_as_3 (.S(comparator_12_eq), .R(comparator_13_eq), .Q(run_t));  // open: nQ
  DipSwitch dipswitch_6 (.out(dipswitch_6_out));
  Multiplexer multiplexer_1 (.sel(dipswitch_7_out), .in_0(dipswitch_6_out), .in_1(C), .out(C_t));
  DipSwitch dipswitch_7 (.out(dipswitch_7_out));
  not not_1 (not_1_out, I_responce_t);
  assign CT_BUS__IDM = not_1_out ? 1'b1 : 1'bz;  // Driver driver_3
  and and_15 (and_15_out, I_responce_t, ft_e);
  assign CT_RF__PCSE = and_15_out ? 1'b1 : 1'bz;  // Driver driver_4
  assign CT_BUS__IAR = and_15_out ? 1'b1 : 1'bz;  // Driver driver_5
  assign CT_BUS__IAG = ft_e ? 1'b1 : 1'bz;  // Driver driver_6
  assign I_LD = ft_e ? 1'b1 : 1'bz;  // Driver driver_7
  or or_3 (or_3_out, issue, INT_acp);
  Comparator #(.Bits(32)) comparator_14 (.a(PCS), .b(mVec), .gt(comparator_14_gt));  // open: eq, lt
  BitExtender #(.inputBits(16), .outputBits(32)) bitextender_1 (.in({byte_D2, byte_D3}), .out(bitextender_1_out));
  RS_FF rs_ff_2 (.S(Fl_INT), .C(C_t), .R(CT_INTM), .nQ(rs_ff_2_nq));  // open: Q
  and and_16 (Fl_INT, rs_ff_2_nq, int_accept);
  PullDown pulldown_4 (.out(CT_ISCS));
  PullDown pulldown_5 (.out(CT_ISCM));
  PullDown pulldown_6 (.out(CT_ISCE));
  PullDown pulldown_7 (.out(CT_ILVE));
  or or_4 (or_4_out, halted, waiting);
  D_FF d_ff_1 (.D(INT_in), .C(C_t), .Q(d_ff_1_q));  // open: nQ
  D_FF #(.Bits(4)) d_ff_2 (.D(INT_lev), .C(C_t), .Q(d_ff_2_q));  // open: nQ
  Register #(.Bits(5)) level (.D(ILV_i), .C(C_t), .en(CT_ILVE), .Q(ILV));
  Register #(.Bits(32)) register_3 (.D(ISC_i), .C(C_t), .en(CT_ISCE), .Q(ISC));
  Register #(.Bits(32)) register_4 (.D(INT_vec), .C(C_t), .en(int_accept), .Q(int_vec_t));
  and and_17 (and_17_out, nor_1_out, CT_RF__W1, CT_RF__EX1);
  LED led_1 (.in(Fl_MEM));
  LED led_2 (.in(epoch_IS));
  // Probe ID on inst_DP
  id_manager_debug id_manager_debug_1 (
    .C(C_t), .\use (or_3_out), .S1_inst(V1_inst), .S2_inst(V2_inst), .E_inst(INT_inst), .clr(clr),
    .clr_self(clr_self), .clr_ep(clr_ep), .clr_id(clr_id), .epoch(epoch_IS), .id(inst_IS),
    .V(id_manager_debug_1_v), .com1(com1), .com1_id(com1_inst), .com1_ep(com1_ep), .com2(com2),
    .com2_id(com2_inst), .com2_ep(com2_ep), .ext_en(ext_en), .cmks_16(icmks_16), .clrs_16(clrs_16),
    .VV1(id_manager_debug_1_vv1), .VV2(id_manager_debug_1_vv2), .US(id_manager_debug_1_us),
    .C16(id_manager_debug_1_c16), .eclr_v(Fl_ECLR), .eclr_id(id_manager_debug_1_eclr_id),
    .eclr_ep(id_manager_debug_1_eclr_ep), .eclr(flush_mux_1_e_acp));
  flush_mux flush_mux_1 (
    .M_self(Fl_MFM__SF), .M_v(Fl_MEM), .M_id(FL_MEM__ID), .M_ep(FL_MEM__EP), .J_v(Fl_JPU),
    .J_id(Fl_JPU__INST), .J_ep(Fl_JPU__EP), .I_v(Fl_INT), .I_id(com2_inst), .I_ep(com2_ep), .sel(clr_sel),
    .self(clr_self), .m_v_2(clr), .m_id_2(clr_id), .m_ep_2(clr_ep), .E_v(Fl_ECLR),
    .E_id(id_manager_debug_1_eclr_id), .E_ep(id_manager_debug_1_eclr_ep), .E_acp(flush_mux_1_e_acp));
  Add #(.Bits(32)) add_1 (.a(R_A), .b(bitextender_1_out), .c_i(1'b0), .s(add_1_s));  // open: c_o
  and and_18 (and_18_out, or_4_out, INT_in);
  D_FF d_ff_3 (.D(CT_INT__W), .C(C_t), .Q(INT_req));  // open: nQ
  D_FF #(.Bits(6)) d_ff_4 (.D(CT_INT__D), .C(C_t), .Q(INT_rid__bus));  // open: nQ
  Demultiplexer #(.Selector_Bits(3)) demultiplexer_1 (
    .sel(CT_RF__R1[2:0]), .in(and_17_out), .out_0(demultiplexer_1_out_0[0]),
    .out_1(demultiplexer_1_out_0[1]), .out_2(demultiplexer_1_out_0[2]), .out_3(demultiplexer_1_out_0[3]),
    .out_4(demultiplexer_1_out_0[4]), .out_5(demultiplexer_1_out_0[5]), .out_6(demultiplexer_1_out_0[6]),
    .out_7(demultiplexer_1_out_0[7]));
  and and_19 (and_19_out, 1'b0, ~comparator_14_gt);  // And
  Comparator #(.Bits(5)) comparator_15 (.a({1'b0, d_ff_2_q}), .b(ILV), .gt(comparator_15_gt));  // open: eq, lt
  nor nor_1 (nor_1_out, CT_RF__R1[7], CT_RF__R1[6], CT_RF__R1[5], CT_RF__R1[4], CT_RF__R1[3]);
  LED led_3 (.in(LDB_B__ST));
  LED led_4 (.in(JPU_CALL));
  LED led_5 (.in(CT_RET__LD));
  LED led_6 (.in(LDB_forward));
  LED led_7 (.in(halt_frontend));
  LED led_8 (.in(clr));
  LED led_9 (.in(LDB_B__RD));
  // Probe FU on FU_free
  // Probe INST on {byte_I0, byte_I1, byte_I2, byte_I3}
  // Probe INST on {byte_D0, byte_D1, byte_D2, byte_D3}
  not not_2 (id_full, id_manager_debug_1_v);
  RS_FF u_mode (.S(and_19_out), .C(C_t), .R(comparator_14_gt), .Q(mode));  // open: nQ
  Register #(.Bits(32)) MVR (.D(add_1_s), .C(C_t), .en(CT_MVR), .Q(mVec));
  RS_FF rs_ff_3 (.S(Fl_INT), .C(C_t), .R(INT_acp), .Q(INT_HALT));  // open: nQ
  RS_FF rs_ff_4 (.S(Fl_INT), .C(C_t), .R(INT_acp), .Q(rs_ff_4_q));  // open: nQ
  Comparator #(.Bits(4)) comparator_16 (.a(inst_IS), .b(com1_inst), .eq(comparator_16_eq));  // open: gt, lt
  assign CT_JPU__LD = INT_acp ? 1'b1 : 1'bz;  // Driver driver_8
  assign JPU_INT = INT_acp ? 1'b1 : 1'bz;  // Driver driver_9
  assign CT_ISS__OSTB = INT_acp ? 1'b1 : 1'bz;  // Driver driver_10
  and and_20 (int_accept, d_ff_1_q, comparator_15_gt);
  Register #(.Bits(32)) register_5 (.D(pca_i), .C(C_t), .en(INT_acp), .Q(int_pc));
  Register #(.Bits(4)) register_6 (.D(inst_IS), .C(C_t), .en(INT_acp), .Q(int_inst_t));
  Register register_7 (.D(epoch_IS), .C(C_t), .en(INT_acp), .Q(int_epoch));
  assign {or_5_out[7:6], RX_PGLME, RX_PGBSE, RX_ILVE, RX_ISCE, RX_PVECE, or_5_out[0]} = {demultiplexer_2_out_0[7:5], RX_PGLMM, RX_ILVM, RX_ISCM, RX_PVECM, demultiplexer_2_out_0[0]} | demultiplexer_1_out_0;  // Or or_5, 8 bits wide
  assign byte_I0_iv = ~byte_I0;  // Not not_3, 8 bits wide
  assign byte_D0_iv = ~byte_D0;  // Not not_4, 8 bits wide
  or or_6 (or_6_out, clr, \wait );
  or or_7 (or_7_out, run_t, Fl_INT);
  D_FF d_ff_5 (.D(clr), .C(C_t), .Q(d_ff_5_q));  // open: nQ
  D_FF d_ff_6 (.D(B), .C(C_t), .Q(d_ff_6_q));  // open: nQ
  PullDown pulldown_8 (.out(JPU_INT));
  PullDown pulldown_9 (.out(CT_ILVSM));
  and and_21 (and_21_out, nor_2_out, CT_RF__W2, CT_RF__EX2);
  LED led_10 (.in(MMU_LD));
  LED led_11 (.in(Fl_MFM__SF));
  not not_5 (not_5_out, or_6_out);
  RS_FF FT (.S(or_7_out), .C(C_t), .R(\wait ), .Q(FT_q), .nQ(waiting));
  not not_6 (not_6_out, halt_frontend);
  D_FF d_ff_7 (.D(d_ff_6_q), .C(C_t), .nQ(d_ff_7_nq));  // open: Q
  and and_22 (INT_acp, rs_ff_4_q, comparator_16_eq, ~STB_busy);  // And
  nor nor_2 (nor_2_out, CT_RF__R2[7], CT_RF__R2[6], CT_RF__R2[5], CT_RF__R2[4], CT_RF__R2[3]);
  Demultiplexer #(.Selector_Bits(3)) demultiplexer_2 (
    .sel(CT_RF__R2[2:0]), .in(and_21_out), .out_0(demultiplexer_2_out_0[0]), .out_1(RX_PVECM),
    .out_2(RX_ISCM), .out_3(RX_ILVM), .out_4(RX_PGLMM), .out_5(demultiplexer_2_out_0[5]),
    .out_6(demultiplexer_2_out_0[6]), .out_7(demultiplexer_2_out_0[7]));
  and and_23 (and_23_out, byte_D0_iv[0], byte_D0[1], byte_D0[2], byte_D0_iv[3], byte_D0[4], byte_D0[5], byte_D0[6], byte_D0_iv[7], CT_DISP);
  and and_24 (and_24_out, byte_D0[0], byte_D0[1], byte_D0[2], byte_D0_iv[3], byte_D0[4], byte_D0[5], byte_D0[6], byte_D0_iv[7], CT_DISP);
  and and_25 (and_25_out, byte_D0_iv[1], byte_D0_iv[2], byte_D0[3], byte_D0[4], byte_D0[5], byte_D0[6], byte_D0_iv[7], CT_DISP);
  assign CT_BUS__IAR = d_ff_5_q ? 1'b1 : 1'bz;  // Driver driver_11
  assign CT_RF__PCSE = d_ff_5_q ? 1'b1 : 1'bz;  // Driver driver_12
  and and_26 (boot_t, d_ff_6_q, d_ff_7_nq);
  // Probe V1_inst on V1_inst
  // Probe VG1_inst on id_manager_debug_1_vv1
  // Probe V2_inst on V2_inst
  // Probe VG2_inst on id_manager_debug_1_vv2
  // Probe U_inst on id_manager_debug_1_us
  // Probe CLR_inst on id_manager_debug_1_c16
  D_FF d_ff_8 (.D(INT_acp), .C(C_t), .Q(CT_INTM));  // open: nQ
  and and_27 (and_27_out, not_5_out, FT_q);
  Register DC (.D(and_27_out), .C(C_t), .en(or_8_out), .Q(DC_q));
  and and_28 (ft_e, FT_q, not_6_out);
  or or_8 (or_8_out, not_6_out, d_ff_5_q, or_6_out);
  assign CT_RF__PCSE = boot_t ? 1'b1 : 1'bz;  // Driver driver_13
  DipSwitch dipswitch_8 (.out(dipswitch_8_out));
  DipSwitch dipswitch_9 (.out(dipswitch_9_out));
  assign CT_MB__LD = CT_INTM ? 1'b1 : 1'bz;  // Driver driver_14
  assign CT_MB__OFFM = CT_INTM ? 1'b1 : 1'bz;  // Driver driver_15
  assign CT_MB__ST = CT_INTM ? 1'b1 : 1'bz;  // Driver driver_16
  assign CT_FU__INST = CT_INTM ? int_inst_t : 4'bz;  // Driver driver_17
  assign CT_FU__EPOCH = CT_INTM ? int_epoch : 1'bz;  // Driver driver_18
  Multiplexer #(.Bits(32)) multiplexer_2 (.sel(RX_ISCM), .in_0(CT_RF__D1), .in_1(CT_RF__D2), .out(multiplexer_2_out));
  Multiplexer #(.Bits(5)) multiplexer_3 (
    .sel(RX_ILVM), .in_0(CT_RF__D1[4:0]), .in_1(CT_RF__D2[4:0]), .out(multiplexer_3_out));
  PullDown pulldown_10 (.out(CT_PVECE));
  Register #(.Bits(32)) u_PVEC (.D(PVEC_i), .C(C_t), .en(CT_PVECE), .Q(PVEC));
  assign CT_FU__EPOCH = and_23_out ? epoch_DP : 1'bz;  // Driver driver_19
  assign CT_FU__INST = and_23_out ? inst_DP : 4'bz;  // Driver driver_20
  assign CT_TRAP__LD = and_23_out ? 1'b1 : 1'bz;  // Driver driver_21
  assign CT_INT = and_23_out ? 1'b1 : 1'bz;  // Driver driver_22
  assign CT_INTID = and_23_out ? byte_D3 : 8'bz;  // Driver driver_23
  assign CT_FU__EPOCH = and_24_out ? epoch_DP : 1'bz;  // Driver driver_24
  assign CT_FU__INST = and_24_out ? inst_DP : 4'bz;  // Driver driver_25
  assign CT_TRAP__LD = and_24_out ? 1'b1 : 1'bz;  // Driver driver_26
  assign CT_BLOCK = and_25_out ? 1'b1 : 1'bz;  // Driver driver_27
  assign issue = and_25_out ? 1'b1 : 1'bz;  // Driver driver_28
  assign CT_ISS__HALT = and_25_out ? 1'b1 : 1'bz;  // Driver driver_29
  assign CT_ISS__UMM = and_25_out ? 1'b1 : 1'bz;  // Driver driver_30
  assign CT_ISS__UFU = and_25_out ? 3'b100 : 3'bz;  // Driver driver_31
  and and_29 (and_29_out, not_5_out, DC_q);
  Register ISS (.D(and_29_out), .C(C_t), .en(or_9_out), .Q(ISS_q));
  and and_30 (dc_e, DC_q, not_6_out);
  or or_9 (or_9_out, not_6_out, or_6_out);
  or or_10 (halt_frontend, id_full, RS_full, INT_HALT, dipswitch_8_out, dipswitch_9_out, LDB_busy, STB_busy);
  assign \wait  = Fl_ECLR ? 1'b1 : 1'bz;  // Driver driver_32
  assign CT_RF__PCH = Fl_ECLR ? 1'b1 : 1'bz;  // Driver driver_33
  assign CT_RF__PCSE = Fl_ECLR ? 1'b1 : 1'bz;  // Driver driver_34
  assign CT_RF__PCJ = Fl_ECLR ? 1'b1 : 1'bz;  // Driver driver_35
  nor nor_3 (nor_3_out, CT_DIR__EXID[7], CT_DIR__EXID[6], CT_DIR__EXID[5], CT_DIR__EXID[4], CT_DIR__EXID[3]);
  Multiplexer #(.Selector_Bits(3), .Bits(32)) multiplexer_4 (
    .sel(CT_DIR__EXID[2:0]), .in_0(32'h1), .in_1(PVEC), .in_2(ISC), .in_3({{27{1'b0}}, ILV}),
    .in_4({32{1'b0}}), .in_5({32{1'b0}}), .in_6({32{1'b0}}), .in_7({32{1'b0}}), .out(multiplexer_4_out));
  and and_31 (issue_e, ISS_q, BUS_INSTV, not_6_out);
  PullDown pulldown_11 (.out(CT_DISP));
  Multiplexer #(.Bits(32)) multiplexer_5 (.sel(CT_ISCS), .in_0(multiplexer_2_out), .in_1(ISC_sc), .out(ISC_i));
  assign CT_ISCE = RX_ISCE ? 1'b1 : 1'bz;  // Driver driver_36
  Multiplexer #(.Bits(5)) multiplexer_6 (
    .sel(int_accept), .in_0(multiplexer_3_out), .in_1({1'b1, INT_lev}), .out(ILV_i));
  assign CT_ILVE = RX_ILVE ? 1'b1 : 1'bz;  // Driver driver_37
  assign CT_ILVE = int_accept ? 1'b1 : 1'bz;  // Driver driver_38
  assign RX_SEL = bitextender_2_out & multiplexer_4_out;  // And and_32, 32 bits wide
  assign CT_ISCM = CT_INTM ? 1'b1 : 1'bz;  // Driver driver_39
  assign CT_ISCE = CT_INTM ? 1'b1 : 1'bz;  // Driver driver_40
  assign CT_RF__SCD = CT_INTM ? 1'b1 : 1'bz;  // Driver driver_41
  assign CT_RF__SCN = CT_INTM ? 3'b100 : 3'bz;  // Driver driver_42
  assign CT_ISCS = CT_INTM ? 1'b1 : 1'bz;  // Driver driver_43
  Multiplexer #(.Bits(32)) multiplexer_7 (.sel(RX_PVECM), .in_0(CT_RF__D1), .in_1(CT_RF__D2), .out(PVEC_i));
  assign CT_PVECE = RX_PVECE ? 1'b1 : 1'bz;  // Driver driver_44
  BitExtender #(.inputBits(1), .outputBits(32)) bitextender_2 (.in(nor_3_out), .out(bitextender_2_out));
  DipSwitch dipswitch_10 (.out(BTB_packet[0]));
  BTB btb_1 (
    .C(C_t), .E(JPU_BTB__ST), .V_in(1'b1), .id(JPU_PC[5:2]), .tag(JPU_PC[17:6]), .pred(JPU_pred),
    .tar(JPU_ADDR), .R_id(PCS[5:2]), .R_tag(PCS[17:6]), .V(BTB_packet[1]), .J(BTB_JP),
    .pred_O(BTB_packet[4:3]), .tar_O(BTB_packet[36:5]));
  and and_33 (and_33_out, ~MEM_LD, D_recieved_t);  // And
  Comparator #(.Bits(4)) comparator_17 (.a(TRAP_INST), .b(com1_inst), .eq(comparator_17_eq));  // open: gt, lt
  Comparator #(.Bits(4)) comparator_18 (.a(TRAP_INST), .b(com2_inst), .eq(comparator_18_eq));  // open: gt, lt
  Register #(.Bits(4)) register_8 (.D(CT_FU__INST), .C(C_t), .en(CT_TRAP__LD), .Q(TRAP_INST));
  Register register_9 (.D(CT_FU__EPOCH), .C(C_t), .en(CT_TRAP__LD), .Q(TRAP_EP));
  D_FF d_ff_9 (.D(CT_INT), .C(C_t), .Q(d_ff_9_q));  // open: nQ
  D_FF d_ff_10 (.D(CT_TRAP__LD), .C(C_t), .Q(d_ff_10_q));  // open: nQ
  Register #(.Bits(8)) register_10 (.D(CT_INTID), .C(C_t), .en(CT_TRAP__LD), .Q({register_10_q, TRAP_INT}));
  RS_FF rs_ff_5 (.S(CT_TRAP__LD), .C(C_t), .R(FU_CLR[4]), .Q(TRAP_RD));  // open: nQ
  ROB_SC rob_sc_1 (
    .C(C_t), .E(CT_RF__SCSRE), .D(ISC_sc), .inst(inst_DP), .com1(com1), .com2(com2), .com1_id(com1_inst),
    .com2_id(com2_inst), .clr_16(clrs_16), .roll(clr_id), .roll_sf(clr_self), .SCA(SCA), .W1(CT_SC__W1),
    .D1(CT_SC__D1), .W2(CT_SC__W2), .D2(CT_SC__D2), .D3(CT_SC__FD));
  Register #(.Bits(32)) register_11 (.D(PCS), .C(C_t), .en(CT_BUS__IAR), .Q(PCS_FT));
  or or_11 (or_11_out, STB_M__V, LDB_M__V);
  not not_7 (not_7_out, B_used);
  RS_FF rs_ff_6 (.S(MEM_LD), .C(C_t), .R(and_33_out), .Q(rs_ff_6_q), .nQ(rs_ff_6_nq));
  and and_34 (and_34_out, com1, comparator_17_eq);
  and and_35 (and_35_out, com2, comparator_18_eq);
  // ROB_gen rob_gen_1: pin names not known; wires that end beside it: C_t, CT_ROB__GEN__STA, CT_ROB__GEN__STB, ROB_GEN_DA, ROB_GEN_DB, ROB_GEN_WA, ROB_GEN_WB, ROB_GEN_EX1, ROB_GEN_EX2, ROB_GEN_INSTA, ROB_GEN_INSTB, com1, com2, com1_inst, com2_inst, clrs_16, RET_INST, CT_RF__D1, CT_RF__R1, CT_RF__W1, CT_RF__EX1, CT_RF__D2, CT_RF__R2, CT_RF__W2, CT_RF__EX2, CT_RF__DR
  ROB_PC rob_pc_1 (
    .C(C_t), .E(issue), .D(PCS_DC), .inst(inst_IS), .com_id(com1_inst), .read_id(inst_DP), .ret_id(RET_INST),
    .D1(pca_i), .D2(pc_read), .D3(pc_ret));
  and and_36 (MEM_RD, not_7_out, rs_ff_6_q);
  or or_12 (or_12_out, rs_ff_6_nq, D_recieved_t);
  and and_37 (and_37_out, ~D_LD, MEM_LD__REC);  // And
  or or_13 (or_13_out, and_34_out, and_35_out);
  inst_sfcomp inst_sfcomp_1 (
    .A_id(TRAP_INST), .A_ep(TRAP_EP), .B_id(clr_id), .B_ep(clr_ep), .B_eq(clr_self),
    .A_new(inst_sfcomp_1_a_new));
  and and_38 (TRAP_IRD, ~FU_CLR[4], d_ff_9_q, d_ff_10_q);  // And
  and and_39 (and_39_out, byte_D0[3], byte_D0[0]);
  and and_40 (and_40_out, byte_D0[2], byte_D0[0]);
  and and_41 (and_41_out, byte_D0_iv[3], byte_D0_iv[2], byte_D0[1], byte_D0_iv[0]);
  and and_42 (and_42_out, byte_D0_iv[4], byte_D0[3], byte_D0[2], byte_D0[1]);
  and and_43 (and_43_out, byte_D0[4], byte_D0_iv[3], byte_D0_iv[2], byte_D0[1], byte_D0[0]);
  and and_44 (and_44_out[7], byte_D0_iv[4], byte_D0[3], byte_D0[2]);
  and and_45 (and_45_out, byte_D0[4], byte_D0[2], byte_D0_iv[1]);
  and and_46 (and_46_out, byte_D0[4], byte_D0_iv[3], byte_D0_iv[2]);
  and and_47 (and_47_out, byte_D0_iv[4], byte_D0_iv[3], byte_D0_iv[2]);
  and and_48 (and_48_out, byte_D0_iv[4], byte_D0_iv[3]);
  and and_49 (and_49_out, byte_D0_iv[4], byte_D0[3], byte_D0_iv[2], byte_D0_iv[1]);
  and and_50 (and_50_out, byte_D0_iv[4], byte_D0[3], byte_D0_iv[2]);
  and and_51 (and_51_out, byte_D0[4], byte_D0[3]);
  and and_52 (and_52_out, byte_D0_iv[4], byte_D0_iv[3], byte_D0[2], byte_D0_iv[1]);
  and and_53 (and_53_out, byte_D0[4], byte_D0[2], byte_D0[1]);
  and and_54 (and_54_out, byte_D0_iv[4], byte_D0_iv[3], byte_D0_iv[2], byte_D0[1], byte_D0[0]);
  and and_55 (and_55_out, byte_D0_iv[2], byte_D0_iv[0]);
  and and_56 (and_56_out, byte_D0[2], byte_D0[0]);
  and and_57 (and_57_out, byte_D0[1], byte_D0[2], byte_D0[4]);
  and and_58 (and_58_out, byte_D0[3], byte_D0[4]);
  Register #(.Bits(32)) register_12 (.D(PCS_FT), .C(C_t), .en(dc_e), .Q(PCS_DC));
  not not_8 (MEM_LD__REC, LDB_forward);
  RS_FF rs_ff_7 (.S(D_LD), .C(C_t), .R(and_37_out), .Q(MEM_LD__RD), .nQ(D_listen));
  Register #(.Bits(32)) register_13 (.D(D_D__bus), .C(C_t), .en(D_LD), .Q(MEM_LD__D));
  Register #(.Bits(6)) register_14 (.D(D_MID), .C(C_t), .en(D_LD), .Q(MEM_LD__AMID));
  Register register_15 (.D(MEM_EP), .C(C_t), .en(D_LD), .Q(MEM_LD__EP));
  and and_59 (and_59_out, ~FU_CLR[4], ~d_ff_9_q, d_ff_10_q);  // And
  and and_60 (MEM_LD, or_11_out, or_12_out);
  and and_61 (and_61_out, or_13_out, hlt, rs_ff_8_q);
  and and_62 (and_62_out, or_13_out, rs_ff_8_q);
  or or_14 (or_14_out, and_59_out, FU_I__V[0]);
  and and_63 (TRAP_busy, TRAP_RD, ~TRAP_ST);  // And
  or or_15 (and_44_out[9], and_39_out, and_40_out, and_41_out);
  or or_16 (and_44_out[6], and_45_out, and_42_out, and_43_out);
  or or_17 (and_44_out[5], and_44_out[7], and_45_out, and_46_out);
  or or_18 (and_44_out[4], and_52_out, and_53_out, and_47_out);
  or or_19 (and_44_out[3], and_48_out, and_53_out, and_49_out);
  or or_20 (and_44_out[2], and_50_out, and_51_out);
  or or_21 (and_44_out[1], and_52_out, and_53_out, and_54_out);
  or or_22 (and_44_out[0], byte_D0[3], byte_D0[1], and_55_out, and_56_out);
  nor nor_4 (nor_4_out, and_57_out, and_58_out);
  ROB_FL rob_fl_1 (
    .C(C_t), .E1(CT_ROB__FL__STA), .E2(CT_ROB__FL__STB), .D1(ROB_FL_A), .D2(ROB_FL_B), .inst1(ROB_FL_INSTA),
    .inst2(ROB_FL_INSTB), .com1(com1), .com2(com2), .com1_id(com1_inst), .com2_id(com2_inst),
    .clr_16(clrs_16), .W1_O(CT_FL__W1), .D1_O(CT_FL__D1), .W2_O(CT_FL__W2), .D2_O(CT_FL__D2));
  or or_23 (or_23_out, clr_sel[0], CT_JMP);
  Register #(.Bits(37)) BTB_F (
    .D({BTB_packet[36:3], BTB_JP, BTB_packet[1:0]}), .C(C_t), .en(CT_BUS__IAR), .Q(BTB_fetch));
  Register #(.Bits(32)) I_A__R (.D(PCS), .C(C_t), .en(CT_BUS__IAR), .Q(I_A__R_q));
  xor xor_1 (xor_1_out, STB_M__EP, LDB_M__EP);
  Comparator #(.Bits(4)) comparator_19 (
    .a(LDB_M__ID), .b(STB_M__ID), .gt(comparator_19_gt), .lt(comparator_19_lt));  // open: eq
  Register #(.Bits(32)) register_16 (.D(pc_read), .C(C_t), .en(CT_TRAP__LD), .Q(HALT_PC));
  and and_64 (and_64_out, inst_sfcomp_1_a_new, clr, ~CT_TRAP__LD);  // And
  and and_65 (and_65_out, and_62_out, ~CT_TRAP__LD);  // And
  nor nor_5 (nor_5_out[1], byte_D1[1], nor_5_out[2]);
  nor nor_6 (nor_5_out[2], byte_D1[0], byte_D1[1], byte_D1[2]);
  and and_66 (and_66_out, byte_D0_iv[7], byte_D0_iv[6], byte_D0[5], CT_DISP);
  and and_67 (and_67_out, byte_D0_iv[7], byte_D0[6], byte_D0_iv[5], CT_DISP);
  PriorityEncoder #(.Selector_Bits(2)) priorityencoder_1 (
    .in0(clr_sel[1]), .in1(or_23_out), .in2(CT_RF__PCH), .in3(1'b0), .num(priorityencoder_1_num));  // open: any
  assign I_A__bus = CT_BUS__IAG ? I_A__R_q : 32'bz;  // Driver driver_45
  and and_68 (and_68_out, STB_M__V, LDB_M__V);
  Multiplexer multiplexer_8 (
    .sel(xor_1_out), .in_0(comparator_19_gt), .in_1(comparator_19_lt), .out(multiplexer_8_out));
  RS_FF u_HLT (.S(and_61_out), .C(C_t), .R(run_t), .Q(halted));  // open: nQ
  or or_24 (or_24_out, and_64_out, and_65_out);
  not not_9 (TRAP_free, TRAP_busy);
  and and_69 (and_69_out, byte_D0_iv[0], byte_D0_iv[1], byte_D0[2], byte_D0[3], byte_D0[4], byte_D0_iv[5], byte_D0_iv[6], byte_D0_iv[7], CT_DISP);
  and and_70 (and_70_out, byte_D0[1], byte_D0_iv[2], byte_D0[3], byte_D0[4], byte_D0_iv[5], byte_D0_iv[6], byte_D0_iv[7], CT_DISP);
  and and_71 (and_71_out, byte_D0[1], byte_D0[2], byte_D0[3], byte_D0[4], byte_D0_iv[5], byte_D0_iv[6], byte_D0_iv[7], CT_DISP);
  or or_25 (or_25_out[1], byte_D1[1], byte_D1[2], byte_D1[0]);
  or or_26 (or_26_out, and_67_out, and_66_out);
  and and_72 (and_72_out, com1, CT_RF__W1, ~CT_RF__EX1);  // And
  and and_73 (and_73_out, com2, CT_RF__W2, ~CT_RF__EX2);  // And
  PullDown #(.Bits(16)) pulldown_12 (.out(INT_inst));
  PullDown #(.Bits(16)) pulldown_13 (.out(V1_inst));
  PullDown #(.Bits(16)) pulldown_14 (.out(V2_inst));
  PullDown pulldown_15 (.out(CT_RF__SCSRE));
  Multiplexer #(.Selector_Bits(2), .Bits(32)) multiplexer_9 (
    .sel(priorityencoder_1_num), .in_0(MEM_FPC), .in_1(JPU_ADDR), .in_2(HALT_PC), .in_3({32{1'b0}}),
    .out(multiplexer_9_out));
  Multiplexer multiplexer_10 (.sel(and_68_out), .in_0(STB_M__V), .in_1(multiplexer_8_out), .out(multiplexer_10_out));
  RS_FF rs_ff_8 (.S(CT_TRAP__LD), .C(C_t), .R(or_24_out), .Q(rs_ff_8_q));  // open: nQ
  and and_74 (FU_CLR[4], inst_sfcomp_1_a_new, clr);
  bus16x2_demux bus16x2_demux_1 (.bus_1(V1_inst), .bus_2(V2_inst), .E(or_14_out), .id(TRAP_INST));
  bus16_demux bus16_demux_1 (.bus(INT_inst), .E(or_14_out), .id(TRAP_INST));
  and and_75 (and_75_out, CT_DISP, byte_D0[4], byte_D0[3], byte_D0_iv[1], byte_D0_iv[2], byte_D0_iv[5], byte_D0_iv[6], byte_D0_iv[7]);
  or or_27 (or_27_out, and_69_out, and_70_out);
  not not_10 (not_10_out, multiplexer_10_out);
  Multiplexer #(.Bits(32)) multiplexer_11 (
    .sel(multiplexer_10_out), .in_0(LDB_M__A), .in_1(STB_M__A), .out(multiplexer_11_out));
  Multiplexer #(.Bits(2)) multiplexer_12 (
    .sel(multiplexer_10_out), .in_0(LDB_M__MD), .in_1(STB_M__MD), .out(multiplexer_12_out));
  and and_76 (and_76_out, and_71_out, byte_D0[0]);
  and and_77 (and_77_out, byte_D0_iv[0], and_71_out);
  regFile regfile_1 (
    .C(C_t), .E1(and_72_out), .E2(and_73_out), .D1(CT_RF__D1), .D2(CT_RF__D2), .RW1(CT_RF__R1[7:3]),
    .MW1(CT_RF__R1[2:0]), .RW2(CT_RF__R2[7:3]), .MW2(CT_RF__R2[2:0]), .RA(CT_RF__RA), .MA(CT_RF__MA),
    .RB(CT_RF__RB), .MB(CT_RF__MB), .PCS_i(pcs_i), .PCS_e(CT_RF__PCSE), .PCA_i(pca_i), .PCA_e(CT_RF__PCAE),
    .SCS_i(ISC_sc), .SC_sel(CT_RF__SCSS), .SCS_e(CT_RF__SCSE), .SCA_i(sca_i), .SCA_sel(CT_RF__SCAE),
    .SCA_e(CT_RF__SCAE), .FL_i({{23{1'b0}}, FL[14], fl_i}), .FL_sel(CT_RF__FLS), .FL_e(4'b0001),
    .PC_read(pc_read), .R_A(R_A), .R_B(R_B), .PCS_O(PCS), .PCA_O(PCA), .SCS_O(SCS), .SCA_O(SCA), .FL_O(FL));
  PriorityEncoder #(.Selector_Bits(2)) priorityencoder_2 (
    .in0(1'b1), .in1(BTB_JP), .in2(CT_RF__PCJ), .in3(boot_t), .num(priorityencoder_2_num));  // open: any
  or or_28 (or_28_out, boot_t, clr_self, or_23_out, BTB_JP);
  Register #(.Bits(37)) BTB_D (.D(BTB_fetch), .C(C_t), .en(dc_e), .Q(BTB_pack__iss));
  Register #(.Bits(32)) I_D__R (.D(I_D__bus), .C(C_t), .en(dc_e), .Q({byte_I0, byte_I1, byte_I2, byte_I3}));
  Register register_17 (.D(CT_BUS__IDM), .C(C_t), .en(dc_e), .Q(register_17_q));
  and and_78 (MB_LDB__LD, LDB_M__V, MEM_LD, not_10_out);
  and and_79 (MB_STB__LD, multiplexer_10_out, MEM_LD);
  Register register_18 (.D(multiplexer_10_out), .C(C_t), .en(MEM_LD), .Q(MEM_TYPE__ST));
  Register register_19 (.D(LDB_M__EP), .C(C_t), .en(MEM_LD), .Q(MEM_EP));
  Register #(.Bits(6)) register_20 (.D(LDB_MID), .C(C_t), .en(MEM_LD), .Q(register_20_q));
  Register #(.Bits(32)) register_21 (.D(multiplexer_11_out), .C(C_t), .en(MEM_LD), .Q(register_21_q));
  Register #(.Bits(2)) register_22 (.D(multiplexer_12_out), .C(C_t), .en(MEM_LD), .Q(register_22_q));
  Register #(.Bits(32)) register_23 (.D(STB_M__D), .C(C_t), .en(MEM_LD), .Q(register_23_q));
  Register register_24 (.D(LDB_D__MMU), .C(C_t), .en(MEM_LD), .Q(register_24_q));
  assign {CT_RF__RA, CT_RF__MA} = or_30_out ? byte_D1 : 8'bz;  // Driver driver_46
  assign {CT_RF__RB, CT_RF__MB} = or_30_out ? byte_D2 : 8'bz;  // Driver driver_47
  assign CT_ALU__LD = or_30_out ? 1'b1 : 1'bz;  // Driver driver_48
  assign CT_ALU__CT = or_30_out ? {1'b0, and_44_out[7:0]} : 9'bz;  // Driver driver_49
  assign CT_ALU__M = or_30_out ? and_44_out[9] : 1'bz;  // Driver driver_50
  assign CT_FU__INST = or_30_out ? inst_DP : 4'bz;  // Driver driver_51
  assign CT_FU__EPOCH = or_30_out ? epoch_DP : 1'bz;  // Driver driver_52
  assign CT_FU__WR = or_30_out ? byte_D1 : 8'bz;  // Driver driver_53
  assign CT_ALU__WD = or_30_out ? nor_4_out : 1'bz;  // Driver driver_54
  assign CT_ALU__WF = or_30_out ? 1'b1 : 1'bz;  // Driver driver_55
  assign {CT_RF__RA, CT_RF__MA} = or_27_out ? byte_D2 : 8'bz;  // Driver driver_56
  assign CT_DIR__LD = or_27_out ? 1'b1 : 1'bz;  // Driver driver_57
  assign CT_DIR__M = or_27_out ? and_70_out : 1'bz;  // Driver driver_58
  assign CT_DIR__MS = or_27_out ? byte_D0[0] : 1'bz;  // Driver driver_59
  assign CT_FU__INST = or_27_out ? inst_DP : 4'bz;  // Driver driver_60
  assign CT_FU__EPOCH = or_27_out ? epoch_DP : 1'bz;  // Driver driver_61
  assign CT_FU__WR = or_27_out ? byte_D1 : 8'bz;  // Driver driver_62
  assign CT_RF__SCSS = and_71_out ? 1'b1 : 1'bz;  // Driver driver_63
  assign {CT_RF__RB, CT_RF__MB} = and_71_out ? 8'hf0 : 8'bz;  // Driver driver_64
  assign {CT_RF__RA, CT_RF__MA} = and_76_out ? byte_D1 : 8'bz;  // Driver driver_65
  assign CT_FU__WR = and_77_out ? byte_D1 : 8'bz;  // Driver driver_66
  assign CT_MB__LD = and_71_out ? 1'b1 : 1'bz;  // Driver driver_67
  assign CT_MB__ST = and_76_out ? 1'b1 : 1'bz;  // Driver driver_68
  assign CT_SP__MOF = and_76_out ? {1'b1, or_25_out[1], byte_D1[1]} : 3'bz;  // Driver driver_69
  assign CT_MB__OFFM = and_71_out ? 1'b1 : 1'bz;  // Driver driver_70
  assign CT_RF__SCSE = and_71_out ? 1'b1 : 1'bz;  // Driver driver_71
  assign CT_RF__SCN = and_71_out ? {nor_5_out, byte_D1[1]} : 3'bz;  // Driver driver_72
  assign CT_RF__SCD = and_76_out ? 1'b1 : 1'bz;  // Driver driver_73
  assign CT_FU__INST = and_71_out ? inst_DP : 4'bz;  // Driver driver_74
  assign CT_FU__EPOCH = and_71_out ? epoch_DP : 1'bz;  // Driver driver_75
  assign CT_RF__SCSRE = and_71_out ? 1'b1 : 1'bz;  // Driver driver_76
  assign CT_FU__EPOCH = or_26_out ? epoch_DP : 1'bz;  // Driver driver_77
  assign CT_FU__INST = or_26_out ? inst_DP : 4'bz;  // Driver driver_78
  assign {CT_RF__RB, CT_RF__MB} = or_26_out ? {byte_D0[4:0], 3'b000} : 8'bz;  // Driver driver_79
  assign {CT_RF__RA, CT_RF__MA} = and_67_out ? byte_D1 : 8'bz;  // Driver driver_80
  assign CT_FU__WR = and_66_out ? byte_D1 : 8'bz;  // Driver driver_81
  assign CT_MB__LD = or_26_out ? 1'b1 : 1'bz;  // Driver driver_82
  assign CT_MB__ST = and_67_out ? 1'b1 : 1'bz;  // Driver driver_83
  or or_29 (CT_RF__PCAE, com1, com2);
  ROB_INT rob_int_1 (
    .C(C_t), .E1(CT_ROB__INT__STA), .E2(CT_ROB__INT__STB), .D1(ROB_INT_A), .D2(ROB_INT_B),
    .inst1(ROB_INT_INSTA), .inst2(ROB_INT_INSTB), .com1(com1), .com2(com2), .com1_id(com1_inst),
    .com2_id(com2_inst), .clr_16(clrs_16), .W_O(CT_INT__W), .D_O(CT_INT__D));
  Multiplexer #(.Selector_Bits(2), .Bits(32)) multiplexer_13 (
    .sel(priorityencoder_2_num), .in_0(PCS), .in_1(BTB_packet[36:5]), .in_2(multiplexer_9_out),
    .in_3(reset_vec), .out(multiplexer_13_out));
  not not_11 (BUS_INSTV, register_17_q);
  assign D_MID = MEM_RD ? register_20_q : 6'bz;  // Driver driver_84
  assign D_A__bus = MEM_RD ? register_21_q : 32'bz;  // Driver driver_85
  assign D_MD = MEM_RD ? register_22_q : 2'bz;  // Driver driver_86
  assign D_D__bus = D_ST ? register_23_q : 32'bz;  // Driver driver_87
  and and_80 (D_MMU, MEM_RD, register_24_q);
  Register register_25 (.D(CT_KILL), .C(C_t), .en(CT_TRAP__LD), .Q(hlt));
  and and_81 (and_81_out, byte_D0_iv[7], byte_D0_iv[6], CT_DISP, byte_D0_iv[5], byte_D0_iv[4]);
  and and_82 (and_82_out, byte_D0_iv[7], byte_D0_iv[6], byte_D0_iv[5], byte_D0[4], byte_D0_iv[3], CT_DISP);
  Multiplexer #(.Bits(32)) multiplexer_14 (
    .sel(or_28_out), .in_0(add_4c32_1_s), .in_1(multiplexer_13_out), .out(pcs_i));
  add_4c32 add_4c32_1 (.a(multiplexer_13_out), .b(4'b0100), .s(add_4c32_1_s));  // open: c
  and and_83 (D_LD, ~MEM_TYPE__ST, MEM_RD);  // And
  and and_84 (D_ST, MEM_RD, MEM_TYPE__ST);
  PullDown pulldown_16 (.out(CT_INT));
  PullDown #(.Bits(8)) pulldown_17 (.out(CT_INTID));
  or or_30 (or_30_out, and_81_out, and_75_out, and_82_out);
  BitExtender #(.inputBits(1), .outputBits(8)) bitextender_3 (.in(byte_D0[3]), .out(bitextender_3_out));
  assign xor_2_out = FL[7:0] ^ bitextender_3_out;  // XOr xor_2, 8 bits wide
  and and_85 (and_85_out, com1, CT_SC__W1);
  and and_86 (and_86_out, com2, CT_SC__W2);
  Multiplexer #(.Bits(32)) multiplexer_15 (.sel(and_86_out), .in_0(CT_SC__D1), .in_1(CT_SC__D2), .out(sca_i));
  and and_87 (and_87_out, byte_D2[7], CT_DIR__MS);
  BitExtender #(.inputBits(1)) bitextender_4 (.in(and_87_out), .out(bitextender_4_out));
  Multiplexer #(.Bits(3)) multiplexer_16 (
    .sel(CT_MB__ST), .in_0(CT_FU__WR[2:0]), .in_1(CT_RF__MA), .out(multiplexer_16_out));
  and and_88 (and_88_out, byte_D0[1], byte_D0_iv[2], byte_D0[3], byte_D0[4], byte_D0[5], byte_D0[6], byte_D0_iv[7], CT_DISP);
  or or_31 (CT_RF__SCAE, and_85_out, and_86_out);
  Multiplexer multiplexer_17 (.sel(and_100_out[2]), .in_0(nand_1_out[2]), .in_1(1'b1), .out(multiplexer_17_out));
  not not_12 (not_12_out[0], register_26_q[0]);
  xor xor_3 (not_12_out[1], register_26_q[0], register_26_q[1]);
  xor xor_4 (not_12_out[2], register_26_q[1], register_26_q[2]);
  Multiplexer #(.Bits(32)) multiplexer_18 (
    .sel(CT_ALU__M), .in_0(R_B), .in_1({{16{1'b0}}, byte_D2, byte_D3}), .out(multiplexer_18_out));
  PullDown #(.Bits(8)) pulldown_18 (.out(CT_DIR__EXID));
  PullDown pulldown_19 (.out(CT_DIR__EXM));
  PullDown pulldown_20 (.out(CT_FU__EX));
  and and_89 (and_89_out, byte_D0_iv[4], byte_D0[5], byte_D0[6], byte_D0_iv[7], CT_DISP);
  Multiplexer #(.Selector_Bits(3)) multiplexer_19 (
    .sel(byte_D0[2:0]), .in_0(xor_2_out[0]), .in_1(xor_2_out[1]), .in_2(xor_2_out[2]), .in_3(xor_2_out[3]),
    .in_4(xor_2_out[4]), .in_5(xor_2_out[5]), .in_6(xor_2_out[6]), .in_7(xor_2_out[7]),
    .out(multiplexer_19_out));
  and and_90 (and_90_out, multiplexer_17_out, CT_ALU__LD);
  Register register_26 (.D(and_90_out), .C(C_t), .en(or_32_out), .Q(register_26_q[2]));
  not not_13 (not_13_out, multiplexer_17_out);
  or or_32 (or_32_out, not_13_out, multiplexer_20_out[2]);
  Multiplexer #(.Bits(3)) multiplexer_20 (
    .sel(or_33_out), .in_0(not_12_out), .in_1(and_100_out), .out(multiplexer_20_out));
  or or_33 (or_33_out, and_100_out[0], and_100_out[1], and_100_out[2]);
  Register #(.Bits(4)) register_27 (.D(CT_FU__INST), .C(C_t), .en(multiplexer_20_out[2]), .Q(register_27_q));
  Register register_28 (.D(CT_FU__EPOCH), .C(C_t), .en(multiplexer_20_out[2]), .Q(register_28_q));
  Register register_29 (.D(CT_ALU__WD), .C(C_t), .en(multiplexer_20_out[2]), .Q(register_29_q));
  Register register_30 (.D(CT_ALU__WF), .C(C_t), .en(multiplexer_20_out[2]), .Q(register_30_q));
  Register #(.Bits(32)) register_31 (.D(R_A), .C(C_t), .en(multiplexer_20_out[2]), .Q(register_31_q));
  Register #(.Bits(32)) register_32 (.D(multiplexer_18_out), .C(C_t), .en(multiplexer_20_out[2]), .Q(register_32_q));
  Register #(.Bits(8)) register_33 (.D(FL[7:0]), .C(C_t), .en(multiplexer_20_out[2]), .Q(register_33_q));
  Register #(.Bits(9)) register_34 (.D(CT_ALU__CT), .C(C_t), .en(multiplexer_20_out[2]), .Q(register_34_q));
  Register #(.Bits(8)) register_35 (.D(CT_FU__WR), .C(C_t), .en(multiplexer_20_out[2]), .Q(register_35_q));
  Multiplexer #(.Bits(32)) multiplexer_21 (
    .sel(CT_DIR__M), .in_0(R_A), .in_1({bitextender_4_out, byte_D2, byte_D3}), .out(multiplexer_21_out));
  Multiplexer #(.Bits(32)) multiplexer_22 (.sel(CT_INTM), .in_0(pc_read), .in_1(int_pc), .out(multiplexer_22_out));
  or or_34 (or_34_out, CT_INTM, CT_CALLM);
  or or_35 (or_35_out, multiplexer_16_out[0], multiplexer_16_out[2]);
  not not_14 (not_14_out, multiplexer_16_out[1]);
  and and_91 (and_91_out, byte_D0_iv[0], byte_D0_iv[1], byte_D0_iv[2], byte_D0_iv[3], byte_D0[4], byte_D0[5], byte_D0[6], byte_D0_iv[7], CT_DISP);
  and and_92 (and_92_out, byte_D0[0], byte_D0_iv[1], byte_D0_iv[2], byte_D0_iv[3], byte_D0[4], byte_D0[5], byte_D0[6], byte_D0_iv[7], CT_DISP);
  and and_93 (and_93_out, byte_D0_iv[1], byte_D0[2], byte_D0_iv[3], byte_D0[4], byte_D0[5], byte_D0[6], byte_D0_iv[7], CT_DISP);
  and and_94 (and_94_out, byte_D0[0], byte_D0_iv[1], byte_D0[2], byte_D0[3], byte_D0[4], byte_D0_iv[5], byte_D0_iv[6], byte_D0_iv[7], CT_DISP);
  and and_95 (and_95_out, byte_D0[0], and_88_out);
  and and_96 (and_96_out, and_88_out, byte_D0_iv[0]);
  Multiplexer multiplexer_23 (
    .sel(and_100_out[1]), .in_0(nand_1_out[1]), .in_1(nand_1_out[2]), .out(multiplexer_23_out));
  Multiplexer multiplexer_24 (
    .sel(register_26_q[2]), .in_0(CT_ALU__LD), .in_1(register_26_q[2]), .out(multiplexer_24_out));
  Multiplexer #(.Bits(4)) multiplexer_25 (
    .sel(register_26_q[2]), .in_0(CT_FU__INST), .in_1(register_27_q), .out(multiplexer_25_out));
  inst_sfcomp inst_sfcomp_2 (
    .A_id(register_27_q), .A_ep(register_28_q), .B_id(clr_id), .B_ep(clr_ep), .B_eq(clr_self),
    .A_new(inst_sfcomp_2_a_new));
  Multiplexer multiplexer_26 (
    .sel(register_26_q[2]), .in_0(CT_FU__EPOCH), .in_1(register_28_q), .out(multiplexer_26_out));
  Multiplexer multiplexer_27 (
    .sel(register_26_q[2]), .in_0(CT_ALU__WD), .in_1(register_29_q), .out(multiplexer_27_out));
  Multiplexer multiplexer_28 (
    .sel(register_26_q[2]), .in_0(CT_ALU__WF), .in_1(register_30_q), .out(multiplexer_28_out));
  Multiplexer #(.Bits(32)) multiplexer_29 (
    .sel(register_26_q[2]), .in_0(R_A), .in_1(register_31_q), .out(multiplexer_29_out));
  Multiplexer #(.Bits(32)) multiplexer_30 (
    .sel(register_26_q[2]), .in_0(multiplexer_18_out), .in_1(register_32_q), .out(multiplexer_30_out));
  Multiplexer #(.Bits(8)) multiplexer_31 (
    .sel(register_26_q[2]), .in_0(FL[7:0]), .in_1(register_33_q), .out(multiplexer_31_out));
  Multiplexer #(.Bits(9)) multiplexer_32 (
    .sel(register_26_q[2]), .in_0(CT_ALU__CT), .in_1(register_34_q), .out(multiplexer_32_out));
  Multiplexer #(.Bits(8)) multiplexer_33 (
    .sel(register_26_q[2]), .in_0(CT_FU__WR), .in_1(register_35_q), .out(multiplexer_33_out));
  Multiplexer multiplexer_34 (.sel(and_103_out[2]), .in_0(nand_4_out[2]), .in_1(1'b1), .out(multiplexer_34_out));
  not not_15 (not_15_out[0], register_51_q[0]);
  xor xor_5 (not_15_out[1], register_51_q[0], register_51_q[1]);
  xor xor_6 (not_15_out[2], register_51_q[1], register_51_q[2]);
  Multiplexer #(.Bits(32)) multiplexer_35 (
    .sel(CT_DIR__EXM), .in_0(multiplexer_21_out), .in_1(RX_SEL), .out(multiplexer_35_out));
  add_4c32 add_4c32_2 (.a(multiplexer_22_out), .b(4'b0100), .s(add_4c32_2_s));  // open: c
  BitExtender #(.inputBits(3)) bitextender_5 (.in(CT_SP__MOF), .out(bitextender_5_out));
  and and_97 (and_97_out[0], or_35_out, not_14_out);
  and and_98 (and_98_out, multiplexer_23_out, multiplexer_24_out);
  not not_16 (not_16_out, multiplexer_23_out);
  or or_36 (or_36_out, not_16_out, multiplexer_20_out[1]);
  or or_37 (register_26_q[1], register_50_q[1], register_26_q[2]);
  nand nand_1 (nand_1_out[2], inst_sfcomp_2_a_new, register_26_q[2], clr);
  Register #(.Bits(4)) register_36 (.D(multiplexer_25_out), .C(C_t), .en(multiplexer_20_out[1]), .Q(register_36_q));
  Register register_37 (.D(multiplexer_26_out), .C(C_t), .en(multiplexer_20_out[1]), .Q(register_37_q));
  Register register_38 (.D(multiplexer_27_out), .C(C_t), .en(multiplexer_20_out[1]), .Q(register_38_q));
  Register register_39 (.D(multiplexer_28_out), .C(C_t), .en(multiplexer_20_out[1]), .Q(register_39_q));
  Register #(.Bits(32)) register_40 (.D(multiplexer_29_out), .C(C_t), .en(multiplexer_20_out[1]), .Q(register_40_q));
  Register #(.Bits(32)) register_41 (.D(multiplexer_30_out), .C(C_t), .en(multiplexer_20_out[1]), .Q(register_41_q));
  Register #(.Bits(8)) register_42 (.D(multiplexer_31_out), .C(C_t), .en(multiplexer_20_out[1]), .Q(register_42_q));
  Register #(.Bits(9)) register_43 (.D(multiplexer_32_out), .C(C_t), .en(multiplexer_20_out[1]), .Q(register_43_q));
  Register #(.Bits(8)) register_44 (.D(multiplexer_33_out), .C(C_t), .en(multiplexer_20_out[1]), .Q(register_44_q));
  and and_99 (and_99_out, multiplexer_34_out, CT_DIR__LD);
  not not_17 (not_17_out, multiplexer_34_out);
  Register #(.Bits(4)) register_45 (.D(CT_FU__INST), .C(C_t), .en(multiplexer_48_out[2]), .Q(register_45_q));
  Register register_46 (.D(CT_FU__EPOCH), .C(C_t), .en(multiplexer_48_out[2]), .Q(register_46_q));
  Register #(.Bits(32)) register_47 (.D(multiplexer_35_out), .C(C_t), .en(multiplexer_48_out[2]), .Q(register_47_q));
  Register #(.Bits(8)) register_48 (.D(CT_FU__WR), .C(C_t), .en(multiplexer_48_out[2]), .Q(register_48_q));
  Register register_49 (.D(CT_FU__EX), .C(C_t), .en(multiplexer_48_out[2]), .Q(register_49_q));
  Multiplexer #(.Bits(32)) multiplexer_36 (.sel(or_34_out), .in_0(R_A), .in_1(add_4c32_2_s), .out(multiplexer_36_out));
  Multiplexer #(.Bits(32)) multiplexer_37 (.sel(CT_INTM), .in_0(R_B), .in_1(ISC), .out(multiplexer_37_out));
  Multiplexer #(.Bits(16)) multiplexer_38 (
    .sel(CT_MB__OFFM), .in_0({byte_D2, byte_D3}), .in_1(bitextender_5_out), .out(multiplexer_38_out));
  assign CT_FU__EPOCH = and_89_out ? epoch_DP : 1'bz;  // Driver driver_88
  assign CT_FU__INST = and_89_out ? inst_DP : 4'bz;  // Driver driver_89
  assign {CT_RF__RA, CT_RF__MA} = and_89_out ? byte_D1 : 8'bz;  // Driver driver_90
  assign CT_JPU__LD = and_89_out ? 1'b1 : 1'bz;  // Driver driver_91
  assign CT_JPU__JP = and_89_out ? multiplexer_19_out : 1'bz;  // Driver driver_92
  assign JPU_A__ST = and_89_out ? 1'b1 : 1'bz;  // Driver driver_93
  assign CT_FU__EPOCH = and_91_out ? epoch_DP : 1'bz;  // Driver driver_94
  assign CT_FU__INST = and_91_out ? inst_DP : 4'bz;  // Driver driver_95
  assign {CT_RF__RA, CT_RF__MA} = and_91_out ? byte_D1 : 8'bz;  // Driver driver_96
  assign {CT_RF__RB, CT_RF__MB} = and_91_out ? 8'hf0 : 8'bz;  // Driver driver_97
  assign CT_JPU__LD = and_91_out ? 1'b1 : 1'bz;  // Driver driver_98
  assign CT_JPU__JP = and_91_out ? 1'b1 : 1'bz;  // Driver driver_99
  assign JPU_A__ST = and_91_out ? 1'b1 : 1'bz;  // Driver driver_100
  assign CT_MB__LD = and_91_out ? 1'b1 : 1'bz;  // Driver driver_101
  assign CT_MB__ST = and_91_out ? 1'b1 : 1'bz;  // Driver driver_102
  assign CT_CALLM = and_91_out ? 1'b1 : 1'bz;  // Driver driver_103
  assign CT_SP__MOF = and_91_out ? 3'b100 : 3'bz;  // Driver driver_104
  assign CT_MB__OFFM = and_91_out ? 1'b1 : 1'bz;  // Driver driver_105
  assign CT_RF__SCSE = and_91_out ? 1'b1 : 1'bz;  // Driver driver_106
  assign CT_RF__SCSS = and_91_out ? 1'b1 : 1'bz;  // Driver driver_107
  assign CT_RF__SCD = and_91_out ? 1'b1 : 1'bz;  // Driver driver_108
  assign CT_RF__SCN = and_91_out ? 3'b100 : 3'bz;  // Driver driver_109
  assign CT_FU__MF = and_91_out ? 1'b1 : 1'bz;  // Driver driver_110
  assign JPU_CALL = and_91_out ? 1'b1 : 1'bz;  // Driver driver_111
  assign CT_RF__SCSRE = and_91_out ? 1'b1 : 1'bz;  // Driver driver_112
  assign CT_FU__EPOCH = and_92_out ? epoch_DP : 1'bz;  // Driver driver_113
  assign CT_FU__INST = and_92_out ? inst_DP : 4'bz;  // Driver driver_114
  assign {CT_RF__RB, CT_RF__MB} = and_92_out ? 8'hf0 : 8'bz;  // Driver driver_115
  assign CT_FU__WR = and_92_out ? 8'he8 : 8'bz;  // Driver driver_116
  assign CT_MB__LD = and_92_out ? 1'b1 : 1'bz;  // Driver driver_117
  assign CT_MB__OFFM = and_92_out ? 1'b1 : 1'bz;  // Driver driver_118
  assign CT_RF__SCSE = and_92_out ? 1'b1 : 1'bz;  // Driver driver_119
  assign CT_RF__SCSS = and_92_out ? 1'b1 : 1'bz;  // Driver driver_120
  assign CT_RF__SCN = and_92_out ? 3'b100 : 3'bz;  // Driver driver_121
  assign CT_FU__MF = and_92_out ? 1'b1 : 1'bz;  // Driver driver_122
  assign CT_RET__LD = and_92_out ? 1'b1 : 1'bz;  // Driver driver_123
  assign CT_RF__SCSRE = and_92_out ? 1'b1 : 1'bz;  // Driver driver_124
  assign CT_KILL = and_93_out ? byte_D0[0] : 1'bz;  // Driver driver_125
  assign CT_FU__EPOCH = and_93_out ? epoch_DP : 1'bz;  // Driver driver_126
  assign CT_FU__INST = and_93_out ? inst_DP : 4'bz;  // Driver driver_127
  assign CT_TRAP__LD = and_93_out ? 1'b1 : 1'bz;  // Driver driver_128
  bus16x2_demux bus16x2_demux_2 (.bus_1(V1_inst), .bus_2(V2_inst), .E(and_94_out), .id(inst_DP));
  assign CT_FU__WR = and_95_out ? byte_D3 : 8'bz;  // Driver driver_129
  assign {CT_RF__RA, CT_RF__MA} = and_95_out ? byte_D1 : 8'bz;  // Driver driver_130
  assign CT_DIR__LD = and_88_out ? 1'b1 : 1'bz;  // Driver driver_131
  assign CT_FU__INST = and_88_out ? inst_DP : 4'bz;  // Driver driver_132
  assign CT_FU__EPOCH = and_88_out ? epoch_DP : 1'bz;  // Driver driver_133
  assign CT_FU__WR = and_96_out ? byte_D1 : 8'bz;  // Driver driver_134
  assign CT_DIR__EXID = and_96_out ? byte_D3 : 8'bz;  // Driver driver_135
  assign CT_DIR__EXM = and_88_out ? 1'b1 : 1'bz;  // Driver driver_136
  assign CT_FU__EX = and_88_out ? 1'b1 : 1'bz;  // Driver driver_137
  Register register_50 (.D(and_98_out), .C(C_t), .en(or_36_out), .Q(register_50_q[1]));
  or or_38 (register_26_q[0], ALU_busy, register_50_q[1], register_26_q[2]);
  assign and_100_out = nand_2_out & register_26_q;  // And and_100, 3 bits wide
  Multiplexer #(.Bits(4)) multiplexer_39 (
    .sel(register_26_q[1]), .in_0(CT_FU__INST), .in_1(register_36_q), .out(multiplexer_39_out));
  inst_sfcomp inst_sfcomp_3 (
    .A_id(register_36_q), .A_ep(register_37_q), .B_id(clr_id), .B_ep(clr_ep), .B_eq(clr_self),
    .A_new(inst_sfcomp_3_a_new));
  Multiplexer multiplexer_40 (
    .sel(register_26_q[1]), .in_0(CT_FU__EPOCH), .in_1(register_37_q), .out(multiplexer_40_out));
  Multiplexer multiplexer_41 (
    .sel(register_26_q[1]), .in_0(CT_ALU__WD), .in_1(register_38_q), .out(multiplexer_41_out));
  Multiplexer multiplexer_42 (
    .sel(register_26_q[1]), .in_0(CT_ALU__WF), .in_1(register_39_q), .out(multiplexer_42_out));
  Multiplexer #(.Bits(32)) multiplexer_43 (
    .sel(register_26_q[1]), .in_0(R_A), .in_1(register_40_q), .out(multiplexer_43_out));
  Multiplexer #(.Bits(32)) multiplexer_44 (
    .sel(register_26_q[1]), .in_0(multiplexer_18_out), .in_1(register_41_q), .out(multiplexer_44_out));
  Multiplexer #(.Bits(8)) multiplexer_45 (
    .sel(register_26_q[1]), .in_0(FL[7:0]), .in_1(register_42_q), .out(multiplexer_45_out));
  Multiplexer #(.Bits(9)) multiplexer_46 (
    .sel(register_26_q[1]), .in_0(CT_ALU__CT), .in_1(register_43_q), .out(multiplexer_46_out));
  Multiplexer #(.Bits(8)) multiplexer_47 (
    .sel(register_26_q[1]), .in_0(CT_FU__WR), .in_1(register_44_q), .out(multiplexer_47_out));
  Register register_51 (.D(and_99_out), .C(C_t), .en(or_39_out), .Q(register_51_q[2]));
  or or_39 (or_39_out, not_17_out, multiplexer_48_out[2]);
  Multiplexer #(.Bits(3)) multiplexer_48 (
    .sel(or_40_out), .in_0(not_15_out), .in_1(and_103_out), .out(multiplexer_48_out));
  or or_40 (or_40_out, and_103_out[0], and_103_out[1], and_103_out[2]);
  Multiplexer #(.Bits(4)) multiplexer_49 (
    .sel(register_51_q[2]), .in_0(CT_FU__INST), .in_1(register_45_q), .out(multiplexer_49_out));
  inst_sfcomp inst_sfcomp_4 (
    .A_id(register_45_q), .A_ep(register_46_q), .B_id(clr_id), .B_ep(clr_ep), .B_eq(clr_self),
    .A_new(inst_sfcomp_4_a_new));
  Multiplexer multiplexer_50 (
    .sel(register_51_q[2]), .in_0(CT_FU__EPOCH), .in_1(register_46_q), .out(multiplexer_50_out));
  Multiplexer #(.Bits(32)) multiplexer_51 (
    .sel(register_51_q[2]), .in_0(multiplexer_35_out), .in_1(register_47_q), .out(multiplexer_51_out));
  Multiplexer #(.Bits(8)) multiplexer_52 (
    .sel(register_51_q[2]), .in_0(CT_FU__WR), .in_1(register_48_q), .out(multiplexer_52_out));
  Multiplexer multiplexer_53 (.sel(register_51_q[2]), .in_0(CT_FU__EX), .in_1(register_49_q), .out(multiplexer_53_out));
  Register register_52 (.D(CT_MB__LD), .C(C_t), .en(1'b1), .Q(MB_any__e));
  Register #(.Bits(4)) register_53 (.D(CT_FU__INST), .C(C_t), .en(CT_MB__LD), .Q(MB_INST));
  Register register_54 (.D(CT_FU__EPOCH), .C(C_t), .en(CT_MB__LD), .Q(MB_ep));
  Register register_55 (.D(CT_MB__ST), .C(C_t), .en(CT_MB__LD), .Q(MB_type__st));
  Register #(.Bits(32)) register_56 (.D(multiplexer_36_out), .C(C_t), .en(CT_MB__LD), .Q(MB_data));
  Register #(.Bits(32)) register_57 (.D(multiplexer_37_out), .C(C_t), .en(CT_MB__LD), .Q(register_57_q));
  Register #(.Bits(16)) register_58 (.D(multiplexer_38_out), .C(C_t), .en(CT_MB__LD), .Q(register_58_q));
  Register #(.Bits(2)) register_59 (.D({multiplexer_16_out[1], and_97_out[0]}), .C(C_t), .en(CT_MB__LD), .Q(MB_MD));
  Register #(.Bits(8)) register_60 (.D(CT_FU__WR), .C(C_t), .en(CT_MB__LD), .Q(MB_WR));
  Register register_61 (.D(CT_FU__MF), .C(C_t), .en(CT_MB__LD), .Q(MB_MF));
  Register #(.Bits(32)) register_62 (.D(pc_read), .C(C_t), .en(CT_MB__LD), .Q(MB_PC));
  Counter #(.Bits(6)) counter_3 (.en(CT_MB__LD), .C(C_t), .clr(boot_t), .out(MB_mid));  // open: ovf
  Multiplexer #(.Bits(32)) multiplexer_54 (.sel(CT_ISCM), .in_0(SCS), .in_1(ISC), .out(multiplexer_54_out));
  Multiplexer multiplexer_55 (
    .sel(and_100_out[0]), .in_0(nand_1_out[0]), .in_1(nand_1_out[1]), .out(multiplexer_55_out));
  Multiplexer multiplexer_56 (
    .sel(register_26_q[1]), .in_0(CT_ALU__LD), .in_1(register_50_q[1]), .out(multiplexer_56_out));
  and and_101 (and_101_out, multiplexer_55_out, multiplexer_56_out);
  nand nand_2 (nand_2_out[2], ALU_busy, register_50_q[1], register_26_q[2]);
  nand nand_3 (nand_1_out[1], inst_sfcomp_3_a_new, register_50_q[1], clr);
  Register #(.Bits(4)) register_63 (.D(multiplexer_39_out), .C(C_t), .en(ALU_A_LD), .Q(ALU_A_INST));
  Register register_64 (.D(multiplexer_40_out), .C(C_t), .en(ALU_A_LD), .Q(register_64_q));
  Register #(.Bits(32)) register_65 (.D(multiplexer_43_out), .C(C_t), .en(ALU_A_LD), .Q(ALU_A_A));
  Register #(.Bits(32)) register_66 (.D(multiplexer_44_out), .C(C_t), .en(ALU_A_LD), .Q(ALU_A_B));
  Register #(.Bits(8)) register_67 (.D(multiplexer_45_out), .C(C_t), .en(ALU_A_LD), .Q(ALU_A_FI));
  Register #(.Bits(9)) register_68 (.D(multiplexer_46_out), .C(C_t), .en(ALU_A_LD), .Q(ALU_A_CT));
  Register #(.Bits(8)) register_69 (.D(multiplexer_47_out), .C(C_t), .en(ALU_A_LD), .Q({ALU_A_WR, ALU_A_RM}));
  Multiplexer multiplexer_57 (
    .sel(and_103_out[1]), .in_0(nand_4_out[1]), .in_1(nand_4_out[2]), .out(multiplexer_57_out));
  Multiplexer multiplexer_58 (
    .sel(register_51_q[2]), .in_0(CT_DIR__LD), .in_1(register_51_q[2]), .out(multiplexer_58_out));
  and and_102 (and_102_out, multiplexer_57_out, multiplexer_58_out);
  not not_18 (not_18_out, multiplexer_57_out);
  nand nand_4 (nand_4_out[2], inst_sfcomp_4_a_new, register_51_q[2], clr);
  Register #(.Bits(4)) register_70 (.D(multiplexer_49_out), .C(C_t), .en(multiplexer_48_out[1]), .Q(register_70_q));
  Register register_71 (.D(multiplexer_50_out), .C(C_t), .en(multiplexer_48_out[1]), .Q(register_71_q));
  Register #(.Bits(32)) register_72 (.D(multiplexer_51_out), .C(C_t), .en(multiplexer_48_out[1]), .Q(register_72_q));
  Register #(.Bits(8)) register_73 (.D(multiplexer_52_out), .C(C_t), .en(multiplexer_48_out[1]), .Q(register_73_q));
  Register register_74 (.D(multiplexer_53_out), .C(C_t), .en(multiplexer_48_out[1]), .Q(register_74_q));
  Multiplexer #(.Bits(32)) multiplexer_59 (
    .sel(clr), .in_0(multiplexer_54_out), .in_1(CT_SC__FD), .out(multiplexer_59_out));
  nand nand_5 (nand_2_out[1], ALU_busy, register_50_q[1]);
  Register register_75 (.D(and_102_out), .C(C_t), .en(or_41_out), .Q(register_75_q[1]));
  or or_41 (or_41_out, not_18_out, multiplexer_48_out[1]);
  or or_42 (register_51_q[1], register_75_q[1], register_51_q[2]);
  assign and_103_out = nand_8_out & register_51_q;  // And and_103, 3 bits wide
  Multiplexer #(.Bits(4)) multiplexer_60 (
    .sel(register_51_q[1]), .in_0(CT_FU__INST), .in_1(register_70_q), .out(multiplexer_60_out));
  inst_sfcomp inst_sfcomp_5 (
    .A_id(register_70_q), .A_ep(register_71_q), .B_id(clr_id), .B_ep(clr_ep), .B_eq(clr_self),
    .A_new(inst_sfcomp_5_a_new));
  Multiplexer multiplexer_61 (
    .sel(register_51_q[1]), .in_0(CT_FU__EPOCH), .in_1(register_71_q), .out(multiplexer_61_out));
  Multiplexer #(.Bits(32)) multiplexer_62 (
    .sel(register_51_q[1]), .in_0(multiplexer_35_out), .in_1(register_72_q), .out(multiplexer_62_out));
  Multiplexer #(.Bits(8)) multiplexer_63 (
    .sel(register_51_q[1]), .in_0(CT_FU__WR), .in_1(register_73_q), .out(multiplexer_63_out));
  Multiplexer multiplexer_64 (.sel(register_51_q[1]), .in_0(CT_FU__EX), .in_1(register_74_q), .out(multiplexer_64_out));
  and and_104 (MB_st__e, MB_any__e, MB_type__st);
  and and_105 (MB_ld__e, MB_any__e, ~MB_type__st);  // And
  add_s16c32 add_s16c32_1 (.a(register_57_q), .b(register_58_q), .s(MB_addr));  // open: c
  addsub_4c32 addsub_4c32_1 (.a(multiplexer_59_out), .b({1'b0, CT_RF__SCN}), .sub(CT_RF__SCD), .s(ISC_sc));  // open: c
  assign CT_RF__SCSE = clr ? 1'b1 : 1'bz;  // Driver driver_138
  assign CT_RF__SCSS = clr ? 1'b1 : 1'bz;  // Driver driver_139
  not not_19 (nand_2_out[0], ALU_busy);
  nand nand_6 (nand_1_out[0], or_45_out, ALU_busy, clr);
  inst_sfcomp inst_sfcomp_6 (
    .A_id(ALU_A_INST), .A_ep(register_64_q), .B_id(clr_id), .B_ep(clr_ep), .B_eq(clr_self), .A_new(ALU_A_CMP));
  Multiplexer multiplexer_65 (
    .sel(and_103_out[0]), .in_0(nand_4_out[0]), .in_1(nand_4_out[1]), .out(multiplexer_65_out));
  Multiplexer multiplexer_66 (
    .sel(register_51_q[1]), .in_0(CT_DIR__LD), .in_1(register_75_q[1]), .out(multiplexer_66_out));
  and and_106 (and_106_out, multiplexer_65_out, multiplexer_66_out);
  or or_43 (register_51_q[0], DIR_busy, register_75_q[1], register_51_q[2]);
  nand nand_7 (nand_4_out[1], inst_sfcomp_5_a_new, register_75_q[1], clr);
  Register #(.Bits(4)) register_76 (.D(multiplexer_60_out), .C(C_t), .en(DIR_LD), .Q(DIR_INST));
  Register register_77 (.D(multiplexer_61_out), .C(C_t), .en(DIR_LD), .Q(register_77_q));
  Register #(.Bits(32)) register_78 (.D(multiplexer_62_out), .C(C_t), .en(DIR_LD), .Q(DIR));
  Register #(.Bits(8)) register_79 (.D(multiplexer_63_out), .C(C_t), .en(DIR_LD), .Q(DIR_WR));
  Register register_80 (.D(multiplexer_64_out), .C(C_t), .en(DIR_LD), .Q(DIR_EX));
  Register #(.Bits(4)) register_81 (.D(multiplexer_39_out), .C(C_t), .en(ALU_B_LD), .Q(ALU_B_INST));
  Register register_82 (.D(multiplexer_40_out), .C(C_t), .en(ALU_B_LD), .Q(register_82_q));
  Register #(.Bits(32)) register_83 (.D(multiplexer_43_out), .C(C_t), .en(ALU_B_LD), .Q(ALU_B_A));
  Register #(.Bits(32)) register_84 (.D(multiplexer_44_out), .C(C_t), .en(ALU_B_LD), .Q(ALU_B_B));
  Register #(.Bits(8)) register_85 (.D(multiplexer_45_out), .C(C_t), .en(ALU_B_LD), .Q(ALU_B_FI));
  Register #(.Bits(9)) register_86 (.D(multiplexer_46_out), .C(C_t), .en(ALU_B_LD), .Q(ALU_B_CT));
  Register #(.Bits(8)) register_87 (.D(multiplexer_47_out), .C(C_t), .en(ALU_B_LD), .Q({ALU_B_WR, ALU_B_RM}));
  nand nand_8 (nand_8_out[2], DIR_busy, register_75_q[1], register_51_q[2]);
  and and_107 (LDB_forward, MB_ld__e, LDB_ldV);
  or or_44 (or_44_out, MEM_LD__RD, LDB_forward);
  and and_108 (and_108_out[0], ALU_A_LD, multiplexer_41_out);
  BitExtender #(.inputBits(1), .outputBits(2)) bitextender_6 (.in(ALU_A_CLR), .out(bitextender_6_out));
  and and_109 (and_108_out[1], ALU_A_LD, multiplexer_42_out);
  and and_110 (and_110_out[0], ALU_B_LD, multiplexer_41_out);
  BitExtender #(.inputBits(1), .outputBits(2)) bitextender_7 (.in(ALU_B_CLR), .out(bitextender_7_out));
  and and_111 (and_110_out[1], ALU_B_LD, multiplexer_42_out);
  or or_45 (or_45_out, ALU_A_CMP, ALU_B_CMP);
  nand nand_9 (nand_8_out[1], DIR_busy, register_75_q[1]);
  not not_20 (nand_8_out[0], DIR_busy);
  inst_sfcomp inst_sfcomp_7 (
    .A_id(DIR_INST), .A_ep(register_77_q), .B_id(clr_id), .B_ep(clr_ep), .B_eq(clr_self),
    .A_new(inst_sfcomp_7_a_new));
  and and_112 (and_112_out, MMU_acp_t, MMU_store);
  and and_113 (and_113_out, CT_ISS__OSTB, ~clr);  // And
  Multiplexer #(.Bits(32)) multiplexer_67 (
    .sel(LDB_forward), .in_0(MEM_LD__D), .in_1(LDB_ldD), .out(multiplexer_67_out));
  and and_114 (and_114_out, CT_ISS__OLDB, ~clr);  // And
  and and_115 (and_115_out, ~and_108_out[0], ALU_A_STD);  // And
  and and_116 (and_116_out, ~and_108_out[1], ALU_A_STF);  // And
  and and_117 (and_117_out, ~and_110_out[0], ALU_B_STD);  // And
  and and_118 (and_118_out, ~and_110_out[1], ALU_B_STF);  // And
  inst_sfcomp inst_sfcomp_8 (
    .A_id(ALU_B_INST), .A_ep(register_82_q), .B_id(clr_id), .B_ep(clr_ep), .B_eq(clr_self), .A_new(ALU_B_CMP));
  nand nand_10 (nand_4_out[0], inst_sfcomp_7_a_new, DIR_busy, clr);
  and and_119 (and_119_out, byte_I0[3], byte_I0[0]);
  and and_120 (and_120_out, byte_I0[2], byte_I0[0]);
  and and_121 (and_121_out, byte_I0_iv[3], byte_I0_iv[2], byte_I0[1], byte_I0_iv[0]);
  and and_122 (and_122_out, byte_I0_iv[2], byte_I0_iv[0]);
  and and_123 (and_123_out, byte_I0[2], byte_I0[0]);
  and and_124 (and_124_out, byte_I0[1], byte_I0[2], byte_I0[4]);
  and and_125 (and_125_out, byte_I0[3], byte_I0[4]);
  D_FF #(.Bits(2)) d_ff_11 (.D(and_108_out), .C(C_t), .Q(d_ff_11_q));  // open: nQ
  assign and_126_out = d_ff_11_q & ~bitextender_6_out;  // And and_126, 2 bits wide
  RS_FF rs_ff_9 (.S(and_108_out[0]), .C(C_t), .R(and_115_out), .nQ(rs_ff_9_nq));  // open: Q
  RS_FF rs_ff_10 (.S(and_108_out[1]), .C(C_t), .R(and_116_out), .nQ(rs_ff_10_nq));  // open: Q
  D_FF #(.Bits(2)) d_ff_12 (.D(and_110_out), .C(C_t), .Q(d_ff_12_q));  // open: nQ
  assign and_127_out = d_ff_12_q & ~bitextender_7_out;  // And and_127, 2 bits wide
  RS_FF rs_ff_11 (.S(and_110_out[0]), .C(C_t), .R(and_117_out), .nQ(rs_ff_11_nq));  // open: Q
  RS_FF rs_ff_12 (.S(and_110_out[1]), .C(C_t), .R(and_118_out), .nQ(rs_ff_12_nq));  // open: Q
  and and_128 (and_128_out, ~and_106_out, DIR_ST);  // And
  and and_129 (DIR_CLR, clr, inst_sfcomp_7_a_new);
  store_buffer_debug store_buffer_debug_1 (
    .res(boot_t), .C(C_t), .LD(MB_STB__LD), .W_p(and_112_out), .mid_WP(MMU_amid_t), .PA(MMU_phys_t),
    .W_d(MB_st__e), .inst_W(MB_INST), .D(MB_data), .A(MB_addr), .MD(MB_MD), .MID(MB_mid), .W_id(and_113_out),
    .epoch(epoch_IS), .inst(inst_IS), .com1(com1), .com2(com2), .com1_id(com1_inst), .com2_id(com2_inst),
    .ld_ep(MB_ep), .ld_id(MB_INST), .ld_addr(MB_addr), .clr(clr), .clr_self(clr_self), .clr_ep(clr_ep),
    .clr_id(clr_id), .full(STB_busy), .V(STB_M__V), .D_O(STB_M__D), .PA_O(STB_M__A), .MD_O(STB_M__MD),
    .id_O(STB_M__ID), .ep_O(STB_M__EP), .ld_V(LDB_ldV), .ld_D(LDB_ldD));
  load_buffer_debug load_buffer_debug_1 (
    .res(boot_t), .C(C_t), .LD(MB_LDB__LD), .LDB(FU_D__V[3]), .W_MMU(MMU_acp_t), .mid_WP(MMU_amid_t),
    .W_FWD(LDB_forward), .W_d(or_44_out), .mid_WD(MEM_LD__AMID), .D(multiplexer_67_out), .W_a(MB_ld__e),
    .inst_WA(MB_INST), .A(MB_addr), .MD(MB_MD), .MID(MB_mid), .MF(MB_MF), .WR(MB_WR), .PC(MB_PC),
    .W_id(and_114_out), .epoch(epoch_IS), .inst(inst_IS), .com1(com1), .com2(com2), .com1_id(com1_inst),
    .com2_id(com2_inst), .st(MB_st__e), .st_ep(MB_ep), .st_id(MB_INST), .st_addr(MB_addr), .st_data(MB_data),
    .st_md(MB_MD), .clr(clr), .clr_sf(clr_self), .clr_ep(clr_ep), .clr_id(clr_id), .full(LDB_busy),
    .V(load_buffer_debug_1_v), .D_O(LDB_B__D), .id_O(LDB_B__INST), .WR_O(LDB_B__WR), .MF_O(LDB_B__MF),
    .M_V(LDB_M__V), .M_D__MMU(LDB_D__MMU), .M_A(LDB_M__A), .M_MD(LDB_M__MD), .M_mid(LDB_MID),
    .M_id(LDB_M__ID), .M_ep(LDB_M__EP), .fl(Fl_MEM), .fl_ep(FL_MEM__EP), .fl_id(FL_MEM__ID), .fl_PC(MEM_FPC));  // open: fl_sf
  and and_130 (and_130_out, byte_I0_iv[7], byte_I0_iv[6], byte_I0[5], issue_e);
  and and_131 (and_131_out, byte_I0_iv[7], byte_I0[6], byte_I0_iv[5], issue_e);
  D_FF #(.Bits(2)) d_ff_13 (.D(and_126_out), .C(C_t), .Q(d_ff_13_q));  // open: nQ
  and and_132 (ALU_A_UUD, rs_ff_9_nq, ALU_A_V);
  and and_133 (ALU_A_UUF, rs_ff_10_nq, ALU_A_V);
  D_FF #(.Bits(2)) d_ff_14 (.D(and_127_out), .C(C_t), .Q(d_ff_14_q));  // open: nQ
  and and_134 (ALU_B_UUD, rs_ff_11_nq, ALU_B_V);
  and and_135 (ALU_B_UUF, rs_ff_12_nq, ALU_B_V);
  or or_46 (or_46_out, ALU_A_CLR, and_155_out);
  or or_47 (or_47_out, ALU_B_CLR, and_156_out);
  // alu_32 alu_32_1: pin names not known; wires that end beside it: ALU_A_A, ALU_A_B, ALU_A_FI, ALU_A_CT, ALU_A_RM, alu_32_1_p6, alu_32_1_p6, alu_32_1_p8, alu_32_1_p9, alu_32_1_p9, alu_32_1_p11, alu_32_1_p12, alu_32_1_p12, alu_32_1_p14, ALU_A_R, ALU_A_F
  alu_32 alu_32_2 (
    .A(ALU_B_A), .B(ALU_B_B), .F_I(ALU_B_FI), .CT(ALU_B_CT), .RM(ALU_B_RM), .E_A(alu_32_1_p8),
    .E_B(alu_32_1_p11), .E(alu_32_1_p14), .R_O(ALU_B_R), .F_O(ALU_B_F));
  RS_FF rs_ff_13 (.S(and_106_out), .C(C_t), .R(and_128_out), .nQ(rs_ff_13_nq));  // open: Q
  D_FF V (.D(DIR_LD), .C(C_t), .Q(V_q));  // open: nQ
  bus16x2_demux bus16x2_demux_3 (.bus_1(V1_inst), .bus_2(V2_inst), .E(DIR_V), .id(DIR_INST));
  and and_136 (and_136_out, issue_e, byte_I0[4], byte_I0[3], byte_I0_iv[1], byte_I0_iv[2], byte_I0_iv[5], byte_I0_iv[6], byte_I0_iv[7]);
  or or_48 (or_48_out, and_119_out, and_120_out, and_121_out);
  nor nor_7 (nor_7_out, byte_I0[3], byte_I0[1], and_122_out, and_123_out);
  nor nor_8 (nor_8_out, and_124_out, and_125_out);
  and and_137 (and_137_out, byte_I0_iv[0], byte_I0_iv[1], byte_I0[2], byte_I0[3], byte_I0[4], byte_I0_iv[5], byte_I0_iv[6], byte_I0_iv[7], issue_e);
  and and_138 (and_138_out, byte_I0[1], byte_I0_iv[2], byte_I0[3], byte_I0[4], byte_I0_iv[5], byte_I0_iv[6], byte_I0_iv[7], issue_e);
  and and_139 (and_139_out, byte_I0_iv[4], byte_I0[5], byte_I0[6], byte_I0_iv[7], issue_e);
  assign {ALU_A_FRE, ALU_A_DRE} = d_ff_13_q & ~bitextender_6_out;  // And and_140, 2 bits wide
  assign {ALU_B_FRE, ALU_B_DRE} = d_ff_14_q & ~bitextender_7_out;  // And and_141, 2 bits wide
  and and_142 (and_142_out, ALU_A_VD, ~or_46_out);  // And
  and and_143 (and_143_out, ALU_A_VF, ~or_46_out);  // And
  and and_144 (and_144_out, ALU_B_VD, ~or_47_out);  // And
  and and_145 (and_145_out, ALU_B_VF, ~or_47_out);  // And
  PullDown #(.Bits(32)) pulldown_21 (.out(alu_32_1_p12));
  PullDown #(.Bits(32)) pulldown_22 (.out(alu_32_1_p14));
  or or_49 (DIR_free, DIR_ST, rs_ff_13_nq);
  and and_146 (DIR_RD, V_q, ~DIR_CLR);  // And
  and and_147 (and_147_out, byte_I0[1], byte_I0[2], byte_I0[3], byte_I0[4], byte_I0_iv[5], byte_I0_iv[6], byte_I0_iv[7], issue_e);
  or or_50 (or_50_out, and_130_out, and_131_out);
  Comparator #(.Bits(3)) comparator_20 (.a(byte_I0[2:0]), .b(3'b110), .eq(comparator_20_eq));  // open: gt, lt
  RS_FF rs_ff_14 (.S(ALU_A_DRE), .C(C_t), .R(ALU_A_DRD), .Q(ALU_A_DRD));  // open: nQ
  RS_FF rs_ff_15 (.S(ALU_A_FRE), .C(C_t), .R(ALU_A_FRD), .Q(ALU_A_FRD));  // open: nQ
  RS_FF rs_ff_16 (.S(ALU_B_DRE), .C(C_t), .R(ALU_B_DRD), .Q(ALU_B_DRD));  // open: nQ
  RS_FF rs_ff_17 (.S(ALU_B_FRE), .C(C_t), .R(ALU_B_FRD), .Q(ALU_B_FRD));  // open: nQ
  RS_FF rs_ff_18 (.S(and_142_out), .C(C_t), .R(or_46_out), .Q(rs_ff_18_q));  // open: nQ
  RS_FF rs_ff_19 (.S(and_143_out), .C(C_t), .R(or_46_out), .Q(rs_ff_19_q));  // open: nQ
  RS_FF rs_ff_20 (.S(and_144_out), .C(C_t), .R(or_47_out), .Q(rs_ff_20_q));  // open: nQ
  RS_FF rs_ff_21 (.S(and_145_out), .C(C_t), .R(or_47_out), .Q(rs_ff_21_q));  // open: nQ
  assign CT_RF__PCSE = Fl_MEM ? 1'b1 : 1'bz;  // Driver driver_140
  assign CT_RF__PCJ = Fl_MEM ? 1'b1 : 1'bz;  // Driver driver_141
  assign Fl_MFM__SF = Fl_MEM ? 1'b1 : 1'bz;  // Driver driver_142
  and and_148 (and_148_out, byte_I0_iv[7], byte_I0_iv[6], issue_e, byte_I0_iv[5], byte_I0_iv[4]);
  and and_149 (and_149_out, byte_I0_iv[7], byte_I0_iv[6], byte_I0_iv[5], byte_I0[4], byte_I0_iv[3], issue_e);
  or or_51 (or_51_out, and_137_out, and_138_out);
  and and_150 (and_150_out, byte_I0[0], byte_I0_iv[1], byte_I0[2], byte_I0[3], byte_I0[4], byte_I0_iv[5], byte_I0_iv[6], byte_I0_iv[7], issue_e);
  not not_21 (not_21_out, comparator_20_eq);
  or or_52 (or_52_out, ALU_A_VD, ALU_A_UUD, rs_ff_18_q);
  or or_53 (or_53_out, ALU_A_VF, ALU_A_UUF, rs_ff_19_q);
  or or_54 (or_54_out, ALU_B_VD, ALU_B_UUD, rs_ff_20_q);
  or or_55 (or_55_out, ALU_B_VF, ALU_B_UUF, rs_ff_21_q);
  and and_151 (DIR_LD, and_106_out, DIR_free);
  not not_22 (DIR_busy, DIR_free);
  and and_152 (and_152_out, load_buffer_debug_1_v, ~FU_D__V[3]);  // And
  PullDown pulldown_23 (.out(Fl_MFM__SF));
  not not_23 (not_23_out, or_48_out);
  and and_153 (and_153_out, and_147_out, byte_I0[0]);
  and and_154 (and_154_out, byte_I0_iv[0], and_147_out);
  or or_56 (or_56_out, ALU_A_STD, rs_ff_9_nq);
  or or_57 (or_57_out, ALU_A_STF, rs_ff_10_nq);
  or or_58 (or_58_out, ALU_B_STD, rs_ff_11_nq);
  or or_59 (or_59_out, ALU_B_STF, rs_ff_12_nq);
  and and_155 (and_155_out, or_52_out, ~ALU_A_CLR, or_53_out);  // And
  bus16x2_demux bus16x2_demux_4 (.bus_1(V1_inst), .bus_2(V2_inst), .E(and_155_out), .id(ALU_A_INST));
  and and_156 (and_156_out, or_54_out, ~ALU_B_CLR, or_55_out);  // And
  bus16x2_demux bus16x2_demux_5 (.bus_1(V1_inst), .bus_2(V2_inst), .E(and_156_out), .id(ALU_B_INST));
  nor nor_9 (ALU_busy, ALU_A_LRD, ALU_B_LRD);
  or or_60 (ALU_free, ALU_A_LRD, ALU_B_LRD);
  Register #(.Bits(32)) register_88 (.D(ALU_A_R), .C(C_t), .en(ALU_A_DRE), .Q(ALU_A_T__R));
  Register #(.Bits(8)) register_89 (.D(ALU_A_F), .C(C_t), .en(ALU_A_FRE), .Q(ALU_A_T__F));
  Register #(.Bits(32)) register_90 (.D(ALU_B_R), .C(C_t), .en(ALU_B_DRE), .Q(ALU_B_T__R));
  Register #(.Bits(8)) register_91 (.D(ALU_B_F), .C(C_t), .en(ALU_B_FRE), .Q(ALU_B_T__F));
  D_FF d_ff_15 (.D(and_152_out), .C(C_t), .nQ(d_ff_15_nq));  // open: Q
  or or_61 (or_61_out, and_148_out, and_136_out, and_149_out);
  assign issue = or_61_out ? 1'b1 : 1'bz;  // Driver driver_143
  assign CT_ISS__URA = or_61_out ? 1'b1 : 1'bz;  // Driver driver_144
  assign CT_ISS__URB = or_61_out ? not_23_out : 1'bz;  // Driver driver_145
  assign CT_ISS__RA = or_61_out ? byte_I1[7:3] : 5'bz;  // Driver driver_146
  assign CT_ISS__RB = or_61_out ? byte_I2[7:3] : 5'bz;  // Driver driver_147
  assign CT_ISS__UFL = or_61_out ? nor_7_out : 1'bz;  // Driver driver_148
  assign CT_ISS__ORC = or_61_out ? nor_8_out : 1'bz;  // Driver driver_149
  assign CT_ISS__RC = or_61_out ? byte_I1[7:3] : 5'bz;  // Driver driver_150
  assign CT_ISS__OFL = or_61_out ? 1'b1 : 1'bz;  // Driver driver_151
  assign CT_ISS__UFU = or_61_out ? 3'b001 : 3'bz;  // Driver driver_152
  assign CT_ISS__URA = and_137_out ? 1'b1 : 1'bz;  // Driver driver_153
  assign CT_ISS__RA = and_137_out ? byte_I2[7:3] : 5'bz;  // Driver driver_154
  assign issue = or_51_out ? 1'b1 : 1'bz;  // Driver driver_155
  assign CT_ISS__ORC = or_51_out ? 1'b1 : 1'bz;  // Driver driver_156
  assign CT_ISS__RC = or_51_out ? byte_I1[7:3] : 5'bz;  // Driver driver_157
  assign CT_ISS__UFU = or_51_out ? 3'b010 : 3'bz;  // Driver driver_158
  assign issue = and_147_out ? 1'b1 : 1'bz;  // Driver driver_159
  assign CT_ISS__URB = and_147_out ? 1'b1 : 1'bz;  // Driver driver_160
  assign CT_ISS__RB = and_147_out ? 5'b11110 : 5'bz;  // Driver driver_161
  assign CT_ISS__OSC = and_147_out ? 1'b1 : 1'bz;  // Driver driver_162
  assign CT_ISS__UMM = and_147_out ? 1'b1 : 1'bz;  // Driver driver_163
  assign CT_ISS__UFU = and_147_out ? 3'b011 : 3'bz;  // Driver driver_164
  assign CT_ISS__URA = and_153_out ? 1'b1 : 1'bz;  // Driver driver_165
  assign CT_ISS__RA = and_153_out ? byte_I1[7:3] : 5'bz;  // Driver driver_166
  assign CT_ISS__OSTB = and_153_out ? 1'b1 : 1'bz;  // Driver driver_167
  assign CT_ISS__ORC = and_154_out ? 1'b1 : 1'bz;  // Driver driver_168
  assign CT_ISS__RC = and_154_out ? byte_I1[7:3] : 5'bz;  // Driver driver_169
  assign CT_ISS__OLDB = and_154_out ? 1'b1 : 1'bz;  // Driver driver_170
  assign issue = or_50_out ? 1'b1 : 1'bz;  // Driver driver_171
  assign CT_ISS__URA = or_50_out ? 1'b1 : 1'bz;  // Driver driver_172
  assign CT_ISS__RA = or_50_out ? byte_I0[4:0] : 5'bz;  // Driver driver_173
  assign CT_ISS__UMM = or_50_out ? 1'b1 : 1'bz;  // Driver driver_174
  assign CT_ISS__UFU = or_50_out ? 3'b011 : 3'bz;  // Driver driver_175
  assign CT_ISS__URB = and_131_out ? 1'b1 : 1'bz;  // Driver driver_176
  assign CT_ISS__RB = and_131_out ? byte_I1[7:3] : 5'bz;  // Driver driver_177
  assign CT_ISS__ORC = and_130_out ? 1'b1 : 1'bz;  // Driver driver_178
  assign CT_ISS__RC = and_130_out ? byte_I1[7:3] : 5'bz;  // Driver driver_179
  assign CT_ISS__OLDB = and_130_out ? 1'b1 : 1'bz;  // Driver driver_180
  assign CT_ISS__OSTB = and_131_out ? 1'b1 : 1'bz;  // Driver driver_181
  assign issue = and_150_out ? 1'b1 : 1'bz;  // Driver driver_182
  assign CT_BLOCK = and_150_out ? 1'b1 : 1'bz;  // Driver driver_183
  assign CT_UBTB = and_139_out ? 1'b1 : 1'bz;  // Driver driver_184
  assign issue = and_139_out ? 1'b1 : 1'bz;  // Driver driver_185
  assign CT_ISS__URA = and_139_out ? 1'b1 : 1'bz;  // Driver driver_186
  assign CT_ISS__RA = and_139_out ? byte_I1[7:3] : 5'bz;  // Driver driver_187
  assign CT_ISS__UFL = and_139_out ? not_21_out : 1'bz;  // Driver driver_188
  assign CT_ISS__UFU = and_139_out ? 3'b111 : 3'bz;  // Driver driver_189
  and and_157 (and_157_out, com1, CT_FL__W1);
  and and_158 (and_158_out, com2, CT_FL__W2);
  and and_159 (and_159_out, ~MMU_MB__MF, and_112_out);  // And
  and and_160 (and_160_out, ~LDB_B__MF, FU_D__V[3]);  // And
  and and_161 (LDB_B__RD, load_buffer_debug_1_v, d_ff_15_nq);
  bus16x2_demux bus16x2_demux_6 (.bus_1(V1_inst), .bus_2(V2_inst), .E(Fl_MFM__SF), .id(FL_MEM__ID));
  Multiplexer #(.Bits(8)) multiplexer_68 (.sel(and_158_out), .in_0(CT_FL__D1), .in_1(CT_FL__D2), .out(fl_i));
  and and_162 (ALU_A_LD, and_101_out, or_57_out, or_56_out);
  and and_163 (ALU_A_LRD, or_56_out, or_57_out);
  nand nand_11 (nand_11_out, or_56_out, or_57_out);
  and and_164 (ALU_B_LD, nand_11_out, and_101_out, or_59_out, or_58_out);
  and and_165 (ALU_B_LRD, or_58_out, or_59_out);
  and and_166 (and_166_out, ~ALU_A_LD, or_46_out);  // And
  and and_167 (and_167_out, ~ALU_B_LD, or_47_out);  // And
  bus16_demux bus16_demux_2 (.bus(V1_inst), .E(and_112_out), .id(MMU_INST));
  bus16_demux bus16_demux_3 (.bus(V2_inst), .E(and_159_out), .id(MMU_INST));
  bus16_demux bus16_demux_4 (.bus(V1_inst), .E(FU_D__V[3]), .id(LDB_B__INST));
  bus16_demux bus16_demux_5 (.bus(V2_inst), .E(and_160_out), .id(LDB_B__INST));
  or or_62 (CT_RF__FLS, and_157_out, and_158_out);
  and and_168 (ALU_A_CLR, clr, ALU_A_CMP);
  and and_169 (ALU_B_CLR, clr, ALU_B_CMP);
  RS_FF rs_ff_22 (.S(ALU_A_LD), .C(C_t), .R(and_166_out), .Q(ALU_A_V));  // open: nQ
  RS_FF rs_ff_23 (.S(ALU_B_LD), .C(C_t), .R(and_167_out), .Q(ALU_B_V));  // open: nQ
  and and_170 (and_170_out, byte_I0[1], byte_I0_iv[2], byte_I0[3], byte_I0[4], byte_I0[5], byte_I0[6], byte_I0_iv[7], issue_e);
  and and_171 (and_171_out, byte_I0_iv[0], byte_I0_iv[1], byte_I0_iv[2], byte_I0_iv[3], byte_I0[4], byte_I0[5], byte_I0[6], byte_I0_iv[7], issue_e);
  and and_172 (and_172_out, byte_I0[0], byte_I0_iv[1], byte_I0_iv[2], byte_I0_iv[3], byte_I0[4], byte_I0[5], byte_I0[6], byte_I0_iv[7], issue_e);
  and and_173 (and_173_out, byte_I0_iv[1], byte_I0[2], byte_I0_iv[3], byte_I0[4], byte_I0[5], byte_I0[6], byte_I0_iv[7], issue_e);
  and and_174 (and_174_out, byte_I0[0], and_170_out);
  and and_175 (and_175_out, and_170_out, byte_I0_iv[0]);
  and and_176 (and_176_out, byte_I0_iv[0], byte_I0[1], byte_I0[2], byte_I0_iv[3], byte_I0[4], byte_I0[5], byte_I0[6], byte_I0_iv[7], issue_e);
  and and_177 (and_177_out, byte_I0[0], byte_I0[1], byte_I0[2], byte_I0_iv[3], byte_I0[4], byte_I0[5], byte_I0[6], byte_I0_iv[7], issue_e);
  and and_178 (and_178_out, byte_I0_iv[1], byte_I0_iv[2], byte_I0[3], byte_I0[4], byte_I0[5], byte_I0[6], byte_I0_iv[7], issue_e);
  store_controller store_controller_1 (
    .C(C_t), .in1(ALU_A_DRD), .in2(ALU_B_DRD), .in3(DIR_RD), .in4(LDB_B__RD), .in5(1'b0), .in6(1'b0),
    .in7(1'b0), .in8(1'b0), .clr({3'b000, FU_CLR[4], 1'b0, DIR_CLR, ALU_B_CLR, ALU_A_CLR}),
    .D1_sel(store_controller_1_d1_sel), .D2_sel(store_controller_1_d2_sel), .ST1(CT_ROB__GEN__STA),
    .ST2(CT_ROB__GEN__STB), .out1(ALU_A_STD), .out2(ALU_B_STD), .out3(DIR_ST), .out4(LDB_B__ST),
    .V({FU_D__V, DIR_V, ALU_B_VD, ALU_A_VD}));  // open: out5, out6, out7, out8
  store_controller_half store_controller_half_1 (
    .C(C_t), .in1(ALU_A_FRD), .in2(ALU_B_FRD), .in3(1'b0), .in4(1'b0),
    .clr({1'b0, DIR_CLR, ALU_B_CLR, ALU_A_CLR}), .D1_sel(store_controller_half_1_d1_sel),
    .D2_sel(store_controller_half_1_d2_sel), .ST1(CT_ROB__FL__STA), .ST2(CT_ROB__FL__STB), .out1(ALU_A_STF),
    .out2(ALU_B_STF), .V({FU_F__V, ALU_B_VF, ALU_A_VF}));  // open: out3, out4
  store_controller_half store_controller_half_2 (
    .C(C_t), .in1(TRAP_IRD), .in2(1'b0), .in3(1'b0), .in4(1'b0), .clr({3'b000, FU_CLR[4]}),
    .D1_sel(store_controller_half_2_d1_sel), .D2_sel(store_controller_half_2_d2_sel), .ST1(CT_ROB__INT__STA),
    .ST2(CT_ROB__INT__STB), .out1(TRAP_ST), .V(FU_I__V));  // open: out2, out3, out4
  Demultiplexer #(.Selector_Bits(4)) demultiplexer_3 (
    .sel(priorityencoder_3_num), .in(and_194_out), .out_0(demultiplexer_3_out_0[0]),
    .out_1(demultiplexer_3_out_0[1]), .out_2(demultiplexer_3_out_0[2]), .out_3(demultiplexer_3_out_0[3]),
    .out_4(demultiplexer_3_out_0[4]), .out_5(demultiplexer_3_out_0[5]), .out_6(demultiplexer_3_out_0[6]),
    .out_7(demultiplexer_3_out_0[7]), .out_8(demultiplexer_3_out_0[8]), .out_9(demultiplexer_3_out_0[9]),
    .out_10(demultiplexer_3_out_0[10]), .out_11(demultiplexer_3_out_0[11]),
    .out_12(demultiplexer_3_out_0[12]), .out_13(demultiplexer_3_out_0[13]),
    .out_14(demultiplexer_3_out_0[14]), .out_15(demultiplexer_3_out_0[15]));
  Demultiplexer #(.Selector_Bits(4)) demultiplexer_4 (
    .sel(CT_FU__INST), .in(CT_RET__LD), .out_0(demultiplexer_4_out_0[0]), .out_1(demultiplexer_4_out_0[1]),
    .out_2(demultiplexer_4_out_0[2]), .out_3(demultiplexer_4_out_0[3]), .out_4(demultiplexer_4_out_0[4]),
    .out_5(demultiplexer_4_out_0[5]), .out_6(demultiplexer_4_out_0[6]), .out_7(demultiplexer_4_out_0[7]),
    .out_8(demultiplexer_4_out_0[8]), .out_9(demultiplexer_4_out_0[9]), .out_10(demultiplexer_4_out_0[10]),
    .out_11(demultiplexer_4_out_0[11]), .out_12(demultiplexer_4_out_0[12]),
    .out_13(demultiplexer_4_out_0[13]), .out_14(demultiplexer_4_out_0[14]), .out_15(demultiplexer_4_out_0[15]));
  or or_63 (or_63_out, JPU_INT, JPU_RET);
  nor nor_10 (nor_10_out, JPU_INT, JPU_RET);
  nor nor_11 (nor_11_out, JPU_INT, JPU_RET);
  not not_24 (not_24_out[0], or_73_out[0]);
  assign ISS_kernel = and_173_out ? byte_I0[0] : 1'bz;  // Driver driver_190
  assign CT_ISS__HALT = and_173_out ? 1'b1 : 1'bz;  // Driver driver_191
  assign CT_BLOCK = and_173_out ? 1'b1 : 1'bz;  // Driver driver_192
  assign issue = and_173_out ? 1'b1 : 1'bz;  // Driver driver_193
  assign CT_ISS__UMM = and_173_out ? 1'b1 : 1'bz;  // Driver driver_194
  assign CT_ISS__UFU = and_173_out ? 3'b100 : 3'bz;  // Driver driver_195
  assign CT_ISS__URA = and_174_out ? 1'b1 : 1'bz;  // Driver driver_196
  assign CT_ISS__RA = and_174_out ? byte_I1[7:3] : 5'bz;  // Driver driver_197
  assign ISS_kernel = and_170_out ? 1'b1 : 1'bz;  // Driver driver_198
  assign issue = and_170_out ? 1'b1 : 1'bz;  // Driver driver_199
  assign CT_ISS__UFU = and_170_out ? 3'b010 : 3'bz;  // Driver driver_200
  assign CT_BLOCK = and_170_out ? 1'b1 : 1'bz;  // Driver driver_201
  assign CT_ISS__UMM = and_170_out ? 1'b1 : 1'bz;  // Driver driver_202
  assign CT_ISS__ORC = and_175_out ? 1'b1 : 1'bz;  // Driver driver_203
  assign CT_ISS__RC = and_175_out ? byte_I1[7:3] : 5'bz;  // Driver driver_204
  assign CT_BLOCK = and_176_out ? 1'b1 : 1'bz;  // Driver driver_205
  assign issue = and_176_out ? 1'b1 : 1'bz;  // Driver driver_206
  assign CT_ISS__HALT = and_176_out ? 1'b1 : 1'bz;  // Driver driver_207
  assign CT_ISS__UMM = and_176_out ? 1'b1 : 1'bz;  // Driver driver_208
  assign CT_ISS__UFU = and_176_out ? 3'b100 : 3'bz;  // Driver driver_209
  assign ISS_kernel = and_177_out ? 1'b1 : 1'bz;  // Driver driver_210
  assign CT_BLOCK = and_177_out ? 1'b1 : 1'bz;  // Driver driver_211
  assign issue = and_177_out ? 1'b1 : 1'bz;  // Driver driver_212
  assign CT_ISS__HALT = and_177_out ? 1'b1 : 1'bz;  // Driver driver_213
  assign CT_ISS__UMM = and_177_out ? 1'b1 : 1'bz;  // Driver driver_214
  assign CT_ISS__UFU = and_177_out ? 3'b100 : 3'bz;  // Driver driver_215
  assign CT_BLOCK = and_178_out ? 1'b1 : 1'bz;  // Driver driver_216
  assign issue = and_178_out ? 1'b1 : 1'bz;  // Driver driver_217
  assign CT_ISS__HALT = and_178_out ? 1'b1 : 1'bz;  // Driver driver_218
  assign CT_ISS__UMM = and_178_out ? 1'b1 : 1'bz;  // Driver driver_219
  assign CT_ISS__UFU = and_178_out ? 3'b100 : 3'bz;  // Driver driver_220
  Multiplexer #(.Bits(32)) multiplexer_69 (.sel(JPU_INT), .in_0(CT_RF__DR), .in_1(int_vec_t), .out(multiplexer_69_out));
  BitExtender #(.inputBits(1)) bitextender_8 (.in(nor_10_out), .out(bitextender_8_out));
  BitExtender #(.inputBits(1), .outputBits(37)) bitextender_9 (.in(nor_11_out), .out(bitextender_9_out));
  BitExtender #(.inputBits(1)) bitextender_10 (.in(CT_FU__EPOCH), .out(bitextender_10_out));
  assign not_25_out = ~demultiplexer_4_out_0;  // Not not_25, 16 bits wide
  BitExtender #(.inputBits(1)) bitextender_11 (.in(CT_FU__EPOCH), .out(bitextender_11_out));
  Multiplexer multiplexer_70 (.sel(and_187_out[2]), .in_0(nand_12_out[2]), .in_1(1'b1), .out(multiplexer_70_out));
  and and_179 (and_179_out, multiplexer_70_out, MB_any__e);
  xor xor_7 (not_24_out[1], or_73_out[0], or_73_out[1]);
  xor xor_8 (not_24_out[2], or_73_out[1], register_99_q[2]);
  Register #(.Bits(4)) register_92 (.D(MB_INST), .C(C_t), .en(multiplexer_75_out[2]), .Q(register_92_q));
  Register register_93 (.D(MB_ep), .C(C_t), .en(multiplexer_75_out[2]), .Q(register_93_q));
  Register #(.Bits(32)) register_94 (.D(MB_addr), .C(C_t), .en(multiplexer_75_out[2]), .Q(register_94_q));
  Register #(.Bits(2)) register_95 (.D(MB_MD), .C(C_t), .en(multiplexer_75_out[2]), .Q(register_95_q));
  Register #(.Bits(6)) register_96 (.D(MB_mid), .C(C_t), .en(multiplexer_75_out[2]), .Q(register_96_q));
  Register register_97 (.D(MB_type__st), .C(C_t), .en(multiplexer_75_out[2]), .Q(register_97_q));
  Register register_98 (.D(MB_MF), .C(C_t), .en(multiplexer_75_out[2]), .Q(register_98_q));
  assign issue = and_171_out ? 1'b1 : 1'bz;  // Driver driver_221
  assign CT_ISS__URA = and_171_out ? 1'b1 : 1'bz;  // Driver driver_222
  assign CT_ISS__RA = and_171_out ? byte_I1[7:3] : 5'bz;  // Driver driver_223
  assign CT_ISS__URB = and_171_out ? 1'b1 : 1'bz;  // Driver driver_224
  assign CT_ISS__RB = and_171_out ? 5'b11110 : 5'bz;  // Driver driver_225
  assign CT_ISS__OSC = and_171_out ? 1'b1 : 1'bz;  // Driver driver_226
  assign CT_ISS__UMM = and_171_out ? 1'b1 : 1'bz;  // Driver driver_227
  assign CT_ISS__UFU = and_171_out ? 3'b110 : 3'bz;  // Driver driver_228
  assign CT_ISS__OSTB = and_171_out ? 1'b1 : 1'bz;  // Driver driver_229
  assign CT_UBTB = and_171_out ? 1'b1 : 1'bz;  // Driver driver_230
  assign issue = and_172_out ? 1'b1 : 1'bz;  // Driver driver_231
  assign CT_ISS__URB = and_172_out ? 1'b1 : 1'bz;  // Driver driver_232
  assign CT_ISS__RB = and_172_out ? 5'b11110 : 5'bz;  // Driver driver_233
  assign CT_ISS__OSC = and_172_out ? 1'b1 : 1'bz;  // Driver driver_234
  assign CT_ISS__UMM = and_172_out ? 1'b1 : 1'bz;  // Driver driver_235
  assign CT_ISS__UFU = and_172_out ? 3'b110 : 3'bz;  // Driver driver_236
  assign CT_ISS__OLDB = and_172_out ? 1'b1 : 1'bz;  // Driver driver_237
  assign CT_UBTB = and_172_out ? 1'b1 : 1'bz;  // Driver driver_238
  Multiplexer #(.Bits(32)) multiplexer_71 (.sel(JPU_RET), .in_0(pc_read), .in_1(pc_ret), .out(multiplexer_71_out));
  Multiplexer #(.Bits(4)) multiplexer_72 (.sel(JPU_RET), .in_0(CT_FU__INST), .in_1(RET_INST), .out(multiplexer_72_out));
  Multiplexer multiplexer_73 (.sel(JPU_RET), .in_0(CT_FU__EPOCH), .in_1(RET_EPOCH), .out(multiplexer_73_out));
  Multiplexer #(.Bits(32)) multiplexer_74 (
    .sel(or_63_out), .in_0(R_A), .in_1(multiplexer_69_out), .out(multiplexer_74_out));
  assign and_180_out = {byte_D2, byte_D3} & bitextender_8_out;  // And and_180, 16 bits wide
  assign and_181_out = BTB_DP & bitextender_9_out;  // And and_181, 37 bits wide
  or or_64 (or_64_out, CT_JPU__JP, JPU_INT, JPU_RET);
  or or_65 (or_65_out, CT_FU__MF, JPU_RET);
  assign not_26_out = ~demultiplexer_3_out_0;  // Not not_26, 16 bits wide
  assign or_66_out = bitextender_10_out | not_25_out;  // Or or_66, 16 bits wide
  assign and_182_out = bitextender_11_out & demultiplexer_4_out_0;  // And and_182, 16 bits wide
  Register register_99 (.D(and_179_out), .C(C_t), .en(or_67_out), .Q(register_99_q[2]));
  not not_27 (not_27_out, multiplexer_70_out);
  or or_67 (or_67_out, not_27_out, multiplexer_75_out[2]);
  Multiplexer #(.Bits(3)) multiplexer_75 (
    .sel(or_68_out), .in_0(not_24_out), .in_1(and_187_out), .out(multiplexer_75_out));
  or or_68 (or_68_out, and_187_out[0], and_187_out[1], and_187_out[2]);
  Multiplexer #(.Bits(32)) multiplexer_76 (
    .sel(register_99_q[2]), .in_0(MB_addr), .in_1(register_94_q), .out(multiplexer_76_out));
  Multiplexer #(.Bits(2)) multiplexer_77 (
    .sel(register_99_q[2]), .in_0(MB_MD), .in_1(register_95_q), .out(multiplexer_77_out));
  Multiplexer #(.Bits(6)) multiplexer_78 (
    .sel(register_99_q[2]), .in_0(MB_mid), .in_1(register_96_q), .out(multiplexer_78_out));
  Multiplexer multiplexer_79 (
    .sel(register_99_q[2]), .in_0(MB_type__st), .in_1(register_97_q), .out(multiplexer_79_out));
  Multiplexer multiplexer_80 (.sel(register_99_q[2]), .in_0(MB_MF), .in_1(register_98_q), .out(multiplexer_80_out));
  and and_183 (and_183_out, ~CT_JPU__LD, JPU_BTB__ST);  // And
  assign or_69_out = register_116_q | demultiplexer_4_out_0;  // Or or_69, 16 bits wide
  assign or_70_out = register_117_q | and_182_out;  // Or or_70, 16 bits wide
  Multiplexer multiplexer_81 (
    .sel(and_187_out[1]), .in_0(nand_12_out[1]), .in_1(nand_12_out[2]), .out(multiplexer_81_out));
  Multiplexer multiplexer_82 (
    .sel(register_99_q[2]), .in_0(MB_any__e), .in_1(register_99_q[2]), .out(multiplexer_82_out));
  Multiplexer #(.Bits(4)) multiplexer_83 (
    .sel(register_99_q[2]), .in_0(MB_INST), .in_1(register_92_q), .out(multiplexer_83_out));
  inst_sfcomp inst_sfcomp_9 (
    .A_id(register_92_q), .A_ep(register_93_q), .B_id(clr_id), .B_ep(clr_ep), .B_eq(clr_self),
    .A_new(inst_sfcomp_9_a_new));
  Multiplexer multiplexer_84 (.sel(register_99_q[2]), .in_0(MB_ep), .in_1(register_93_q), .out(multiplexer_84_out));
  // data_select_32 data_select_32_1: pin names not known; wires that end beside it: store_controller_1_d1_sel, store_controller_1_d2_sel, ALU_A_T__R, ALU_B_T__R, DIR, LDB_B__D, {32{1'b0}}, {32{1'b0}}, {32{1'b0}}, {32{1'b0}}, ROB_GEN_DA, ROB_GEN_DB
  data_select_8H data_select_8h_1 (
    .D1_sel(store_controller_half_1_d1_sel), .D2_sel(store_controller_half_1_d2_sel), .in1(ALU_A_T__F),
    .in2(ALU_B_T__F), .in3({8{1'b0}}), .in4({8{1'b0}}), .out1(ROB_FL_A), .out2(ROB_FL_B));
  data_select_6H data_select_6h_1 (
    .D1_sel(store_controller_half_2_d1_sel), .D2_sel(store_controller_half_2_d2_sel), .in1(TRAP_INT),
    .in2({6{1'b0}}), .in3({6{1'b0}}), .in4({6{1'b0}}), .out1(ROB_INT_A), .out2(ROB_INT_B));
  RS_FF rs_ff_24 (.S(CT_JPU__LD), .C(C_t), .R(and_183_out), .Q(JPU_BTB__ST), .nQ(rs_ff_24_nq));
  Register #(.Bits(32)) register_100 (.D(multiplexer_71_out), .C(C_t), .en(JPU_LD), .Q(JPU_PC));
  Register #(.Bits(4)) register_101 (.D(multiplexer_72_out), .C(C_t), .en(JPU_LD), .Q(Fl_JPU__INST));
  Register register_102 (.D(multiplexer_73_out), .C(C_t), .en(JPU_LD), .Q(Fl_JPU__EP));
  Register #(.Bits(32)) register_103 (.D(multiplexer_74_out), .C(C_t), .en(JPU_LD), .Q(register_103_q));
  Register #(.Bits(16)) register_104 (.D(and_180_out), .C(C_t), .en(JPU_LD), .Q(register_104_q));
  Register #(.Bits(37)) register_105 (
    .D(and_181_out), .C(C_t), .en(JPU_LD),
    .Q({JPU_BTB__tar, JPU_BTB__pred, JPU_BTB__J, JPU_BTB__V, JPU_BTBPK[0]}));
  Register register_106 (.D(or_64_out), .C(C_t), .en(JPU_LD), .Q(JPU_JP));
  Register register_107 (.D(or_65_out), .C(C_t), .en(JPU_LD), .Q(JPU_MF));
  assign and_184_out = icmks_16 & not_26_out & or_69_out;  // And and_184, 16 bits wide
  or or_71 (or_71_out, CT_RET__LD, and_194_out, ext_en);
  assign and_185_out = or_66_out & or_70_out;  // And and_185, 16 bits wide
  and and_186 (and_186_out, multiplexer_81_out, multiplexer_82_out);
  Register register_108 (.D(and_186_out), .C(C_t), .en(or_72_out), .Q(register_99_q[1]));
  not not_28 (not_28_out, multiplexer_81_out);
  or or_72 (or_72_out, not_28_out, multiplexer_75_out[1]);
  or or_73 (or_73_out[1], register_99_q[1], register_99_q[2]);
  nand nand_12 (nand_12_out[2], inst_sfcomp_9_a_new, register_99_q[2], clr);
  Register #(.Bits(4)) register_109 (.D(multiplexer_83_out), .C(C_t), .en(multiplexer_75_out[1]), .Q(register_109_q));
  Register register_110 (.D(multiplexer_84_out), .C(C_t), .en(multiplexer_75_out[1]), .Q(register_110_q));
  Register #(.Bits(32)) register_111 (.D(multiplexer_76_out), .C(C_t), .en(multiplexer_75_out[1]), .Q(register_111_q));
  Register #(.Bits(2)) register_112 (.D(multiplexer_77_out), .C(C_t), .en(multiplexer_75_out[1]), .Q(register_112_q));
  Register #(.Bits(6)) register_113 (.D(multiplexer_78_out), .C(C_t), .en(multiplexer_75_out[1]), .Q(register_113_q));
  Register register_114 (.D(multiplexer_79_out), .C(C_t), .en(multiplexer_75_out[1]), .Q(register_114_q));
  Register register_115 (.D(multiplexer_80_out), .C(C_t), .en(multiplexer_75_out[1]), .Q(register_115_q));
  or or_74 (or_74_out, rs_ff_24_nq, JPU_BTB__ST);
  Multiplexer multiplexer_85 (
    .sel(and_187_out[0]), .in_0(nand_12_out[0]), .in_1(nand_12_out[1]), .out(multiplexer_85_out));
  Multiplexer multiplexer_86 (.sel(or_73_out[1]), .in_0(MB_any__e), .in_1(register_99_q[1]), .out(multiplexer_86_out));
  or or_75 (or_73_out[0], MB_busy, register_99_q[1], register_99_q[2]);
  assign and_187_out = nand_13_out & {register_99_q[2], or_73_out};  // And and_187, 3 bits wide
  Multiplexer #(.Bits(4)) multiplexer_87 (
    .sel(or_73_out[1]), .in_0(MB_INST), .in_1(register_109_q), .out(multiplexer_87_out));
  inst_sfcomp inst_sfcomp_10 (
    .A_id(register_109_q), .A_ep(register_110_q), .B_id(clr_id), .B_ep(clr_ep), .B_eq(clr_self),
    .A_new(inst_sfcomp_10_a_new));
  Multiplexer multiplexer_88 (.sel(or_73_out[1]), .in_0(MB_ep), .in_1(register_110_q), .out(multiplexer_88_out));
  Multiplexer #(.Bits(32)) multiplexer_89 (
    .sel(or_73_out[1]), .in_0(MB_addr), .in_1(register_111_q), .out(multiplexer_89_out));
  Multiplexer #(.Bits(2)) multiplexer_90 (
    .sel(or_73_out[1]), .in_0(MB_MD), .in_1(register_112_q), .out(multiplexer_90_out));
  Multiplexer #(.Bits(6)) multiplexer_91 (
    .sel(or_73_out[1]), .in_0(MB_mid), .in_1(register_113_q), .out(multiplexer_91_out));
  Multiplexer multiplexer_92 (.sel(or_73_out[1]), .in_0(MB_type__st), .in_1(register_114_q), .out(multiplexer_92_out));
  Multiplexer multiplexer_93 (.sel(or_73_out[1]), .in_0(MB_MF), .in_1(register_115_q), .out(multiplexer_93_out));
  and and_188 (JPU_LD, CT_JPU__LD, or_74_out);
  Multiplexer #(.Bits(32)) multiplexer_94 (
    .sel(JPU_JP), .in_0(JPU_PC), .in_1(register_103_q), .out(multiplexer_94_out));
  Multiplexer #(.Bits(16)) multiplexer_95 (.sel(JPU_JP), .in_0(16'h4), .in_1(register_104_q), .out(multiplexer_95_out));
  Register #(.Bits(16)) register_116 (.D(and_184_out), .C(C_t), .en(or_71_out), .Q(register_116_q));
  Register #(.Bits(16)) register_117 (.D(and_185_out), .C(C_t), .en(or_71_out), .Q(register_117_q));
  and and_189 (and_189_out, multiplexer_85_out, multiplexer_86_out);
  nand nand_13 (nand_13_out[2], MB_busy, register_99_q[1], register_99_q[2]);
  nand nand_14 (nand_12_out[1], inst_sfcomp_10_a_new, register_99_q[1], clr);
  Register #(.Bits(4)) register_118 (.D(multiplexer_87_out), .C(C_t), .en(MMU_LD), .Q(MMU_INST));
  Register register_119 (.D(multiplexer_88_out), .C(C_t), .en(MMU_LD), .Q(register_119_q));
  Register #(.Bits(32)) register_120 (.D(multiplexer_89_out), .C(C_t), .en(MMU_LD), .Q(MMU_virt));
  Register #(.Bits(2)) register_121 (.D(multiplexer_90_out), .C(C_t), .en(MMU_LD), .Q(MMU_md));
  Register #(.Bits(6)) register_122 (.D(multiplexer_91_out), .C(C_t), .en(MMU_LD), .Q(MMU_mid));
  Register register_123 (.D(multiplexer_92_out), .C(C_t), .en(MMU_LD), .Q(MMU_store));
  Register register_124 (.D(multiplexer_93_out), .C(C_t), .en(MMU_LD), .Q(MMU_MB__MF));
  add_s16c32 add_s16c32_2 (.a(multiplexer_94_out), .b(multiplexer_95_out), .s(JPU_ADDR));  // open: c
  assign and_190_out = V1_inst & register_116_q;  // And and_190, 16 bits wide
  BitSelector #(.Selector_Bits(4)) bitselector_1 (
    .in(register_117_q), .sel(priorityencoder_3_num), .out(bitselector_1_out));
  nand nand_15 (nand_13_out[1], MB_busy, register_99_q[1]);
  inst_sfcomp inst_sfcomp_11 (
    .A_id(MMU_INST), .A_ep(register_119_q), .B_id(clr_id), .B_ep(clr_ep), .B_eq(clr_self),
    .A_new(inst_sfcomp_11_a_new));
  PullDown #(.Bits(3)) pulldown_24 (.out(CT_ISS__UFU));
  PullDown pulldown_25 (.out(CT_ISS__OSTB));
  PullDown pulldown_26 (.out(clr));
  PullDown pulldown_27 (.out(clr_ep));
  PullDown #(.Bits(4)) pulldown_28 (.out(clr_id));
  PullDown pulldown_29 (.out(CT_ALU__M));
  PullDown pulldown_30 (.out(CT_ALU__LD));
  PullDown pulldown_31 (.out(CT_ALU__WD));
  PullDown pulldown_32 (.out(CT_ALU__WF));
  PullDown pulldown_33 (.out(CT_FU__EPOCH));
  PullDown #(.Bits(4)) pulldown_34 (.out(CT_FU__INST));
  PullDown #(.Bits(8)) pulldown_35 (.out(CT_FU__WR));
  PullDown pulldown_36 (.out(CT_DIR__LD));
  PullDown pulldown_37 (.out(CT_DIR__M));
  PullDown pulldown_38 (.out(CT_DIR__MS));
  PullDown pulldown_39 (.out(MB_ep));
  PullDown #(.Bits(4)) pulldown_40 (.out(LD_id));
  PullDown #(.Bits(32)) pulldown_41 (.out(LD_addr));
  PullDown pulldown_42 (.out(CT_STB__LD));
  PullDown pulldown_43 (.out(CT_LDB__LD));
  PullDown pulldown_44 (.out(CT_MB__LD));
  PullDown pulldown_45 (.out(CT_MB__ST));
  PullDown pulldown_46 (.out(CT_ISS__OLDB));
  PullDown pulldown_47 (.out(CT_UBTB));
  PullDown pulldown_48 (.out(CT_USCB));
  and and_191 (and_191_out, ~JPU_MF, JPU_BTB__ST);  // And
  not not_29 (nand_13_out[0], MB_busy);
  nand nand_16 (nand_12_out[0], inst_sfcomp_11_a_new, MB_busy, clr);
  data_select_8 data_select_8_1 (
    .D1_sel(store_controller_1_d1_sel), .D2_sel(store_controller_1_d2_sel), .in1({ALU_A_WR, ALU_A_RM}),
    .in2({ALU_B_WR, ALU_B_RM}), .in3(DIR_WR), .in4(LDB_B__WR), .in5({8{1'b0}}), .in6({8{1'b0}}),
    .in7({8{1'b0}}), .in8({8{1'b0}}), .out1(ROB_GEN_WA), .out2(ROB_GEN_WB));
  data_select_4H data_select_4h_1 (
    .D1_sel(store_controller_half_1_d1_sel), .D2_sel(store_controller_half_1_d2_sel), .in1(ALU_A_INST),
    .in2(ALU_B_INST), .in3(4'b0000), .in4(4'b0000), .out1(ROB_FL_INSTA), .out2(ROB_FL_INSTB));
  data_select_4H data_select_4h_2 (
    .D1_sel(store_controller_half_2_d1_sel), .D2_sel(store_controller_half_2_d2_sel), .in1(TRAP_INST),
    .in2(4'b0000), .in3(4'b0000), .in4(4'b0000), .out1(ROB_INT_INSTA), .out2(ROB_INT_INSTB));
  PriorityEncoder #(.Selector_Bits(4)) priorityencoder_3 (
    .in0(and_190_out[0]), .in1(and_190_out[1]), .in2(and_190_out[2]), .in3(and_190_out[3]),
    .in4(and_190_out[4]), .in5(and_190_out[5]), .in6(and_190_out[6]), .in7(and_190_out[7]),
    .in8(and_190_out[8]), .in9(and_190_out[9]), .in10(and_190_out[10]), .in11(and_190_out[11]),
    .in12(and_190_out[12]), .in13(and_190_out[13]), .in14(and_190_out[14]), .in15(and_190_out[15]),
    .num(priorityencoder_3_num), .any(priorityencoder_3_any));
  and and_192 (and_192_out, ~and_189_out, or_76_out);  // And
  and and_193 (MMU_CLR, clr, inst_sfcomp_11_a_new);
  PullDown pulldown_49 (.out(CT_BLOCK));
  bus16_demux bus16_demux_6 (.bus(V1_inst), .E(and_191_out), .id(Fl_JPU__INST));
  bus16_demux bus16_demux_7 (.bus(V2_inst), .E(JPU_BTB__ST), .id(Fl_JPU__INST));
  not not_30 (not_30_out, BTB_override);
  and and_194 (and_194_out, FU_D__V[3], priorityencoder_3_any);
  or or_76 (or_76_out, MMU_acp_t, MMU_CLR);
  xor xor_9 (JPU_MISS, JPU_BTB__J, JPU_JP);
  not not_31 (not_31_out, JPU_BTB__pred[0]);
  RS_FF rs_ff_25 (.S(and_189_out), .C(C_t), .R(and_192_out), .nQ(rs_ff_25_nq));  // open: Q
  D_FF V_2 (.D(MMU_LD), .C(C_t), .Q(MMU_req));  // open: nQ
  PullDown pulldown_50 (.out(kernel_inst));
  PullDown pulldown_51 (.out(CT_RF__E));
  PullDown pulldown_52 (.out(CT_RF__DM));
  PullDown #(.Bits(5)) pulldown_53 (.out(CT_RF__WS));
  PullDown #(.Bits(3)) pulldown_54 (.out(CT_RF__WM));
  PullDown #(.Bits(5)) pulldown_55 (.out(CT_RF__RA));
  PullDown #(.Bits(3)) pulldown_56 (.out(CT_RF__MA));
  PullDown #(.Bits(5)) pulldown_57 (.out(CT_RF__RB));
  PullDown #(.Bits(3)) pulldown_58 (.out(CT_RF__MB));
  PullDown pulldown_59 (.out(CT_RF__PCSE));
  PullDown pulldown_60 (.out(CT_RF__PCJ));
  PullDown pulldown_61 (.out(CT_RF__PCR));
  PullDown #(.Bits(3)) pulldown_62 (.out(CT_RF__SCN));
  PullDown pulldown_63 (.out(CT_RF__SCD));
  PullDown #(.Bits(9)) pulldown_64 (.out(CT_ALU__CT));
  PullDown pulldown_65 (.out(CT_ALU__M));
  PullDown pulldown_66 (.out(CT_ALU__M2));
  PullDown pulldown_67 (.out(CT_BUS__IAR));
  PullDown pulldown_68 (.out(CT_BUS__IAG));
  PullDown pulldown_69 (.out(CT_BUS__IDR));
  PullDown pulldown_70 (.out(CT_BUS__IDM));
  PullDown pulldown_71 (.out(CT_BUS__DAR));
  PullDown pulldown_72 (.out(CT_BUS__DAM));
  PullDown pulldown_73 (.out(CT_BUS__DAG));
  PullDown pulldown_74 (.out(CT_BUS__DDR));
  PullDown pulldown_75 (.out(CT_BUS__DDG));
  PullDown pulldown_76 (.out(I_LD));
  PullDown pulldown_77 (.out(D_LD));
  PullDown pulldown_78 (.out(D_ST));
  PullDown #(.Bits(2)) pulldown_79 (.out(D_MD));
  PullDown pulldown_80 (.out(CT_MVR));
  and and_195 (and_195_out, JPU_BTB__pred[0], JPU_BTB__pred[1]);
  and and_196 (and_196_out, JPU_BTB__pred[0], JPU_JP);
  and and_197 (and_197_out, JPU_BTB__pred[1], JPU_JP);
  and and_198 (and_198_out, not_31_out, not_30_out, JPU_BTB__pred[1]);
  and and_199 (and_199_out, not_31_out, not_30_out, JPU_JP);
  and and_200 (and_200_out, JPU_BTB__pred[1], not_30_out, JPU_JP);
  D_FF #(.Bits(4)) d_ff_16 (.D(priorityencoder_3_num), .C(C_t), .Q(RET_INST));  // open: nQ
  D_FF d_ff_17 (.D(bitselector_1_out), .C(C_t), .Q(RET_EPOCH));  // open: nQ
  nand nand_17 (JPU_free, nand_18_out, and_194_out);
  and and_201 (and_201_out, nand_18_out, and_194_out);
  inst_sfcomp inst_sfcomp_12 (
    .A_id(priorityencoder_3_num), .A_ep(bitselector_1_out), .B_id(clr_id), .B_ep(clr_ep), .B_eq(clr_self),
    .A_new(inst_sfcomp_12_a_new));
  or or_77 (MB_free, or_76_out, rs_ff_25_nq);
  PullDown pulldown_81 (.out(CT_TRAP__LD));
  PullDown pulldown_82 (.out(CT_KILL));
  PullDown pulldown_83 (.out(ISS_kernel));
  data_select_4 data_select_4_1 (
    .D1_sel(store_controller_1_d1_sel), .D2_sel(store_controller_1_d2_sel), .in1(ALU_A_INST),
    .in2(ALU_B_INST), .in3(DIR_INST), .in4(LDB_B__INST), .in5(4'b0000), .in6(4'b0000), .in7(4'b0000),
    .in8(4'b0000), .out1(ROB_GEN_INSTA), .out2(ROB_GEN_INSTB));
  and and_202 (and_202_out[6], MB_free, JPU_free);
  or or_78 (JPU_pred[1], and_195_out, and_196_out, and_197_out, BTB_override);
  or or_79 (JPU_pred[0], and_198_out, and_199_out, and_200_out);
  and and_203 (MMU_LD, and_189_out, MB_free);
  not not_32 (MB_busy, MB_free);
  not not_33 (not_33_out, E_t);
  D_FF d_ff_18 (.D(and_201_out), .C(C_t), .Q(d_ff_18_q));  // open: nQ
  nand nand_18 (nand_18_out, inst_sfcomp_12_a_new, clr);
  res_station_debug res_station_debug_1 (
    .C(C_t), .res(not_33_out), .E(issue), .D({byte_I0, byte_I1, byte_I2, byte_I3}), .BTB_PK(BTB_pack__iss),
    .ep_I(epoch_IS), .inst(inst_IS), .URA(CT_ISS__URA), .URB(CT_ISS__URB), .RA(CT_ISS__RA), .RB(CT_ISS__RB),
    .UMM(CT_ISS__UMM), .UFL(CT_ISS__UFL), .UFU(CT_ISS__UFU), .ORC(CT_ISS__ORC), .RC(CT_ISS__RC),
    .OSC(CT_ISS__OSC), .OFL(CT_ISS__OFL), .BLOCK(CT_BLOCK), .com1(com1), .com2(com2), .com1_inst(com1_inst),
    .com2_inst(com2_inst), .clr(clr), .clr_self(clr_self), .clr_ep(clr_ep), .clr_id(clr_id),
    .FU_free(FU_free), .V(CT_DISP), .disp_32({byte_D0, byte_D1, byte_D2, byte_D3}), .BTB_DP(BTB_DP),
    .ep_O(epoch_DP), .disp(inst_DP), .full(RS_full));
  PullDown pulldown_84 (.out(ex_nop));
  PullDown pulldown_85 (.out(CT_ISS__HALT));
  Comparator #(.Bits(32)) comparator_21 (.a(JPU_ADDR), .b(JPU_BTB__tar), .eq(comparator_21_eq));  // open: gt, lt
  PullDown pulldown_86 (.out(issue));
  PullDown pulldown_87 (.out(CT_ISS__URA));
  PullDown pulldown_88 (.out(CT_ISS__URB));
  PullDown #(.Bits(5)) pulldown_89 (.out(CT_ISS__RA));
  PullDown #(.Bits(5)) pulldown_90 (.out(CT_ISS__RB));
  PullDown pulldown_91 (.out(CT_ISS__UMM));
  PullDown pulldown_92 (.out(CT_ISS__UFL));
  PullDown pulldown_93 (.out(CT_ISS__ORC));
  PullDown #(.Bits(5)) pulldown_94 (.out(CT_ISS__RC));
  PullDown pulldown_95 (.out(CT_ISS__OSC));
  PullDown pulldown_96 (.out(CT_ISS__OFL));
  PullDown pulldown_97 (.out(CT_ROB__EX__E));
  PullDown pulldown_98 (.out(CT_ROB__ST__E));
  PullDown #(.Bits(3)) pulldown_99 (.out(CT_SP__MOF));
  PullDown pulldown_100 (.out(CT_BUS__DDM));
  PullDown pulldown_101 (.out(CT_RF__PCH));
  PullDown pulldown_102 (.out(\wait ));
  nand nand_19 (nand_19_out, JPU_BTB__V, comparator_21_eq);
  and and_204 (and_204_out, JPU_MISS, JPU_BTB__V, comparator_21_eq);
  and and_205 (Fl_JPU, or_80_out, JPU_BTB__ST);
  assign CT_JPU__LD = d_ff_18_q ? 1'b1 : 1'bz;  // Driver driver_239
  assign JPU_RET = d_ff_18_q ? 1'b1 : 1'bz;  // Driver driver_240
  Comparator #(.Bits(3)) comparator_22 (
    .a(store_controller_1_d1_sel), .b(3'b010), .eq(comparator_22_eq));  // open: gt, lt
  Comparator #(.Bits(3)) comparator_23 (
    .a(store_controller_1_d2_sel), .b(3'b010), .eq(comparator_23_eq));  // open: gt, lt
  D_FF #(.Bits(8)) d_ff_19 (
    .D({JPU_free, and_202_out[6], 1'b0, TRAP_free, MB_free, DIR_free, ALU_free, 1'b1}), .C(C_t), .Q(FU_free));  // open: nQ
  and and_206 (ROB_GEN_EX1, comparator_22_eq, DIR_EX);
  and and_207 (ROB_GEN_EX2, comparator_23_eq, DIR_EX);
  and and_208 (BTB_override, JPU_JP, nand_19_out);
  and and_209 (and_209_out, nand_19_out, JPU_BTB__J);
  or or_80 (or_80_out, and_204_out, and_209_out, BTB_override);
  assign CT_RF__PCSE = Fl_JPU ? 1'b1 : 1'bz;  // Driver driver_241
  assign CT_RF__PCJ = Fl_JPU ? 1'b1 : 1'bz;  // Driver driver_242
  assign CT_JMP = Fl_JPU ? 1'b1 : 1'bz;  // Driver driver_243
  PullDown pulldown_103 (.out(CT_RF__SCSRE));
  PullDown pulldown_104 (.out(CT_RF__SCSE));
  PullDown pulldown_105 (.out(CT_RF__SCSS));
  PullDown pulldown_106 (.out(CT_JPU__JP));
  PullDown pulldown_107 (.out(JPU_A__ST));
  PullDown pulldown_108 (.out(CT_MB__OFFM));
  PullDown pulldown_109 (.out(JPU_BTB__ST));
  PullDown pulldown_110 (.out(CT_JPU__LD));
  PullDown pulldown_111 (.out(CT_JMP));
  PullDown pulldown_112 (.out(CT_FU__MF));
  PullDown pulldown_113 (.out(CT_CALL__LD));
  PullDown pulldown_114 (.out(CT_RET__LD));
  PullDown pulldown_115 (.out(JPU_RET));
  PullDown pulldown_116 (.out(JPU_free));
  PullDown pulldown_117 (.out(JPU_CALL));
  PullDown pulldown_118 (.out(CT_CALLM));

  assign CSH_mode = 2'b00;
  assign CSH_run = 1'b0;
  assign INT_pstr = 1'b0;
  assign INT_ret = 1'b0;
  assign INT_vstr = 1'b0;
  assign MMU_base = {32{1'b0}};
  assign MMU_dis = 1'b0;
  assign MMU_en = 1'b0;
  assign MMU_limit = {32{1'b0}};
  assign MMU_src = {32{1'b0}};

  // Other names for the same wires on the sheet: FU_CLR[2:0] = {DIR_CLR, ALU_B_CLR, ALU_A_CLR};
  //   ALU_A_WR[2:0] = ALU_A_RM; ALU_B_WR[2:0] = ALU_B_RM; BTB_packet[2] = BTB_JP; BTB_pred[1:0] = BTB_packet[4:3];
  //   BTB_tar[31:0] = BTB_packet[36:5]; BTB_V = BTB_packet[1]; Fl_INT__EP = com2_ep; Fl_INT__INST[3:0] = com2_inst;
  //   CT_RF__SCAS = CT_RF__SCAE; D_amid_t[5:0] = D_MID; D_responce_t = D_LD;
  //   disp_32[31:0] = {byte_D0, byte_D1, byte_D2, byte_D3}; imm16_2[15:0] = {byte_D2, byte_D3}; disp_e = CT_DISP;
  //   fl_i[8] = FL[14]; int_proc = FL[14]; trap = FL[15]; FU_D__V[2:0] = {DIR_V, ALU_B_VD, ALU_A_VD};
  //   LDB_B__V = FU_D__V[3]; FU_F__V[1:0] = {ALU_B_VF, ALU_A_VF}; TRAP_VI = FU_I__V[0]; INT_ISS = INT_acp;
  //   issue_32[31:0] = {byte_I0, byte_I1, byte_I2, byte_I3};
  //   JPU_BTBPK[36:1] = {JPU_BTB__tar, JPU_BTB__pred, JPU_BTB__J, JPU_BTB__V}; JPU_EN = JPU_BTB__ST;
  //   JPU_ST = JPU_BTB__ST; MB_LD = CT_MB__LD; run_int = Fl_INT; scs_i[31:0] = ISC_sc; TRAP_CLR = FU_CLR[4]

  // Notes on the sheet:
  //   C: Hz: 50000
  //   reset_vec: default 4294967040
  //   D_MD: 0:32
  //   1:16
  //   2:8
  //   3:u.u
  //   tests
  //   contents of rom_1 (hex, n*v repeats v):
  //   39,38,38,37,a,38,37,35,36,a
  //   decode circuit
  //   IO pins
  //   primeary signals
  //   pipeline controller
  //   kernal mode system
  //   interrupt system
  //   ext system
  //   syscall
  //   iret
  //   intervec/pri
  //   inst id manager
  //   interrupt commit
  //   ALU
  //   register
  //   stack
  //   RAM
  //   register system
  //   ROB
  //   program counter controller
  //   bus system
  //   data bus ctrl
  //   trap
  //   jump
  //   call
  //   return
  //   wait/halt
  //   block
  //   exld/st
  //   stack circuit
  //   ALU system
  //   dir circuit
  //   load/store circuit
  //   issue circuit
  //   flag circuit
  //   FU aribiter
  //   jmp circuit
  //   return unit
  //   MMU circuit
  //   control bus
endmodule
