// Digital circuit inst-min.dig as structural Verilog
module inst_min (
  input  [3:0] A_id,
  input  A_ep,
  input  [3:0] B_id,
  input  B_ep,
  input  A_v,
  input  B_v,
  output [3:0] m_id,
  output m_ep,
  output m_v
);

  wire and_1_out, comparator_1_gt, comparator_1_lt, multiplexer_1_out, xor_1_out;

  Comparator #(.Bits(4)) comparator_1 (.a(A_id), .b(B_id), .gt(comparator_1_gt), .lt(comparator_1_lt));  // open: eq
  xor xor_1 (xor_1_out, A_ep, B_ep);
  Multiplexer multiplexer_1 (.sel(xor_1_out), .in_0(comparator_1_gt), .in_1(comparator_1_lt), .out(multiplexer_1_out));
  and and_1 (and_1_out, B_v, multiplexer_1_out);
  or or_1 (m_v, A_v, B_v);
  Multiplexer #(.Bits(4)) multiplexer_2 (.sel(and_1_out), .in_0(A_id), .in_1(B_id), .out(m_id));
  Multiplexer multiplexer_3 (.sel(and_1_out), .in_0(A_ep), .in_1(B_ep), .out(m_ep));
endmodule
