// Digital circuit ram-test.dig as structural Verilog
module ram_test (
  input  [31:0] D2,
  input  [31:0] D1,
  input  str,
  input  ld1,
  input  C,
  input  [31:0] _2A,
  input  [31:0] _1A,
  input  [31:0] D_in,
  input  [1:0] mode,
  input  ld2
);

  wire and_1_out, or_1_out, R0_e, R1_e, R2_e, R3_e;
  wire [3:0] and_2_out, bitextender_1_out;
  wire [3:1] mask;
  wire [7:0] bitextender_2_out, bitextender_3_out, bitextender_4_out, bitextender_5_out, R0, R0_d, R1, R1_d,
       R2, R2_d, R3, R3_d, R4, R5, R6, R7;
  wire [23:0] addr_plus_1, multiplexer_1_out, multiplexer_2_out, multiplexer_3_out;
  wire [31:0] and_3_out, multiplexer_6_out, multiplexer_7_out;

  Add #(.Bits(24), .generic("this.Bits=int(args.addrBits-2);")) add_1 (
    .a({24{1'b0}}), .b(_1A[25:2]), .c_i(1'b1), .s(addr_plus_1));  // open: c_o
  nor nor_1 (mask[3], mode[0], mode[1]);
  not not_1 (mask[1], mode[1]);
  BitExtender #(.inputBits(1), .outputBits(4)) bitextender_1 (.in(str), .out(bitextender_1_out));
  or or_1 (or_1_out, _1A[0], _1A[1]);
  and and_1 (and_1_out, _1A[0], _1A[1]);
  assign and_2_out = bitextender_1_out & {{2{mask[3]}}, mask[1], 1'b1};  // And and_2, 4 bits wide
  Multiplexer #(.Bits(24), .generic("this.Bits=int(args.addrBits-2);")) multiplexer_1 (
    .sel(or_1_out), .in_0(_1A[25:2]), .in_1(addr_plus_1), .out(multiplexer_1_out));
  Multiplexer #(.Bits(24), .generic("this.Bits=int(args.addrBits-2);")) multiplexer_2 (
    .sel(_1A[1]), .in_0(_1A[25:2]), .in_1(addr_plus_1), .out(multiplexer_2_out));
  Multiplexer #(.Bits(24), .generic("this.Bits=int(args.addrBits-2);")) multiplexer_3 (
    .sel(and_1_out), .in_0(_1A[25:2]), .in_1(addr_plus_1), .out(multiplexer_3_out));
  RAMDualPort #(.AddrBits(24), .Bits(8)) u_R0 (.A(multiplexer_1_out), .Din(R0_d), .str(R0_e), .C(C), .ld(1'b1), .D(R0));
  RAMDualPort #(.AddrBits(24), .Bits(8)) u_R1 (.A(multiplexer_2_out), .Din(R1_d), .str(R1_e), .C(C), .ld(1'b1), .D(R1));
  RAMDualPort #(.AddrBits(24), .Bits(8)) u_R2 (.A(multiplexer_3_out), .Din(R2_d), .str(R2_e), .C(C), .ld(1'b1), .D(R2));
  RAMDualPort #(.AddrBits(24), .Bits(8)) u_R3 (.A(_1A[25:2]), .Din(R3_d), .str(R3_e), .C(C), .ld(1'b1), .D(R3));
  Multiplexer #(.Selector_Bits(2), .Bits(32)) multiplexer_4 (
    .sel(_1A[1:0]), .in_0(D_in), .in_1({D_in[23:0], D_in[31:24]}), .in_2({D_in[15:0], D_in[31:16]}),
    .in_3({D_in[7:0], D_in[31:8]}), .out({R3_d, R2_d, R1_d, R0_d}));
  Multiplexer #(.Selector_Bits(2), .Bits(4)) multiplexer_5 (
    .sel(_1A[1:0]), .in_0(and_2_out), .in_1({and_2_out[2:0], and_2_out[3]}),
    .in_2({and_2_out[1:0], and_2_out[3:2]}), .in_3({and_2_out[0], and_2_out[3:1]}),
    .out({R3_e, R2_e, R1_e, R0_e}));
  RAMDualPort #(.AddrBits(24), .Bits(8)) u_R4 (.A(multiplexer_1_out), .Din(R0_d), .str(R0_e), .C(C), .ld(1'b1), .D(R4));
  RAMDualPort #(.AddrBits(24), .Bits(8)) u_R5 (.A(multiplexer_2_out), .Din(R1_d), .str(R1_e), .C(C), .ld(1'b1), .D(R5));
  RAMDualPort #(.AddrBits(24), .Bits(8)) u_R6 (.A(multiplexer_3_out), .Din(R2_d), .str(R2_e), .C(C), .ld(1'b1), .D(R6));
  RAMDualPort #(.AddrBits(24), .Bits(8)) u_R7 (.A(_1A[25:2]), .Din(R3_d), .str(R3_e), .C(C), .ld(1'b1), .D(R7));
  BitExtender #(.inputBits(1), .outputBits(8)) bitextender_2 (.in(1'b1), .out(bitextender_2_out));
  BitExtender #(.inputBits(1), .outputBits(8)) bitextender_3 (.in(mask[1]), .out(bitextender_3_out));
  BitExtender #(.inputBits(1), .outputBits(8)) bitextender_4 (.in(mask[3]), .out(bitextender_4_out));
  BitExtender #(.inputBits(1), .outputBits(8)) bitextender_5 (.in(mask[3]), .out(bitextender_5_out));
  Multiplexer #(.Selector_Bits(2), .Bits(32)) multiplexer_6 (
    .sel(_1A[1:0]), .in_0({R3, R2, R1, R0}), .in_1({R0, R3, R2, R1}), .in_2({R1, R0, R3, R2}),
    .in_3({R2, R1, R0, R3}), .out(multiplexer_6_out));
  Multiplexer #(.Selector_Bits(2), .Bits(32)) multiplexer_7 (
    .sel(_1A[1:0]), .in_0({R7, R6, R5, R4}), .in_1({R4, R7, R6, R5}), .in_2({R5, R4, R7, R6}),
    .in_3({R6, R5, R4, R7}), .out(multiplexer_7_out));
  assign and_3_out = {bitextender_5_out, bitextender_4_out, bitextender_3_out, bitextender_2_out} & multiplexer_6_out;  // And and_3, 32 bits wide
  assign D1 = ld1 ? and_3_out : 32'bz;  // Driver driver_1
  assign D2 = ld2 ? multiplexer_7_out : 32'bz;  // Driver driver_2

  // Other names for the same wires on the sheet: mask[2] = mask[3]; A_0 = _1A[0]; A_01[1:0] = _1A[1:0]; A_1 = _1A[1];
  //   addr[23:0] = _1A[25:2]; _1D_in[31:0] = D_in; E = str; md[1:0] = mode
endmodule
