// Digital circuit regFile4.dig as structural Verilog
module regFile4 (
  input  C,
  input  [31:0] FL_i,
  input  FL_sel,
  input  [3:0] FL_e,
  input  [2:0] MW1,
  input  [4:0] RW1,
  input  [4:0] RA,
  input  [4:0] RB,
  input  [2:0] MA,
  input  [2:0] MB,
  input  E1,
  input  [31:0] D1,
  input  [31:0] PCS_i,
  input  PCS_e,
  input  SCA_sel,
  input  SCS_e,
  input  [31:0] SCS_i,
  input  [31:0] D2,
  input  [2:0] MW2,
  input  [4:0] RW2,
  input  [31:0] PCA_i,
  input  PCA_e,
  input  SCA_e,
  input  [31:0] SCA_i,
  input  E2,
  input  [31:0] PC_read,
  input  SC_sel,
  output [31:0] R_A,
  output [31:0] R_B,
  output [31:0] PCS_O,
  output [31:0] FL_O,
  output [31:0] SCS_O,
  output [31:0] PCA_O,
  output [31:0] SCA_O
);

  wire a_mux_a1, a_mux_a2, a_mux_c2, a_mux_d1, a_mux_d2, and_1_out, and_2_out, and_3_out, and_12_out,
       and_13_out, and_14_out, and_15_out, b_mux_a1, b_mux_a2, b_mux_c2, b_mux_d1, b_mux_d2, comparator_1_eq,
       comparator_2_eq, comparator_3_eq, comparator_4_eq, multiplexer_13_out, multiplexer_14_out, nand_1_out,
       nand_2_out, nand_3_out, nand_4_out, nor_3_out, nor_4_out, xor_1_out, xor_2_out;
  wire [3:0] bitextender_1_out, bitextender_2_out, bitextender_3_out, bitextender_4_out, FL_e_t, FLM, GR1_e,
       GR2_e, multiplexer_4_out, multiplexer_5_out, multiplexer_6_out, or_1_out, or_3_out, R1_e, R2_e, R3_e,
       R4_e, R5_e, R6_e, R7_e, R8_e, R9_e, R10_e, R11_e, R12_e, R13_e, R14_e, R15_e, R16_e, R17_e, R18_e,
       R19_e, R20_e, R21_e, R22_e, R23_e, R24_e, R25_e, RM1, RM2, RM3, RM4, RM5, RM6, RM7, RM8, RM9, RM10,
       RM11, RM12, RM13, RM14, RM15, RM16, RM17, RM18, RM19, RM20, RM21, RM22, RM23, RM24, RM25, SBP_e, SBPM,
       SCA_e_t, SCAM;
  wire [6:6] FL_d_o;
  wire [7:0] and_16_out, and_17_out, and_18_out, and_19_out, and_20_out, and_21_out, bitextender_5_out,
       bitextender_6_out, bitextender_7_out, bitextender_8_out, bitextender_9_out, bitextender_10_out,
       bitextender_11_out, bitextender_12_out, multiplexer_7_out, multiplexer_8_out, multiplexer_9_out,
       multiplexer_10_out;
  wire [29:26] demultiplexer_6_out_26, demultiplexer_7_out_26, demultiplexer_8_out_26,
       demultiplexer_9_out_26, or_11_out, or_12_out, or_13_out, or_14_out;
  wire [31:0] demultiplexer_2_out_0, demultiplexer_3_out_0, demultiplexer_4_out_0, demultiplexer_5_out_0,
       multiplexer_1_out, multiplexer_2_out, multiplexer_3_out, mux8x4_1_d_o, mux8x4_2_d_o, R1, R2, R3, R4,
       R5, R6, R7, R8, R9, R10, R11, R12, R13, R14, R15, R16, R17, R18, R19, R20, R21, R22, R23, R24, R25,
       R_A_t, R_B_t, SBP;
  wire [31:8] R1_i, R2_i;

  Comparator #(.Bits(5)) comparator_1 (.a(5'b11110), .b(RW1), .eq(comparator_1_eq));  // open: gt, lt
  Comparator #(.Bits(5)) comparator_2 (.a(5'b11110), .b(RW2), .eq(comparator_2_eq));  // open: gt, lt
  mux8x4 mux8x4_1 (.D_o(mux8x4_1_d_o), .D1({R1_i, D1[7:0]}), .D2({R2_i, D2[7:0]}), .S(SCAM));
  nand nand_1 (nand_1_out, E1, comparator_1_eq);
  nand nand_2 (nand_2_out, E2, comparator_2_eq);
  mux8x4 mux8x4_2 (.D_o(mux8x4_2_d_o), .D1({R1_i, D1[7:0]}), .D2({R2_i, D2[7:0]}), .S(FLM));
  reg8x4M u_R1 (.C(C), .D1({R1_i, D1[7:0]}), .D2({R2_i, D2[7:0]}), .S(RM1), .E(R1_e), .D_o(R1));
  reg8x4M u_R5 (.C(C), .D1({R1_i, D1[7:0]}), .D2({R2_i, D2[7:0]}), .S(RM5), .E(R5_e), .D_o(R5));
  reg8x4M u_R9 (.C(C), .D1({R1_i, D1[7:0]}), .D2({R2_i, D2[7:0]}), .S(RM9), .E(R9_e), .D_o(R9));
  reg8x4M u_R13 (.C(C), .D1({R1_i, D1[7:0]}), .D2({R2_i, D2[7:0]}), .S(RM13), .E(R13_e), .D_o(R13));
  reg8x4M u_R17 (.C(C), .D1({R1_i, D1[7:0]}), .D2({R2_i, D2[7:0]}), .S(RM17), .E(R17_e), .D_o(R17));
  reg8x4M u_R21 (.C(C), .D1({R1_i, D1[7:0]}), .D2({R2_i, D2[7:0]}), .S(RM21), .E(R21_e), .D_o(R21));
  reg8x4M u_R25 (.C(C), .D1({R1_i, D1[7:0]}), .D2({R2_i, D2[7:0]}), .S(RM25), .E(R25_e), .D_o(R25));
  reg8x4M R26 (.C(C), .D1({R1_i, D1[7:0]}), .D2({R2_i, D2[7:0]}), .S(SBPM), .E(SBP_e), .D_o(SBP));
  Comparator #(.Bits(5)) comparator_3 (.a({5{1'b1}}), .b(RW1), .eq(comparator_3_eq));  // open: gt, lt
  Comparator #(.Bits(5)) comparator_4 (.a({5{1'b1}}), .b(RW2), .eq(comparator_4_eq));  // open: gt, lt
  and and_1 (and_1_out, SCA_sel, nand_2_out, nand_1_out);
  and and_2 (and_2_out, SC_sel, nand_2_out, nand_1_out);
  nand nand_3 (nand_3_out, E1, comparator_3_eq);
  nand nand_4 (nand_4_out, E2, comparator_4_eq);
  Multiplexer #(.Bits(32)) multiplexer_1 (.sel(and_1_out), .in_0(mux8x4_1_d_o), .in_1(SCA_i), .out(multiplexer_1_out));
  BitExtender #(.inputBits(1), .outputBits(4)) bitextender_1 (.in(SCA_e), .out(bitextender_1_out));
  Multiplexer #(.Bits(32)) multiplexer_2 (.sel(and_2_out), .in_0(mux8x4_1_d_o), .in_1(SCS_i), .out(multiplexer_2_out));
  BitExtender #(.inputBits(1), .outputBits(4)) bitextender_2 (.in(SCS_e), .out(bitextender_2_out));
  Multiplexer #(.Bits(32)) multiplexer_3 (.sel(and_3_out), .in_0(mux8x4_2_d_o), .in_1(FL_i), .out(multiplexer_3_out));
  and and_3 (and_3_out, nand_3_out, nand_4_out, FL_sel);
  reg8x4M u_R2 (.C(C), .D1({R1_i, D1[7:0]}), .D2({R2_i, D2[7:0]}), .S(RM2), .E(R2_e), .D_o(R2));
  reg8x4M u_R6 (.C(C), .D1({R1_i, D1[7:0]}), .D2({R2_i, D2[7:0]}), .S(RM6), .E(R6_e), .D_o(R6));
  reg8x4M u_R10 (.C(C), .D1({R1_i, D1[7:0]}), .D2({R2_i, D2[7:0]}), .S(RM10), .E(R10_e), .D_o(R10));
  reg8x4M u_R14 (.C(C), .D1({R1_i, D1[7:0]}), .D2({R2_i, D2[7:0]}), .S(RM14), .E(R14_e), .D_o(R14));
  reg8x4M u_R18 (.C(C), .D1({R1_i, D1[7:0]}), .D2({R2_i, D2[7:0]}), .S(RM18), .E(R18_e), .D_o(R18));
  reg8x4M u_R22 (.C(C), .D1({R1_i, D1[7:0]}), .D2({R2_i, D2[7:0]}), .S(RM22), .E(R22_e), .D_o(R22));
  BitExtender #(.inputBits(1), .outputBits(4)) bitextender_3 (.in(PCS_e), .out(bitextender_3_out));
  BitExtender #(.inputBits(1), .outputBits(4)) bitextender_4 (.in(PCA_e), .out(bitextender_4_out));
  Multiplexer #(.Bits(4)) multiplexer_4 (
    .sel(SCA_sel), .in_0(SCA_e_t), .in_1(bitextender_1_out), .out(multiplexer_4_out));
  Multiplexer #(.Bits(4)) multiplexer_5 (
    .sel(SC_sel), .in_0(SCA_e_t), .in_1(bitextender_2_out), .out(multiplexer_5_out));
  Multiplexer #(.Bits(4)) multiplexer_6 (.sel(and_3_out), .in_0(FL_e_t), .in_1(FL_e), .out(multiplexer_6_out));
  reg8x4 PC (.C(C), .D(PCS_i), .E(bitextender_3_out), .D_o(PCS_O));
  reg8x4 PC_2 (.C(C), .D(PCA_i), .E(bitextender_4_out), .D_o(PCA_O));
  reg8x4 SC (.C(C), .D(multiplexer_1_out), .E(multiplexer_4_out), .D_o(SCA_O));
  reg8x4 SC_2 (.C(C), .D(multiplexer_2_out), .E(multiplexer_5_out), .D_o(SCS_O));
  reg8x4 FL (.C(C), .D(multiplexer_3_out), .E(multiplexer_6_out), .D_o({FL_O[31:7], FL_d_o[6], FL_O[5:0]}));
  reg8x4M u_R3 (.C(C), .D1({R1_i, D1[7:0]}), .D2({R2_i, D2[7:0]}), .S(RM3), .E(R3_e), .D_o(R3));
  reg8x4M u_R7 (.C(C), .D1({R1_i, D1[7:0]}), .D2({R2_i, D2[7:0]}), .S(RM7), .E(R7_e), .D_o(R7));
  reg8x4M u_R11 (.C(C), .D1({R1_i, D1[7:0]}), .D2({R2_i, D2[7:0]}), .S(RM11), .E(R11_e), .D_o(R11));
  reg8x4M u_R15 (.C(C), .D1({R1_i, D1[7:0]}), .D2({R2_i, D2[7:0]}), .S(RM15), .E(R15_e), .D_o(R15));
  reg8x4M u_R19 (.C(C), .D1({R1_i, D1[7:0]}), .D2({R2_i, D2[7:0]}), .S(RM19), .E(R19_e), .D_o(R19));
  reg8x4M u_R23 (.C(C), .D1({R1_i, D1[7:0]}), .D2({R2_i, D2[7:0]}), .S(RM23), .E(R23_e), .D_o(R23));
  reg8x4M u_R4 (.C(C), .D1({R1_i, D1[7:0]}), .D2({R2_i, D2[7:0]}), .S(RM4), .E(R4_e), .D_o(R4));
  reg8x4M u_R8 (.C(C), .D1({R1_i, D1[7:0]}), .D2({R2_i, D2[7:0]}), .S(RM8), .E(R8_e), .D_o(R8));
  reg8x4M u_R12 (.C(C), .D1({R1_i, D1[7:0]}), .D2({R2_i, D2[7:0]}), .S(RM12), .E(R12_e), .D_o(R12));
  reg8x4M u_R16 (.C(C), .D1({R1_i, D1[7:0]}), .D2({R2_i, D2[7:0]}), .S(RM16), .E(R16_e), .D_o(R16));
  reg8x4M u_R20 (.C(C), .D1({R1_i, D1[7:0]}), .D2({R2_i, D2[7:0]}), .S(RM20), .E(R20_e), .D_o(R20));
  reg8x4M u_R24 (.C(C), .D1({R1_i, D1[7:0]}), .D2({R2_i, D2[7:0]}), .S(RM24), .E(R24_e), .D_o(R24));
  and and_4 (a_mux_c2, MA[2], MA[1]);
  nor nor_1 (a_mux_d1, MA[2], MA[1], MA[0]);
  and and_5 (b_mux_c2, MB[2], MB[1]);
  nor nor_2 (b_mux_d1, MB[2], MB[1], MB[0]);
  nor nor_3 (nor_3_out, MW1[2], MW1[1], MW1[0]);
  nor nor_4 (nor_4_out, MW2[2], MW2[1], MW2[0]);
  and and_6 (a_mux_a1, MA[1], MA[0]);
  and and_7 (a_mux_a2, MA[2], ~MA[1], ~MA[0]);  // And
  not not_1 (a_mux_d2, MA[1]);
  and and_8 (b_mux_a1, MB[1], MB[0]);
  and and_9 (b_mux_a2, MB[2], ~MB[1], ~MB[0]);  // And
  not not_2 (b_mux_d2, MB[1]);
  xor xor_1 (xor_1_out, MW1[0], MW1[1]);
  xor xor_2 (xor_2_out, MW2[0], MW2[1]);
  nor nor_5 (or_1_out[3], MW1[1], MW1[0]);
  or or_1 (or_1_out[1], nor_3_out, MW1[0]);
  or or_2 (or_1_out[0], xor_1_out, nor_3_out);
  nor nor_6 (or_3_out[3], MW2[1], MW2[0]);
  or or_3 (or_3_out[1], nor_4_out, MW2[0]);
  or or_4 (or_3_out[0], xor_2_out, nor_4_out);
  // Probe R1 on R1
  // Probe R2 on R2
  // Probe R3 on R3
  // Probe R4 on R4
  // Probe R5 on R5
  // Probe R6 on R6
  // Probe R7 on R7
  // Probe R8 on R8
  // Probe R9 on R9
  // Probe R10 on R10
  // Probe R11 on R11
  // Probe R12 on R12
  // Probe R13 on R13
  // Probe R14 on R14
  // Probe R15 on R15
  // Probe R16 on R16
  // Probe R17 on R17
  // Probe R18 on R18
  // Probe R19 on R19
  // Probe R20 on R20
  // Probe R21 on R21
  // Probe R22 on R22
  // Probe R23 on R23
  // Probe R24 on R24
  // Probe R25 on R25
  // Probe R26 on SBP
  // Probe R27 on {32{1'b0}}
  // Probe R28 on 32'h1
  // Probe R29 on {32{1'b1}}
  // Probe R30 on PC_read
  // Probe R31 on SCS_O
  // Probe R32 on {FL_O[31:7], 1'b1, FL_O[5:0]}
  Multiplexer #(.Bits(8)) multiplexer_7 (
    .sel(a_mux_a2), .in_0(R_A_t[15:8]), .in_1(R_A_t[31:24]), .out(multiplexer_7_out));
  Multiplexer #(.Bits(8)) multiplexer_8 (
    .sel(a_mux_a1), .in_0(R_A_t[7:0]), .in_1(R_A_t[15:8]), .out(multiplexer_8_out));
  Multiplexer #(.Bits(8)) multiplexer_9 (
    .sel(b_mux_a2), .in_0(R_B_t[15:8]), .in_1(R_B_t[31:24]), .out(multiplexer_9_out));
  Multiplexer #(.Bits(8)) multiplexer_10 (
    .sel(b_mux_a1), .in_0(R_B_t[7:0]), .in_1(R_B_t[15:8]), .out(multiplexer_10_out));
  assign GR1_e = {{2{or_1_out[3]}}, or_1_out[1:0]} & {4{E1}};  // And and_10, 4 bits wide
  assign GR2_e = {{2{or_3_out[3]}}, or_3_out[1:0]} & {4{E2}};  // And and_11, 4 bits wide
  Multiplexer #(.Bits(8)) multiplexer_11 (
    .sel(a_mux_a2), .in_0(multiplexer_8_out), .in_1(R_A_t[23:16]), .out(R_A[7:0]));
  Multiplexer #(.Bits(8)) multiplexer_12 (
    .sel(b_mux_a2), .in_0(multiplexer_10_out), .in_1(R_B_t[23:16]), .out(R_B[7:0]));
  BitExtender #(.inputBits(1), .outputBits(8)) bitextender_5 (.in(a_mux_d1), .out(bitextender_5_out));
  and and_12 (and_12_out, MA[2], multiplexer_13_out);
  Multiplexer multiplexer_13 (.sel(MA[1]), .in_0(multiplexer_7_out[7]), .in_1(R_A[7]), .out(multiplexer_13_out));
  and and_13 (and_13_out, R_A[7], a_mux_c2);
  BitExtender #(.inputBits(1), .outputBits(8)) bitextender_6 (.in(b_mux_d1), .out(bitextender_6_out));
  and and_14 (and_14_out, MB[2], multiplexer_14_out);
  Multiplexer multiplexer_14 (.sel(MB[1]), .in_0(multiplexer_9_out[7]), .in_1(R_B[7]), .out(multiplexer_14_out));
  and and_15 (and_15_out, R_B[7], b_mux_c2);
  Multiplexer #(.Selector_Bits(5), .Bits(32)) multiplexer_15 (
    .sel(RA), .in_0(R1), .in_1(R2), .in_2(R3), .in_3(R4), .in_4(R5), .in_5(R6), .in_6(R7), .in_7(R8),
    .in_8(R9), .in_9(R10), .in_10(R11), .in_11(R12), .in_12(R13), .in_13(R14), .in_14(R15), .in_15(R16),
    .in_16(R17), .in_17(R18), .in_18(R19), .in_19(R20), .in_20(R21), .in_21(R22), .in_22(R23), .in_23(R24),
    .in_24(R25), .in_25(SBP), .in_26({32{1'b0}}), .in_27(32'h1), .in_28({32{1'b1}}), .in_29(PC_read),
    .in_30(SCS_O), .in_31({FL_O[31:7], 1'b1, FL_O[5:0]}), .out(R_A_t));
  assign and_16_out = bitextender_5_out & R_A_t[31:24];  // And and_16, 8 bits wide
  assign and_17_out = bitextender_5_out & R_A_t[23:16];  // And and_17, 8 bits wide
  BitExtender #(.inputBits(1), .outputBits(8)) bitextender_7 (.in(a_mux_d2), .out(bitextender_7_out));
  assign and_18_out = bitextender_6_out & R_B_t[31:24];  // And and_18, 8 bits wide
  assign and_19_out = bitextender_6_out & R_B_t[23:16];  // And and_19, 8 bits wide
  BitExtender #(.inputBits(1), .outputBits(8)) bitextender_8 (.in(b_mux_d2), .out(bitextender_8_out));
  Multiplexer #(.Bits(8)) multiplexer_16 (.sel(MW1[2]), .in_0(D1[31:24]), .in_1(D1[15:8]), .out(R1_i[31:24]));
  Multiplexer #(.Bits(8)) multiplexer_17 (.sel(MW1[2]), .in_0(D1[23:16]), .in_1(D1[7:0]), .out(R1_i[23:16]));
  Multiplexer #(.Bits(8)) multiplexer_18 (.sel(MW1[1]), .in_0(D1[15:8]), .in_1(D1[7:0]), .out(R1_i[15:8]));
  Multiplexer #(.Bits(8)) multiplexer_19 (.sel(MW2[2]), .in_0(D2[31:24]), .in_1(D2[15:8]), .out(R2_i[31:24]));
  Multiplexer #(.Bits(8)) multiplexer_20 (.sel(MW2[2]), .in_0(D2[23:16]), .in_1(D2[7:0]), .out(R2_i[23:16]));
  Multiplexer #(.Bits(8)) multiplexer_21 (.sel(MW2[1]), .in_0(D2[15:8]), .in_1(D2[7:0]), .out(R2_i[15:8]));
  BitExtender #(.inputBits(1), .outputBits(8)) bitextender_9 (.in(and_12_out), .out(bitextender_9_out));
  assign and_20_out = bitextender_7_out & multiplexer_7_out;  // And and_20, 8 bits wide
  BitExtender #(.inputBits(1), .outputBits(8)) bitextender_10 (.in(and_13_out), .out(bitextender_10_out));
  BitExtender #(.inputBits(1), .outputBits(8)) bitextender_11 (.in(and_14_out), .out(bitextender_11_out));
  assign and_21_out = bitextender_8_out & multiplexer_9_out;  // And and_21, 8 bits wide
  BitExtender #(.inputBits(1), .outputBits(8)) bitextender_12 (.in(and_15_out), .out(bitextender_12_out));
  Multiplexer #(.Selector_Bits(5), .Bits(32)) multiplexer_22 (
    .sel(RB), .in_0(R1), .in_1(R2), .in_2(R3), .in_3(R4), .in_4(R5), .in_5(R6), .in_6(R7), .in_7(R8),
    .in_8(R9), .in_9(R10), .in_10(R11), .in_11(R12), .in_12(R13), .in_13(R14), .in_14(R15), .in_15(R16),
    .in_16(R17), .in_17(R18), .in_18(R19), .in_19(R20), .in_20(R21), .in_21(R22), .in_22(R23), .in_23(R24),
    .in_24(R25), .in_25(SBP), .in_26({32{1'b0}}), .in_27(32'h1), .in_28({32{1'b1}}), .in_29(PC_read),
    .in_30(SCS_O), .in_31({FL_O[31:7], 1'b1, FL_O[5:0]}), .out(R_B_t));
  assign R_A[31:24] = and_16_out | bitextender_9_out;  // Or or_5, 8 bits wide
  assign R_A[23:16] = and_17_out | bitextender_9_out;  // Or or_6, 8 bits wide
  assign R_A[15:8] = and_20_out | bitextender_10_out;  // Or or_7, 8 bits wide
  assign R_B[31:24] = and_18_out | bitextender_11_out;  // Or or_8, 8 bits wide
  assign R_B[23:16] = and_19_out | bitextender_11_out;  // Or or_9, 8 bits wide
  assign R_B[15:8] = and_21_out | bitextender_12_out;  // Or or_10, 8 bits wide
  Demultiplexer #(.Selector_Bits(5)) demultiplexer_1 (
    .sel(RW2), .in(E2));  // open: out_0, out_1, out_2, out_3, out_4, out_5, out_6, out_7, out_8, out_9, out_10, out_11, out_12, out_13, out_14, out_15, out_16, out_17, out_18, out_19, out_20, out_21, out_22, out_23, out_24, out_25, out_26, out_27, out_28, out_29, out_30, out_31
  Demultiplexer #(.Selector_Bits(5)) demultiplexer_2 (
    .sel(RW1), .in(GR1_e[0]), .out_0(demultiplexer_2_out_0[0]), .out_1(demultiplexer_2_out_0[1]),
    .out_2(demultiplexer_2_out_0[2]), .out_3(demultiplexer_2_out_0[3]), .out_4(demultiplexer_2_out_0[4]),
    .out_5(demultiplexer_2_out_0[5]), .out_6(demultiplexer_2_out_0[6]), .out_7(demultiplexer_2_out_0[7]),
    .out_8(demultiplexer_2_out_0[8]), .out_9(demultiplexer_2_out_0[9]), .out_10(demultiplexer_2_out_0[10]),
    .out_11(demultiplexer_2_out_0[11]), .out_12(demultiplexer_2_out_0[12]),
    .out_13(demultiplexer_2_out_0[13]), .out_14(demultiplexer_2_out_0[14]),
    .out_15(demultiplexer_2_out_0[15]), .out_16(demultiplexer_2_out_0[16]),
    .out_17(demultiplexer_2_out_0[17]), .out_18(demultiplexer_2_out_0[18]),
    .out_19(demultiplexer_2_out_0[19]), .out_20(demultiplexer_2_out_0[20]),
    .out_21(demultiplexer_2_out_0[21]), .out_22(demultiplexer_2_out_0[22]),
    .out_23(demultiplexer_2_out_0[23]), .out_24(demultiplexer_2_out_0[24]),
    .out_25(demultiplexer_2_out_0[25]), .out_26(demultiplexer_2_out_0[26]),
    .out_27(demultiplexer_2_out_0[27]), .out_28(demultiplexer_2_out_0[28]),
    .out_29(demultiplexer_2_out_0[29]), .out_30(demultiplexer_2_out_0[30]), .out_31(demultiplexer_2_out_0[31]));
  Demultiplexer #(.Selector_Bits(5)) demultiplexer_3 (
    .sel(RW1), .in(GR1_e[1]), .out_0(demultiplexer_3_out_0[0]), .out_1(demultiplexer_3_out_0[1]),
    .out_2(demultiplexer_3_out_0[2]), .out_3(demultiplexer_3_out_0[3]), .out_4(demultiplexer_3_out_0[4]),
    .out_5(demultiplexer_3_out_0[5]), .out_6(demultiplexer_3_out_0[6]), .out_7(demultiplexer_3_out_0[7]),
    .out_8(demultiplexer_3_out_0[8]), .out_9(demultiplexer_3_out_0[9]), .out_10(demultiplexer_3_out_0[10]),
    .out_11(demultiplexer_3_out_0[11]), .out_12(demultiplexer_3_out_0[12]),
    .out_13(demultiplexer_3_out_0[13]), .out_14(demultiplexer_3_out_0[14]),
    .out_15(demultiplexer_3_out_0[15]), .out_16(demultiplexer_3_out_0[16]),
    .out_17(demultiplexer_3_out_0[17]), .out_18(demultiplexer_3_out_0[18]),
    .out_19(demultiplexer_3_out_0[19]), .out_20(demultiplexer_3_out_0[20]),
    .out_21(demultiplexer_3_out_0[21]), .out_22(demultiplexer_3_out_0[22]),
    .out_23(demultiplexer_3_out_0[23]), .out_24(demultiplexer_3_out_0[24]),
    .out_25(demultiplexer_3_out_0[25]), .out_26(demultiplexer_3_out_0[26]),
    .out_27(demultiplexer_3_out_0[27]), .out_28(demultiplexer_3_out_0[28]),
    .out_29(demultiplexer_3_out_0[29]), .out_30(demultiplexer_3_out_0[30]), .out_31(demultiplexer_3_out_0[31]));
  Demultiplexer #(.Selector_Bits(5)) demultiplexer_4 (
    .sel(RW1), .in(GR1_e[2]), .out_0(demultiplexer_4_out_0[0]), .out_1(demultiplexer_4_out_0[1]),
    .out_2(demultiplexer_4_out_0[2]), .out_3(demultiplexer_4_out_0[3]), .out_4(demultiplexer_4_out_0[4]),
    .out_5(demultiplexer_4_out_0[5]), .out_6(demultiplexer_4_out_0[6]), .out_7(demultiplexer_4_out_0[7]),
    .out_8(demultiplexer_4_out_0[8]), .out_9(demultiplexer_4_out_0[9]), .out_10(demultiplexer_4_out_0[10]),
    .out_11(demultiplexer_4_out_0[11]), .out_12(demultiplexer_4_out_0[12]),
    .out_13(demultiplexer_4_out_0[13]), .out_14(demultiplexer_4_out_0[14]),
    .out_15(demultiplexer_4_out_0[15]), .out_16(demultiplexer_4_out_0[16]),
    .out_17(demultiplexer_4_out_0[17]), .out_18(demultiplexer_4_out_0[18]),
    .out_19(demultiplexer_4_out_0[19]), .out_20(demultiplexer_4_out_0[20]),
    .out_21(demultiplexer_4_out_0[21]), .out_22(demultiplexer_4_out_0[22]),
    .out_23(demultiplexer_4_out_0[23]), .out_24(demultiplexer_4_out_0[24]),
    .out_25(demultiplexer_4_out_0[25]), .out_26(demultiplexer_4_out_0[26]),
    .out_27(demultiplexer_4_out_0[27]), .out_28(demultiplexer_4_out_0[28]),
    .out_29(demultiplexer_4_out_0[29]), .out_30(demultiplexer_4_out_0[30]), .out_31(demultiplexer_4_out_0[31]));
  Demultiplexer #(.Selector_Bits(5)) demultiplexer_5 (
    .sel(RW1), .in(GR1_e[3]), .out_0(demultiplexer_5_out_0[0]), .out_1(demultiplexer_5_out_0[1]),
    .out_2(demultiplexer_5_out_0[2]), .out_3(demultiplexer_5_out_0[3]), .out_4(demultiplexer_5_out_0[4]),
    .out_5(demultiplexer_5_out_0[5]), .out_6(demultiplexer_5_out_0[6]), .out_7(demultiplexer_5_out_0[7]),
    .out_8(demultiplexer_5_out_0[8]), .out_9(demultiplexer_5_out_0[9]), .out_10(demultiplexer_5_out_0[10]),
    .out_11(demultiplexer_5_out_0[11]), .out_12(demultiplexer_5_out_0[12]),
    .out_13(demultiplexer_5_out_0[13]), .out_14(demultiplexer_5_out_0[14]),
    .out_15(demultiplexer_5_out_0[15]), .out_16(demultiplexer_5_out_0[16]),
    .out_17(demultiplexer_5_out_0[17]), .out_18(demultiplexer_5_out_0[18]),
    .out_19(demultiplexer_5_out_0[19]), .out_20(demultiplexer_5_out_0[20]),
    .out_21(demultiplexer_5_out_0[21]), .out_22(demultiplexer_5_out_0[22]),
    .out_23(demultiplexer_5_out_0[23]), .out_24(demultiplexer_5_out_0[24]),
    .out_25(demultiplexer_5_out_0[25]), .out_26(demultiplexer_5_out_0[26]),
    .out_27(demultiplexer_5_out_0[27]), .out_28(demultiplexer_5_out_0[28]),
    .out_29(demultiplexer_5_out_0[29]), .out_30(demultiplexer_5_out_0[30]), .out_31(demultiplexer_5_out_0[31]));
  Demultiplexer #(.Selector_Bits(5)) demultiplexer_6 (
    .sel(RW2), .in(GR2_e[0]), .out_0(RM1[0]), .out_1(RM2[0]), .out_2(RM3[0]), .out_3(RM4[0]), .out_4(RM5[0]),
    .out_5(RM6[0]), .out_6(RM7[0]), .out_7(RM8[0]), .out_8(RM9[0]), .out_9(RM10[0]), .out_10(RM11[0]),
    .out_11(RM12[0]), .out_12(RM13[0]), .out_13(RM14[0]), .out_14(RM15[0]), .out_15(RM16[0]),
    .out_16(RM17[0]), .out_17(RM18[0]), .out_18(RM19[0]), .out_19(RM20[0]), .out_20(RM21[0]),
    .out_21(RM22[0]), .out_22(RM23[0]), .out_23(RM24[0]), .out_24(RM25[0]), .out_25(SBPM[0]),
    .out_26(demultiplexer_6_out_26[26]), .out_27(demultiplexer_6_out_26[27]),
    .out_28(demultiplexer_6_out_26[28]), .out_29(demultiplexer_6_out_26[29]), .out_30(SCAM[0]),
    .out_31(FLM[0]));
  Demultiplexer #(.Selector_Bits(5)) demultiplexer_7 (
    .sel(RW2), .in(GR2_e[1]), .out_0(RM1[1]), .out_1(RM2[1]), .out_2(RM3[1]), .out_3(RM4[1]), .out_4(RM5[1]),
    .out_5(RM6[1]), .out_6(RM7[1]), .out_7(RM8[1]), .out_8(RM9[1]), .out_9(RM10[1]), .out_10(RM11[1]),
    .out_11(RM12[1]), .out_12(RM13[1]), .out_13(RM14[1]), .out_14(RM15[1]), .out_15(RM16[1]),
    .out_16(RM17[1]), .out_17(RM18[1]), .out_18(RM19[1]), .out_19(RM20[1]), .out_20(RM21[1]),
    .out_21(RM22[1]), .out_22(RM23[1]), .out_23(RM24[1]), .out_24(RM25[1]), .out_25(SBPM[1]),
    .out_26(demultiplexer_7_out_26[26]), .out_27(demultiplexer_7_out_26[27]),
    .out_28(demultiplexer_7_out_26[28]), .out_29(demultiplexer_7_out_26[29]), .out_30(SCAM[1]),
    .out_31(FLM[1]));
  Demultiplexer #(.Selector_Bits(5)) demultiplexer_8 (
    .sel(RW2), .in(GR2_e[2]), .out_0(RM1[2]), .out_1(RM2[2]), .out_2(RM3[2]), .out_3(RM4[2]), .out_4(RM5[2]),
    .out_5(RM6[2]), .out_6(RM7[2]), .out_7(RM8[2]), .out_8(RM9[2]), .out_9(RM10[2]), .out_10(RM11[2]),
    .out_11(RM12[2]), .out_12(RM13[2]), .out_13(RM14[2]), .out_14(RM15[2]), .out_15(RM16[2]),
    .out_16(RM17[2]), .out_17(RM18[2]), .out_18(RM19[2]), .out_19(RM20[2]), .out_20(RM21[2]),
    .out_21(RM22[2]), .out_22(RM23[2]), .out_23(RM24[2]), .out_24(RM25[2]), .out_25(SBPM[2]),
    .out_26(demultiplexer_8_out_26[26]), .out_27(demultiplexer_8_out_26[27]),
    .out_28(demultiplexer_8_out_26[28]), .out_29(demultiplexer_8_out_26[29]), .out_30(SCAM[2]),
    .out_31(FLM[2]));
  Demultiplexer #(.Selector_Bits(5)) demultiplexer_9 (
    .sel(RW2), .in(GR2_e[3]), .out_0(RM1[3]), .out_1(RM2[3]), .out_2(RM3[3]), .out_3(RM4[3]), .out_4(RM5[3]),
    .out_5(RM6[3]), .out_6(RM7[3]), .out_7(RM8[3]), .out_8(RM9[3]), .out_9(RM10[3]), .out_10(RM11[3]),
    .out_11(RM12[3]), .out_12(RM13[3]), .out_13(RM14[3]), .out_14(RM15[3]), .out_15(RM16[3]),
    .out_16(RM17[3]), .out_17(RM18[3]), .out_18(RM19[3]), .out_19(RM20[3]), .out_20(RM21[3]),
    .out_21(RM22[3]), .out_22(RM23[3]), .out_23(RM24[3]), .out_24(RM25[3]), .out_25(SBPM[3]),
    .out_26(demultiplexer_9_out_26[26]), .out_27(demultiplexer_9_out_26[27]),
    .out_28(demultiplexer_9_out_26[28]), .out_29(demultiplexer_9_out_26[29]), .out_30(SCAM[3]),
    .out_31(FLM[3]));
  assign {FL_e_t[0], SCA_e_t[0], or_11_out, SBP_e[0], R25_e[0], R24_e[0], R23_e[0], R22_e[0], R21_e[0], R20_e[0], R19_e[0], R18_e[0], R17_e[0], R16_e[0], R15_e[0], R14_e[0], R13_e[0], R12_e[0], R11_e[0], R10_e[0], R9_e[0], R8_e[0], R7_e[0], R6_e[0], R5_e[0], R4_e[0], R3_e[0], R2_e[0], R1_e[0]} = demultiplexer_2_out_0 | {FLM[0], SCAM[0], demultiplexer_6_out_26, SBPM[0], RM25[0], RM24[0], RM23[0], RM22[0], RM21[0], RM20[0], RM19[0], RM18[0], RM17[0], RM16[0], RM15[0], RM14[0], RM13[0], RM12[0], RM11[0], RM10[0], RM9[0], RM8[0], RM7[0], RM6[0], RM5[0], RM4[0], RM3[0], RM2[0], RM1[0]};  // Or or_11, 32 bits wide
  assign {FL_e_t[1], SCA_e_t[1], or_12_out, SBP_e[1], R25_e[1], R24_e[1], R23_e[1], R22_e[1], R21_e[1], R20_e[1], R19_e[1], R18_e[1], R17_e[1], R16_e[1], R15_e[1], R14_e[1], R13_e[1], R12_e[1], R11_e[1], R10_e[1], R9_e[1], R8_e[1], R7_e[1], R6_e[1], R5_e[1], R4_e[1], R3_e[1], R2_e[1], R1_e[1]} = demultiplexer_3_out_0 | {FLM[1], SCAM[1], demultiplexer_7_out_26, SBPM[1], RM25[1], RM24[1], RM23[1], RM22[1], RM21[1], RM20[1], RM19[1], RM18[1], RM17[1], RM16[1], RM15[1], RM14[1], RM13[1], RM12[1], RM11[1], RM10[1], RM9[1], RM8[1], RM7[1], RM6[1], RM5[1], RM4[1], RM3[1], RM2[1], RM1[1]};  // Or or_12, 32 bits wide
  assign {FL_e_t[2], SCA_e_t[2], or_13_out, SBP_e[2], R25_e[2], R24_e[2], R23_e[2], R22_e[2], R21_e[2], R20_e[2], R19_e[2], R18_e[2], R17_e[2], R16_e[2], R15_e[2], R14_e[2], R13_e[2], R12_e[2], R11_e[2], R10_e[2], R9_e[2], R8_e[2], R7_e[2], R6_e[2], R5_e[2], R4_e[2], R3_e[2], R2_e[2], R1_e[2]} = demultiplexer_4_out_0 | {FLM[2], SCAM[2], demultiplexer_8_out_26, SBPM[2], RM25[2], RM24[2], RM23[2], RM22[2], RM21[2], RM20[2], RM19[2], RM18[2], RM17[2], RM16[2], RM15[2], RM14[2], RM13[2], RM12[2], RM11[2], RM10[2], RM9[2], RM8[2], RM7[2], RM6[2], RM5[2], RM4[2], RM3[2], RM2[2], RM1[2]};  // Or or_13, 32 bits wide
  assign {FL_e_t[3], SCA_e_t[3], or_14_out, SBP_e[3], R25_e[3], R24_e[3], R23_e[3], R22_e[3], R21_e[3], R20_e[3], R19_e[3], R18_e[3], R17_e[3], R16_e[3], R15_e[3], R14_e[3], R13_e[3], R12_e[3], R11_e[3], R10_e[3], R9_e[3], R8_e[3], R7_e[3], R6_e[3], R5_e[3], R4_e[3], R3_e[3], R2_e[3], R1_e[3]} = demultiplexer_5_out_0 | {FLM[3], SCAM[3], demultiplexer_9_out_26, SBPM[3], RM25[3], RM24[3], RM23[3], RM22[3], RM21[3], RM20[3], RM19[3], RM18[3], RM17[3], RM16[3], RM15[3], RM14[3], RM13[3], RM12[3], RM11[3], RM10[3], RM9[3], RM8[3], RM7[3], RM6[3], RM5[3], RM4[3], RM3[3], RM2[3], RM1[3]};  // Or or_14, 32 bits wide

  assign FL_O[6] = 1'b1;

  // Other names for the same wires on the sheet: FL (some bits) = {FL_O[31:7], FL_O[5:0]}; D_A[31:0] = R_A;
  //   D_B[31:0] = R_B; A_mode[2:0] = MA; a_mux_b1 = MA[1]; a_mux_c1 = MA[2]; B_mode[2:0] = MB; b_mux_b1 = MB[1];
  //   b_mux_c1 = MB[2]; D1_I[31:0] = D1; R1_i[7:0] = D1[7:0]; D2_I[31:0] = D2; R2_i[7:0] = D2[7:0];
  //   FL_e__EX[3:0] = FL_e; PCA[31:0] = PCA_O; PCA_e__EX = PCA_e; PCS[31:0] = PCS_O; PCS_e__EX = PCS_e;
  //   RA_sel[4:0] = RA; RB_sel[4:0] = RB; RW1_sel[4:0] = RW1; RW2_sel[4:0] = RW2; SCA[31:0] = SCA_O;
  //   SCA_e__EX = SCA_e; SCS[31:0] = SCS_O; SCS_e__EX = SCS_e; SCS_sel = SC_sel; W1_mode[2:0] = MW1;
  //   w1_mux_3 = MW1[1]; w1_mux_1 = MW1[2]; w1_mux_2 = MW1[2]; W2_mode[2:0] = MW2; w2_mux_3 = MW2[1];
  //   w2_mux_1 = MW2[2]; w2_mux_2 = MW2[2]

  // Notes on the sheet:
  //   FL_i: data input for FL
  //   FL_sel: enable FL extern mode
  //   FL_e: FL register enable
  //   MW1: write mode:
  //   0: 32
  //   1: 16L
  //   2: 8L
  //   3: 8H
  //   4: 16H
  //   5: S16L (=16L)
  //   6: S8L (=8L)
  //   7: S8H (=8H)
  //   RW1: register to write:
  //   0~25: general
  //   26: zero
  //   27: one
  //   28: full
  //   29: program counter
  //   30: stack counter
  //   31: flag
  //   RA: register to read:
  //   0~25: general
  //   26: zero
  //   27: one
  //   28: full
  //   29: program counter
  //   30: stack counter
  //   31: flag
  //   RB: register to read:
  //   0~25: general
  //   26: zero
  //   27: one
  //   28: full
  //   29: program counter
  //   30: stack counter
  //   31: flag
  //   MA: read mode:
  //   0: 32
  //   1: 16L
  //   2: 8L
  //   3: 8H
  //   4: 16H
  //   5: S16L
  //   6: S8L
  //   7: S8H
  //   MB: read mode:
  //   0: 32
  //   1: 16L
  //   2: 8L
  //   3: 8H
  //   4: 16H
  //   5: S16L
  //   6: S8L
  //   7: S8H
  //   R_A: register out a
  //   R_B: register out b
  //   PCS_O: speculative PC out
  //   FL_O: FL out
  //   E1: enable
  //   D1: data in
  //   PCS_i: data input for speculative PC
  //   PCS_e: speculative PC register enable
  //   SCS_O: speculative SC out
  //   SCA_sel: enable architectual SC extern mode
  //   SCS_e: speculative SC register enable
  //   SCS_i: data input for speculative SC
  //   D2: data in
  //   MW2: write mode:
  //   0: 32
  //   1: 16L
  //   2: 8L
  //   3: 8H
  //   4: 16H
  //   5: S16L (=16L)
  //   6: S8L (=8L)
  //   7: S8H (=8H)
  //   RW2: register to write:
  //   0~25: general
  //   26: zero
  //   27: one
  //   28: full
  //   29: program counter
  //   30: stack counter
  //   31: flag
  //   PCA_i: data input for architectual PC
  //   PCA_e: architectual PC register enable
  //   PCA_O: architectual PC out
  //   SCA_e: speculative SC register enable
  //   SCA_i: data input for speculative SC
  //   E2: enable
  //   PC_read: cur instruction's PC value
  //   SCA_O: architectual SC out
  //   SC_sel: speculative SC extern mode
endmodule
