// Digital circuit store-buffer.dig as structural Verilog
module store_buffer (
  input  W_d,
  input  C,
  input  [31:0] D,
  input  [31:0] A,
  input  [3:0] inst,
  input  [3:0] com1_id,
  input  [3:0] com2_id,
  input  com1,
  input  com2,
  input  ld_ep,
  input  [3:0] ld_id,
  input  epoch,
  input  [31:0] ld_addr,
  input  W_id,
  input  [3:0] inst_W,
  input  LD,
  input  [1:0] MD,
  input  clr,
  input  [3:0] clr_id,
  input  clr_ep,
  output [31:0] D_O,
  output [31:0] A_O,
  output V,
  output full,
  output ld_V,
  output [31:0] ld_D,
  output [3:0] id_O,
  output ep_O,
  output [1:0] MD_O,
  output [3:0] SEL,
  output WD,
  output ERROR
);

  wire and_5_out, and_6_out, and_10_out, and_13_out, and_14_out, and_16_out, and_21_out, and_22_out,
       and_26_out, and_29_out, and_30_out, and_34_out, comparator_1_eq, comparator_2_eq, comparator_3_eq,
       comparator_4_eq, comparator_5_eq, comparator_6_eq, comparator_7_eq, comparator_8_eq, comparator_9_eq,
       comparator_10_eq, comparator_11_eq, comparator_12_eq, comparator_13_eq, comparator_14_eq,
       comparator_15_eq, comparator_16_eq, inst_comp_1_a_old, inst_comp_2_a_old, inst_comp_3_a_old,
       inst_comp_4_a_old, inst_comp_5_a_old, inst_comp_6_a_old, inst_comp_7_a_old, inst_comp_8_a_old, M1_CLR,
       M1_CMP, M1_COM, M1_DE, M1_epoch, M1_IE, M1_OLD, M1_RS, M1_VO, M2_CLR, M2_CMP, M2_COM, M2_DE, M2_epoch,
       M2_IE, M2_OLD, M2_RS, M2_VO, M3_CLR, M3_CMP, M3_COM, M3_DE, M3_epoch, M3_IE, M3_OLD, M3_RS, M3_VO,
       M4_CLR, M4_CMP, M4_COM, M4_DE, M4_epoch, M4_IE, M4_OLD, M4_RS, M4_VO, nor_1_out, or_2_out, or_4_out,
       or_5_out, or_6_out, or_8_out, or_10_out, or_11_out, or_13_out, priorityencoder_2_any, V_t;
  wire [1:0] empty_id, M1_MD, M2_MD, M3_MD, M4_MD, priorityencoder_1_num, sel_com;
  wire [3:0] and_1_out, and_7_out, and_17_out, and_23_out, and_31_out, bitextender_1_out, bitextender_2_out,
       bitextender_3_out, bitextender_4_out, bitextender_5_out, bitextender_6_out, bitextender_7_out,
       bitextender_8_out, bitextender_9_out, demultiplexer_2_out_0, M1_inst, M2_inst, M3_inst, M4_inst,
       not_1_out, not_3_out, or_3_out, or_7_out, or_9_out, or_12_out, rs_ff_3_q, rs_ff_9_q, rs_ff_15_q,
       rs_ff_21_q;
  wire [31:0] M1_A, M1_D, M2_A, M2_D, M3_A, M3_D, M4_A, M4_D;

  Multiplexer #(.Selector_Bits(2), .Bits(4)) multiplexer_1 (
    .sel(sel_com), .in_0(M1_inst), .in_1(M2_inst), .in_2(M3_inst), .in_3(M4_inst), .out(id_O));
  PriorityEncoder #(.Selector_Bits(2)) priorityencoder_1 (
    .in0(M1_CMP), .in1(M2_CMP), .in2(M3_CMP), .in3(M4_CMP), .num(priorityencoder_1_num), .any(ld_V));
  Multiplexer #(.Selector_Bits(2), .Bits(32)) multiplexer_2 (
    .sel(sel_com), .in_0(M1_D), .in_1(M2_D), .in_2(M3_D), .in_3(M4_D), .out(D_O));
  // Probe instM1 on M1_inst
  // Probe instM2 on M2_inst
  // Probe instM3 on M3_inst
  // Probe instM4 on M4_inst
  // Probe vM1 on M1_VO
  // Probe vM2 on M2_VO
  // Probe vM3 on M3_VO
  // Probe vM4 on M4_VO
  // Probe comM1 on M1_COM
  // Probe comM2 on M2_COM
  // Probe comM3 on M3_COM
  // Probe comM4 on M4_COM
  assign not_1_out = ~{M4_VO, M3_VO, M2_VO, M1_VO};  // Not not_1, 4 bits wide
  BitExtender #(.inputBits(1), .outputBits(4)) bitextender_1 (.in(W_d), .out(bitextender_1_out));
  assign and_1_out = ~{M4_CLR, M3_CLR, M2_CLR, M1_CLR} & {M4_OLD, M3_OLD, M2_OLD, M1_OLD} & {M4_COM, M3_COM, M2_COM, M1_COM};  // And and_1, 4 bits wide
  PriorityEncoder #(.Selector_Bits(2)) priorityencoder_2 (
    .in0(not_1_out[0]), .in1(not_1_out[1]), .in2(not_1_out[2]), .in3(not_1_out[3]), .num(empty_id),
    .any(priorityencoder_2_any));
  assign {M4_DE, M3_DE, M2_DE, M1_DE} = SEL & bitextender_1_out;  // And and_2, 4 bits wide
  nor nor_1 (nor_1_out, SEL[0], SEL[1], SEL[2], SEL[3]);
  and and_3 (ERROR, W_d, nor_1_out);
  Multiplexer #(.Selector_Bits(2)) multiplexer_3 (
    .sel(sel_com), .in_0(M1_epoch), .in_1(M2_epoch), .in_2(M3_epoch), .in_3(M4_epoch), .out(ep_O));
  Multiplexer #(.Selector_Bits(2), .Bits(32)) multiplexer_4 (
    .sel(priorityencoder_1_num), .in_0(M1_D), .in_1(M2_D), .in_2(M3_D), .in_3(M4_D), .out(ld_D));
  not not_2 (full, priorityencoder_2_any);
  Multiplexer #(.Selector_Bits(2), .Bits(32)) multiplexer_5 (
    .sel(sel_com), .in_0(M1_A), .in_1(M2_A), .in_2(M3_A), .in_3(M4_A), .out(A_O));
  PriorityEncoder #(.Selector_Bits(2)) priorityencoder_3 (
    .in0(and_1_out[0]), .in1(and_1_out[1]), .in2(and_1_out[2]), .in3(and_1_out[3]), .num(sel_com), .any(V));
  Demultiplexer #(.Selector_Bits(2)) demultiplexer_1 (
    .sel(empty_id), .in(W_id), .out_0(M1_IE), .out_1(M2_IE), .out_2(M3_IE), .out_3(M4_IE));
  Demultiplexer #(.Selector_Bits(2)) demultiplexer_2 (
    .sel(sel_com), .in(V_t), .out_0(demultiplexer_2_out_0[0]), .out_1(demultiplexer_2_out_0[1]),
    .out_2(demultiplexer_2_out_0[2]), .out_3(demultiplexer_2_out_0[3]));
  and and_4 (V_t, V, LD);
  Multiplexer #(.Selector_Bits(2), .Bits(2)) multiplexer_6 (
    .sel(sel_com), .in_0(M1_MD), .in_1(M2_MD), .in_2(M3_MD), .in_3(M4_MD), .out(MD_O));
  assign {M4_RS, M3_RS, M2_RS, M1_RS} = {M4_CLR, M3_CLR, M2_CLR, M1_CLR} | demultiplexer_2_out_0;  // Or or_1, 4 bits wide
  assign not_3_out = ~{M4_VO, M3_VO, M2_VO, M1_VO};  // Not not_3, 4 bits wide
  and and_5 (and_5_out, or_4_out, ~M1_RS);  // And
  BitExtender #(.inputBits(1), .outputBits(4)) bitextender_2 (.in(or_2_out), .out(bitextender_2_out));
  BitExtender #(.inputBits(1), .outputBits(4)) bitextender_3 (.in(M1_RS), .out(bitextender_3_out));
  RS_FF rs_ff_1 (.S(M1_IE), .C(C), .R(M1_RS), .Q(M1_VO));  // open: nQ
  or or_2 (or_2_out, M1_IE, M1_VO);
  Comparator #(.Bits(32)) comparator_1 (.a(ld_addr), .b(M1_A), .eq(comparator_1_eq));  // open: gt, lt
  Register #(.Bits(32)) register_1 (.D(A), .C(C), .en(M1_DE), .Q(M1_A));
  Register #(.Bits(32)) register_2 (.D(D), .C(C), .en(M1_DE), .Q(M1_D));
  Register #(.Bits(2)) register_3 (.D(MD), .C(C), .en(M1_DE), .Q(M1_MD));
  Comparator #(.Bits(4)) comparator_2 (.a(M1_inst), .b(inst_W), .eq(comparator_2_eq));  // open: gt, lt
  RS_FF rs_ff_2 (.S(and_5_out), .C(C), .R(M1_RS), .Q(M1_COM));  // open: nQ
  and and_6 (and_6_out, com2, M1_VO, comparator_4_eq);
  Comparator #(.Bits(4)) comparator_3 (.a(M1_inst), .b(com1_id), .eq(comparator_3_eq));  // open: gt, lt
  Comparator #(.Bits(4)) comparator_4 (.a(M1_inst), .b(com2_id), .eq(comparator_4_eq));  // open: gt, lt
  Register #(.Bits(4)) register_4 (.D(inst), .C(C), .en(M1_IE), .Q(M1_inst));
  Register register_5 (.D(epoch), .C(C), .en(M1_IE), .Q(M1_epoch));
  inst_comp inst_comp_1 (.A_id(ld_id), .A_ep(ld_ep), .B_id(M1_inst), .B_ep(M1_epoch), .A_old(inst_comp_1_a_old));
  inst_comp inst_comp_2 (.A_id(M1_inst), .A_ep(M1_epoch), .B_id(clr_id), .B_ep(clr_ep), .A_old(inst_comp_2_a_old));
  assign and_7_out = {M4_IE, M3_IE, M2_IE, M1_IE} & bitextender_2_out & ~bitextender_3_out;  // And and_7, 4 bits wide
  assign or_3_out = {not_3_out[3:1], 1'b0} | rs_ff_3_q;  // Or or_3, 4 bits wide
  RS_FF rs_ff_3 (.S(and_7_out[0]), .C(C), .R(bitextender_3_out[0]), .Q(rs_ff_3_q[0]));  // open: nQ
  RS_FF rs_ff_4 (.S(and_7_out[1]), .C(C), .R(bitextender_3_out[1]), .Q(rs_ff_3_q[1]));  // open: nQ
  RS_FF rs_ff_5 (.S(and_7_out[2]), .C(C), .R(bitextender_3_out[2]), .Q(rs_ff_3_q[2]));  // open: nQ
  RS_FF rs_ff_6 (.S(and_7_out[3]), .C(C), .R(bitextender_3_out[3]), .Q(rs_ff_3_q[3]));  // open: nQ
  and and_8 (M1_CMP, M1_VO, comparator_1_eq, inst_comp_1_a_old, 1'b1);
  and and_9 (SEL[0], M1_VO, comparator_2_eq);
  or or_4 (or_4_out, and_6_out, and_10_out);
  and and_10 (and_10_out, comparator_3_eq, M1_VO, com1);
  and and_11 (M1_CLR, inst_comp_2_a_old, clr);
  and and_12 (M1_OLD, or_3_out[0], or_3_out[1], or_3_out[2], or_3_out[3]);
  and and_13 (and_13_out, or_6_out, ~M2_RS);  // And
  and and_14 (and_14_out, com2, M2_VO, comparator_8_eq);
  BitExtender #(.inputBits(1), .outputBits(4)) bitextender_4 (.in(or_5_out), .out(bitextender_4_out));
  BitExtender #(.inputBits(1), .outputBits(4)) bitextender_5 (.in(M2_RS), .out(bitextender_5_out));
  RS_FF rs_ff_7 (.S(M2_IE), .C(C), .R(M2_RS), .Q(M2_VO));  // open: nQ
  or or_5 (or_5_out, M2_IE, M2_VO);
  Comparator #(.Bits(32)) comparator_5 (.a(ld_addr), .b(M2_A), .eq(comparator_5_eq));  // open: gt, lt
  Register #(.Bits(32)) register_6 (.D(A), .C(C), .en(M2_DE), .Q(M2_A));
  Register #(.Bits(32)) register_7 (.D(D), .C(C), .en(M2_DE), .Q(M2_D));
  Register #(.Bits(2)) register_8 (.D(MD), .C(C), .en(M2_DE), .Q(M2_MD));
  Comparator #(.Bits(4)) comparator_6 (.a(M2_inst), .b(inst_W), .eq(comparator_6_eq));  // open: gt, lt
  and and_15 (SEL[1], M2_VO, comparator_6_eq);
  RS_FF rs_ff_8 (.S(and_13_out), .C(C), .R(M2_RS), .Q(M2_COM));  // open: nQ
  or or_6 (or_6_out, and_14_out, and_16_out);
  and and_16 (and_16_out, comparator_7_eq, M2_VO, com1);
  Comparator #(.Bits(4)) comparator_7 (.a(M2_inst), .b(com1_id), .eq(comparator_7_eq));  // open: gt, lt
  Comparator #(.Bits(4)) comparator_8 (.a(M2_inst), .b(com2_id), .eq(comparator_8_eq));  // open: gt, lt
  Register #(.Bits(4)) register_9 (.D(inst), .C(C), .en(M2_IE), .Q(M2_inst));
  Register register_10 (.D(epoch), .C(C), .en(M2_IE), .Q(M2_epoch));
  inst_comp inst_comp_3 (.A_id(ld_id), .A_ep(ld_ep), .B_id(M2_inst), .B_ep(M2_epoch), .A_old(inst_comp_3_a_old));
  inst_comp inst_comp_4 (.A_id(M2_inst), .A_ep(M2_epoch), .B_id(clr_id), .B_ep(clr_ep), .A_old(inst_comp_4_a_old));
  assign and_17_out = {M4_IE, M3_IE, M2_IE, M1_IE} & bitextender_4_out & ~bitextender_5_out;  // And and_17, 4 bits wide
  assign or_7_out = {not_3_out[3:2], 1'b0, not_3_out[0]} | rs_ff_9_q;  // Or or_7, 4 bits wide
  RS_FF rs_ff_9 (.S(and_17_out[0]), .C(C), .R(bitextender_5_out[0]), .Q(rs_ff_9_q[0]));  // open: nQ
  RS_FF rs_ff_10 (.S(and_17_out[1]), .C(C), .R(bitextender_5_out[1]), .Q(rs_ff_9_q[1]));  // open: nQ
  RS_FF rs_ff_11 (.S(and_17_out[2]), .C(C), .R(bitextender_5_out[2]), .Q(rs_ff_9_q[2]));  // open: nQ
  RS_FF rs_ff_12 (.S(and_17_out[3]), .C(C), .R(bitextender_5_out[3]), .Q(rs_ff_9_q[3]));  // open: nQ
  and and_18 (M2_CMP, M2_VO, comparator_5_eq, inst_comp_3_a_old, 1'b1);
  and and_19 (M2_CLR, inst_comp_4_a_old, clr);
  and and_20 (M2_OLD, or_7_out[0], or_7_out[1], or_7_out[2], or_7_out[3]);
  or or_8 (or_8_out, M3_IE, M3_VO);
  and and_21 (and_21_out, or_10_out, ~M3_RS);  // And
  and and_22 (and_22_out, com2, M3_VO, comparator_12_eq);
  BitExtender #(.inputBits(1), .outputBits(4)) bitextender_6 (.in(or_8_out), .out(bitextender_6_out));
  assign and_23_out = {M4_IE, M3_IE, M2_IE, M1_IE} & bitextender_6_out & ~bitextender_7_out;  // And and_23, 4 bits wide
  assign or_9_out = {not_3_out[3], 1'b0, not_3_out[1:0]} | rs_ff_15_q;  // Or or_9, 4 bits wide
  BitExtender #(.inputBits(1), .outputBits(4)) bitextender_7 (.in(M3_RS), .out(bitextender_7_out));
  RS_FF rs_ff_13 (.S(M3_IE), .C(C), .R(M3_RS), .Q(M3_VO));  // open: nQ
  and and_24 (M3_CMP, M3_VO, comparator_9_eq, inst_comp_5_a_old, 1'b1);
  Comparator #(.Bits(32)) comparator_9 (.a(ld_addr), .b(M3_A), .eq(comparator_9_eq));  // open: gt, lt
  Register #(.Bits(32)) register_11 (.D(A), .C(C), .en(M3_DE), .Q(M3_A));
  Register #(.Bits(32)) register_12 (.D(D), .C(C), .en(M3_DE), .Q(M3_D));
  Register #(.Bits(2)) register_13 (.D(MD), .C(C), .en(M3_DE), .Q(M3_MD));
  Comparator #(.Bits(4)) comparator_10 (.a(M3_inst), .b(inst_W), .eq(comparator_10_eq));  // open: gt, lt
  and and_25 (SEL[2], M3_VO, comparator_10_eq);
  RS_FF rs_ff_14 (.S(and_21_out), .C(C), .R(M3_RS), .Q(M3_COM));  // open: nQ
  or or_10 (or_10_out, and_22_out, and_26_out);
  and and_26 (and_26_out, comparator_11_eq, M3_VO, com1);
  Comparator #(.Bits(4)) comparator_11 (.a(M3_inst), .b(com1_id), .eq(comparator_11_eq));  // open: gt, lt
  Comparator #(.Bits(4)) comparator_12 (.a(M3_inst), .b(com2_id), .eq(comparator_12_eq));  // open: gt, lt
  Register #(.Bits(4)) register_14 (.D(inst), .C(C), .en(M3_IE), .Q(M3_inst));
  Register register_15 (.D(epoch), .C(C), .en(M3_IE), .Q(M3_epoch));
  inst_comp inst_comp_5 (.A_id(ld_id), .A_ep(ld_ep), .B_id(M3_inst), .B_ep(M3_epoch), .A_old(inst_comp_5_a_old));
  inst_comp inst_comp_6 (.A_id(M3_inst), .A_ep(M3_epoch), .B_id(clr_id), .B_ep(clr_ep), .A_old(inst_comp_6_a_old));
  and and_27 (M3_CLR, inst_comp_6_a_old, clr);
  and and_28 (M3_OLD, or_9_out[0], or_9_out[1], or_9_out[2], or_9_out[3]);
  RS_FF rs_ff_15 (.S(and_23_out[0]), .C(C), .R(bitextender_7_out[0]), .Q(rs_ff_15_q[0]));  // open: nQ
  RS_FF rs_ff_16 (.S(and_23_out[1]), .C(C), .R(bitextender_7_out[1]), .Q(rs_ff_15_q[1]));  // open: nQ
  RS_FF rs_ff_17 (.S(and_23_out[2]), .C(C), .R(bitextender_7_out[2]), .Q(rs_ff_15_q[2]));  // open: nQ
  RS_FF rs_ff_18 (.S(and_23_out[3]), .C(C), .R(bitextender_7_out[3]), .Q(rs_ff_15_q[3]));  // open: nQ
  and and_29 (and_29_out, or_13_out, ~M4_RS);  // And
  RS_FF rs_ff_19 (.S(M4_IE), .C(C), .R(M4_RS), .Q(M4_VO));  // open: nQ
  or or_11 (or_11_out, M4_IE, M4_VO);
  Comparator #(.Bits(32)) comparator_13 (.a(ld_addr), .b(M4_A), .eq(comparator_13_eq));  // open: gt, lt
  Register #(.Bits(32)) register_16 (.D(A), .C(C), .en(M4_DE), .Q(M4_A));
  Register #(.Bits(32)) register_17 (.D(D), .C(C), .en(M4_DE), .Q(M4_D));
  Register #(.Bits(2)) register_18 (.D(MD), .C(C), .en(M4_DE), .Q(M4_MD));
  Comparator #(.Bits(4)) comparator_14 (.a(M4_inst), .b(inst_W), .eq(comparator_14_eq));  // open: gt, lt
  RS_FF rs_ff_20 (.S(and_29_out), .C(C), .R(M4_RS), .Q(M4_COM));  // open: nQ
  and and_30 (and_30_out, com2, M4_VO, comparator_16_eq);
  Comparator #(.Bits(4)) comparator_15 (.a(M4_inst), .b(com1_id), .eq(comparator_15_eq));  // open: gt, lt
  Comparator #(.Bits(4)) comparator_16 (.a(M4_inst), .b(com2_id), .eq(comparator_16_eq));  // open: gt, lt
  Register #(.Bits(4)) register_19 (.D(inst), .C(C), .en(M4_IE), .Q(M4_inst));
  Register register_20 (.D(epoch), .C(C), .en(M4_IE), .Q(M4_epoch));
  inst_comp inst_comp_7 (.A_id(ld_id), .A_ep(ld_ep), .B_id(M4_inst), .B_ep(M4_epoch), .A_old(inst_comp_7_a_old));
  inst_comp inst_comp_8 (.A_id(M4_inst), .A_ep(M4_epoch), .B_id(clr_id), .B_ep(clr_ep), .A_old(inst_comp_8_a_old));
  BitExtender #(.inputBits(1), .outputBits(4)) bitextender_8 (.in(or_11_out), .out(bitextender_8_out));
  assign and_31_out = {M4_IE, M3_IE, M2_IE, M1_IE} & bitextender_8_out & ~bitextender_9_out;  // And and_31, 4 bits wide
  assign or_12_out = {1'b0, not_3_out[2:0]} | rs_ff_21_q;  // Or or_12, 4 bits wide
  RS_FF rs_ff_21 (.S(and_31_out[0]), .C(C), .R(bitextender_9_out[0]), .Q(rs_ff_21_q[0]));  // open: nQ
  RS_FF rs_ff_22 (.S(and_31_out[1]), .C(C), .R(bitextender_9_out[1]), .Q(rs_ff_21_q[1]));  // open: nQ
  BitExtender #(.inputBits(1), .outputBits(4)) bitextender_9 (.in(M4_RS), .out(bitextender_9_out));
  RS_FF rs_ff_23 (.S(and_31_out[2]), .C(C), .R(bitextender_9_out[2]), .Q(rs_ff_21_q[2]));  // open: nQ
  RS_FF rs_ff_24 (.S(and_31_out[3]), .C(C), .R(bitextender_9_out[3]), .Q(rs_ff_21_q[3]));  // open: nQ
  and and_32 (M4_CMP, M4_VO, comparator_13_eq, inst_comp_7_a_old, 1'b1);
  and and_33 (SEL[3], M4_VO, comparator_14_eq);
  or or_13 (or_13_out, and_30_out, and_34_out);
  and and_34 (and_34_out, comparator_15_eq, M4_VO, com1);
  and and_35 (M4_CLR, inst_comp_8_a_old, clr);
  and and_36 (M4_OLD, or_12_out[0], or_12_out[1], or_12_out[2], or_12_out[3]);

  assign WD = W_d;

  // Other names for the same wires on the sheet: clear = clr; comp_addr[31:0] = ld_addr; comp_ep = ld_ep;
  //   comp_id[3:0] = ld_id; ld_O[31:0] = ld_D; M1_SEL = SEL[0]; M2_SEL = SEL[1]; M3_SEL = SEL[2]; M4_SEL = SEL[3];
  //   V_out = V
endmodule
