// Digital circuit store-controller.dig as structural Verilog
module store_controller (
  input  in1,
  input  C,
  input  in2,
  input  in3,
  input  in4,
  input  in5,
  input  in6,
  input  in7,
  input  in8,
  output out1,
  output out2,
  output out3,
  output out4,
  output out5,
  output out6,
  output out7,
  output out8,
  output ST2,
  output ST1,
  output [2:0] D2_sel,
  output [2:0] D1_sel
);

  wire E, not_1_out, not_2_out, or_1_out, or_2_out, priority_8_1_v, priority_8_2_v;
  wire [1:0] not_3_out, priorityencoder_1_num;
  wire [2:0] index_compressor_1_out0, index_compressor_1_out1, index_compressor_1_out2,
       index_compressor_1_out3, index_compressor_1_out4, index_compressor_1_out5, index_compressor_1_out6,
       index_compressor_1_out7, priorityencoder_2_num, register_1_q, register_2_q, register_3_q,
       register_4_q, register_5_q, register_6_q;
  wire [3:0] multiplexer_3_out, multiplexer_4_out, multiplexer_5_out, multiplexer_6_out;
  wire [3:2] demultiplexer_1_out_0, demultiplexer_1_out_1, demultiplexer_1_out_2, demultiplexer_1_out_3,
       demultiplexer_1_out_4, demultiplexer_1_out_5, demultiplexer_1_out_6, demultiplexer_1_out_7;
  wire [5:0] register_1_q_2;
  wire [7:0] and_1_out, bitextender_1_out, index_compressor_1_v, priority_8_1_out8, priority_8_2_out8,
       xor_1_out;
  wire [31:0] multiplexer_1_out, multiplexer_2_out;

  DipSwitch #(.dipDefault("true")) dipswitch_1 (.out(E));
  not not_1 (not_1_out, register_1_q_2[4]);
  priority_8 priority_8_1 (
    .on(1'b1), .in1(in8), .in2(in7), .in3(in6), .in4(in5), .in5(in4), .in6(in3), .in7(in2), .in8(in1),
    .out1(priority_8_1_out8[7]), .out2(priority_8_1_out8[6]), .out3(priority_8_1_out8[5]),
    .out4(priority_8_1_out8[4]), .out5(priority_8_1_out8[3]), .out6(priority_8_1_out8[2]),
    .out7(priority_8_1_out8[1]), .out8(priority_8_1_out8[0]), .v(priority_8_1_v));
  index_compressor index_compressor_1 (
    .in0(in1), .in1(in2), .in2(in3), .in3(in4), .in4(in5), .in5(in6), .in6(in7), .in7(in8),
    .out0(index_compressor_1_out0), .out1(index_compressor_1_out1), .out2(index_compressor_1_out2),
    .out3(index_compressor_1_out3), .out4(index_compressor_1_out4), .out5(index_compressor_1_out5),
    .out6(index_compressor_1_out6), .out7(index_compressor_1_out7), .V(index_compressor_1_v));
  BitExtender #(.inputBits(1), .outputBits(8)) bitextender_1 (.in(not_1_out), .out(bitextender_1_out));
  assign and_1_out = bitextender_1_out & priority_8_1_out8;  // And and_1, 8 bits wide
  assign xor_1_out = {in8, in7, in6, in5, in4, in3, in2, in1} ^ priority_8_1_out8;  // XOr xor_1, 8 bits wide
  not not_2 (not_2_out, register_1_q_2[5]);
  priority_8 priority_8_2 (
    .on(not_2_out), .in1(xor_1_out[7]), .in2(xor_1_out[6]), .in3(xor_1_out[5]), .in4(xor_1_out[4]),
    .in5(xor_1_out[3]), .in6(xor_1_out[2]), .in7(xor_1_out[1]), .in8(xor_1_out[0]),
    .out1(priority_8_2_out8[7]), .out2(priority_8_2_out8[6]), .out3(priority_8_2_out8[5]),
    .out4(priority_8_2_out8[4]), .out5(priority_8_2_out8[3]), .out6(priority_8_2_out8[2]),
    .out7(priority_8_2_out8[1]), .out8(priority_8_2_out8[0]), .v(priority_8_2_v));
  PriorityEncoder #(.Selector_Bits(2)) priorityencoder_1 (
    .in0(1'b1), .in1(not_3_out[0]), .in2(not_3_out[1]), .in3(1'b0), .num(priorityencoder_1_num));  // open: any
  assign not_3_out = ~register_1_q_2[5:4];  // Not not_3, 2 bits wide
  Multiplexer #(.Selector_Bits(2), .Bits(32)) multiplexer_1 (
    .sel(priorityencoder_1_num),
    .in_0({index_compressor_1_v[7], index_compressor_1_out7, index_compressor_1_v[6], index_compressor_1_out6, index_compressor_1_v[5], index_compressor_1_out5, index_compressor_1_v[4], index_compressor_1_out4, index_compressor_1_v[3], index_compressor_1_out3, index_compressor_1_v[2], index_compressor_1_out2, index_compressor_1_v[1], index_compressor_1_out1, index_compressor_1_v[0], index_compressor_1_out0}),
    .in_1({4'b0000, index_compressor_1_v[7], index_compressor_1_out7, index_compressor_1_v[6], index_compressor_1_out6, index_compressor_1_v[5], index_compressor_1_out5, index_compressor_1_v[4], index_compressor_1_out4, index_compressor_1_v[3], index_compressor_1_out3, index_compressor_1_v[2], index_compressor_1_out2, index_compressor_1_v[1], index_compressor_1_out1}),
    .in_2({{8{1'b0}}, index_compressor_1_v[7], index_compressor_1_out7, index_compressor_1_v[6], index_compressor_1_out6, index_compressor_1_v[5], index_compressor_1_out5, index_compressor_1_v[4], index_compressor_1_out4, index_compressor_1_v[3], index_compressor_1_out3, index_compressor_1_v[2], index_compressor_1_out2}),
    .in_3({32{1'b0}}), .out(multiplexer_1_out));
  PriorityEncoder #(.Selector_Bits(3)) priorityencoder_2 (
    .in0(1'b1), .in1(register_1_q_2[3]), .in2(register_1_q_2[2]), .in3(register_1_q_2[1]),
    .in4(register_1_q_2[0]), .in5(1'b0), .in6(1'b0), .in7(1'b0), .num(priorityencoder_2_num));  // open: any
  Multiplexer #(.Selector_Bits(3), .Bits(32)) multiplexer_2 (
    .sel(priorityencoder_2_num), .in_0(multiplexer_1_out), .in_1({multiplexer_1_out[27:0], 4'b0000}),
    .in_2({multiplexer_1_out[23:0], {8{1'b0}}}), .in_3({multiplexer_1_out[19:0], {12{1'b0}}}),
    .in_4({multiplexer_1_out[15:0], {16{1'b0}}}), .in_5({multiplexer_1_out[11:0], {20{1'b0}}}),
    .in_6({32{1'b0}}), .in_7({32{1'b0}}), .out(multiplexer_2_out));
  Register #(.Bits(4)) register_1 (.D(multiplexer_2_out[23:20]), .C(C), .en(E), .Q({register_1_q_2[0], register_1_q}));
  Register #(.Bits(4)) register_2 (.D(multiplexer_2_out[19:16]), .C(C), .en(E), .Q({register_1_q_2[1], register_2_q}));
  Multiplexer #(.Bits(4)) multiplexer_3 (
    .sel(register_1_q_2[0]), .in_0(multiplexer_2_out[15:12]), .in_1({register_1_q_2[0], register_1_q}),
    .out(multiplexer_3_out));
  Register #(.Bits(4)) register_3 (.D(multiplexer_3_out), .C(C), .en(E), .Q({register_1_q_2[2], register_3_q}));
  Multiplexer #(.Bits(4)) multiplexer_4 (
    .sel(register_1_q_2[1]), .in_0(multiplexer_2_out[11:8]), .in_1({register_1_q_2[1], register_2_q}),
    .out(multiplexer_4_out));
  Register #(.Bits(4)) register_4 (.D(multiplexer_4_out), .C(C), .en(E), .Q({register_1_q_2[3], register_4_q}));
  Multiplexer #(.Bits(4)) multiplexer_5 (
    .sel(register_1_q_2[2]), .in_0(multiplexer_2_out[7:4]), .in_1({register_1_q_2[2], register_3_q}),
    .out(multiplexer_5_out));
  Register #(.Bits(4)) register_5 (.D(multiplexer_5_out), .C(C), .en(E), .Q({register_1_q_2[4], register_5_q}));
  Multiplexer #(.Bits(4)) multiplexer_6 (
    .sel(register_1_q_2[3]), .in_0(multiplexer_2_out[3:0]), .in_1({register_1_q_2[3], register_4_q}),
    .out(multiplexer_6_out));
  Multiplexer #(.Bits(3)) multiplexer_7 (
    .sel(register_1_q_2[4]), .in_0(index_compressor_1_out1), .in_1(register_5_q), .out(D2_sel));
  Multiplexer #(.Bits(3)) multiplexer_8 (
    .sel(register_1_q_2[5]), .in_0(index_compressor_1_out0), .in_1(register_6_q), .out(D1_sel));
  Register #(.Bits(4)) register_6 (.D(multiplexer_6_out), .C(C), .en(E), .Q({register_1_q_2[5], register_6_q}));
  or or_1 (or_1_out, priority_8_2_v, register_1_q_2[5]);
  or or_2 (or_2_out, priority_8_1_v, register_1_q_2[4]);
  Demultiplexer #(.Selector_Bits(3)) demultiplexer_1 (
    .sel(register_6_q), .in(register_1_q_2[5]), .out_0(demultiplexer_1_out_0[3]),
    .out_1(demultiplexer_1_out_1[3]), .out_2(demultiplexer_1_out_2[3]), .out_3(demultiplexer_1_out_3[3]),
    .out_4(demultiplexer_1_out_4[3]), .out_5(demultiplexer_1_out_5[3]), .out_6(demultiplexer_1_out_6[3]),
    .out_7(demultiplexer_1_out_7[3]));
  or or_3 (ST1, or_1_out, or_2_out);
  and and_2 (ST2, or_1_out, or_2_out);
  Demultiplexer #(.Selector_Bits(3)) demultiplexer_2 (
    .sel(register_5_q), .in(register_1_q_2[4]), .out_0(demultiplexer_1_out_0[2]),
    .out_1(demultiplexer_1_out_1[2]), .out_2(demultiplexer_1_out_2[2]), .out_3(demultiplexer_1_out_3[2]),
    .out_4(demultiplexer_1_out_4[2]), .out_5(demultiplexer_1_out_5[2]), .out_6(demultiplexer_1_out_6[2]),
    .out_7(demultiplexer_1_out_7[2]));
  or or_4 (out1, demultiplexer_1_out_0[3], demultiplexer_1_out_0[2], priority_8_2_out8[0], and_1_out[0]);
  or or_5 (out8, and_1_out[7], priority_8_2_out8[7], demultiplexer_1_out_7[2], demultiplexer_1_out_7[3]);
  or or_6 (out2, demultiplexer_1_out_1[3], demultiplexer_1_out_1[2], priority_8_2_out8[1], and_1_out[1]);
  or or_7 (out7, and_1_out[6], priority_8_2_out8[6], demultiplexer_1_out_6[2], demultiplexer_1_out_6[3]);
  or or_8 (out3, demultiplexer_1_out_2[3], demultiplexer_1_out_2[2], priority_8_2_out8[2], and_1_out[2]);
  or or_9 (out6, and_1_out[5], priority_8_2_out8[5], demultiplexer_1_out_5[2], demultiplexer_1_out_5[3]);
  or or_10 (out4, demultiplexer_1_out_3[3], demultiplexer_1_out_3[2], priority_8_2_out8[3], and_1_out[3]);
  or or_11 (out5, and_1_out[4], priority_8_2_out8[4], demultiplexer_1_out_4[2], demultiplexer_1_out_4[3]);

  // Other names for the same wires on the sheet: I1 = in1; I2 = in2; I3 = in3; I4 = in4; I5 = in5; I6 = in6; I7 = in7;
  //   I8 = in8; O1 = out1; O2 = out2; O3 = out3; O4 = out4; O5 = out5; O6 = out6; O7 = out7; O8 = out8
endmodule
