// Digital circuit cpu-32 test.dig as structural Verilog
module cpu_32_test (
  input  C,
  input  bus_e,
  input  E,
  input  [31:0] I_D__bus,
  input  [31:0] D_D__bus,
  input  [31:0] I_A__bus,
  input  [31:0] D_A__bus,
  input  INT_nor,
  input  INT_nmk,
  input  run,
  input  I_valid,
  input  D_valid,
  output I_LD,
  output D_LD,
  output D_ST,
  output [1:0] MMU_sel,
  output MMU_str,
  output [2:0] DMA_sel,
  output DMA_str,
  output INT_str,
  output CLK_str,
  output [1:0] CSH_mode,
  output CSH_run,
  output INT_out,
  output [1:0] D_MD
);

  wire add_4c32_1_c, alu_32_1_p6, alu_32_1_p9, ALU_A_DRD, ALU_A_FRD, ALU_A_LD, ALU_A_LRD, ALU_A_RE,
       ALU_A_STD, ALU_A_STF, ALU_B_DRD, ALU_B_FRD, ALU_B_LD, ALU_B_LRD, ALU_B_RE, ALU_B_STD, ALU_B_STF,
       ALU_busy, ALU_free, and_1_out, and_2_out, and_3_out, and_7_out, and_8_out, and_9_out, and_10_out,
       and_11_out, and_12_out, and_14_out, and_15_out, and_16_out, and_17_out, and_18_out, and_19_out,
       and_20_out, and_21_out, and_22_out, and_23_out, and_24_out, and_25_out, and_26_out, and_27_out,
       and_28_out, and_29_out, and_30_out, and_33_out, and_34_out, and_35_out, and_36_out, and_37_out,
       and_38_out, and_39_out, and_40_out, and_46_out, and_49_out, and_50_out, and_51_out, and_52_out,
       and_53_out, and_54_out, and_55_out, and_56_out, and_61_out, and_62_out, and_63_out, and_64_out,
       and_65_out, and_66_out, and_67_out, and_68_out, and_69_out, and_71_out, and_72_out, and_74_out,
       and_79_out, and_80_out, and_81_out, and_82_out, and_83_out, and_84_out, and_85_out, and_86_out,
       and_87_out, and_88_out, and_89_out, and_90_out, and_91_out, and_92_out, and_93_out, and_94_out,
       and_95_out, and_96_out, and_97_out, and_98_out, and_99_out, and_100_out, and_101_out, and_102_out,
       C_ct, C_dt, clr, clr_ep, cm_e, cm_e__bf, com1, com1_M, com2, comparator_1_gt, comparator_2_eq,
       comparator_3_eq, CT_ALU__LD, CT_ALU__M, CT_ALU__M2, CT_ALU__WD, CT_ALU__WF, CT_BUS__DAG, CT_BUS__DAM,
       CT_BUS__DAR, CT_BUS__DDG, CT_BUS__DDM, CT_BUS__DDR, CT_BUS__IAG, CT_BUS__IAR, CT_BUS__IDM,
       CT_BUS__IDR, CT_DEP__EA, CT_DEP__EB, CT_DIR__LD, CT_DIR__M, CT_DIR__MS, CT_DISP, CT_FL__W1, CT_FL__W2,
       CT_haz, CT_ISS__OFL, CT_ISS__ORC, CT_ISS__OSC, CT_ISS__OSTB, CT_ISS__UFL, CT_ISS__URA, CT_ISS__URB,
       CT_ISS__USC, CT_MVR, CT_RF__DM, CT_RF__E, CT_RF__FLS, CT_RF__PCAE, CT_RF__PCH, CT_RF__PCJ, CT_RF__PCR,
       CT_RF__PCSE, CT_RF__SCAE, CT_RF__SCAS, CT_RF__SCD, CT_RF__SCSE, CT_RF__W1, CT_RF__W2, CT_ROB__EX__E,
       CT_ROB__FL__STA, CT_ROB__FL__STB, CT_ROB__GEN__STA, CT_ROB__GEN__STB, CT_ROB__ST__E, CT_rollback,
       CT_SC__D1, CT_SC__D2, CT_SC__W1, CT_SC__W2, CT_STB__LD, DC_B_q, dc_e, DC_q, dipswitch_2_out,
       dipswitch_3_out, dipswitch_4_out, DIR_busy, DIR_free, DIR_LD, DIR_RD, DIR_ST, dispatch, dp_e,
       dp_e__bf, ecm_e__bf, epoch_DP, epoch_IS, ex_e, ex_e__bf, ex_nop, ft_e, FT_q, hlt, id_full,
       id_gen2_1_v, int_run, issue, kernel_inst, LD_ep, mode, multiplexer_7_out, multiplexer_8_out,
       multiplexer_9_out, multiplexer_11_out, multiplexer_13_out, multiplexer_18_out, multiplexer_19_out,
       multiplexer_27_out, multiplexer_28_out, multiplexer_36_out, multiplexer_41_out, multiplexer_45_out,
       nand_1_out, nor_1_out, nor_2_out, nor_5_out, not_1_out, not_3_out, not_7_out, not_8_out, not_9_out,
       not_10_out, not_13_out, not_14_out, not_15_out, not_16_out, or_11_out, or_12_out, or_13_out,
       or_14_out, or_17_out, or_18_out, or_19_out, or_20_out, or_21_out, or_22_out, or_23_out, or_24_out,
       or_25_out, or_26_out, or_28_out, or_29_out, or_31_out, or_32_out, or_33_out, or_34_out, or_35_out,
       or_36_out, or_38_out, or_39_out, or_40_out, or_41_out, or_42_out, pc_ov, register_12_q, register_15_q,
       register_16_q, register_17_q, register_22_q, register_23_q, register_24_q, register_31_q,
       register_32_q, register_33_q, register_34_q, register_35_q, register_36_q, register_37_q,
       register_38_q, register_39_q, register_40_q, register_41_q, register_57_q, register_68_q, rf_e,
       rs_ff_1_nq, rs_ff_2_nq, rs_ff_3_nq, rs_ff_4_nq, rs_ff_5_nq, rs_ff_11_q, rs_ff_12_q, rs_ff_13_q,
       rs_ff_14_q, sc_ov, st, st_e__bf, STB_busy, STB_free, STB_LD, store_buffer_1_ld_v, store_buffer_1_v,
       xor_2_out, xor_3_out, xor_4_out, xor_5_out, xor_6_out, xor_7_out, xor_8_out;
  wire [0:0] and_45_out;
  wire [1:0] and_31_out, and_57_out, and_59_out, CT_ALU__M_old, d_ff_1_q, d_ff_2_q;
  wire [1:1] d_ff_3_q, d_ff_4_q;
  wire [2:0] ALU_A_RM, ALU_B_RM, and_42_out, and_44_out, CT_BUS__DASDN, CT_DEP__UMA, CT_DEP__UMB,
       CT_ISS__UFU, CT_RF__MA, CT_RF__MB, CT_RF__SCN, CT_RF__WM, CT_SC__O1, CT_SC__O2, multiplexer_29_out,
       register_10_q, register_11_q, register_13_q, register_14_q, store_controller_1_d1_sel,
       store_controller_1_d2_sel, store_controller_2_d1_sel, store_controller_2_d2_sel;
  wire [2:1] and_43_out;
  wire [3:0] ALU_A_INST, ALU_B_INST, clr_id, com1_inst, com2_inst, CT_FU__INST, DIR_INST, inst_DP, inst_EX,
       inst_EXT, inst_IS, inst_ST, LD_id, multiplexer_6_out, multiplexer_17_out, multiplexer_25_out,
       multiplexer_35_out, multiplexer_40_out, multiplexer_44_out, multiplexer_48_out, register_21_q,
       register_30_q, register_47_q, register_52_q, register_56_q, register_71_q, ROB_FL_INSTA, ROB_FL_INSTB,
       ROB_GEN_INSTA, ROB_GEN_INSTB, STB_INST;
  wire [3:3] register_11_q_2;
  wire [4:0] CT_DEP__URA, CT_DEP__URB, CT_ISS__RA, CT_ISS__RB, CT_ISS__RC, CT_RF__RA, CT_RF__RB, CT_RF__WS;
  wire [7:0] ALU_A_F, ALU_A_FI, ALU_A_T__F, ALU_B_F, ALU_B_FI, ALU_B_T__F, bitextender_2_out, byte_D0,
       byte_D0_iv, byte_D1, byte_D1_ex, byte_D1_st, byte_D2, byte_D2_ex, byte_D3, byte_D3_ex, byte_I0,
       byte_I0_iv, byte_I1, byte_I2, byte_I3, CT_FL__D1, CT_FL__D2, CT_FU__WR, CT_RF__R1, CT_RF__R2, DIR_WR,
       fl_i, FU_free, multiplexer_4_out, multiplexer_22_out, multiplexer_24_out, multiplexer_32_out,
       multiplexer_34_out, multiplexer_43_out, multiplexer_47_out, register_27_q, register_29_q,
       register_44_q, register_46_q, register_55_q, register_70_q, ROB_FL_A, ROB_FL_B, ROB_GEN_WA,
       ROB_GEN_WB, xor_1_out;
  wire [7:3] ALU_A_WR, ALU_B_WR;
  wire [8:0] ALU_A_CT, ALU_B_CT, CT_ALU__CT, multiplexer_23_out, multiplexer_33_out, register_28_q,
       register_45_q;
  wire [9:0] and_13_out;
  wire [15:0] bitextender_3_out, multiplexer_16_out, multiplexer_39_out, register_20_q, register_51_q,
       register_60_q, V_inst;
  wire [31:0] add_1_s, add_4c32_1_s, add_s16c32_1_s, alu_32_1_p8, alu_32_1_p11, alu_32_1_p12, alu_32_1_p14,
       ALU_A_A, ALU_A_B, ALU_A_R, ALU_A_T__R, ALU_B_A, ALU_B_B, ALU_B_R, ALU_B_T__R, bitextender_1_out,
       CT_RF__D1, CT_RF__D2, D_A__R_q, DIR, FL, I_A__R_q, I_D__R_q, LD_addr, multiplexer_2_out,
       multiplexer_3_out, multiplexer_10_out, multiplexer_14_out, multiplexer_15_out, multiplexer_20_out,
       multiplexer_21_out, multiplexer_26_out, multiplexer_30_out, multiplexer_31_out, multiplexer_37_out,
       multiplexer_38_out, multiplexer_42_out, multiplexer_46_out, mVec, OD_D__R_q, pc_read, PCA, pca_i, PCS,
       PCS_DC, PCS_FT, pcs_i, PCS_IS, R_A, R_B, ramdualaccess_1_d1, ramdualaccess_1_d2, register_4_q,
       register_5_q, register_18_q, register_19_q, register_25_q, register_26_q, register_42_q,
       register_43_q, register_49_q, register_50_q, register_54_q, register_58_q, register_59_q,
       register_69_q, ROB_GEN_DA, ROB_GEN_DB, SCA, sca_i, SCS, scs_i, store_buffer_1_a_o, store_buffer_1_d_o,
       store_buffer_1_ld_d, sub_4c32_1_s;
  wire [31:24] res_station_1_p32;

  Comparator #(.Bits(32)) comparator_1 (.a(PCS), .b(mVec), .gt(comparator_1_gt));  // open: eq, lt
  BitExtender #(.inputBits(16), .outputBits(32)) bitextender_1 (.in({byte_D2_ex, byte_D3_ex}), .out(bitextender_1_out));
  and and_1 (and_1_out, FL[14], INT_nor);
  and and_2 (and_2_out, 1'b0, ~comparator_1_gt);  // And
  Add #(.Bits(32)) add_1 (.a(R_A), .b(bitextender_1_out), .c_i(1'b0), .s(add_1_s));  // open: c_o
  or or_1 (int_run, and_1_out, INT_nmk);
  PullDown pulldown_1 (.out(CT_haz));
  RS_FF u_mode (.S(and_2_out), .C(C_dt), .R(comparator_1_gt), .Q(mode));  // open: nQ
  Register #(.Bits(32)) MVR (.D(add_1_s), .C(C_dt), .en(CT_MVR), .Q(mVec));
  and and_3 (and_3_out, CT_haz, dp_e);
  assign CT_RF__PCSE = ft_e ? 1'b1 : 1'bz;  // Driver driver_1
  assign CT_BUS__IAR = ft_e ? 1'b1 : 1'bz;  // Driver driver_2
  assign CT_BUS__IAG = ft_e ? 1'b1 : 1'bz;  // Driver driver_3
  assign I_LD = ft_e ? 1'b1 : 1'bz;  // Driver driver_4
  id_gen2 id_gen2_1 (
    .C(C_ct), .\use (issue), .V_inst(V_inst), .epoch(epoch_IS), .id(inst_IS), .V(id_gen2_1_v), .com1(com1),
    .com1_id(com1_inst), .com2(com2), .com2_id(com2_inst));
  RS_FF FT (.S(run), .C(C_ct), .R(hlt), .Q(FT_q));  // open: nQ
  not not_1 (not_1_out, and_3_out);
  assign ex_nop = and_3_out ? 1'b1 : 1'bz;  // Driver driver_5
  not not_2 (id_full, id_gen2_1_v);
  and and_4 (dispatch, CT_DISP, dp_e__bf);
  and and_5 (ft_e, FT_q, not_1_out);
  Register DC_B (.D(FT_q), .C(C_dt), .en(1'b1), .Q(DC_B_q));
  Register #(.Bits(32)) register_1 (.D(PCS), .C(C_dt), .en(CT_RF__PCSE), .Q(PCS_FT));
  Register DC (.D(FT_q), .C(C_ct), .en(1'b1), .Q(DC_q));
  not not_3 (not_3_out, I_valid);
  DipSwitch dipswitch_1 (.out(CT_rollback));
  and and_6 (dc_e, DC_q, not_1_out);
  Register DP_B (.D(DC_B_q), .C(C_dt), .en(1'b1), .Q(dp_e__bf));
  Register #(.Bits(32)) register_2 (.D(PCS_FT), .C(C_dt), .en(CT_RF__PCSE), .Q(PCS_DC));
  assign CT_BUS__IDM = not_3_out ? 1'b1 : 1'bz;  // Driver driver_6
  Register DP (.D(DC_q), .C(C_ct), .en(1'b1), .Q(dp_e));
  Register #(.Bits(4)) EX (.D(inst_DP), .C(C_dt), .en(dp_e), .Q(inst_EX));
  Register EX_B (.D(dp_e__bf), .C(C_dt), .en(1'b1), .Q(ex_e__bf));
  Register #(.Bits(32)) register_3 (.D(PCS_DC), .C(C_dt), .en(CT_RF__PCSE), .Q(PCS_IS));
  Register #(.Bits(4)) u_ST (.D(inst_EX), .C(C_dt), .en(ex_e), .Q(inst_ST));
  DipSwitch dipswitch_2 (.out(dipswitch_2_out));
  Multiplexer multiplexer_1 (.sel(dipswitch_3_out), .in_0(dipswitch_2_out), .in_1(C), .out(C_dt));
  DipSwitch dipswitch_3 (.out(dipswitch_3_out));
  not not_4 (C_ct, C_dt);
  Register EX_2 (.D(dp_e), .C(C_ct), .en(1'b1), .Q(ex_e));
  PullDown pulldown_2 (.out(CT_DISP));
  PullDown pulldown_3 (.out(CT_rollback));
  PullDown pulldown_4 (.out(com2));
  PullDown #(.Bits(4)) pulldown_5 (.out(com2_inst));
  PullDown pulldown_6 (.out(com1_M));
  PullDown pulldown_7 (.out(com1));
  PullDown #(.Bits(4)) pulldown_8 (.out(com1_inst));
  Multiplexer #(.Bits(32)) multiplexer_2 (.sel(CT_RF__DM), .in_0(ALU_A_T__R), .in_1(D_D__bus), .out(multiplexer_2_out));
  and and_7 (and_7_out, rf_e, CT_RF__E);
  Register ST_B (.D(ex_e__bf), .C(C_dt), .en(1'b1), .Q(st_e__bf));
  Register #(.Bits(4)) EXT (.D(inst_ST), .C(C_dt), .en(rf_e), .Q(inst_EXT));
  // Probe on multiplexer_2_out
  // Probe on CT_RF__WS
  // Probe on CT_RF__WM
  // Probe on CT_RF__RA
  // Probe on CT_RF__MA
  // Probe on CT_RF__RB
  // Probe on CT_RF__MB
  Register #(.Bits(32)) register_4 (.D(ALU_A_T__R), .C(C_dt), .en(CT_RF__E), .Q(register_4_q));
  Register ST_2 (.D(ex_e), .C(C_ct), .en(1'b1), .Q(rf_e));
  Register #(.Bits(32)) register_5 (.D(multiplexer_2_out), .C(C_dt), .en(and_7_out), .Q(register_5_q));
  // Probe on and_7_out
  // Probe M on CT_RF__WM
  // Probe REG st on register_4_q
  // Probe INST on {byte_I0, byte_I1, byte_I2, byte_I3}
  Register CM_B___EXT_B (.D(st_e__bf), .C(C_dt), .en(1'b1), .Q(cm_e__bf));
  // Probe on register_5_q
  // Probe S on CT_RF__WS
  assign byte_I0_iv = ~byte_I0;  // Not not_5, 8 bits wide
  assign byte_D0_iv = ~byte_D0;  // Not not_6, 8 bits wide
  Register CM___EXT (.D(rf_e), .C(C_ct), .en(1'b1), .Q(cm_e));
  // Probe inst on {byte_I0, byte_I1, byte_I2, byte_I3}
  // Probe R_A on R_A
  // Probe R_B on R_B
  // Probe PC on PCS
  // Probe SC on SCS
  // Probe FL on FL
  // Probe CT_BUS-_IDM on CT_BUS__IDM
  // Probe C_i on C_dt
  Register EXT_CM_B (.D(cm_e__bf), .C(C_dt), .en(1'b1), .Q(ecm_e__bf));
  // Probe com1_inst on com1_inst
  // Probe com2_inst on com2_inst
  // Probe inst_ST on inst_ST
  // Probe PC_inst on inst_IS
  // Probe inst_EX on inst_EX
  Register #(.Bits(8)) register_6 (.D(byte_D1), .C(C_ct), .en(ex_e__bf), .Q(byte_D1_ex));
  Register #(.Bits(8)) register_7 (.D(byte_D2), .C(C_ct), .en(ex_e__bf), .Q(byte_D2_ex));
  Register #(.Bits(8)) register_8 (.D(byte_D3), .C(C_ct), .en(ex_e__bf), .Q(byte_D3_ex));
  RAMDualAccess #(.AddrBits(24), .isProgramMemory("true"), .Bits(32)) ramdualaccess_1 (
    .str(D_ST), .C(C_dt), .ld(1'b1), .A1(D_A__bus[25:2]), .Din1(D_D__bus), .A2(I_A__bus[25:2]),
    .D1(ramdualaccess_1_d1), .D2(ramdualaccess_1_d2));
  assign D_D__bus = D_LD ? ramdualaccess_1_d1 : 32'bz;  // Driver driver_7
  assign I_D__bus = I_LD ? ramdualaccess_1_d2 : 32'bz;  // Driver driver_8
  Register #(.Bits(8)) register_9 (.D(byte_D1_ex), .C(C_ct), .en(st_e__bf), .Q(byte_D1_st));
  sub_4c32 sub_4c32_1 (.a(SCS), .b({1'b0, CT_BUS__DASDN}), .s(sub_4c32_1_s));
  Multiplexer #(.Bits(32)) multiplexer_3 (
    .sel(CT_BUS__DAM), .in_0(ALU_A_T__R), .in_1(sub_4c32_1_s), .out(multiplexer_3_out));
  and and_8 (and_8_out, byte_D0[3], byte_D0[0]);
  and and_9 (and_9_out, byte_D0[2], byte_D0[0]);
  and and_10 (and_10_out, byte_D0_iv[3], byte_D0_iv[2], byte_D0[1], byte_D0_iv[0]);
  and and_11 (and_11_out, byte_D0_iv[4], byte_D0[3], byte_D0[2], byte_D0[1]);
  and and_12 (and_12_out, byte_D0[4], byte_D0_iv[3], byte_D0_iv[2], byte_D0[1], byte_D0[0]);
  and and_13 (and_13_out[7], byte_D0_iv[4], byte_D0[3], byte_D0[2]);
  and and_14 (and_14_out, byte_D0[4], byte_D0[2], byte_D0_iv[1]);
  and and_15 (and_15_out, byte_D0[4], byte_D0_iv[3], byte_D0_iv[2]);
  and and_16 (and_16_out, byte_D0_iv[4], byte_D0_iv[3], byte_D0_iv[2]);
  and and_17 (and_17_out, byte_D0_iv[4], byte_D0_iv[3]);
  and and_18 (and_18_out, byte_D0_iv[4], byte_D0[3], byte_D0_iv[2], byte_D0_iv[1]);
  and and_19 (and_19_out, byte_D0_iv[4], byte_D0[3], byte_D0_iv[2]);
  and and_20 (and_20_out, byte_D0[4], byte_D0[3]);
  and and_21 (and_21_out, byte_D0_iv[4], byte_D0_iv[3], byte_D0[2], byte_D0_iv[1]);
  and and_22 (and_22_out, byte_D0[4], byte_D0[2], byte_D0[1]);
  and and_23 (and_23_out, byte_D0_iv[4], byte_D0_iv[3], byte_D0_iv[2], byte_D0[1], byte_D0[0]);
  and and_24 (and_24_out, byte_D0_iv[2], byte_D0_iv[0]);
  and and_25 (and_25_out, byte_D0[2], byte_D0[0]);
  and and_26 (and_26_out, byte_D0[1], byte_D0[2], byte_D0[4]);
  and and_27 (and_27_out, byte_D0[3], byte_D0[4]);
  and and_28 (and_28_out, ft_e, CT_BUS__IAR);
  Multiplexer #(.Bits(8)) multiplexer_4 (
    .sel(CT_BUS__IDM), .in_0(I_D__bus[31:24]), .in_1(8'h72), .out(multiplexer_4_out));
  and and_29 (and_29_out, ex_e, CT_BUS__DAR);
  and and_30 (and_30_out, ex_e, CT_BUS__DDR);
  or or_2 (and_31_out[1], CT_RF__PCH, CT_RF__PCR);
  and and_31 (and_31_out[0], ~CT_RF__PCH, CT_RF__PCJ);  // And
  nor nor_1 (nor_1_out, CT_RF__PCR, CT_RF__PCJ);
  or or_3 (and_13_out[9], and_8_out, and_9_out, and_10_out);
  or or_4 (and_13_out[6], and_14_out, and_11_out, and_12_out);
  or or_5 (and_13_out[5], and_13_out[7], and_14_out, and_15_out);
  or or_6 (and_13_out[4], and_21_out, and_22_out, and_16_out);
  or or_7 (and_13_out[3], and_17_out, and_22_out, and_18_out);
  or or_8 (and_13_out[2], and_19_out, and_20_out);
  or or_9 (and_13_out[1], and_21_out, and_22_out, and_23_out);
  or or_10 (and_13_out[0], byte_D0[3], byte_D0[1], and_24_out, and_25_out);
  nor nor_2 (nor_2_out, and_26_out, and_27_out);
  add_4c32 add_4c32_1 (.a(PCS), .b(4'b0100), .s(add_4c32_1_s), .c(add_4c32_1_c));
  Register #(.Bits(32)) I_A__R (.D(PCS), .C(C_dt), .en(and_28_out), .Q(I_A__R_q));
  Register #(.Bits(32)) I_D__R (.D({multiplexer_4_out, I_D__bus[23:0]}), .C(C_dt), .en(dc_e), .Q(I_D__R_q));
  Register #(.Bits(32)) D_A__R (.D(multiplexer_3_out), .C(C_dt), .en(and_29_out), .Q(D_A__R_q));
  Register #(.Bits(32)) OD_D__R (.D(R_B), .C(C_dt), .en(and_30_out), .Q(OD_D__R_q));
  Multiplexer #(.Selector_Bits(2), .Bits(32)) multiplexer_5 (
    .sel(and_31_out), .in_0(add_4c32_1_s), .in_1(ALU_A_T__R), .in_2(PCA), .in_3(D_D__bus), .out(pcs_i));
  and and_32 (pc_ov, add_4c32_1_c, nor_1_out);
  assign I_A__bus = and_35_out ? I_A__R_q : 32'bz;  // Driver driver_9
  D_FF #(.Bits(32)) INST_3 (.D(I_D__R_q), .C(C_ct), .Q({byte_I0, byte_I1, byte_I2, byte_I3}));  // open: nQ
  assign D_A__bus = and_36_out ? D_A__R_q : 32'bz;  // Driver driver_10
  assign D_D__bus = and_37_out ? OD_D__R_q : 32'bz;  // Driver driver_11
  and and_33 (and_33_out, byte_D0_iv[0], byte_D0_iv[1], byte_D0[2], byte_D0[3], byte_D0[4], byte_D0_iv[5], byte_D0_iv[6], byte_D0_iv[7]);
  and and_34 (and_34_out, byte_D0[1], byte_D0_iv[2], byte_D0[3], byte_D0[4], byte_D0_iv[5], byte_D0_iv[6], byte_D0_iv[7]);
  and and_35 (and_35_out, CT_BUS__IAG, bus_e);
  and and_36 (and_36_out, CT_BUS__DAG, bus_e);
  and and_37 (and_37_out, CT_BUS__DDG, bus_e);
  and and_38 (and_38_out, byte_D0[4], byte_D0[3], byte_D0_iv[1], byte_D0_iv[2], byte_D0_iv[5], byte_D0_iv[6], byte_D0_iv[7]);
  or or_11 (or_11_out, and_33_out, and_34_out);
  and and_39 (and_39_out, byte_D0_iv[7], byte_D0_iv[6], byte_D0_iv[5], byte_D0_iv[4]);
  and and_40 (and_40_out, byte_D0_iv[7], byte_D0_iv[6], byte_D0_iv[5], byte_D0[4], byte_D0_iv[3]);
  assign {CT_RF__RA, CT_RF__MA} = or_12_out ? byte_D1 : 8'bz;  // Driver driver_12
  assign {CT_RF__RB, CT_RF__MB} = or_12_out ? byte_D2 : 8'bz;  // Driver driver_13
  assign CT_ALU__LD = or_12_out ? 1'b1 : 1'bz;  // Driver driver_14
  assign CT_ALU__CT = or_12_out ? {1'b0, and_13_out[7:0]} : 9'bz;  // Driver driver_15
  assign CT_ALU__M = or_12_out ? and_13_out[9] : 1'bz;  // Driver driver_16
  assign CT_FU__INST = or_12_out ? inst_DP : 4'bz;  // Driver driver_17
  assign CT_FU__WR = or_12_out ? byte_D1 : 8'bz;  // Driver driver_18
  assign CT_ALU__WD = or_12_out ? nor_2_out : 1'bz;  // Driver driver_19
  assign CT_ALU__WF = or_12_out ? 1'b1 : 1'bz;  // Driver driver_20
  assign {CT_RF__RB, CT_RF__MB} = or_11_out ? byte_D2 : 8'bz;  // Driver driver_21
  assign CT_DIR__LD = or_11_out ? 1'b1 : 1'bz;  // Driver driver_22
  assign CT_DIR__M = or_11_out ? and_34_out : 1'bz;  // Driver driver_23
  assign CT_DIR__MS = or_11_out ? byte_D0[0] : 1'bz;  // Driver driver_24
  assign CT_FU__INST = or_11_out ? inst_DP : 4'bz;  // Driver driver_25
  assign CT_FU__WR = or_11_out ? byte_D1 : 8'bz;  // Driver driver_26
  or or_12 (or_12_out, and_39_out, and_38_out, and_40_out);
  Multiplexer #(.Bits(4)) multiplexer_6 (.sel(com2), .in_0(com1_inst), .in_1(com2_inst), .out(multiplexer_6_out));
  BitExtender #(.inputBits(1), .outputBits(8)) bitextender_2 (.in(register_11_q_2[3]), .out(bitextender_2_out));
  ROB_gen rob_gen_1 (
    .D1_O(CT_RF__D1), .R1_O(CT_RF__R1), .W1_O(CT_RF__W1), .D2_O(CT_RF__D2), .R2_O(CT_RF__R2),
    .W2_O(CT_RF__W2), .C(C_dt), .E1(CT_ROB__GEN__STA), .E2(CT_ROB__GEN__STB), .D1(ROB_GEN_DA),
    .D2(ROB_GEN_DB), .R1(ROB_GEN_WA), .R2(ROB_GEN_WB), .inst1(ROB_GEN_INSTA), .inst2(ROB_GEN_INSTB),
    .com1(com1), .com2(com2), .com1_id(com1_inst), .com2_id(com2_inst));
  ROB_PC rob_pc_1 (
    .C(C_dt), .E(issue), .D(PCS_DC), .inst(inst_IS), .com_id(multiplexer_6_out), .read_id(inst_DP),
    .D1(pca_i), .D2(pc_read));
  ROB_SC rob_sc_1 (
    .C(C_dt), .E(CT_RF__SCSE), .dec(CT_RF__SCD), .off(CT_RF__SCN), .inst(inst_DP), .com1(com1), .com2(com2),
    .com1_id(com1_inst), .com2_id(com2_inst), .W1(CT_SC__W1), .dec1(CT_SC__D1), .off1(CT_SC__O1),
    .W2(CT_SC__W2), .dec2(CT_SC__D2), .off2(CT_SC__O2));
  ROB_FL rob_fl_1 (
    .C(C_dt), .E1(CT_ROB__FL__STA), .E2(CT_ROB__FL__STB), .D1(ALU_A_T__F), .D2(ALU_B_T__F),
    .inst1(ROB_FL_INSTA), .inst2(ROB_FL_INSTB), .com1(com1), .com2(com2), .com1_id(com1_inst),
    .com2_id(com2_inst), .W1_O(CT_FL__W1), .D1_O(CT_FL__D1), .W2_O(CT_FL__W2), .D2_O(CT_FL__D2));
  assign xor_1_out = FL[7:0] ^ bitextender_2_out;  // XOr xor_1, 8 bits wide
  not not_7 (not_7_out, byte_D1_ex[1]);
  or or_13 (or_13_out, byte_D1_ex[2], byte_D1_ex[0]);
  and and_41 (and_42_out[2], byte_D0_iv[7], byte_D0_iv[6], byte_D0[5]);
  and and_42 (and_42_out[1], byte_D0_iv[7], byte_D0[6], byte_D0_iv[5]);
  or or_14 (or_14_out, byte_D1_ex[0], byte_D1_ex[2]);
  Multiplexer #(.Selector_Bits(3)) multiplexer_7 (
    .sel(register_11_q), .in_0(xor_1_out[0]), .in_1(xor_1_out[1]), .in_2(xor_1_out[2]), .in_3(xor_1_out[3]),
    .in_4(xor_1_out[4]), .in_5(xor_1_out[5]), .in_6(xor_1_out[6]), .in_7(xor_1_out[7]),
    .out(multiplexer_7_out));
  and and_43 (and_43_out[1], not_7_out, or_13_out);
  nor nor_3 (and_43_out[2], byte_D1_ex[2], byte_D1_ex[1], byte_D1_ex[0]);
  not not_8 (not_8_out, byte_D1_ex[1]);
  not not_9 (not_9_out, byte_D0[0]);
  and and_44 (and_44_out[0], byte_D0[1], byte_D0[2], byte_D0[3], byte_D0[4], byte_D0_iv[5], byte_D0_iv[6], byte_D0_iv[7]);
  Register #(.Bits(3)) register_10 (.D({and_43_out, byte_D1_ex[1]}), .C(C_ct), .en(st_e__bf), .Q(register_10_q));
  or or_15 (and_42_out[0], and_42_out[2], and_42_out[1]);
  and and_45 (and_45_out[0], or_14_out, not_8_out);
  and and_46 (and_46_out, byte_D0_iv[4], byte_D0[5], byte_D0[6], byte_D0_iv[7]);
  Comparator #(.Bits(3)) comparator_2 (.a(byte_D0[2:0]), .b(3'b110), .eq(comparator_2_eq));  // open: gt, lt
  Register #(.Bits(4)) register_11 (.D(byte_D0[3:0]), .C(C_ct), .en(ex_e__bf), .Q({register_11_q_2[3], register_11_q}));
  Register register_12 (.D(xor_2_out), .C(C_ct), .en(st_e__bf), .Q(register_12_q));
  and and_47 (and_44_out[1], and_44_out[0], byte_D0[0]);
  and and_48 (and_44_out[2], not_9_out, and_44_out[0]);
  Multiplexer multiplexer_8 (.sel(ex_nop), .in_0(and_46_out), .in_1(1'b0), .out(multiplexer_8_out));
  assign st = register_12_q ? 1'b1 : 1'bz;  // Driver driver_27
  not not_10 (not_10_out, comparator_2_eq);
  xor xor_2 (xor_2_out, multiplexer_9_out, register_15_q);
  and and_49 (and_49_out, com1, CT_RF__W1);
  and and_50 (and_50_out, com2, CT_RF__W2);
  assign CT_BUS__DAM = and_44_out[0] ? 1'b1 : 1'bz;  // Driver driver_28
  assign CT_BUS__DAR = and_44_out[0] ? 1'b1 : 1'bz;  // Driver driver_29
  assign {CT_RF__RB, CT_RF__MB} = and_44_out[1] ? byte_D1_ex : 8'bz;  // Driver driver_30
  assign CT_BUS__DDR = and_44_out[1] ? 1'b1 : 1'bz;  // Driver driver_31
  Driver driver_32 (.in(1'b1), .en(and_44_out[2]));  // open: out
  assign CT_BUS__DASDN = and_44_out[2] ? {and_43_out, byte_D1_ex[1]} : 3'bz;  // Driver driver_33
  Register #(.Bits(3)) register_13 (.D(and_44_out), .C(C_ct), .en(st_e__bf), .Q(register_13_q));
  assign CT_BUS__DAG = register_13_q[0] ? 1'b1 : 1'bz;  // Driver driver_34
  assign CT_RF__SCSE = register_13_q[0] ? 1'b1 : 1'bz;  // Driver driver_35
  assign CT_RF__SCAS = register_13_q[0] ? 1'b1 : 1'bz;  // Driver driver_36
  assign D_ST = register_13_q[1] ? 1'b1 : 1'bz;  // Driver driver_37
  assign CT_RF__SCN = register_13_q[1] ? register_10_q : 3'bz;  // Driver driver_38
  assign CT_BUS__DDG = register_13_q[1] ? 1'b1 : 1'bz;  // Driver driver_39
  assign D_LD = register_13_q[2] ? 1'b1 : 1'bz;  // Driver driver_40
  assign CT_RF__SCD = register_13_q[2] ? 1'b1 : 1'bz;  // Driver driver_41
  assign CT_RF__SCN = register_13_q[2] ? register_10_q : 3'bz;  // Driver driver_42
  assign CT_RF__DM = register_13_q[2] ? 1'b1 : 1'bz;  // Driver driver_43
  assign {CT_RF__WS, CT_RF__WM} = register_13_q[2] ? byte_D1_st : 8'bz;  // Driver driver_44
  assign CT_RF__E = register_13_q[2] ? 1'b1 : 1'bz;  // Driver driver_45
  assign st = register_13_q[0] ? 1'b1 : 1'bz;  // Driver driver_46
  assign D_MD = and_42_out[0] ? {byte_D1_ex[1], and_45_out[0]} : 2'bz;  // Driver driver_47
  assign {CT_RF__RA, CT_RF__MA} = and_42_out[0] ? {byte_D0[4:0], 3'b000} : 8'bz;  // Driver driver_48
  assign CT_ALU__CT = and_42_out[0] ? 9'h19 : 9'bz;  // Driver driver_49
  assign CT_ALU__M_old = and_42_out[0] ? 2'b11 : 2'bz;  // Driver driver_50
  assign CT_BUS__DAR = and_42_out[0] ? 1'b1 : 1'bz;  // Driver driver_51
  assign {CT_RF__RB, CT_RF__MB} = and_42_out[1] ? byte_D1_ex : 8'bz;  // Driver driver_52
  assign CT_BUS__DDR = and_42_out[1] ? 1'b1 : 1'bz;  // Driver driver_53
  Driver driver_54 (.in(1'b1), .en(and_42_out[2]));  // open: out
  Register #(.Bits(3)) register_14 (.D(and_42_out), .C(C_ct), .en(st_e__bf), .Q(register_14_q));
  assign CT_BUS__DAG = register_14_q[0] ? 1'b1 : 1'bz;  // Driver driver_55
  assign D_ST = register_14_q[1] ? 1'b1 : 1'bz;  // Driver driver_56
  assign CT_BUS__DDG = register_14_q[1] ? 1'b1 : 1'bz;  // Driver driver_57
  assign D_LD = register_14_q[2] ? 1'b1 : 1'bz;  // Driver driver_58
  assign CT_RF__DM = register_14_q[2] ? 1'b1 : 1'bz;  // Driver driver_59
  assign {CT_RF__WS, CT_RF__WM} = register_14_q[2] ? byte_D1_st : 8'bz;  // Driver driver_60
  assign CT_RF__E = register_14_q[2] ? 1'b1 : 1'bz;  // Driver driver_61
  assign st = register_14_q[0] ? 1'b1 : 1'bz;  // Driver driver_62
  assign CT_DEP__EA = and_46_out ? 1'b1 : 1'bz;  // Driver driver_63
  assign {CT_DEP__URA, CT_DEP__UMA} = and_46_out ? byte_D1 : 8'bz;  // Driver driver_64
  assign CT_DEP__EB = and_46_out ? not_10_out : 1'bz;  // Driver driver_65
  assign {CT_DEP__URB, CT_DEP__UMB} = and_46_out ? 8'hf8 : 8'bz;  // Driver driver_66
  Register register_15 (.D(multiplexer_8_out), .C(C_ct), .en(ex_e__bf), .Q(register_15_q));
  assign ex_nop = multiplexer_9_out ? 1'b1 : 1'bz;  // Driver driver_67
  assign CT_BUS__IDM = multiplexer_9_out ? 1'b1 : 1'bz;  // Driver driver_68
  assign CT_ALU__CT = multiplexer_9_out ? 9'h19 : 9'bz;  // Driver driver_69
  assign CT_ALU__M_old = multiplexer_9_out ? 2'b11 : 2'bz;  // Driver driver_70
  assign {CT_RF__RA, CT_RF__MA} = multiplexer_9_out ? byte_D1_ex : 8'bz;  // Driver driver_71
  Register register_16 (.D(multiplexer_9_out), .C(C_ct), .en(st_e__bf), .Q(register_16_q));
  assign CT_RF__PCSE = register_16_q ? 1'b1 : 1'bz;  // Driver driver_72
  assign CT_RF__PCJ = register_16_q ? 1'b1 : 1'bz;  // Driver driver_73
  assign CT_BUS__IDM = register_16_q ? 1'b1 : 1'bz;  // Driver driver_74
  assign st = register_16_q ? 1'b1 : 1'bz;  // Driver driver_75
  Register register_17 (.D(register_16_q), .C(C_ct), .en(cm_e__bf), .Q(register_17_q));
  assign CT_BUS__IDM = register_17_q ? 1'b1 : 1'bz;  // Driver driver_76
  PullDown #(.Bits(16)) pulldown_9 (.out(V_inst));
  Multiplexer multiplexer_9 (.sel(multiplexer_7_out), .in_0(1'b0), .in_1(register_15_q), .out(multiplexer_9_out));
  regFile4 regfile4_1 (
    .C(C_dt), .E1(and_49_out), .E2(and_50_out), .D1(CT_RF__D1), .D2(CT_RF__D2), .RW1(CT_RF__R1[7:3]),
    .MW1(CT_RF__R1[2:0]), .RW2(CT_RF__R2[7:3]), .MW2(CT_RF__R2[2:0]), .RA(CT_RF__RA), .MA(CT_RF__MA),
    .RB(CT_RF__RB), .MB(CT_RF__MB), .PCS_i(pcs_i), .PCS_e(CT_RF__PCSE), .PCA_i(pca_i), .PCA_e(CT_RF__PCAE),
    .SCS_i(scs_i), .SCS_e(CT_RF__SCSE), .SCA_i(sca_i), .SCA_sel(CT_RF__SCAS), .SCA_e(CT_RF__SCAE),
    .FL_i({{24{1'b0}}, fl_i}), .FL_sel(CT_RF__FLS), .FL_e(4'b0001), .PC_read(pc_read), .R_A(R_A), .R_B(R_B),
    .PCS_O(PCS), .PCA_O(PCA), .SCS_O(SCS), .SCA_O(SCA), .FL_O(FL));
  PullDown pulldown_10 (.out(CT_RF__PCAE));
  PullDown pulldown_11 (.out(CT_RF__SCAE));
  and and_51 (and_51_out, com1, CT_SC__W1);
  and and_52 (and_52_out, com2, CT_SC__W2);
  and and_53 (and_53_out, byte_I0[0], byte_I0_iv[1], byte_I0_iv[2], byte_I0_iv[3], byte_I0[4], byte_I0[5], byte_I0[6], byte_I0_iv[7]);
  Multiplexer #(.Bits(32)) multiplexer_10 (
    .sel(CT_ALU__M), .in_0(R_B), .in_1({{16{1'b0}}, byte_D2_ex, byte_D3_ex}), .out(multiplexer_10_out));
  and and_54 (and_54_out, byte_D2_ex[7], CT_DIR__MS);
  BitExtender #(.inputBits(1)) bitextender_3 (.in(and_54_out), .out(bitextender_3_out));
  Multiplexer multiplexer_11 (.sel(STB_free), .in_0(xor_4_out), .in_1(register_31_q), .out(multiplexer_11_out));
  Register #(.Bits(32)) register_18 (.D(R_A), .C(C_dt), .en(multiplexer_11_out), .Q(register_18_q));
  Register #(.Bits(32)) register_19 (.D(R_B), .C(C_dt), .en(multiplexer_11_out), .Q(register_19_q));
  Register #(.Bits(16)) register_20 (
    .D({byte_D2_ex, byte_D3_ex}), .C(C_dt), .en(multiplexer_11_out), .Q(register_20_q));
  Register #(.Bits(4)) register_21 (.D(CT_FU__INST), .C(C_ct), .en(multiplexer_11_out), .Q(register_21_q));
  and and_55 (and_55_out, byte_I0_iv[0], byte_I0_iv[1], byte_I0_iv[2], byte_I0_iv[3], byte_I0[4], byte_I0[5], byte_I0[6], byte_I0_iv[7]);
  and and_56 (and_56_out, byte_I0[0], byte_I0[1], byte_I0_iv[2], byte_I0_iv[3], byte_I0[4], byte_I0[5], byte_I0[6], byte_I0_iv[7]);
  Multiplexer multiplexer_12 (.sel(ex_nop), .in_0(and_56_out), .in_1(1'b0));  // open: out
  or or_16 (CT_RF__SCAE, and_51_out, and_52_out);
  Register register_22 (.D(CT_ALU__LD), .C(C_ct), .en(multiplexer_13_out), .Q(register_22_q));
  Multiplexer multiplexer_13 (.sel(ALU_free), .in_0(xor_3_out), .in_1(register_22_q), .out(multiplexer_13_out));
  Register register_23 (.D(CT_ALU__WD), .C(C_ct), .en(multiplexer_13_out), .Q(register_23_q));
  Register register_24 (.D(CT_ALU__WF), .C(C_ct), .en(multiplexer_13_out), .Q(register_24_q));
  Register #(.Bits(32)) register_25 (.D(R_A), .C(C_dt), .en(multiplexer_13_out), .Q(register_25_q));
  Register #(.Bits(32)) register_26 (.D(multiplexer_10_out), .C(C_dt), .en(multiplexer_13_out), .Q(register_26_q));
  Register #(.Bits(8)) register_27 (.D(FL[7:0]), .C(C_dt), .en(multiplexer_13_out), .Q(register_27_q));
  Register #(.Bits(9)) register_28 (.D(CT_ALU__CT), .C(C_ct), .en(multiplexer_13_out), .Q(register_28_q));
  Register #(.Bits(8)) register_29 (.D(CT_FU__WR), .C(C_ct), .en(multiplexer_13_out), .Q(register_29_q));
  Register #(.Bits(4)) register_30 (.D(CT_FU__INST), .C(C_ct), .en(multiplexer_13_out), .Q(register_30_q));
  Register register_31 (.D(CT_STB__LD), .C(C_ct), .en(multiplexer_11_out), .Q(register_31_q));
  Multiplexer #(.Bits(32)) multiplexer_14 (
    .sel(register_31_q), .in_0(R_A), .in_1(register_18_q), .out(multiplexer_14_out));
  Multiplexer #(.Bits(32)) multiplexer_15 (
    .sel(register_31_q), .in_0(R_B), .in_1(register_19_q), .out(multiplexer_15_out));
  Multiplexer #(.Bits(16)) multiplexer_16 (
    .sel(register_31_q), .in_0({byte_D2_ex, byte_D3_ex}), .in_1(register_20_q), .out(multiplexer_16_out));
  Multiplexer #(.Bits(4)) multiplexer_17 (
    .sel(register_31_q), .in_0(CT_FU__INST), .in_1(register_21_q), .out(multiplexer_17_out));
  Multiplexer multiplexer_18 (.sel(ex_nop), .in_0(and_55_out), .in_1(1'b0), .out(multiplexer_18_out));
  Multiplexer multiplexer_19 (.sel(ex_nop), .in_0(and_53_out), .in_1(1'b0), .out(multiplexer_19_out));
  xor xor_3 (xor_3_out, ALU_busy, register_22_q);
  or or_17 (or_17_out, CT_ALU__WD, register_23_q);
  or or_18 (or_18_out, CT_ALU__WF, register_24_q);
  Multiplexer #(.Bits(32)) multiplexer_20 (
    .sel(register_22_q), .in_0(R_A), .in_1(register_25_q), .out(multiplexer_20_out));
  Multiplexer #(.Bits(32)) multiplexer_21 (
    .sel(register_22_q), .in_0(multiplexer_10_out), .in_1(register_26_q), .out(multiplexer_21_out));
  Multiplexer #(.Bits(8)) multiplexer_22 (
    .sel(register_22_q), .in_0(FL[7:0]), .in_1(register_27_q), .out(multiplexer_22_out));
  Multiplexer #(.Bits(9)) multiplexer_23 (
    .sel(register_22_q), .in_0(CT_ALU__CT), .in_1(register_28_q), .out(multiplexer_23_out));
  Multiplexer #(.Bits(8)) multiplexer_24 (
    .sel(register_22_q), .in_0(CT_FU__WR), .in_1(register_29_q), .out(multiplexer_24_out));
  Multiplexer #(.Bits(4)) multiplexer_25 (
    .sel(register_22_q), .in_0(CT_FU__INST), .in_1(register_30_q), .out(multiplexer_25_out));
  Multiplexer #(.Bits(32)) multiplexer_26 (
    .sel(CT_DIR__M), .in_0(R_A), .in_1({bitextender_3_out, byte_D2_ex, byte_D3_ex}), .out(multiplexer_26_out));
  or or_19 (or_19_out, CT_STB__LD, register_31_q);
  xor xor_4 (xor_4_out, STB_busy, register_31_q);
  assign CT_DEP__EA = and_55_out ? 1'b1 : 1'bz;  // Driver driver_77
  assign {CT_DEP__URA, CT_DEP__UMA} = and_55_out ? byte_I1 : 8'bz;  // Driver driver_78
  Register register_32 (.D(multiplexer_18_out), .C(C_ct), .en(ex_e__bf), .Q(register_32_q));
  assign ex_nop = register_32_q ? 1'b1 : 1'bz;  // Driver driver_79
  assign CT_BUS__IDM = register_32_q ? 1'b1 : 1'bz;  // Driver driver_80
  assign {CT_RF__RA, CT_RF__MA} = register_32_q ? byte_D1_ex : 8'bz;  // Driver driver_81
  assign CT_ALU__CT = register_32_q ? 9'h19 : 9'bz;  // Driver driver_82
  assign CT_ALU__M_old = register_32_q ? 2'b11 : 2'bz;  // Driver driver_83
  assign {CT_RF__RB, CT_RF__MB} = register_32_q ? 8'he8 : 8'bz;  // Driver driver_84
  assign CT_BUS__DAM = register_32_q ? 1'b1 : 1'bz;  // Driver driver_85
  assign CT_BUS__DAR = register_32_q ? 1'b1 : 1'bz;  // Driver driver_86
  assign CT_BUS__DDR = register_32_q ? 1'b1 : 1'bz;  // Driver driver_87
  Register register_33 (.D(register_32_q), .C(C_ct), .en(st_e__bf), .Q(register_33_q));
  assign CT_BUS__IDM = register_33_q ? 1'b1 : 1'bz;  // Driver driver_88
  assign CT_RF__SCSE = register_33_q ? 1'b1 : 1'bz;  // Driver driver_89
  assign CT_RF__SCAS = register_33_q ? 1'b1 : 1'bz;  // Driver driver_90
  assign CT_RF__SCN = register_33_q ? 3'b100 : 3'bz;  // Driver driver_91
  assign CT_RF__PCSE = register_33_q ? 1'b1 : 1'bz;  // Driver driver_92
  assign CT_RF__PCJ = register_33_q ? 1'b1 : 1'bz;  // Driver driver_93
  assign CT_BUS__DAG = register_33_q ? 1'b1 : 1'bz;  // Driver driver_94
  assign CT_BUS__DDG = register_33_q ? 1'b1 : 1'bz;  // Driver driver_95
  assign D_ST = register_33_q ? 1'b1 : 1'bz;  // Driver driver_96
  assign st = register_33_q ? 1'b1 : 1'bz;  // Driver driver_97
  Register register_34 (.D(register_33_q), .C(C_ct), .en(cm_e__bf), .Q(register_34_q));
  assign CT_BUS__IDM = register_34_q ? 1'b1 : 1'bz;  // Driver driver_98
  Register register_35 (.D(multiplexer_19_out), .C(C_ct), .en(ex_e__bf), .Q(register_35_q));
  assign ex_nop = register_35_q ? 1'b1 : 1'bz;  // Driver driver_99
  assign CT_BUS__IDM = register_35_q ? 1'b1 : 1'bz;  // Driver driver_100
  assign CT_BUS__DAM = register_35_q ? 1'b1 : 1'bz;  // Driver driver_101
  assign CT_BUS__DAR = register_35_q ? 1'b1 : 1'bz;  // Driver driver_102
  assign CT_BUS__DASDN = register_35_q ? 3'b100 : 3'bz;  // Driver driver_103
  Register register_36 (.D(register_35_q), .C(C_ct), .en(st_e__bf), .Q(register_36_q));
  assign CT_BUS__IDM = register_36_q ? 1'b1 : 1'bz;  // Driver driver_104
  assign D_LD = register_36_q ? 1'b1 : 1'bz;  // Driver driver_105
  assign CT_RF__SCSE = register_36_q ? 1'b1 : 1'bz;  // Driver driver_106
  assign CT_RF__SCD = register_36_q ? 1'b1 : 1'bz;  // Driver driver_107
  assign CT_RF__SCN = register_36_q ? 3'b100 : 3'bz;  // Driver driver_108
  assign CT_RF__SCAS = register_36_q ? 1'b1 : 1'bz;  // Driver driver_109
  assign CT_RF__PCSE = register_36_q ? 1'b1 : 1'bz;  // Driver driver_110
  assign CT_RF__PCJ = register_36_q ? 1'b1 : 1'bz;  // Driver driver_111
  assign CT_RF__PCR = register_36_q ? 1'b1 : 1'bz;  // Driver driver_112
  assign CT_BUS__DAG = register_36_q ? 1'b1 : 1'bz;  // Driver driver_113
  assign st = register_36_q ? 1'b1 : 1'bz;  // Driver driver_114
  Register register_37 (.D(register_36_q), .C(C_ct), .en(cm_e__bf), .Q(register_37_q));
  assign CT_BUS__IDM = register_37_q ? 1'b1 : 1'bz;  // Driver driver_115
  Register register_38 (.D(1'b0), .C(C_ct), .en(ex_e__bf), .Q(register_38_q));
  assign ex_nop = register_38_q ? 1'b1 : 1'bz;  // Driver driver_116
  assign hlt = register_38_q ? 1'b1 : 1'bz;  // Driver driver_117
  assign CT_BUS__IDM = register_38_q ? 1'b1 : 1'bz;  // Driver driver_118
  assign CT_BUS__IDM = register_38_q ? 1'b1 : 1'bz;  // Driver driver_119
  Register register_39 (.D(register_38_q), .C(C_ct), .en(st_e__bf), .Q(register_39_q));
  assign CT_RF__PCH = register_39_q ? 1'b1 : 1'bz;  // Driver driver_120
  assign CT_RF__PCSE = register_39_q ? 1'b1 : 1'bz;  // Driver driver_121
  assign CT_BUS__IDM = register_39_q ? 1'b1 : 1'bz;  // Driver driver_122
  assign st = register_39_q ? 1'b1 : 1'bz;  // Driver driver_123
  or or_20 (or_20_out, CT_ALU__LD, register_22_q);
  Multiplexer multiplexer_27 (.sel(ALU_free), .in_0(xor_6_out), .in_1(ALU_busy), .out(multiplexer_27_out));
  Register register_40 (.D(or_17_out), .C(C_ct), .en(multiplexer_27_out), .Q(register_40_q));
  Register register_41 (.D(or_18_out), .C(C_ct), .en(multiplexer_27_out), .Q(register_41_q));
  Register #(.Bits(32)) register_42 (.D(multiplexer_20_out), .C(C_dt), .en(multiplexer_27_out), .Q(register_42_q));
  Register #(.Bits(32)) register_43 (.D(multiplexer_21_out), .C(C_dt), .en(multiplexer_27_out), .Q(register_43_q));
  Register #(.Bits(8)) register_44 (.D(multiplexer_22_out), .C(C_dt), .en(multiplexer_27_out), .Q(register_44_q));
  Register #(.Bits(9)) register_45 (.D(multiplexer_23_out), .C(C_ct), .en(multiplexer_27_out), .Q(register_45_q));
  Register #(.Bits(8)) register_46 (.D(multiplexer_24_out), .C(C_ct), .en(multiplexer_27_out), .Q(register_46_q));
  Register #(.Bits(4)) register_47 (.D(multiplexer_25_out), .C(C_ct), .en(multiplexer_27_out), .Q(register_47_q));
  Register register_48 (.D(or_19_out), .C(C_ct), .en(multiplexer_28_out), .Q(STB_busy));
  Multiplexer multiplexer_28 (.sel(STB_free), .in_0(xor_5_out), .in_1(STB_busy), .out(multiplexer_28_out));
  Register #(.Bits(32)) register_49 (.D(multiplexer_14_out), .C(C_dt), .en(multiplexer_28_out), .Q(register_49_q));
  Register #(.Bits(32)) register_50 (.D(multiplexer_15_out), .C(C_dt), .en(multiplexer_28_out), .Q(register_50_q));
  Register #(.Bits(16)) register_51 (.D(multiplexer_16_out), .C(C_dt), .en(multiplexer_28_out), .Q(register_51_q));
  Register #(.Bits(4)) register_52 (.D(multiplexer_17_out), .C(C_ct), .en(multiplexer_28_out), .Q(register_52_q));
  Multiplexer #(.Bits(3)) multiplexer_29 (
    .sel(and_52_out), .in_0(CT_SC__O1), .in_1(CT_SC__O2), .out(multiplexer_29_out));
  Register register_53 (.D(or_20_out), .C(C_ct), .en(multiplexer_27_out), .Q(ALU_busy));
  Multiplexer #(.Bits(32)) multiplexer_30 (.sel(ALU_busy), .in_0(R_A), .in_1(register_42_q), .out(multiplexer_30_out));
  Multiplexer #(.Bits(32)) multiplexer_31 (
    .sel(ALU_busy), .in_0(multiplexer_10_out), .in_1(register_43_q), .out(multiplexer_31_out));
  Multiplexer #(.Bits(8)) multiplexer_32 (
    .sel(ALU_busy), .in_0(FL[7:0]), .in_1(register_44_q), .out(multiplexer_32_out));
  Multiplexer #(.Bits(9)) multiplexer_33 (
    .sel(ALU_busy), .in_0(CT_ALU__CT), .in_1(register_45_q), .out(multiplexer_33_out));
  Multiplexer #(.Bits(8)) multiplexer_34 (
    .sel(ALU_busy), .in_0(CT_FU__WR), .in_1(register_46_q), .out(multiplexer_34_out));
  Multiplexer #(.Bits(4)) multiplexer_35 (
    .sel(ALU_busy), .in_0(CT_FU__INST), .in_1(register_47_q), .out(multiplexer_35_out));
  Multiplexer multiplexer_36 (.sel(DIR_free), .in_0(xor_7_out), .in_1(register_57_q), .out(multiplexer_36_out));
  Register #(.Bits(32)) register_54 (.D(multiplexer_26_out), .C(C_dt), .en(multiplexer_36_out), .Q(register_54_q));
  Register #(.Bits(8)) register_55 (.D(CT_FU__WR), .C(C_ct), .en(multiplexer_36_out), .Q(register_55_q));
  Register #(.Bits(4)) register_56 (.D(CT_FU__INST), .C(C_ct), .en(multiplexer_36_out), .Q(register_56_q));
  xor xor_5 (xor_5_out, STB_busy, STB_busy);
  Multiplexer #(.Bits(32)) multiplexer_37 (.sel(STB_busy), .in_0(R_A), .in_1(register_49_q), .out(multiplexer_37_out));
  Multiplexer #(.Bits(32)) multiplexer_38 (.sel(STB_busy), .in_0(R_B), .in_1(register_50_q), .out(multiplexer_38_out));
  Multiplexer #(.Bits(16)) multiplexer_39 (
    .sel(STB_busy), .in_0({byte_D2_ex, byte_D3_ex}), .in_1(register_51_q), .out(multiplexer_39_out));
  Multiplexer #(.Bits(4)) multiplexer_40 (
    .sel(STB_busy), .in_0(CT_FU__INST), .in_1(register_52_q), .out(multiplexer_40_out));
  Multiplexer multiplexer_41 (.sel(and_52_out), .in_0(CT_SC__D1), .in_1(CT_SC__D2), .out(multiplexer_41_out));
  or or_21 (or_21_out, CT_ALU__LD, ALU_busy);
  xor xor_6 (xor_6_out, ALU_busy, ALU_busy);
  or or_22 (or_22_out, CT_ALU__WD, register_40_q);
  or or_23 (or_23_out, CT_ALU__WF, register_41_q);
  Register register_57 (.D(CT_DIR__LD), .C(C_ct), .en(multiplexer_36_out), .Q(register_57_q));
  xor xor_7 (xor_7_out, register_68_q, register_57_q);
  Multiplexer #(.Bits(32)) multiplexer_42 (
    .sel(register_57_q), .in_0(multiplexer_26_out), .in_1(register_54_q), .out(multiplexer_42_out));
  Multiplexer #(.Bits(8)) multiplexer_43 (
    .sel(register_57_q), .in_0(CT_FU__WR), .in_1(register_55_q), .out(multiplexer_43_out));
  Multiplexer #(.Bits(4)) multiplexer_44 (
    .sel(register_57_q), .in_0(CT_FU__INST), .in_1(register_56_q), .out(multiplexer_44_out));
  or or_24 (or_24_out, CT_STB__LD, STB_busy);
  Register #(.Bits(32)) register_58 (.D(multiplexer_37_out), .C(C_dt), .en(STB_LD), .Q(register_58_q));
  Register #(.Bits(32)) register_59 (.D(multiplexer_38_out), .C(C_dt), .en(STB_LD), .Q(register_59_q));
  Register #(.Bits(16)) register_60 (.D(multiplexer_39_out), .C(C_dt), .en(STB_LD), .Q(register_60_q));
  Register #(.Bits(4)) register_61 (.D(multiplexer_40_out), .C(C_ct), .en(STB_LD), .Q(STB_INST));
  addsub_4c32 addsub_4c32_1 (.a(SCS), .b({1'b0, CT_RF__SCN}), .sub(CT_RF__SCD), .s(scs_i), .c(sc_ov));
  addsub_4c32 addsub_4c32_2 (.a(SCA), .b({1'b0, multiplexer_29_out}), .sub(multiplexer_41_out), .s(sca_i), .c(sc_ov));
  Register #(.Bits(32)) register_62 (.D(multiplexer_30_out), .C(C_dt), .en(ALU_A_LD), .Q(ALU_A_A));
  Register #(.Bits(32)) register_63 (.D(multiplexer_31_out), .C(C_dt), .en(ALU_A_LD), .Q(ALU_A_B));
  Register #(.Bits(8)) register_64 (.D(multiplexer_32_out), .C(C_dt), .en(ALU_A_LD), .Q(ALU_A_FI));
  Register #(.Bits(9)) register_65 (.D(multiplexer_33_out), .C(C_ct), .en(ALU_A_LD), .Q(ALU_A_CT));
  Register #(.Bits(8)) register_66 (.D(multiplexer_34_out), .C(C_ct), .en(ALU_A_LD), .Q({ALU_A_WR, ALU_A_RM}));
  Register #(.Bits(4)) register_67 (.D(multiplexer_35_out), .C(C_ct), .en(ALU_A_LD), .Q(ALU_A_INST));
  or or_25 (or_25_out, CT_DIR__LD, register_57_q);
  Multiplexer multiplexer_45 (.sel(DIR_free), .in_0(xor_8_out), .in_1(register_68_q), .out(multiplexer_45_out));
  and and_57 (and_57_out[0], ALU_A_LD, or_22_out);
  and and_58 (and_57_out[1], ALU_A_LD, or_23_out);
  and and_59 (and_59_out[0], ALU_B_LD, or_22_out);
  and and_60 (and_59_out[1], ALU_B_LD, or_23_out);
  Register register_68 (.D(or_25_out), .C(C_ct), .en(multiplexer_45_out), .Q(register_68_q));
  Register #(.Bits(32)) register_69 (.D(multiplexer_42_out), .C(C_dt), .en(multiplexer_45_out), .Q(register_69_q));
  Register #(.Bits(8)) register_70 (.D(multiplexer_43_out), .C(C_ct), .en(multiplexer_45_out), .Q(register_70_q));
  Register #(.Bits(4)) register_71 (.D(multiplexer_44_out), .C(C_ct), .en(multiplexer_45_out), .Q(register_71_q));
  add_s16c32 add_s16c32_1 (.a(register_59_q), .b(register_60_q), .s(add_s16c32_1_s));  // open: c
  or or_26 (or_26_out, CT_DIR__LD, register_68_q);
  xor xor_8 (xor_8_out, DIR_busy, register_68_q);
  Multiplexer #(.Bits(32)) multiplexer_46 (
    .sel(register_68_q), .in_0(multiplexer_26_out), .in_1(register_69_q), .out(multiplexer_46_out));
  Multiplexer #(.Bits(8)) multiplexer_47 (
    .sel(register_68_q), .in_0(CT_FU__WR), .in_1(register_70_q), .out(multiplexer_47_out));
  Multiplexer #(.Bits(4)) multiplexer_48 (
    .sel(register_68_q), .in_0(CT_FU__INST), .in_1(register_71_q), .out(multiplexer_48_out));
  and and_61 (and_61_out, or_24_out, STB_free);
  and and_62 (and_62_out, ~and_57_out[0], ALU_A_STD);  // And
  and and_63 (and_63_out, ~and_57_out[1], ALU_A_STF);  // And
  and and_64 (and_64_out, ~and_59_out[0], ALU_A_STD);  // And
  and and_65 (and_65_out, ~and_59_out[1], ALU_A_STF);  // And
  Register #(.Bits(32)) register_72 (.D(multiplexer_30_out), .C(C_dt), .en(ALU_B_LD), .Q(ALU_B_A));
  Register #(.Bits(32)) register_73 (.D(multiplexer_31_out), .C(C_dt), .en(ALU_B_LD), .Q(ALU_B_B));
  Register #(.Bits(8)) register_74 (.D(multiplexer_32_out), .C(C_dt), .en(ALU_B_LD), .Q(ALU_B_FI));
  Register #(.Bits(9)) register_75 (.D(multiplexer_33_out), .C(C_ct), .en(ALU_A_LD), .Q(ALU_B_CT));
  Register #(.Bits(8)) register_76 (.D(multiplexer_34_out), .C(C_ct), .en(ALU_B_LD), .Q({ALU_B_WR, ALU_B_RM}));
  Register #(.Bits(4)) register_77 (.D(multiplexer_35_out), .C(C_ct), .en(ALU_B_LD), .Q(ALU_B_INST));
  Register #(.Bits(32)) register_78 (.D(multiplexer_46_out), .C(C_dt), .en(DIR_LD), .Q(DIR));
  Register #(.Bits(8)) register_79 (.D(multiplexer_47_out), .C(C_ct), .en(DIR_LD), .Q(DIR_WR));
  Register #(.Bits(4)) register_80 (.D(multiplexer_48_out), .C(C_ct), .en(DIR_LD), .Q(DIR_INST));
  DipSwitch dipswitch_4 (.out(dipswitch_4_out));
  D_FF #(.Bits(2)) d_ff_1 (.D(and_57_out), .C(C_ct), .Q(d_ff_1_q));  // open: nQ
  RS_FF rs_ff_1 (.S(and_57_out[0]), .C(C_ct), .R(and_62_out), .nQ(rs_ff_1_nq));  // open: Q
  RS_FF rs_ff_2 (.S(and_57_out[1]), .C(C_ct), .R(and_63_out), .nQ(rs_ff_2_nq));  // open: Q
  D_FF #(.Bits(2)) d_ff_2 (.D(and_59_out), .C(C_ct), .Q(d_ff_2_q));  // open: nQ
  RS_FF rs_ff_3 (.S(and_59_out[0]), .C(C_ct), .R(and_64_out), .nQ(rs_ff_3_nq));  // open: Q
  RS_FF rs_ff_4 (.S(and_59_out[1]), .C(C_ct), .R(and_65_out), .nQ(rs_ff_4_nq));  // open: Q
  and and_66 (and_66_out, ~or_26_out, DIR_ST);  // And
  and and_67 (and_67_out, ~or_26_out, DIR_RD);  // And
  bus16_demux bus16_demux_1 (.bus(V_inst), .E(and_61_out), .id(STB_INST));
  store_buffer store_buffer_1 (
    .C(C_dt), .LD(dipswitch_4_out), .W_d(or_24_out), .inst_W(STB_INST), .D(register_58_q),
    .A(add_s16c32_1_s), .W_id(CT_ISS__OSTB), .epoch(epoch_IS), .inst(inst_IS), .com1(com1), .com2(com2),
    .com1_id(com1_inst), .com2_id(com2_inst), .ld_ep(LD_ep), .ld_id(LD_id), .ld_addr(LD_addr),
    .full(STB_busy), .V(store_buffer_1_v), .D_O(store_buffer_1_d_o), .A_O(store_buffer_1_a_o),
    .ld_V(store_buffer_1_ld_v), .ld_D(store_buffer_1_ld_d));
  D_FF #(.Bits(2)) d_ff_3 (.D(d_ff_1_q), .C(C_ct), .Q({d_ff_3_q[1], ALU_A_RE}));  // open: nQ
  D_FF #(.Bits(2)) d_ff_4 (.D(d_ff_2_q), .C(C_ct), .Q({d_ff_4_q[1], ALU_B_RE}));  // open: nQ
  RS_FF rs_ff_5 (.S(or_26_out), .C(C_ct), .R(and_66_out), .nQ(rs_ff_5_nq));  // open: Q
  RS_FF rs_ff_6 (.S(or_26_out), .C(C_ct), .R(and_67_out), .Q(DIR_RD));  // open: nQ
  not not_11 (STB_free, STB_busy);
  and and_68 (and_68_out, ALU_B_STD, ~and_74_out);  // And
  and and_69 (and_69_out, ALU_B_STF, ~and_74_out);  // And
  or or_27 (DIR_free, DIR_ST, rs_ff_5_nq);
  bus16_demux bus16_demux_2 (.bus(V_inst), .E(DIR_ST), .id(DIR_INST));
  and and_70 (STB_LD, CT_STB__LD, STB_free);
  and and_71 (and_71_out, com1, CT_FL__W1);
  and and_72 (and_72_out, com2, CT_FL__W2);
  RS_FF rs_ff_7 (.S(ALU_A_RE), .C(C_ct), .R(ALU_A_FRD), .Q(ALU_A_DRD));  // open: nQ
  RS_FF rs_ff_8 (.S(d_ff_3_q[1]), .C(C_ct), .R(ALU_A_FRD), .Q(ALU_A_FRD));  // open: nQ
  RS_FF rs_ff_9 (.S(ALU_B_RE), .C(C_ct), .R(ALU_B_DRD), .Q(ALU_B_DRD));  // open: nQ
  RS_FF rs_ff_10 (.S(d_ff_4_q[1]), .C(C_ct), .R(ALU_B_FRD), .Q(ALU_B_FRD));  // open: nQ
  RS_FF rs_ff_11 (.S(and_68_out), .C(C_ct), .R(and_74_out), .Q(rs_ff_11_q));  // open: nQ
  RS_FF rs_ff_12 (.S(and_69_out), .C(C_ct), .R(and_74_out), .Q(rs_ff_12_q));  // open: nQ
  // alu_32 alu_32_1: pin names not known; wires that end beside it: ALU_A_A, ALU_A_B, ALU_A_FI, ALU_A_CT, ALU_A_RM, alu_32_1_p6, alu_32_1_p6, alu_32_1_p8, alu_32_1_p9, alu_32_1_p9, alu_32_1_p11, alu_32_1_p12, alu_32_1_p12, alu_32_1_p14, ALU_A_R, ALU_A_F
  alu_32 alu_32_2 (
    .A(ALU_B_A), .B(ALU_B_B), .F_I(ALU_B_FI), .CT(ALU_B_CT), .RM(ALU_B_RM), .E_A(alu_32_1_p8),
    .E_B(alu_32_1_p11), .E(alu_32_1_p14), .R_O(ALU_B_R), .F_O(ALU_B_F));
  or or_28 (or_28_out, ALU_B_STD, rs_ff_11_q);
  or or_29 (or_29_out, ALU_B_STF, rs_ff_12_q);
  PullDown #(.Bits(32)) pulldown_12 (.out(alu_32_1_p12));
  PullDown #(.Bits(32)) pulldown_13 (.out(alu_32_1_p14));
  and and_73 (DIR_LD, or_26_out, DIR_free);
  not not_12 (DIR_busy, DIR_free);
  or or_30 (CT_RF__FLS, and_71_out, and_72_out);
  or or_31 (or_31_out, ALU_A_STD, rs_ff_1_nq);
  or or_32 (or_32_out, ALU_A_STF, rs_ff_2_nq);
  or or_33 (or_33_out, ALU_B_STD, rs_ff_3_nq);
  or or_34 (or_34_out, ALU_B_STF, rs_ff_4_nq);
  and and_74 (and_74_out, or_28_out, or_29_out);
  bus16_demux bus16_demux_3 (.bus(V_inst), .E(and_74_out), .id(ALU_B_INST));
  and and_75 (ALU_A_LD, or_21_out, or_32_out, or_31_out);
  and and_76 (ALU_A_LRD, or_31_out, or_32_out);
  nand nand_1 (nand_1_out, or_31_out, or_32_out);
  and and_77 (ALU_B_LD, nand_1_out, CT_ALU__LD, or_34_out, or_33_out);
  and and_78 (ALU_B_LRD, or_33_out, or_34_out);
  and and_79 (and_79_out, ALU_A_STD, ~and_81_out);  // And
  and and_80 (and_80_out, ALU_A_STF, ~and_81_out);  // And
  Register #(.Bits(32)) register_81 (.D(ALU_A_R), .C(C_dt), .en(ALU_A_RE), .Q(ALU_A_T__R));
  Register #(.Bits(8)) register_82 (.D(ALU_A_F), .C(C_dt), .en(ALU_A_RE), .Q(ALU_A_T__F));
  Register #(.Bits(32)) register_83 (.D(ALU_B_R), .C(C_dt), .en(ALU_B_RE), .Q(ALU_B_T__R));
  Register #(.Bits(8)) register_84 (.D(ALU_B_F), .C(C_dt), .en(ALU_B_RE), .Q(ALU_B_T__F));
  RS_FF rs_ff_13 (.S(and_79_out), .C(C_ct), .R(and_81_out), .Q(rs_ff_13_q));  // open: nQ
  RS_FF rs_ff_14 (.S(and_80_out), .C(C_ct), .R(and_81_out), .Q(rs_ff_14_q));  // open: nQ
  Multiplexer #(.Bits(8)) multiplexer_49 (.sel(and_72_out), .in_0(CT_FL__D1), .in_1(CT_FL__D2), .out(fl_i));
  or or_35 (or_35_out, ALU_A_STD, rs_ff_13_q);
  or or_36 (or_36_out, ALU_A_STF, rs_ff_14_q);
  nor nor_4 (ALU_busy, ALU_A_LRD, ALU_B_LRD);
  or or_37 (ALU_free, ALU_A_LRD, ALU_B_LRD);
  and and_81 (and_81_out, or_35_out, or_36_out);
  bus16_demux bus16_demux_4 (.bus(V_inst), .E(and_81_out), .id(ALU_A_INST));
  and and_82 (and_82_out, byte_I0[3], byte_I0[0]);
  and and_83 (and_83_out, byte_I0[2], byte_I0[0]);
  and and_84 (and_84_out, byte_I0_iv[3], byte_I0_iv[2], byte_I0[1], byte_I0_iv[0]);
  and and_85 (and_85_out, byte_I0_iv[2], byte_I0_iv[0]);
  and and_86 (and_86_out, byte_I0[2], byte_I0[0]);
  and and_87 (and_87_out, byte_I0[1], byte_I0[2], byte_I0[4]);
  and and_88 (and_88_out, byte_I0[3], byte_I0[4]);
  and and_89 (and_89_out, byte_I0[4], byte_I0[3], byte_I0_iv[1], byte_I0_iv[2], byte_I0_iv[5], byte_I0_iv[6], byte_I0_iv[7]);
  or or_38 (or_38_out, and_82_out, and_83_out, and_84_out);
  or or_39 (or_39_out, byte_I0[3], byte_I0[1], and_85_out, and_86_out);
  nor nor_5 (nor_5_out, and_87_out, and_88_out);
  and and_90 (and_90_out, byte_I0_iv[7], byte_I0_iv[6], byte_I0[5]);
  and and_91 (and_91_out, byte_I0_iv[7], byte_I0[6], byte_I0_iv[5]);
  PullDown pulldown_14 (.out(CT_ALU__M));
  PullDown pulldown_15 (.out(CT_ALU__LD));
  PullDown pulldown_16 (.out(CT_ALU__WD));
  PullDown pulldown_17 (.out(CT_ALU__WF));
  PullDown #(.Bits(4)) pulldown_18 (.out(CT_FU__INST));
  PullDown #(.Bits(8)) pulldown_19 (.out(CT_FU__WR));
  PullDown pulldown_20 (.out(CT_DIR__LD));
  PullDown pulldown_21 (.out(CT_DIR__M));
  PullDown pulldown_22 (.out(CT_DIR__MS));
  and and_92 (and_92_out, byte_I0_iv[0], byte_I0_iv[1], byte_I0[2], byte_I0[3], byte_I0[4], byte_I0_iv[5], byte_I0_iv[6], byte_I0_iv[7]);
  and and_93 (and_93_out, byte_I0[1], byte_I0_iv[2], byte_I0[3], byte_I0[4], byte_I0_iv[5], byte_I0_iv[6], byte_I0_iv[7]);
  and and_94 (and_94_out, byte_I0[1], byte_I0[2], byte_I0[3], byte_I0[4], byte_I0_iv[5], byte_I0_iv[6], byte_I0_iv[7]);
  or or_40 (or_40_out, and_90_out, and_91_out);
  and and_95 (and_95_out, byte_I0_iv[7], byte_I0_iv[6], byte_I0_iv[5], byte_I0_iv[4]);
  and and_96 (and_96_out, byte_I0_iv[7], byte_I0_iv[6], byte_I0_iv[5], byte_I0[4], byte_I0_iv[3]);
  or or_41 (or_41_out, and_92_out, and_93_out);
  not not_13 (not_13_out, byte_I0[0]);
  not not_14 (not_14_out, or_38_out);
  and and_97 (and_97_out, and_94_out, byte_I0[0]);
  and and_98 (and_98_out, not_13_out, and_94_out);
  or or_42 (or_42_out, and_95_out, and_89_out, and_96_out);
  assign issue = or_42_out ? dp_e : 1'bz;  // Driver driver_124
  assign CT_ISS__URA = or_42_out ? 1'b1 : 1'bz;  // Driver driver_125
  assign CT_ISS__URB = or_42_out ? not_14_out : 1'bz;  // Driver driver_126
  assign CT_ISS__RA = or_42_out ? byte_I1[7:3] : 5'bz;  // Driver driver_127
  assign CT_ISS__RB = or_42_out ? byte_I2[7:3] : 5'bz;  // Driver driver_128
  assign CT_ISS__UFL = or_42_out ? or_39_out : 1'bz;  // Driver driver_129
  assign CT_ISS__ORC = or_42_out ? nor_5_out : 1'bz;  // Driver driver_130
  assign CT_ISS__RC = or_42_out ? byte_I1[7:3] : 5'bz;  // Driver driver_131
  assign CT_ISS__OFL = or_42_out ? 1'b1 : 1'bz;  // Driver driver_132
  assign CT_ISS__UFU = or_42_out ? 3'b001 : 3'bz;  // Driver driver_133
  assign CT_ISS__URA = and_92_out ? 1'b1 : 1'bz;  // Driver driver_134
  assign CT_ISS__RA = and_92_out ? byte_I2[7:3] : 5'bz;  // Driver driver_135
  assign issue = or_41_out ? dp_e : 1'bz;  // Driver driver_136
  assign CT_ISS__ORC = or_41_out ? 1'b1 : 1'bz;  // Driver driver_137
  assign CT_ISS__RC = or_41_out ? byte_I1[7:3] : 5'bz;  // Driver driver_138
  assign CT_ISS__UFU = or_41_out ? 3'b010 : 3'bz;  // Driver driver_139
  assign issue = and_94_out ? dp_e : 1'bz;  // Driver driver_140
  assign CT_ISS__USC = and_94_out ? 1'b1 : 1'bz;  // Driver driver_141
  assign CT_ISS__OSC = and_94_out ? 1'b1 : 1'bz;  // Driver driver_142
  assign CT_ISS__URA = and_97_out ? 1'b1 : 1'bz;  // Driver driver_143
  assign CT_ISS__RA = and_97_out ? byte_I1[7:3] : 5'bz;  // Driver driver_144
  assign CT_ISS__ORC = and_98_out ? 1'b1 : 1'bz;  // Driver driver_145
  assign CT_ISS__RC = and_98_out ? byte_I1[7:3] : 5'bz;  // Driver driver_146
  assign issue = or_40_out ? dp_e : 1'bz;  // Driver driver_147
  assign CT_ISS__URA = or_40_out ? 1'b1 : 1'bz;  // Driver driver_148
  assign CT_ISS__RA = or_40_out ? byte_I0[4:0] : 5'bz;  // Driver driver_149
  assign CT_ISS__URB = and_91_out ? 1'b1 : 1'bz;  // Driver driver_150
  assign CT_ISS__RB = and_91_out ? byte_I1[7:3] : 5'bz;  // Driver driver_151
  assign CT_ISS__ORC = and_90_out ? 1'b1 : 1'bz;  // Driver driver_152
  assign CT_ISS__RC = and_90_out ? byte_I1[7:3] : 5'bz;  // Driver driver_153
  store_controller store_controller_1 (
    .C(C_ct), .in1(ALU_A_DRD), .in2(ALU_B_DRD), .in3(1'b0), .in4(1'b0), .in5(1'b0), .in6(DIR_RD), .in7(1'b0),
    .in8(1'b0), .D1_sel(store_controller_1_d1_sel), .D2_sel(store_controller_1_d2_sel),
    .ST1(CT_ROB__GEN__STA), .ST2(CT_ROB__GEN__STB), .out1(ALU_A_STD), .out2(ALU_B_STD), .out6(DIR_ST));  // open: out3, out4, out5, out7, out8
  store_controller store_controller_2 (
    .C(C_ct), .in1(ALU_B_FRD), .in2(ALU_A_FRD), .in3(1'b0), .in4(1'b0), .in5(1'b0), .in6(1'b0), .in7(1'b0),
    .in8(1'b0), .D1_sel(store_controller_2_d1_sel), .D2_sel(store_controller_2_d2_sel),
    .ST1(CT_ROB__FL__STA), .ST2(CT_ROB__FL__STB), .out1(ALU_A_STF), .out2(ALU_B_STF));  // open: out3, out4, out5, out6, out7, out8
  D_FF #(.Bits(8)) d_ff_5 (.D({{5{1'b0}}, DIR_free, ALU_free, 1'b1}), .C(C_ct), .Q(FU_free));  // open: nQ
  // data_select_32 data_select_32_1: pin names not known; wires that end beside it: store_controller_1_d1_sel, store_controller_1_d2_sel, ALU_A_T__R, ALU_B_T__R, {32{1'b0}}, {32{1'b0}}, {32{1'b0}}, DIR, {32{1'b0}}, {32{1'b0}}, ROB_GEN_DA, ROB_GEN_DB
  data_select_8 data_select_8_1 (
    .D1_sel(store_controller_2_d1_sel), .D2_sel(store_controller_2_d2_sel), .in1(ALU_A_T__F),
    .in2(ALU_B_T__F), .in3({8{1'b0}}), .in4({8{1'b0}}), .in5({8{1'b0}}), .in6({8{1'b0}}), .in7({8{1'b0}}),
    .in8({8{1'b0}}), .out1(ROB_FL_A), .out2(ROB_FL_B));
  and and_99 (and_99_out, byte_I0_iv[4], byte_I0[5], byte_I0[6], byte_I0_iv[7]);
  Comparator #(.Bits(3)) comparator_3 (.a(byte_I0[2:0]), .b(3'b110), .eq(comparator_3_eq));  // open: gt, lt
  not not_15 (not_15_out, comparator_3_eq);
  and and_100 (and_100_out, byte_I0_iv[0], byte_I0_iv[1], byte_I0_iv[2], byte_I0_iv[3], byte_I0[4], byte_I0[5], byte_I0[6], byte_I0_iv[7]);
  and and_101 (and_101_out, byte_I0[0], byte_I0_iv[1], byte_I0_iv[2], byte_I0_iv[3], byte_I0[4], byte_I0[5], byte_I0[6], byte_I0_iv[7]);
  and and_102 (and_102_out, byte_I0[0], byte_I0[1], byte_I0_iv[2], byte_I0_iv[3], byte_I0[4], byte_I0[5], byte_I0[6], byte_I0_iv[7]);
  assign issue = and_99_out ? dp_e : 1'bz;  // Driver driver_154
  assign CT_ISS__URA = and_99_out ? 1'b1 : 1'bz;  // Driver driver_155
  assign CT_ISS__RA = and_99_out ? byte_I1[7:3] : 5'bz;  // Driver driver_156
  assign CT_ISS__UFL = and_99_out ? not_15_out : 1'bz;  // Driver driver_157
  assign issue = and_100_out ? dp_e : 1'bz;  // Driver driver_158
  assign CT_ISS__URA = and_100_out ? 1'b1 : 1'bz;  // Driver driver_159
  assign CT_ISS__RA = and_100_out ? byte_I1[7:3] : 5'bz;  // Driver driver_160
  assign CT_ISS__USC = and_100_out ? 1'b1 : 1'bz;  // Driver driver_161
  assign CT_ISS__OSC = and_100_out ? 1'b1 : 1'bz;  // Driver driver_162
  assign issue = and_101_out ? dp_e : 1'bz;  // Driver driver_163
  assign CT_ISS__USC = and_101_out ? 1'b1 : 1'bz;  // Driver driver_164
  assign CT_ISS__OSC = and_101_out ? 1'b1 : 1'bz;  // Driver driver_165
  assign issue = and_102_out ? dp_e : 1'bz;  // Driver driver_166
  data_select_8 data_select_8_2 (
    .D1_sel(store_controller_1_d1_sel), .D2_sel(store_controller_1_d2_sel), .in1({ALU_A_WR, ALU_A_RM}),
    .in2({ALU_B_WR, ALU_B_RM}), .in3({8{1'b0}}), .in4({8{1'b0}}), .in5({8{1'b0}}), .in6(DIR_WR),
    .in7({8{1'b0}}), .in8({8{1'b0}}), .out1(ROB_GEN_WA), .out2(ROB_GEN_WB));
  data_select_4 data_select_4_1 (
    .D1_sel(store_controller_2_d1_sel), .D2_sel(store_controller_2_d2_sel), .in1(ALU_A_INST),
    .in2(ALU_B_INST), .in3(4'b0000), .in4(4'b0000), .in5(4'b0000), .in6(4'b0000), .in7(4'b0000),
    .in8(4'b0000), .out1(ROB_FL_INSTA), .out2(ROB_FL_INSTB));
  data_select_4 data_select_4_2 (
    .D1_sel(store_controller_1_d1_sel), .D2_sel(store_controller_1_d2_sel), .in1(ALU_A_INST),
    .in2(ALU_B_INST), .in3(4'b0000), .in4(4'b0000), .in5(4'b0000), .in6(DIR_INST), .in7(4'b0000),
    .in8(4'b0000), .out1(ROB_GEN_INSTA), .out2(ROB_GEN_INSTB));
  not not_16 (not_16_out, E);
  PullDown pulldown_23 (.out(kernel_inst));
  PullDown pulldown_24 (.out(CT_RF__E));
  PullDown pulldown_25 (.out(CT_RF__DM));
  PullDown #(.Bits(5)) pulldown_26 (.out(CT_RF__WS));
  PullDown #(.Bits(3)) pulldown_27 (.out(CT_RF__WM));
  PullDown #(.Bits(5)) pulldown_28 (.out(CT_RF__RA));
  PullDown #(.Bits(3)) pulldown_29 (.out(CT_RF__MA));
  PullDown #(.Bits(5)) pulldown_30 (.out(CT_RF__RB));
  PullDown #(.Bits(3)) pulldown_31 (.out(CT_RF__MB));
  PullDown pulldown_32 (.out(CT_RF__PCSE));
  PullDown pulldown_33 (.out(CT_RF__PCJ));
  PullDown pulldown_34 (.out(CT_RF__PCR));
  PullDown #(.Bits(3)) pulldown_35 (.out(CT_RF__SCN));
  PullDown pulldown_36 (.out(CT_RF__SCD));
  PullDown pulldown_37 (.out(CT_RF__SCAS));
  PullDown pulldown_38 (.out(CT_RF__SCSE));
  PullDown pulldown_39 (.out(CT_RF__FLS));
  PullDown #(.Bits(4)) pulldown_40 (.out(4'b0001));
  PullDown #(.Bits(9)) pulldown_41 (.out(CT_ALU__CT));
  PullDown pulldown_42 (.out(CT_ALU__M));
  PullDown pulldown_43 (.out(CT_ALU__M2));
  PullDown pulldown_44 (.out(CT_BUS__IAR));
  PullDown pulldown_45 (.out(CT_BUS__IAG));
  PullDown pulldown_46 (.out(CT_BUS__IDR));
  PullDown pulldown_47 (.out(CT_BUS__IDM));
  PullDown pulldown_48 (.out(CT_BUS__DAR));
  PullDown pulldown_49 (.out(CT_BUS__DAM));
  PullDown pulldown_50 (.out(CT_BUS__DAG));
  PullDown pulldown_51 (.out(CT_BUS__DDR));
  PullDown pulldown_52 (.out(CT_BUS__DDG));
  PullDown pulldown_53 (.out(I_LD));
  PullDown pulldown_54 (.out(D_LD));
  PullDown pulldown_55 (.out(D_ST));
  PullDown #(.Bits(2)) pulldown_56 (.out(D_MD));
  PullDown pulldown_57 (.out(CT_MVR));
  // res_station res_station_1: pin names not known; wires that end beside it: C_ct, not_16_out, issue, {byte_I0, byte_I1, byte_I2, byte_I3}, epoch_IS, inst_IS, CT_ISS__URA, CT_ISS__URB, CT_ISS__RA, CT_ISS__RB, CT_ISS__USC, CT_ISS__UFL, CT_ISS__UFU, CT_ISS__ORC, CT_ISS__RC, CT_ISS__OSC, CT_ISS__OFL, com1, com2, com1_inst, com2_inst, CT_RF__R1[7:3], CT_RF__R2[7:3], CT_SC__W1, CT_SC__W2, CT_FL__W1, CT_FL__W2, clr, clr_ep, clr_id, CT_DISP, {res_station_1_p32, byte_D1, byte_D2, byte_D3}, epoch_DP, inst_DP
  PullDown pulldown_58 (.out(LD_ep));
  PullDown #(.Bits(4)) pulldown_59 (.out(LD_id));
  PullDown #(.Bits(32)) pulldown_60 (.out(LD_addr));
  PullDown pulldown_61 (.out(CT_STB__LD));
  PullDown #(.Bits(3)) pulldown_62 (.out(CT_ISS__UFU));
  PullDown pulldown_63 (.out(CT_ISS__OSTB));
  Multiplexer #(.Bits(8)) multiplexer_50 (.sel(CT_DISP), .in_0(8'h72), .in_1(res_station_1_p32), .out(byte_D0));
  PullDown pulldown_64 (.out(clr));
  PullDown pulldown_65 (.out(clr_ep));
  PullDown #(.Bits(4)) pulldown_66 (.out(clr_id));
  PullDown pulldown_67 (.out(issue));
  PullDown pulldown_68 (.out(CT_ISS__URA));
  PullDown pulldown_69 (.out(CT_ISS__URB));
  PullDown #(.Bits(5)) pulldown_70 (.out(CT_ISS__RA));
  PullDown #(.Bits(5)) pulldown_71 (.out(CT_ISS__RB));
  PullDown pulldown_72 (.out(CT_ISS__USC));
  PullDown pulldown_73 (.out(CT_ISS__UFL));
  PullDown pulldown_74 (.out(CT_ISS__ORC));
  PullDown #(.Bits(5)) pulldown_75 (.out(CT_ISS__RC));
  PullDown pulldown_76 (.out(CT_ISS__OSC));
  PullDown pulldown_77 (.out(CT_ISS__OFL));
  PullDown pulldown_78 (.out(CT_ROB__EX__E));
  PullDown pulldown_79 (.out(CT_ROB__ST__E));
  PullDown #(.Bits(3)) pulldown_80 (.out(CT_BUS__DASDN));
  PullDown pulldown_81 (.out(CT_BUS__DDM));
  PullDown pulldown_82 (.out(CT_RF__PCH));
  PullDown pulldown_83 (.out(hlt));
  PullDown pulldown_84 (.out(ex_nop));

  assign CLK_str = 1'b0;
  assign CSH_mode = 2'b00;
  assign CSH_run = 1'b0;
  assign DMA_sel = 3'b000;
  assign DMA_str = 1'b0;
  assign INT_out = 1'b0;
  assign INT_str = 1'b0;
  assign MMU_sel = 2'b00;
  assign MMU_str = 1'b0;

  // Other names for the same wires on the sheet: disp_32[31:0] = {byte_D0, byte_D1, byte_D2, byte_D3};
  //   ALU_A_WR[2:0] = ALU_A_RM; ALU_B_WR[2:0] = ALU_B_RM; ALU_R[31:0] = ALU_A_T__R; ALU_T__R[31:0] = ALU_A_T__R;
  //   imm16_2_ex[15:0] = {byte_D2_ex, byte_D3_ex}; C_i = C_dt; ext_e = cm_e; ext_e__bf = cm_e__bf; int_proc = FL[14];
  //   trap = FL[15]; issue_32[31:0] = {byte_I0, byte_I1, byte_I2, byte_I3}; issue_e = dp_e; st_e = rf_e

  // Notes on the sheet:
  //   C: Hz: 4
  //   bus_e: default 1
  //   D_MD: 0:32
  //   1:16
  //   2:8
  //   3:u.u
  //   I_valid: default 1
  //   D_valid: default 1
  //   kernal mode system
  //   interrupt system
  //   pipeline controller
  //   inst id manager
  //   tests
  //   IO pins
  //   primeary signals
  //   decode circuit
  //   ALU
  //   register
  //   program counter controller
  //   bus system
  //   register system
  //   ROB
  //   stack
  //   RAM
  //   jump
  //   call
  //   return
  //   halt
  //   stack circuit
  //   ALU system
  //   dir circuit
  //   store circuit
  //   load circuit
  //   flag circuit
  //   issue circuit
  //   control bus
endmodule
